// Logisim project exam3.circ as structural Verilog: 1 circuit, main circuit fence
module fence (
  input  [7:0] plaintext,
  input  [3:0] row,
  output [7:0] ciphertext
);

  Multiplexer #(.width(8)) multiplexer_1 (
    .in0({plaintext[7], plaintext[5], plaintext[3], plaintext[1], plaintext[6], plaintext[4], plaintext[2], plaintext[0]}),
    .in1({plaintext[7], plaintext[3], plaintext[6], plaintext[2], plaintext[5], plaintext[1], plaintext[4], plaintext[0]}),
    .out(ciphertext), .sel(row[2]));  // open: en
endmodule
