// Logisim project BlessMePassP4.circ as structural Verilog: 20 circuits, main circuit main
module main (
  input  in_1,
  output [31:0] Instr,
  output RegWrite,
  output [4:0] RegAddr,
  output [31:0] RegData,
  output MemWrite,
  output [4:0] MemAddr,
  output [31:0] MemData
);

  wire and_1_out, Branch, clock, comparator_1_eq, controller_1_alusrc, controller_1_j_jal, controller_1_jr,
       controller_1_memread, controller_1_memwrite, controller_1_regwrite, ex_mem_1_memread_o,
       ex_mem_1_memwrite_o, ex_mem_1_regwrite_o, flushE, forwardu_1_frtmsel, id_ex_1_alusrc_o,
       id_ex_1_memread_o, id_ex_1_memwrite_o, id_ex_1_regwrite_o, not_1_out, stallD, stallF;
  wire [1:0] controller_1_ext_op, controller_1_lsel, controller_1_memtoreg, controller_1_regdst,
       controller_1_ssel, d_1_tuse1_d, d_1_tuse2_d, ex_mem_1_lsel_o, ex_mem_1_memreg_o, ex_mem_1_ssel_o,
       forwardu_1_frsdsel, forwardu_1_frsesel, forwardu_1_frtdsel, forwardu_1_frtesel, id_ex_1_lsel_o,
       id_ex_1_memreg_o, id_ex_1_regdst_o, id_ex_1_ssel_o, mex_wb_1_memreg_o;
  wire [3:0] controller_1_alu_op, e_1_tnew_e, ex_mem_1_tnew_m, id_ex_1_aluop_o, mex_wb_1_tnew_w;
  wire [4:0] d_1_s1_d, d_1_s2_d, e_1_des_e, e_1_s1_e, e_1_s2_e, ex_mem_1_writereg_o, id_ex_1_rd_o,
       id_ex_1_rt_o, m_1_des_m, m_1_s2_m, multiplexer_2_out, Rd_D, Rs_D, Rt_D, w_1_des_w;
  wire [5:0] sort_1_func, sort_1_opcode;
  wire [15:0] sort_1_imm16;
  wire [31:0] alu_1_res, aluresult_M, aluresult_W, D_CMP_RS, D_CMP_RT, dm_1_rd, E_ALU_A, E_ALU_B, EtoD,
       ex_mem_1_pc_4_o, ex_mem_1_pc_o, ext_1_out_3, extresult_E, id_ex_1_pc_4_o, id_ex_1_pc_o,
       if_id_1_pc_4_o, if_id_1_pc_8_o, if_id_1_pc_o, ifu_1_pc, Instr_D, Instr_E, Instr_M, Instr_W, M_DM_WD,
       MemAddr_t, MtoD, multiplexer_1_out, npc_1_npc, pc_8_E, pc_8_M, pc_8_W, rd1, rd2, readdata_W, Rs_E,
       Rt_E, writedata_M, WtoD;

  Clock clock_1 (.out(clock));
  IFU ifu_1 (.npc(npc_1_npc), .Instr(Instr), .pc(ifu_1_pc), .StallF(stallF), .clock(clock), .reset(in_1));
  // Probe on Instr
  // Probe on ifu_1_pc
  IF_ID if_id_1 (
    .instr_i(Instr), .pc_i(ifu_1_pc), .instr_o(Instr_D), .pc_o(if_id_1_pc_o), .pc_4_o(if_id_1_pc_4_o),
    .pc_8_o(if_id_1_pc_8_o), .clock(clock), .reset(in_1), .in_5(stallD));
  // Probe on Instr_D
  and and_1 (and_1_out, Branch, comparator_1_eq);
  Sort sort_1 (
    .instrcut(Instr_D), .Opcode(sort_1_opcode), .Rs(Rs_D), .Rt(Rt_D), .Rd(Rd_D), .IMM16(sort_1_imm16),
    .Func(sort_1_func));  // open: Shamt, _26_bits_Address
  NPC npc_1 (
    .oldPC(ifu_1_pc), .ExtResult(ext_1_out_3), .ra(D_CMP_RS), .instr(Instr_D), .NPC(npc_1_npc),
    .toBranch(and_1_out), .Jump(controller_1_j_jal), .Jr(controller_1_jr));
  not not_1 (not_1_out, clock);
  EXT ext_1 (.EXTop(controller_1_ext_op), .IMM16(sort_1_imm16), .out_3(ext_1_out_3));
  GRF grf_1 (
    .A1(Rs_D), .A2(Rt_D), .A3(RegAddr), .WD(RegData), .RD1(rd1), .RD2(rd2), .clk(not_1_out), .reset(in_1),
    .we(RegWrite));
  Controller controller_1 (
    .op(sort_1_opcode), .funct(sort_1_func), .RegWrite(controller_1_regwrite),
    .MemWrite(controller_1_memwrite), .MemRead(controller_1_memread), .MemtoReg(controller_1_memtoreg),
    .Alusrc(controller_1_alusrc), .Alu_op(controller_1_alu_op), .Branch(Branch), .j_jal(controller_1_j_jal),
    .jr(controller_1_jr), .Regdst(controller_1_regdst), .ext_op(controller_1_ext_op),
    .Ssel(controller_1_ssel), .Lsel(controller_1_lsel));
  Comparator #(.width(32)) comparator_1 (.a(D_CMP_RS), .b(D_CMP_RT), .eq(comparator_1_eq));  // open: gt, lt
  ID_EX id_ex_1 (
    .MemWrite_i(controller_1_memwrite), .RD1_i(D_CMP_RS), .RD2_i(D_CMP_RT), .MemRead_i(controller_1_memread),
    .rs_i(Rs_D), .MemReg_i(controller_1_memtoreg), .rt_i(Rt_D), .rd_i(Rd_D), .ALUop(controller_1_alu_op),
    .extresult_i(ext_1_out_3), .ALUSrc_i(controller_1_alusrc), .instr_i(Instr_D),
    .RegWrite_i(controller_1_regwrite), .RegDst_i(controller_1_regdst), .pc_i(if_id_1_pc_o),
    .pc_4_i(if_id_1_pc_4_o), .pc_8_i(if_id_1_pc_8_o), .Ssel_i(controller_1_ssel), .Lsel_i(controller_1_lsel),
    .MemWrite_o(id_ex_1_memwrite_o), .RD1_o(Rs_E), .RD2_o(Rt_E), .MemRead_o(id_ex_1_memread_o),
    .MemReg_o(id_ex_1_memreg_o), .rt_o(id_ex_1_rt_o), .rd_o(id_ex_1_rd_o), .ALUop_o(id_ex_1_aluop_o),
    .extresult_o(extresult_E), .ALUSrc_o(id_ex_1_alusrc_o), .instr_o(Instr_E),
    .RegWrite_o(id_ex_1_regwrite_o), .RegDst_o(id_ex_1_regdst_o), .pc_o(id_ex_1_pc_o),
    .pc_4_o(id_ex_1_pc_4_o), .pc_8_o(pc_8_E), .Ssel_o(id_ex_1_ssel_o), .Lsel_o(id_ex_1_lsel_o),
    .clock(clock), .reset(in_1), .flush(flushE));  // open: rs_o
  // Probe on Instr_E
  Multiplexer #(.width(32), .enable("false")) multiplexer_1 (
    .in0(E_ALU_B), .in1(extresult_E), .out(multiplexer_1_out), .sel(id_ex_1_alusrc_o));
  Multiplexer #(.select(2), .width(5), .enable("false")) multiplexer_2 (
    .in0(id_ex_1_rt_o), .in1(id_ex_1_rd_o), .in2({5{1'b1}}), .out(multiplexer_2_out), .sel(id_ex_1_regdst_o));  // open: in3
  Multiplexer #(.select(2), .width(32), .enable("false")) multiplexer_3 (
    .in0(rd1), .in1(EtoD), .in2(MtoD), .in3({32{1'b0}}), .out(D_CMP_RS), .sel(forwardu_1_frsdsel));
  ALU alu_1 (.A(E_ALU_A), .B(multiplexer_1_out), .ALUop(id_ex_1_aluop_o), .RES(alu_1_res));
  D d_1 (.in_1(Instr_D), .s1_D(d_1_s1_d), .s2_D(d_1_s2_d), .tuse1_D(d_1_tuse1_d), .tuse2_D(d_1_tuse2_d));
  E e_1 (
    .in_1(Instr_E), .pc_8(pc_8_E), .extresult(extresult_E), .s1_E(e_1_s1_e), .s2_E(e_1_s2_e),
    .des_E(e_1_des_e), .tnew_E(e_1_tnew_e), .toD(EtoD));
  M m_1 (.in_1(Instr_M), .pc_8(pc_8_M), .aluresult(aluresult_M), .s2_M(m_1_s2_m), .des_M(m_1_des_m), .toD(MtoD));
  W w_1 (.in_1(Instr_W), .RD(readdata_W), .pc_8(pc_8_W), .aluresult(aluresult_W), .des_W(w_1_des_w), .toD(WtoD));
  Multiplexer #(.select(2), .width(32), .enable("false")) multiplexer_4 (
    .in0(rd2), .in1(EtoD), .in2(MtoD), .in3({32{1'b0}}), .out(D_CMP_RT), .sel(forwardu_1_frtdsel));
  EX_MEM ex_mem_1 (
    .MemWrite_i(id_ex_1_memwrite_o), .MemRead_i(id_ex_1_memread_o), .MemReg_i(id_ex_1_memreg_o),
    .RegWrite_i(id_ex_1_regwrite_o), .aluresult_i(alu_1_res), .Ssel_i(id_ex_1_ssel_o), .writedata_i(E_ALU_B),
    .Lsel_i(id_ex_1_lsel_o), .writereg_i(multiplexer_2_out), .tnew_E(e_1_tnew_e), .pc_i(id_ex_1_pc_o),
    .pc_4_i(id_ex_1_pc_4_o), .pc_8_i(pc_8_E), .instr_i(Instr_E), .MemWrite_o(ex_mem_1_memwrite_o),
    .MemRead_o(ex_mem_1_memread_o), .MemReg_o(ex_mem_1_memreg_o), .RegWrite_o(ex_mem_1_regwrite_o),
    .aluresult_o(aluresult_M), .Ssel_o(ex_mem_1_ssel_o), .writedata_o(writedata_M), .Lsel_o(ex_mem_1_lsel_o),
    .writereg_o(ex_mem_1_writereg_o), .tnew_M(ex_mem_1_tnew_m), .pc_o(ex_mem_1_pc_o),
    .pc_4_o(ex_mem_1_pc_4_o), .pc_8_o(pc_8_M), .instr_o(Instr_M), .clock(clock), .reset(in_1));
  // Probe on Instr_M
  forwardU forwardu_1 (
    .s1_D(d_1_s1_d), .s2_D(d_1_s2_d), .s1_E(e_1_s1_e), .s2_E(e_1_s2_e), .des_E(e_1_des_e),
    .tNew_E(e_1_tnew_e), .s2_M(m_1_s2_m), .tNew_M(ex_mem_1_tnew_m), .des_M(m_1_des_m),
    .tNew_W(mex_wb_1_tnew_w), .des_W(w_1_des_w), .fRsDsel(forwardu_1_frsdsel), .fRtDsel(forwardu_1_frtdsel),
    .fRsEsel(forwardu_1_frsesel), .fRtEsel(forwardu_1_frtesel), .fRtMsel(forwardu_1_frtmsel));
  DM dm_1 (
    .MemAddr(aluresult_M), .MemWrite(ex_mem_1_memwrite_o), .clock(clock), .Lsel(ex_mem_1_lsel_o),
    .Reset(in_1), .WD(M_DM_WD), .Ssel(ex_mem_1_ssel_o), .RD(dm_1_rd), .MemRead(ex_mem_1_memread_o));
  Multiplexer #(.select(2), .width(32), .enable("false")) multiplexer_5 (
    .in0(Rs_E), .in1(MtoD), .in2(WtoD), .in3({32{1'b0}}), .out(E_ALU_A), .sel(forwardu_1_frsesel));
  Multiplexer #(.select(2), .width(32), .enable("false")) multiplexer_6 (
    .in0(Rt_E), .in1(MtoD), .in2(WtoD), .in3({32{1'b0}}), .out(E_ALU_B), .sel(forwardu_1_frtesel));
  Multiplexer #(.width(32), .enable("false")) multiplexer_7 (
    .in0(writedata_M), .in1(WtoD), .out(M_DM_WD), .sel(forwardu_1_frtmsel));
  MEX_WB mex_wb_1 (
    .MemReg_i(ex_mem_1_memreg_o), .RegWrite_i(ex_mem_1_regwrite_o), .writereg_i(ex_mem_1_writereg_o),
    .aluresult_i(aluresult_M), .writedata_i(writedata_M), .readdata_i(dm_1_rd), .tnew_M(ex_mem_1_tnew_m),
    .pc_i(ex_mem_1_pc_o), .pc_4_i(ex_mem_1_pc_4_o), .pc_8_i(pc_8_M), .instr_i(Instr_M),
    .memaddr(aluresult_M), .memdata(M_DM_WD), .MemReg_o(mex_wb_1_memreg_o), .RegWrite_o(RegWrite),
    .writereg_o(RegAddr), .aluresult_o(aluresult_W), .readdata_o(readdata_W), .tnew_W(mex_wb_1_tnew_w),
    .pc_8_o(pc_8_W), .instr_o(Instr_W), .memaddr_2({MemAddr_t[31:7], MemAddr, MemAddr_t[1:0]}),
    .memdata_2(MemData), .clock(clock), .reset(in_1), .MemWrite_o(MemWrite), .MemWrite_i(ex_mem_1_memwrite_o));  // open: writedata_o, pc_o, pc_4_o
  stallU stallu_1 (
    .s1_D(d_1_s1_d), .s2_D(d_1_s2_d), .tUse1_D(d_1_tuse1_d), .tUse2_D(d_1_tuse2_d), .des_E(e_1_des_e),
    .tNew_E(e_1_tnew_e), .tNew_M(ex_mem_1_tnew_m), .des_M(m_1_des_m), .Stall_F(stallF), .Stall_D(stallD),
    .flush_E(flushE));
  // Probe on Instr_W
  Multiplexer #(.select(2), .width(32), .enable("false")) multiplexer_8 (
    .in0(aluresult_W), .in1(readdata_W), .in2(pc_8_W), .out(RegData), .sel(mex_wb_1_memreg_o));  // open: in3
  // AND_Gate and_2 is placed but not wired

  // Other names for the same wires on the sheet: MemAddr_t[6:2] = MemAddr; reset = in_1
endmodule

module GRF (
  input  [4:0] A1,
  input  clk,
  input  reset,
  input  we,
  input  [4:0] A2,
  input  [4:0] A3,
  input  [31:0] WD,
  output [31:0] RD1,
  output [31:0] RD2
);

  wire [31:0] I0, I1, I2, I3, I4, I5, I6, I7, I8, I9, I10, I11, I12, I13, I14, I15, I16, I17, I18, I19, I20,
       I21, I22, I23, I24, I25, I26, I27, I28, I29, I30, I31, O0, O1, O2, O3, O4, O5, O6, O7, O8, O9, O10,
       O11, O12, O13, O14, O15, O16, O17, O18, O19, O20, O21, O22, O23, O24, O25, O26, O27, O28, O29, O30,
       O31;

  Demultiplexer #(.select(5), .width(32), .tristate("true")) demultiplexer_1 (
    .out0(I0), .out1(I1), .out2(I2), .out3(I3), .out4(I4), .out5(I5), .out6(I6), .out7(I7), .out8(I8),
    .out9(I9), .out10(I10), .out11(I11), .out12(I12), .out13(I13), .out14(I14), .out15(I15), .out16(I16),
    .out17(I17), .out18(I18), .out19(I19), .out20(I20), .out21(I21), .out22(I22), .out23(I23), .out24(I24),
    .out25(I25), .out26(I26), .out27(I27), .out28(I28), .out29(I29), .out30(I30), .out31(I31), .in(WD),
    .sel(A3));  // open: en
  Multiplexer #(.select(5), .width(32)) multiplexer_1 (
    .in0(O0), .in1(O1), .in2(O2), .in3(O3), .in4(O4), .in5(O5), .in6(O6), .in7(O7), .in8(O8), .in9(O9),
    .in10(O10), .in11(O11), .in12(O12), .in13(O13), .in14(O14), .in15(O15), .in16(O16), .in17(O17),
    .in18(O18), .in19(O19), .in20(O20), .in21(O21), .in22(O22), .in23(O23), .in24(O24), .in25(O25),
    .in26(O26), .in27(O27), .in28(O28), .in29(O29), .in30(O30), .in31(O31), .out(RD2), .sel(A2));  // open: en
  Multiplexer #(.select(5), .width(32)) multiplexer_2 (
    .in0(O0), .in1(O1), .in2(O2), .in3(O3), .in4(O4), .in5(O5), .in6(O6), .in7(O7), .in8(O8), .in9(O9),
    .in10(O10), .in11(O11), .in12(O12), .in13(O13), .in14(O14), .in15(O15), .in16(O16), .in17(O17),
    .in18(O18), .in19(O19), .in20(O20), .in21(O21), .in22(O22), .in23(O23), .in24(O24), .in25(O25),
    .in26(O26), .in27(O27), .in28(O28), .in29(O29), .in30(O30), .in31(O31), .out(RD1), .sel(A1));  // open: en
  Register #(.width(32)) register_1 (.D({32{1'b0}}), .en(we), .Q(O0), .clk(clk), .clr(reset));
  Register #(.width(32)) register_2 (.D(I8), .en(we), .Q(O8), .clk(clk), .clr(reset));
  Register #(.width(32)) register_3 (.D(I16), .en(we), .Q(O16), .clk(clk), .clr(reset));
  Register #(.width(32)) register_4 (.D(I24), .en(we), .Q(O24), .clk(clk), .clr(reset));
  Register #(.width(32)) register_5 (.D(I1), .en(we), .Q(O1), .clk(clk), .clr(reset));
  Register #(.width(32)) register_6 (.D(I9), .en(we), .Q(O9), .clk(clk), .clr(reset));
  Register #(.width(32)) register_7 (.D(I17), .en(we), .Q(O17), .clk(clk), .clr(reset));
  Register #(.width(32)) register_8 (.D(I25), .en(we), .Q(O25), .clk(clk), .clr(reset));
  Register #(.width(32)) register_9 (.D(I2), .en(we), .Q(O2), .clk(clk), .clr(reset));
  Register #(.width(32)) register_10 (.D(I10), .en(we), .Q(O10), .clk(clk), .clr(reset));
  Register #(.width(32)) register_11 (.D(I18), .en(we), .Q(O18), .clk(clk), .clr(reset));
  Register #(.width(32)) register_12 (.D(I26), .en(we), .Q(O26), .clk(clk), .clr(reset));
  Register #(.width(32)) register_13 (.D(I3), .en(we), .Q(O3), .clk(clk), .clr(reset));
  Register #(.width(32)) register_14 (.D(I11), .en(we), .Q(O11), .clk(clk), .clr(reset));
  Register #(.width(32)) register_15 (.D(I19), .en(we), .Q(O19), .clk(clk), .clr(reset));
  Register #(.width(32)) register_16 (.D(I27), .en(we), .Q(O27), .clk(clk), .clr(reset));
  Register #(.width(32)) register_17 (.D(I4), .en(we), .Q(O4), .clk(clk), .clr(reset));
  Register #(.width(32)) register_18 (.D(I12), .en(we), .Q(O12), .clk(clk), .clr(reset));
  Register #(.width(32)) register_19 (.D(I20), .en(we), .Q(O20), .clk(clk), .clr(reset));
  Register #(.width(32)) register_20 (.D(I28), .en(we), .Q(O28), .clk(clk), .clr(reset));
  Register #(.width(32)) register_21 (.D(I5), .en(we), .Q(O5), .clk(clk), .clr(reset));
  Register #(.width(32)) register_22 (.D(I13), .en(we), .Q(O13), .clk(clk), .clr(reset));
  Register #(.width(32)) register_23 (.D(I21), .en(we), .Q(O21), .clk(clk), .clr(reset));
  Register #(.width(32)) register_24 (.D(I29), .en(we), .Q(O29), .clk(clk), .clr(reset));
  Register #(.width(32)) register_25 (.D(I6), .en(we), .Q(O6), .clk(clk), .clr(reset));
  Register #(.width(32)) register_26 (.D(I14), .en(we), .Q(O14), .clk(clk), .clr(reset));
  Register #(.width(32)) register_27 (.D(I22), .en(we), .Q(O22), .clk(clk), .clr(reset));
  Register #(.width(32)) register_28 (.D(I30), .en(we), .Q(O30), .clk(clk), .clr(reset));
  Register #(.width(32)) register_29 (.D(I7), .en(we), .Q(O7), .clk(clk), .clr(reset));
  Register #(.width(32)) register_30 (.D(I15), .en(we), .Q(O15), .clk(clk), .clr(reset));
  Register #(.width(32)) register_31 (.D(I23), .en(we), .Q(O23), .clk(clk), .clr(reset));
  Register #(.width(32)) register_32 (.D(I31), .en(we), .Q(O31), .clk(clk), .clr(reset));
endmodule

module IFU (
  input  [31:0] npc,
  input  clock,
  input  reset,
  input  StallF,
  output [31:0] Instr,
  output [31:0] pc
);

  wire comparator_1_eq, not_1_out;
  wire [31:0] register_1_q, subtractor_1_out;

  not not_1 (not_1_out, StallF);
  Register #(.width(32)) register_1 (.D(npc), .en(not_1_out), .Q(register_1_q), .clk(clock), .clr(reset));
  Comparator #(.width(32)) comparator_1 (.a({32{1'b0}}), .b(register_1_q), .eq(comparator_1_eq));  // open: gt, lt
  Multiplexer #(.width(32), .enable("false")) multiplexer_1 (
    .in0(register_1_q), .in1(32'h3000), .out(pc), .sel(comparator_1_eq));
  Subtractor #(.width(32)) subtractor_1 (.a(pc), .b(32'h3000), .out(subtractor_1_out));  // open: bin, bout
  ROM #(.addrWidth(10), .dataWidth(32)) rom_1 (.addr(subtractor_1_out[11:2]), .data(Instr));  // open: sel
endmodule

module Sort (
  input  [31:0] instrcut,
  output [5:0] Opcode,
  output [4:0] Rs,
  output [4:0] Rt,
  output [4:0] Rd,
  output [4:0] Shamt,
  output [15:0] IMM16,
  output [5:0] Func,
  output [25:0] _26_bits_Address
);


  assign _26_bits_Address = instrcut[25:0];
  assign Func = instrcut[5:0];
  assign IMM16 = instrcut[15:0];
  assign Opcode = instrcut[31:26];
  assign Rd = instrcut[15:11];
  assign Rs = instrcut[25:21];
  assign Rt = instrcut[20:16];
  assign Shamt = instrcut[10:6];
endmodule

module OpFunc (
  input  [5:0] funct,
  input  [5:0] op,
  output out_3,
  output out_4,
  output out_5,
  output out_6,
  output out_7,
  output out_8,
  output out_9,
  output out_10,
  output out_11,
  output out_12,
  output out_13,
  output out_14,
  output out_15,
  output out_16,
  output out_17,
  output out_18,
  output out_19,
  output CAL_R,
  output CAL_I,
  output B_TYPE,
  output STR,
  output LD
);

  wire not_1_out, not_2_out, not_3_out, not_4_out, not_5_out, not_6_out, not_7_out, not_8_out, not_9_out,
       not_10_out, not_11_out, not_12_out, R;

  not not_1 (not_1_out, op[5]);
  not not_2 (not_2_out, op[4]);
  or u_CAL_R (CAL_R, out_9, out_10);
  or u_CAL_I (CAL_I, out_14, out_5);
  or u_B_TYPE (B_TYPE, out_19, out_7);
  or u_STR (STR, out_15, out_16, out_4);
  or u_LD (LD, out_17, out_18, out_3);
  not not_3 (not_3_out, op[3]);
  not not_4 (not_4_out, op[2]);
  not not_5 (not_5_out, op[1]);
  not not_6 (not_6_out, op[0]);
  and and_1 (out_3, op[5], not_2_out, not_3_out, not_4_out, op[1], op[0]);
  and and_2 (out_4, op[5], not_2_out, op[3], not_4_out, op[1], op[0]);
  and and_3 (R, not_1_out, not_2_out, not_3_out, not_4_out, not_5_out, not_6_out);
  and and_4 (out_5, not_1_out, not_2_out, op[3], op[2], not_5_out, op[0]);
  and and_5 (out_6, not_1_out, not_2_out, not_3_out, not_4_out, op[1], not_6_out);
  and and_6 (out_7, not_1_out, not_2_out, not_3_out, op[2], not_5_out, not_6_out);
  and and_7 (out_8, not_1_out, not_2_out, op[3], op[2], op[1], op[0]);
  and and_8 (out_13, not_1_out, not_2_out, not_3_out, not_4_out, op[1], op[0]);
  and and_9 (out_15, op[5], not_2_out, op[3], not_4_out, not_5_out, not_6_out);
  and and_10 (out_14, not_1_out, not_2_out, op[3], not_4_out, not_5_out, op[0]);
  and and_11 (out_16, op[5], not_2_out, op[3], not_4_out, not_5_out, op[0]);
  and and_12 (out_17, op[5], not_2_out, not_3_out, not_4_out, not_5_out, not_6_out);
  and and_13 (out_18, op[5], not_2_out, not_3_out, not_4_out, not_5_out, op[0]);
  and and_14 (out_19, not_1_out, not_2_out, not_3_out, op[2], not_5_out, op[0]);
  not not_7 (not_7_out, funct[5]);
  not not_8 (not_8_out, funct[4]);
  not not_9 (not_9_out, funct[2]);
  not not_10 (not_10_out, funct[3]);
  not not_11 (not_11_out, funct[1]);
  not not_12 (not_12_out, funct[0]);
  and and_15 (out_9, R, funct[5], not_8_out, not_10_out, not_9_out, not_11_out, funct[0]);
  and and_16 (out_10, R, funct[5], not_8_out, not_10_out, not_9_out, funct[1], funct[0]);
  and and_17 (out_11, R, not_7_out, not_8_out, not_10_out, not_9_out, not_11_out, not_12_out);
  and and_18 (out_12, R, not_7_out, not_8_out, funct[3], not_9_out, not_11_out, not_12_out);

  // Other names for the same wires on the sheet: addiu = out_14; addu = out_9; beq = out_7; bne = out_19; j = out_6;
  //   jal = out_13; jr = out_12; lb = out_17; lh = out_18; lui = out_8; lw = out_3; nop = out_11; ori = out_5;
  //   sb = out_15; sh = out_16; subu = out_10; sw = out_4

  // Notes on the sheet:
  //   B_TYPE暂时别动，可能有隐患！
endmodule

module Controller (
  input  [5:0] op,
  input  [5:0] funct,
  output [1:0] Ssel,
  output RegWrite,
  output [1:0] Lsel,
  output MemWrite,
  output MemRead,
  output [1:0] MemtoReg,
  output Alusrc,
  output [3:0] Alu_op,
  output Branch,
  output j_jal,
  output jr,
  output [1:0] Regdst,
  output [1:0] ext_op
);

  wire addiu, addu, B_TYPE, bne, CAL_I, CAL_R, j, LD, lw, nop, or_1_out, ori, STR, subu, sw;

  OpFunc opfunc_1 (
    .out_3(lw), .out_4(sw), .out_5(ori), .out_6(j), .out_7(Branch), .out_8(ext_op[1]), .out_9(addu),
    .out_10(subu), .out_11(nop), .out_12(jr), .out_13(MemtoReg[1]), .out_14(addiu), .out_15(Ssel[0]),
    .out_16(Ssel[1]), .out_17(Lsel[0]), .out_18(Lsel[1]), .out_19(bne), .op(op), .funct(funct),
    .CAL_R(CAL_R), .CAL_I(CAL_I), .B_TYPE(B_TYPE), .STR(STR), .LD(LD));
  or or_1 (or_1_out, Ssel[1], Ssel[0]);
  or or_2 (MemRead, or_1_out, LD);
  buf or_3 (MemtoReg[0], LD);  // OR_Gate
  buf or_4 (MemWrite, STR);  // OR_Gate
  or or_5 (Alu_op[0], subu, Branch);
  buf or_6 (Alu_op[1], ori);  // OR_Gate
  or or_7 (j_jal, j, MemtoReg[1]);
  buf or_8 (Regdst[0], CAL_R);  // OR_Gate
  or or_9 (ext_op[0], addiu, Branch, LD, STR);
  or or_10 (RegWrite, LD, ext_op[1], CAL_R, CAL_I, MemtoReg[1]);
  or or_11 (Alusrc, ext_op[1], CAL_I, LD, STR);

  assign Alu_op[3:2] = 2'b00;
  assign Regdst[1] = MemtoReg[1];

  // Other names for the same wires on the sheet: beq = Branch; lui = ext_op[1]; lb = Lsel[0]; lh = Lsel[1];
  //   jal = MemtoReg[1]; sb = Ssel[0]; sh = Ssel[1]

  // Notes on the sheet:
  //   不可用类型处理
  //   这里不可以用类型来处理！
endmodule

module EXT (
  input  [1:0] EXTop,
  input  [15:0] IMM16,
  output [31:0] out_3
);

  wire [31:0] bit_extender_1_out, bit_extender_2_out, shifter_1_out;

  assign bit_extender_1_out = {{16{1'b0}}, IMM16};  // Bit_Extender bit_extender_1
  assign bit_extender_2_out = {{16{IMM16[15]}}, IMM16};  // Bit_Extender bit_extender_2
  Shifter #(.width(32)) shifter_1 (.in(bit_extender_1_out), .\dist (5'b10000), .out(shifter_1_out));
  Multiplexer #(.select(2), .width(32), .enable("false")) multiplexer_1 (
    .in0(bit_extender_1_out), .in1(bit_extender_2_out), .in2(shifter_1_out), .out(out_3), .sel(EXTop));  // open: in3
endmodule

module forwardU (
  input  [4:0] s1_D,
  input  [4:0] s2_D,
  input  [4:0] s1_E,
  input  [4:0] s2_E,
  input  [4:0] des_E,
  input  [3:0] tNew_E,
  input  [4:0] s2_M,
  input  [3:0] tNew_M,
  input  [4:0] des_M,
  input  [3:0] tNew_W,
  input  [4:0] des_W,
  output [1:0] fRsDsel,
  output [1:0] fRtDsel,
  output [1:0] fRsEsel,
  output [1:0] fRtEsel,
  output fRtMsel
);

  wire and_1_out, and_2_out, and_3_out, and_4_out, and_5_out, and_6_out, and_7_out, and_8_out, and_9_out,
       comparator_1_eq, comparator_2_eq, comparator_3_eq, comparator_4_eq, comparator_5_eq, comparator_6_eq,
       comparator_7_eq, comparator_8_eq, comparator_9_eq, comparator_10_eq, comparator_11_eq,
       comparator_12_eq, comparator_13_eq, comparator_14_eq, comparator_15_eq, comparator_16_eq,
       comparator_17_eq, comparator_18_eq, comparator_19_eq, comparator_20_eq, comparator_21_eq,
       comparator_22_eq, comparator_23_eq, comparator_24_eq, comparator_25_eq, comparator_26_eq,
       comparator_27_eq, not_1_out, not_2_out, not_3_out, not_4_out, not_5_out, not_6_out, not_7_out,
       not_8_out, not_9_out;
  wire [1:0] multiplexer_1_out, multiplexer_2_out, multiplexer_5_out, multiplexer_6_out;

  not not_1 (not_1_out, comparator_1_eq);
  Comparator #(.width(5), .mode("unsigned")) comparator_1 (
    .a(s1_D), .b({5{1'b0}}), .eq(comparator_1_eq));  // open: gt, lt
  Comparator #(.width(5), .mode("unsigned")) comparator_2 (.a(s1_D), .b(des_M), .eq(comparator_2_eq));  // open: gt, lt
  Comparator #(.width(4), .mode("unsigned")) comparator_3 (
    .a(tNew_M), .b(4'b0000), .eq(comparator_3_eq));  // open: gt, lt
  Comparator #(.width(5), .mode("unsigned")) comparator_4 (
    .a(s1_D), .b({5{1'b0}}), .eq(comparator_4_eq));  // open: gt, lt
  not not_2 (not_2_out, comparator_4_eq);
  Comparator #(.width(5), .mode("unsigned")) comparator_5 (.a(s1_D), .b(des_E), .eq(comparator_5_eq));  // open: gt, lt
  Comparator #(.width(4), .mode("unsigned")) comparator_6 (
    .a(tNew_E), .b(4'b0000), .eq(comparator_6_eq));  // open: gt, lt
  Comparator #(.width(5), .mode("unsigned")) comparator_7 (
    .a(s2_D), .b({5{1'b0}}), .eq(comparator_7_eq));  // open: gt, lt
  Comparator #(.width(5), .mode("unsigned")) comparator_8 (.a(s2_D), .b(des_M), .eq(comparator_8_eq));  // open: gt, lt
  Comparator #(.width(4), .mode("unsigned")) comparator_9 (
    .a(tNew_M), .b(4'b0000), .eq(comparator_9_eq));  // open: gt, lt
  Comparator #(.width(5), .mode("unsigned")) comparator_10 (
    .a(s2_D), .b({5{1'b0}}), .eq(comparator_10_eq));  // open: gt, lt
  Comparator #(.width(5), .mode("unsigned")) comparator_11 (
    .a(s2_D), .b(des_E), .eq(comparator_11_eq));  // open: gt, lt
  Comparator #(.width(4), .mode("unsigned")) comparator_12 (
    .a(tNew_E), .b(4'b0000), .eq(comparator_12_eq));  // open: gt, lt
  and and_1 (and_1_out, not_1_out, comparator_2_eq, comparator_3_eq);
  and and_2 (and_2_out, not_2_out, comparator_5_eq, comparator_6_eq);
  not not_3 (not_3_out, comparator_7_eq);
  not not_4 (not_4_out, comparator_10_eq);
  Multiplexer #(.width(2)) multiplexer_1 (
    .in0(2'b00), .in1(2'b10), .out(multiplexer_1_out), .sel(and_1_out));  // open: en
  and and_3 (and_3_out, not_3_out, comparator_8_eq, comparator_9_eq);
  and and_4 (and_4_out, not_4_out, comparator_11_eq, comparator_12_eq);
  Multiplexer #(.width(2)) multiplexer_2 (
    .in0(2'b00), .in1(2'b10), .out(multiplexer_2_out), .sel(and_3_out));  // open: en
  Multiplexer #(.width(2)) multiplexer_3 (
    .in0(multiplexer_1_out), .in1(2'b01), .out(fRsDsel), .sel(and_2_out));  // open: en
  Multiplexer #(.width(2)) multiplexer_4 (
    .in0(multiplexer_2_out), .in1(2'b01), .out(fRtDsel), .sel(and_4_out));  // open: en
  Comparator #(.width(5), .mode("unsigned")) comparator_13 (
    .a(s1_E), .b({5{1'b0}}), .eq(comparator_13_eq));  // open: gt, lt
  Comparator #(.width(5), .mode("unsigned")) comparator_14 (
    .a(s1_E), .b(des_W), .eq(comparator_14_eq));  // open: gt, lt
  Comparator #(.width(4), .mode("unsigned")) comparator_15 (
    .a(tNew_W), .b(4'b0000), .eq(comparator_15_eq));  // open: gt, lt
  Comparator #(.width(5), .mode("unsigned")) comparator_16 (
    .a(s1_E), .b({5{1'b0}}), .eq(comparator_16_eq));  // open: gt, lt
  Comparator #(.width(5), .mode("unsigned")) comparator_17 (
    .a(s1_E), .b(des_M), .eq(comparator_17_eq));  // open: gt, lt
  Comparator #(.width(4), .mode("unsigned")) comparator_18 (
    .a(tNew_M), .b(4'b0000), .eq(comparator_18_eq));  // open: gt, lt
  Comparator #(.width(5), .mode("unsigned")) comparator_19 (
    .a(s2_E), .b({5{1'b0}}), .eq(comparator_19_eq));  // open: gt, lt
  Comparator #(.width(5), .mode("unsigned")) comparator_20 (
    .a(s2_E), .b(des_W), .eq(comparator_20_eq));  // open: gt, lt
  Comparator #(.width(4), .mode("unsigned")) comparator_21 (
    .a(tNew_W), .b(4'b0000), .eq(comparator_21_eq));  // open: gt, lt
  Comparator #(.width(5), .mode("unsigned")) comparator_22 (
    .a(s2_E), .b({5{1'b0}}), .eq(comparator_22_eq));  // open: gt, lt
  Comparator #(.width(5), .mode("unsigned")) comparator_23 (
    .a(s2_E), .b(des_M), .eq(comparator_23_eq));  // open: gt, lt
  Comparator #(.width(4), .mode("unsigned")) comparator_24 (
    .a(tNew_M), .b(4'b0000), .eq(comparator_24_eq));  // open: gt, lt
  not not_5 (not_5_out, comparator_13_eq);
  not not_6 (not_6_out, comparator_16_eq);
  not not_7 (not_7_out, comparator_19_eq);
  not not_8 (not_8_out, comparator_22_eq);
  and and_5 (and_5_out, not_5_out, comparator_14_eq, comparator_15_eq);
  and and_6 (and_6_out, not_6_out, comparator_17_eq, comparator_18_eq);
  and and_7 (and_7_out, not_7_out, comparator_20_eq, comparator_21_eq);
  and and_8 (and_8_out, not_8_out, comparator_23_eq, comparator_24_eq);
  Multiplexer #(.width(2)) multiplexer_5 (
    .in0(2'b00), .in1(2'b10), .out(multiplexer_5_out), .sel(and_5_out));  // open: en
  Multiplexer #(.width(2)) multiplexer_6 (
    .in0(2'b00), .in1(2'b10), .out(multiplexer_6_out), .sel(and_7_out));  // open: en
  Multiplexer #(.width(2)) multiplexer_7 (
    .in0(multiplexer_5_out), .in1(2'b01), .out(fRsEsel), .sel(and_6_out));  // open: en
  Multiplexer #(.width(2)) multiplexer_8 (
    .in0(multiplexer_6_out), .in1(2'b01), .out(fRtEsel), .sel(and_8_out));  // open: en
  Comparator #(.width(5), .mode("unsigned")) comparator_25 (
    .a(s2_M), .b({5{1'b0}}), .eq(comparator_25_eq));  // open: gt, lt
  not not_9 (not_9_out, comparator_25_eq);
  Comparator #(.width(5), .mode("unsigned")) comparator_26 (
    .a(s2_M), .b(des_W), .eq(comparator_26_eq));  // open: gt, lt
  Comparator #(.width(4), .mode("unsigned")) comparator_27 (
    .a(tNew_W), .b(4'b0000), .eq(comparator_27_eq));  // open: gt, lt
  and and_9 (and_9_out, not_9_out, comparator_26_eq, comparator_27_eq);
  Multiplexer multiplexer_9 (.in0(1'b0), .in1(1'b1), .out(fRtMsel), .sel(and_9_out));  // open: en
endmodule

module stallU (
  input  [4:0] s1_D,
  input  [4:0] s2_D,
  input  [1:0] tUse1_D,
  input  [1:0] tUse2_D,
  input  [4:0] des_E,
  input  [3:0] tNew_E,
  input  [3:0] tNew_M,
  input  [4:0] des_M,
  output Stall_F,
  output Stall_D,
  output flush_E
);

  wire and_1_out, and_2_out, and_3_out, and_4_out, comparator_1_eq, comparator_2_eq, comparator_3_lt,
       comparator_4_eq, comparator_5_eq, comparator_6_lt, comparator_7_eq, comparator_8_eq, comparator_9_lt,
       comparator_10_eq, comparator_11_eq, comparator_12_lt, not_1_out, not_2_out, not_3_out, not_4_out;
  wire [3:0] tUse1_D_t, tUse2_D_t;

  Comparator #(.width(5), .mode("unsigned")) comparator_1 (
    .a(s1_D), .b({5{1'b0}}), .eq(comparator_1_eq));  // open: gt, lt
  Comparator #(.width(5), .mode("unsigned")) comparator_2 (.a(s1_D), .b(des_E), .eq(comparator_2_eq));  // open: gt, lt
  Comparator #(.width(4), .mode("unsigned")) comparator_3 (
    .a(tUse1_D_t), .b(tNew_E), .lt(comparator_3_lt));  // open: gt, eq
  Comparator #(.width(5), .mode("unsigned")) comparator_4 (
    .a(s2_D), .b({5{1'b0}}), .eq(comparator_4_eq));  // open: gt, lt
  Comparator #(.width(5), .mode("unsigned")) comparator_5 (.a(s2_D), .b(des_E), .eq(comparator_5_eq));  // open: gt, lt
  Comparator #(.width(4), .mode("unsigned")) comparator_6 (
    .a(tUse2_D_t), .b(tNew_E), .lt(comparator_6_lt));  // open: gt, eq
  Comparator #(.width(5), .mode("unsigned")) comparator_7 (
    .a(s1_D), .b({5{1'b0}}), .eq(comparator_7_eq));  // open: gt, lt
  Comparator #(.width(5), .mode("unsigned")) comparator_8 (.a(s1_D), .b(des_M), .eq(comparator_8_eq));  // open: gt, lt
  Comparator #(.width(4), .mode("unsigned")) comparator_9 (
    .a(tUse1_D_t), .b(tNew_M), .lt(comparator_9_lt));  // open: gt, eq
  Comparator #(.width(5), .mode("unsigned")) comparator_10 (
    .a(s2_D), .b({5{1'b0}}), .eq(comparator_10_eq));  // open: gt, lt
  Comparator #(.width(5), .mode("unsigned")) comparator_11 (
    .a(s2_D), .b(des_M), .eq(comparator_11_eq));  // open: gt, lt
  Comparator #(.width(4), .mode("unsigned")) comparator_12 (
    .a(tUse2_D_t), .b(tNew_M), .lt(comparator_12_lt));  // open: gt, eq
  assign tUse1_D_t = {{2{1'b0}}, tUse1_D};  // Bit_Extender bit_extender_1
  not not_1 (not_1_out, comparator_1_eq);
  not not_2 (not_2_out, comparator_4_eq);
  not not_3 (not_3_out, comparator_7_eq);
  not not_4 (not_4_out, comparator_10_eq);
  and and_1 (and_1_out, not_1_out, comparator_2_eq, comparator_3_lt);
  and and_2 (and_2_out, not_2_out, comparator_5_eq, comparator_6_lt);
  and and_3 (and_3_out, not_3_out, comparator_8_eq, comparator_9_lt);
  and and_4 (and_4_out, not_4_out, comparator_11_eq, comparator_12_lt);
  assign tUse2_D_t = {{2{1'b0}}, tUse2_D};  // Bit_Extender bit_extender_2
  or or_1 (flush_E, and_1_out, and_2_out, and_3_out, and_4_out);

  assign Stall_D = flush_E;
  assign Stall_F = flush_E;

  // Other names for the same wires on the sheet: stall_flag = flush_E
endmodule

module IF_ID (
  input  clock,
  input  reset,
  input  [31:0] instr_i,
  input  [31:0] pc_i,
  input  in_5,
  output [31:0] instr_o,
  output [31:0] pc_o,
  output [31:0] pc_4_o,
  output [31:0] pc_8_o
);

  wire clk_prime, not_1_out, not_2_out;

  not not_1 (not_1_out, in_5);
  not not_2 (not_2_out, in_5);
  buf and_1 (clk_prime, clock);  // AND_Gate
  Register #(.width(32)) register_1 (.D(instr_i), .en(not_1_out), .Q(instr_o), .clk(clk_prime), .clr(reset));
  Register #(.width(32)) register_2 (.D(pc_i), .en(not_2_out), .Q(pc_o), .clk(clk_prime), .clr(reset));
  Adder #(.width(32)) adder_1 (.a(pc_o), .b(32'h4), .out(pc_4_o));  // open: cin, cout
  Adder #(.width(32)) adder_2 (.a(pc_o), .b(32'h8), .out(pc_8_o));  // open: cin, cout

  // Other names for the same wires on the sheet: clk = clock; F_D_stall = in_5
endmodule

module ID_EX (
  input  clock,
  input  reset,
  input  MemWrite_i,
  input  [31:0] RD1_i,
  input  [31:0] RD2_i,
  input  MemRead_i,
  input  [4:0] rs_i,
  input  [1:0] MemReg_i,
  input  [4:0] rt_i,
  input  [4:0] rd_i,
  input  [3:0] ALUop,
  input  [31:0] extresult_i,
  input  ALUSrc_i,
  input  [31:0] instr_i,
  input  RegWrite_i,
  input  [1:0] RegDst_i,
  input  [31:0] pc_i,
  input  flush,
  input  [31:0] pc_4_i,
  input  [31:0] pc_8_i,
  input  [1:0] Ssel_i,
  input  [1:0] Lsel_i,
  output MemWrite_o,
  output [31:0] RD1_o,
  output [31:0] RD2_o,
  output MemRead_o,
  output [4:0] rs_o,
  output [1:0] MemReg_o,
  output [4:0] rt_o,
  output [4:0] rd_o,
  output [3:0] ALUop_o,
  output [31:0] extresult_o,
  output ALUSrc_o,
  output [31:0] instr_o,
  output RegWrite_o,
  output [1:0] RegDst_o,
  output [31:0] pc_o,
  output [31:0] pc_4_o,
  output [31:0] pc_8_o,
  output [1:0] Ssel_o,
  output [1:0] Lsel_o
);

  wire multiplexer_8_out, multiplexer_9_out, multiplexer_12_out, multiplexer_13_out;
  wire [1:0] multiplexer_10_out, multiplexer_14_out, multiplexer_18_out, multiplexer_19_out;
  wire [3:0] multiplexer_11_out;
  wire [4:0] multiplexer_3_out, multiplexer_4_out, multiplexer_5_out;
  wire [31:0] multiplexer_1_out, multiplexer_2_out, multiplexer_6_out, multiplexer_7_out, multiplexer_15_out,
       multiplexer_16_out, multiplexer_17_out;

  Multiplexer #(.width(32), .enable("false")) multiplexer_1 (
    .in0(RD1_i), .in1({32{1'b0}}), .out(multiplexer_1_out), .sel(flush));
  Multiplexer #(.width(32), .enable("false")) multiplexer_2 (
    .in0(RD2_i), .in1({32{1'b0}}), .out(multiplexer_2_out), .sel(flush));
  Multiplexer #(.width(5), .enable("false")) multiplexer_3 (
    .in0(rs_i), .in1({5{1'b0}}), .out(multiplexer_3_out), .sel(flush));
  Multiplexer #(.width(5), .enable("false")) multiplexer_4 (
    .in0(rt_i), .in1({5{1'b0}}), .out(multiplexer_4_out), .sel(flush));
  Multiplexer #(.width(5), .enable("false")) multiplexer_5 (
    .in0(rd_i), .in1({5{1'b0}}), .out(multiplexer_5_out), .sel(flush));
  Multiplexer #(.width(32), .enable("false")) multiplexer_6 (
    .in0(extresult_i), .in1({32{1'b0}}), .out(multiplexer_6_out), .sel(flush));
  Multiplexer #(.width(32), .enable("false")) multiplexer_7 (
    .in0(instr_i), .in1({32{1'b0}}), .out(multiplexer_7_out), .sel(flush));
  Register #(.width(32)) register_1 (.D(multiplexer_1_out), .Q(RD1_o), .clk(clock), .clr(reset));  // open: en
  Register #(.width(32)) register_2 (.D(multiplexer_2_out), .Q(RD2_o), .clk(clock), .clr(reset));  // open: en
  Register #(.width(5)) register_3 (.D(multiplexer_3_out), .Q(rs_o), .clk(clock), .clr(reset));  // open: en
  Register #(.width(5)) register_4 (.D(multiplexer_4_out), .Q(rt_o), .clk(clock), .clr(reset));  // open: en
  Register #(.width(5)) register_5 (.D(multiplexer_5_out), .Q(rd_o), .clk(clock), .clr(reset));  // open: en
  Register #(.width(32)) register_6 (.D(multiplexer_6_out), .Q(extresult_o), .clk(clock), .clr(reset));  // open: en
  Register #(.width(32)) register_7 (.D(multiplexer_7_out), .Q(instr_o), .clk(clock), .clr(reset));  // open: en
  Multiplexer #(.enable("false")) multiplexer_8 (.in0(MemWrite_i), .in1(1'b0), .out(multiplexer_8_out), .sel(flush));
  Multiplexer #(.enable("false")) multiplexer_9 (.in0(MemRead_i), .in1(1'b0), .out(multiplexer_9_out), .sel(flush));
  Multiplexer #(.width(2), .enable("false")) multiplexer_10 (
    .in0(MemReg_i), .in1(2'b00), .out(multiplexer_10_out), .sel(flush));
  Multiplexer #(.width(4), .enable("false")) multiplexer_11 (
    .in0(ALUop), .in1(4'b0000), .out(multiplexer_11_out), .sel(flush));
  Multiplexer #(.enable("false")) multiplexer_12 (.in0(ALUSrc_i), .in1(1'b0), .out(multiplexer_12_out), .sel(flush));
  Multiplexer #(.enable("false")) multiplexer_13 (.in0(RegWrite_i), .in1(1'b0), .out(multiplexer_13_out), .sel(flush));
  Multiplexer #(.width(2), .enable("false")) multiplexer_14 (
    .in0(RegDst_i), .in1(2'b00), .out(multiplexer_14_out), .sel(flush));
  Multiplexer #(.width(32), .enable("false")) multiplexer_15 (
    .in0(pc_i), .in1({32{1'b0}}), .out(multiplexer_15_out), .sel(flush));
  Multiplexer #(.width(32), .enable("false")) multiplexer_16 (
    .in0(pc_4_i), .in1({32{1'b0}}), .out(multiplexer_16_out), .sel(flush));
  Multiplexer #(.width(32), .enable("false")) multiplexer_17 (
    .in0(pc_8_i), .in1({32{1'b0}}), .out(multiplexer_17_out), .sel(flush));
  Multiplexer #(.width(2), .enable("false")) multiplexer_18 (
    .in0(Ssel_i), .in1(2'b00), .out(multiplexer_18_out), .sel(flush));
  Multiplexer #(.width(2), .enable("false")) multiplexer_19 (
    .in0(Lsel_i), .in1(2'b00), .out(multiplexer_19_out), .sel(flush));
  Register #(.width(1)) register_8 (.D(multiplexer_8_out), .Q(MemWrite_o), .clk(clock), .clr(reset));  // open: en
  Register #(.width(1)) register_9 (.D(multiplexer_9_out), .Q(MemRead_o), .clk(clock), .clr(reset));  // open: en
  Register #(.width(2)) register_10 (.D(multiplexer_10_out), .Q(MemReg_o), .clk(clock), .clr(reset));  // open: en
  Register #(.width(4)) register_11 (.D(multiplexer_11_out), .Q(ALUop_o), .clk(clock), .clr(reset));  // open: en
  Register #(.width(1)) register_12 (.D(multiplexer_12_out), .Q(ALUSrc_o), .clk(clock), .clr(reset));  // open: en
  Register #(.width(1)) register_13 (.D(multiplexer_13_out), .Q(RegWrite_o), .clk(clock), .clr(reset));  // open: en
  Register #(.width(2)) register_14 (.D(multiplexer_14_out), .Q(RegDst_o), .clk(clock), .clr(reset));  // open: en
  Register #(.width(2)) register_15 (.D(multiplexer_18_out), .Q(Ssel_o), .clk(clock), .clr(reset));  // open: en
  Register #(.width(2)) register_16 (.D(multiplexer_19_out), .Q(Lsel_o), .clk(clock), .clr(reset));  // open: en
  Register #(.width(32)) register_17 (.D(multiplexer_15_out), .Q(pc_o), .clk(clock), .clr(reset));  // open: en
  Register #(.width(32)) register_18 (.D(multiplexer_16_out), .Q(pc_4_o), .clk(clock), .clr(reset));  // open: en
  Register #(.width(32)) register_19 (.D(multiplexer_17_out), .Q(pc_8_o), .clk(clock), .clr(reset));  // open: en

  // Other names for the same wires on the sheet: clk = clock; clk_prime = clock
endmodule

module EX_MEM (
  input  MemWrite_i,
  input  MemRead_i,
  input  [1:0] MemReg_i,
  input  RegWrite_i,
  input  clock,
  input  reset,
  input  [31:0] aluresult_i,
  input  [1:0] Ssel_i,
  input  [31:0] writedata_i,
  input  [1:0] Lsel_i,
  input  [4:0] writereg_i,
  input  [3:0] tnew_E,
  input  [31:0] pc_i,
  input  [31:0] pc_4_i,
  input  [31:0] pc_8_i,
  input  [31:0] instr_i,
  output MemWrite_o,
  output MemRead_o,
  output [1:0] MemReg_o,
  output RegWrite_o,
  output [31:0] aluresult_o,
  output [1:0] Ssel_o,
  output [31:0] writedata_o,
  output [1:0] Lsel_o,
  output [4:0] writereg_o,
  output [3:0] tnew_M,
  output [31:0] pc_o,
  output [31:0] pc_4_o,
  output [31:0] pc_8_o,
  output [31:0] instr_o
);

  wire comparator_1_eq;
  wire [3:0] register_8_q, subtractor_1_out;

  Register #(.width(32)) register_1 (.D(aluresult_i), .Q(aluresult_o), .clk(clock), .clr(reset));  // open: en
  Register #(.width(32)) register_2 (.D(pc_i), .Q(pc_o), .clk(clock), .clr(reset));  // open: en
  Register #(.width(32)) register_3 (.D(writedata_i), .Q(writedata_o), .clk(clock), .clr(reset));  // open: en
  Register #(.width(5)) register_4 (.D(writereg_i), .Q(writereg_o), .clk(clock), .clr(reset));  // open: en
  Register #(.width(32)) register_5 (.D(pc_4_i), .Q(pc_4_o), .clk(clock), .clr(reset));  // open: en
  Register #(.width(32)) register_6 (.D(pc_8_i), .Q(pc_8_o), .clk(clock), .clr(reset));  // open: en
  Register #(.width(32)) register_7 (.D(instr_i), .Q(instr_o), .clk(clock), .clr(reset));  // open: en
  Register #(.width(4)) register_8 (.D(tnew_E), .Q(register_8_q), .clk(clock), .clr(reset));  // open: en
  Subtractor #(.width(4)) subtractor_1 (.a(register_8_q), .b(4'b0001), .out(subtractor_1_out));  // open: bin, bout
  Register #(.width(1)) register_9 (.D(MemWrite_i), .Q(MemWrite_o), .clk(clock), .clr(reset));  // open: en
  Register #(.width(1)) register_10 (.D(MemRead_i), .Q(MemRead_o), .clk(clock), .clr(reset));  // open: en
  Register #(.width(2)) register_11 (.D(MemReg_i), .Q(MemReg_o), .clk(clock), .clr(reset));  // open: en
  Register #(.width(1)) register_12 (.D(RegWrite_i), .Q(RegWrite_o), .clk(clock), .clr(reset));  // open: en
  Comparator #(.width(4)) comparator_1 (.a(register_8_q), .b(4'b0000), .eq(comparator_1_eq));  // open: gt, lt
  Register #(.width(2)) register_13 (.D(Ssel_i), .Q(Ssel_o), .clk(clock), .clr(reset));  // open: en
  Register #(.width(2)) register_14 (.D(Lsel_i), .Q(Lsel_o), .clk(clock), .clr(reset));  // open: en
  Multiplexer #(.width(4), .enable("false")) multiplexer_1 (
    .in0(subtractor_1_out), .in1(4'b0000), .out(tnew_M), .sel(comparator_1_eq));

  // Other names for the same wires on the sheet: clk = clock; clk_prime = clock
endmodule

module MEX_WB (
  input  MemWrite_i,
  input  [1:0] MemReg_i,
  input  RegWrite_i,
  input  clock,
  input  reset,
  input  [4:0] writereg_i,
  input  [31:0] aluresult_i,
  input  [31:0] writedata_i,
  input  [31:0] readdata_i,
  input  [3:0] tnew_M,
  input  [31:0] pc_i,
  input  [31:0] pc_4_i,
  input  [31:0] pc_8_i,
  input  [31:0] instr_i,
  input  [31:0] memaddr,
  input  [31:0] memdata,
  output MemWrite_o,
  output [1:0] MemReg_o,
  output RegWrite_o,
  output [4:0] writereg_o,
  output [31:0] aluresult_o,
  output [31:0] writedata_o,
  output [31:0] readdata_o,
  output [3:0] tnew_W,
  output [31:0] pc_o,
  output [31:0] pc_4_o,
  output [31:0] pc_8_o,
  output [31:0] instr_o,
  output [31:0] memaddr_2,
  output [31:0] memdata_2
);

  wire comparator_1_eq;
  wire [3:0] register_11_q, subtractor_1_out;

  Register #(.width(5)) register_1 (.D(writereg_i), .Q(writereg_o), .clk(clock), .clr(reset));  // open: en
  Register #(.width(32)) register_2 (.D(aluresult_i), .Q(aluresult_o), .clk(clock), .clr(reset));  // open: en
  Register #(.width(32)) register_3 (.D(writedata_i), .Q(writedata_o), .clk(clock), .clr(reset));  // open: en
  Register #(.width(32)) register_4 (.D(readdata_i), .Q(readdata_o), .clk(clock), .clr(reset));  // open: en
  Register #(.width(32)) register_5 (.D(pc_i), .Q(pc_o), .clk(clock), .clr(reset));  // open: en
  Register #(.width(32)) register_6 (.D(pc_4_i), .Q(pc_4_o), .clk(clock), .clr(reset));  // open: en
  Register #(.width(32)) register_7 (.D(pc_8_i), .Q(pc_8_o), .clk(clock), .clr(reset));  // open: en
  Register #(.width(32)) register_8 (.D(instr_i), .Q(instr_o), .clk(clock), .clr(reset));  // open: en
  Register #(.width(32)) register_9 (.D(memaddr), .Q(memaddr_2), .clk(clock), .clr(reset));  // open: en
  Register #(.width(32)) register_10 (.D(memdata), .Q(memdata_2), .clk(clock), .clr(reset));  // open: en
  Register #(.width(4)) register_11 (.D(tnew_M), .Q(register_11_q), .clk(clock), .clr(reset));  // open: en
  Subtractor #(.width(4)) subtractor_1 (.a(register_11_q), .b(4'b0001), .out(subtractor_1_out));  // open: bin, bout
  Register #(.width(1)) register_12 (.D(MemWrite_i), .Q(MemWrite_o), .clk(clock), .clr(reset));  // open: en
  Register #(.width(2)) register_13 (.D(MemReg_i), .Q(MemReg_o), .clk(clock), .clr(reset));  // open: en
  Register #(.width(1)) register_14 (.D(RegWrite_i), .Q(RegWrite_o), .clk(clock), .clr(reset));  // open: en
  Comparator #(.width(4)) comparator_1 (.a(register_11_q), .b(4'b0000), .eq(comparator_1_eq));  // open: gt, lt
  Multiplexer #(.width(4), .enable("false")) multiplexer_1 (
    .in0(subtractor_1_out), .in1(4'b0000), .out(tnew_W), .sel(comparator_1_eq));

  // Other names for the same wires on the sheet: clk = clock; clk_prime = clock
endmodule

module D (
  input  [31:0] in_1,
  output [4:0] s1_D,
  output [4:0] s2_D,
  output [1:0] tuse1_D,
  output [1:0] tuse2_D
);

  wire addiu, addu, B_TYPE, beq, bne, CAL_I, CAL_R, j, jal, jr, lb, LD, lh, lui, lw, nop, or_1_out, or_2_out,
       or_3_out, or_4_out, or_5_out, ori, s1_D_out, s2_D_out, sb, sh, STR, subu, sw, tuse1_D_out;
  wire [1:0] bit_extender_1_out;
  wire [4:0] sort_1_rs, sort_1_rt;
  wire [5:0] sort_1_func, sort_1_opcode;

  Sort sort_1 (
    .instrcut(in_1), .Opcode(sort_1_opcode), .Rs(sort_1_rs), .Rt(sort_1_rt), .Func(sort_1_func));  // open: Rd, Shamt, IMM16, _26_bits_Address
  OpFunc opfunc_1 (
    .out_3(lw), .out_4(sw), .out_5(ori), .out_6(j), .out_7(beq), .out_8(lui), .out_9(addu), .out_10(subu),
    .out_11(nop), .out_12(jr), .out_13(jal), .out_14(addiu), .out_15(sb), .out_16(sh), .out_17(lb),
    .out_18(lh), .out_19(bne), .op(sort_1_opcode), .funct(sort_1_func), .CAL_R(CAL_R), .CAL_I(CAL_I),
    .B_TYPE(B_TYPE), .STR(STR), .LD(LD));
  or or_1 (or_1_out, LD, STR);
  or or_2 (or_2_out, CAL_I, CAL_R);
  or u_s2_D (s2_D_out, beq, CAL_R, STR);
  buf or_3 (or_3_out, CAL_R);  // OR_Gate
  Multiplexer #(.width(5), .enable("false")) multiplexer_1 (
    .in0({5{1'b0}}), .in1(sort_1_rt), .out(s2_D), .sel(s2_D_out));
  or u_tuse1_D (tuse1_D_out, or_1_out, or_2_out);
  assign bit_extender_1_out = {{1{1'b0}}, or_3_out};  // Bit_Extender bit_extender_1
  or or_4 (or_4_out, STR, LD);
  or or_5 (or_5_out, CAL_I, CAL_R);
  Multiplexer #(.width(2), .enable("false")) multiplexer_2 (.in0(2'b00), .in1(2'b01), .out(tuse1_D), .sel(tuse1_D_out));
  Multiplexer #(.width(2), .enable("false")) multiplexer_3 (
    .in0(bit_extender_1_out), .in1(2'b10), .out(tuse2_D), .sel(STR));
  or u_s1_D (s1_D_out, or_4_out, or_5_out, jr, beq);
  Multiplexer #(.width(5), .enable("false")) multiplexer_4 (
    .in0({5{1'b0}}), .in1(sort_1_rs), .out(s1_D), .sel(s1_D_out));
endmodule

module E (
  input  [31:0] in_1,
  input  [31:0] pc_8,
  input  [31:0] extresult,
  output [4:0] s1_E,
  output [4:0] s2_E,
  output [4:0] des_E,
  output [3:0] tnew_E,
  output [31:0] toD
);

  wire addiu, addu, B_TYPE, beq, bne, CAL_I, CAL_R, j, jal, jr, lb, LD, lh, lui, lw, nop, or_1_out, or_2_out,
       or_3_out, or_4_out, or_5_out, or_6_out, or_7_out, or_8_out, ori, s1_D_out, s2_E_out, sb, sh, STR,
       subu, sw;
  wire [1:0] bit_extender_1_out, multiplexer_2_out;
  wire [4:0] multiplexer_1_out, multiplexer_4_out, sort_1_rd, sort_1_rs, sort_1_rt;
  wire [5:0] sort_1_func, sort_1_opcode;
  wire [31:0] multiplexer_3_out;

  Sort sort_1 (
    .instrcut(in_1), .Opcode(sort_1_opcode), .Rs(sort_1_rs), .Rt(sort_1_rt), .Rd(sort_1_rd),
    .Func(sort_1_func));  // open: Shamt, IMM16, _26_bits_Address
  OpFunc opfunc_1 (
    .out_3(lw), .out_4(sw), .out_5(ori), .out_6(j), .out_7(beq), .out_8(lui), .out_9(addu), .out_10(subu),
    .out_11(nop), .out_12(jr), .out_13(jal), .out_14(addiu), .out_15(sb), .out_16(sh), .out_17(lb),
    .out_18(lh), .out_19(bne), .op(sort_1_opcode), .funct(sort_1_func), .CAL_R(CAL_R), .CAL_I(CAL_I),
    .B_TYPE(B_TYPE), .STR(STR), .LD(LD));
  or or_1 (or_1_out, addu, subu, ori, addiu);
  buf or_2 (or_2_out, CAL_R);  // OR_Gate
  buf or_3 (or_3_out, LD);  // OR_Gate
  buf or_4 (or_4_out, CAL_I);  // OR_Gate
  or or_5 (or_5_out, lb, lh, lw);
  assign bit_extender_1_out = {{1{1'b0}}, or_1_out};  // Bit_Extender bit_extender_1
  Multiplexer #(.width(5), .enable("false")) multiplexer_1 (
    .in0({5{1'b0}}), .in1(sort_1_rd), .out(multiplexer_1_out), .sel(or_2_out));
  Multiplexer #(.width(2), .enable("false")) multiplexer_2 (
    .in0(bit_extender_1_out), .in1(2'b10), .out(multiplexer_2_out), .sel(or_5_out));
  Multiplexer #(.width(32), .enable("false")) multiplexer_3 (
    .in0({32{1'b0}}), .in1(pc_8), .out(multiplexer_3_out), .sel(jal));
  Multiplexer #(.width(5), .enable("false")) multiplexer_4 (
    .in0(multiplexer_1_out), .in1(sort_1_rt), .out(multiplexer_4_out), .sel(or_6_out));
  or or_6 (or_6_out, or_3_out, or_4_out, lui);
  assign tnew_E = {{2{1'b0}}, multiplexer_2_out};  // Bit_Extender bit_extender_2
  or or_7 (or_7_out, STR, LD);
  or or_8 (or_8_out, CAL_I, CAL_R);
  Multiplexer #(.width(5), .enable("false")) multiplexer_5 (
    .in0(multiplexer_4_out), .in1({5{1'b1}}), .out(des_E), .sel(jal));
  Multiplexer #(.width(32), .enable("false")) multiplexer_6 (
    .in0(multiplexer_3_out), .in1(extresult), .out(toD), .sel(lui));
  or u_s2_E (s2_E_out, CAL_R, STR);
  Multiplexer #(.width(5), .enable("false")) multiplexer_7 (
    .in0({5{1'b0}}), .in1(sort_1_rt), .out(s2_E), .sel(s2_E_out));
  or s1_D (s1_D_out, or_7_out, or_8_out, jr);
  Multiplexer #(.width(5), .enable("false")) multiplexer_8 (
    .in0({5{1'b0}}), .in1(sort_1_rs), .out(s1_E), .sel(s1_D_out));
endmodule

module M (
  input  [31:0] in_1,
  input  [31:0] pc_8,
  input  [31:0] aluresult,
  output [4:0] s2_M,
  output [4:0] des_M,
  output [31:0] toD
);

  wire addiu, addu, B_TYPE, beq, bne, CAL_I, CAL_R, j, jal, jr, lb, LD, lh, lui, lw, nop, or_1_out, or_2_out,
       or_3_out, or_4_out, or_5_out, or_6_out, or_7_out, ori, s2_E_out, sb, sh, STR, subu, sw;
  wire [4:0] multiplexer_1_out, multiplexer_3_out, sort_1_rd, sort_1_rt;
  wire [5:0] sort_1_func, sort_1_opcode;
  wire [31:0] multiplexer_2_out;

  Sort sort_1 (
    .instrcut(in_1), .Opcode(sort_1_opcode), .Rt(sort_1_rt), .Rd(sort_1_rd), .Func(sort_1_func));  // open: Rs, Shamt, IMM16, _26_bits_Address
  OpFunc opfunc_1 (
    .out_3(lw), .out_4(sw), .out_5(ori), .out_6(j), .out_7(beq), .out_8(lui), .out_9(addu), .out_10(subu),
    .out_11(nop), .out_12(jr), .out_13(jal), .out_14(addiu), .out_15(sb), .out_16(sh), .out_17(lb),
    .out_18(lh), .out_19(bne), .op(sort_1_opcode), .funct(sort_1_func), .CAL_R(CAL_R), .CAL_I(CAL_I),
    .B_TYPE(B_TYPE), .STR(STR), .LD(LD));
  buf or_1 (or_1_out, CAL_R);  // OR_Gate
  buf or_2 (or_2_out, LD);  // OR_Gate
  buf or_3 (or_3_out, CAL_I);  // OR_Gate
  Multiplexer #(.width(5), .enable("false")) multiplexer_1 (
    .in0({5{1'b0}}), .in1(sort_1_rd), .out(multiplexer_1_out), .sel(or_1_out));
  Multiplexer #(.width(32), .enable("false")) multiplexer_2 (
    .in0({32{1'b0}}), .in1(pc_8), .out(multiplexer_2_out), .sel(jal));
  buf or_4 (or_4_out, CAL_R);  // OR_Gate
  buf or_5 (or_5_out, STR);  // OR_Gate
  Multiplexer #(.width(5), .enable("false")) multiplexer_3 (
    .in0(multiplexer_1_out), .in1(sort_1_rt), .out(multiplexer_3_out), .sel(or_6_out));
  or or_6 (or_6_out, or_2_out, or_3_out, lui);
  Multiplexer #(.width(32), .enable("false")) multiplexer_4 (
    .in0(multiplexer_2_out), .in1(aluresult), .out(toD), .sel(or_7_out));
  or or_7 (or_7_out, lui, CAL_R, CAL_I);
  Multiplexer #(.width(5), .enable("false")) multiplexer_5 (
    .in0(multiplexer_3_out), .in1({5{1'b1}}), .out(des_M), .sel(jal));
  or s2_E (s2_E_out, or_4_out, or_5_out, beq);
  Multiplexer #(.width(5), .enable("false")) multiplexer_6 (
    .in0({5{1'b0}}), .in1(sort_1_rt), .out(s2_M), .sel(s2_E_out));
endmodule

module W (
  input  [31:0] in_1,
  input  [31:0] RD,
  input  [31:0] pc_8,
  input  [31:0] aluresult,
  output [4:0] des_W,
  output [31:0] toD
);

  wire addiu, addu, B_TYPE, beq, bne, CAL_I, CAL_R, j, jal, jr, lb, LD, lh, lui, lw, nop, or_1_out, or_2_out,
       or_3_out, or_4_out, or_5_out, or_6_out, ori, sb, sh, STR, subu, sw;
  wire [4:0] multiplexer_2_out, multiplexer_4_out, sort_1_rd, sort_1_rt;
  wire [5:0] sort_1_func, sort_1_opcode;
  wire [31:0] multiplexer_1_out, multiplexer_3_out;

  Sort sort_1 (
    .instrcut(in_1), .Opcode(sort_1_opcode), .Rt(sort_1_rt), .Rd(sort_1_rd), .Func(sort_1_func));  // open: Rs, Shamt, IMM16, _26_bits_Address
  OpFunc opfunc_1 (
    .out_3(lw), .out_4(sw), .out_5(ori), .out_6(j), .out_7(beq), .out_8(lui), .out_9(addu), .out_10(subu),
    .out_11(nop), .out_12(jr), .out_13(jal), .out_14(addiu), .out_15(sb), .out_16(sh), .out_17(lb),
    .out_18(lh), .out_19(bne), .op(sort_1_opcode), .funct(sort_1_func), .CAL_R(CAL_R), .CAL_I(CAL_I),
    .B_TYPE(B_TYPE), .STR(STR), .LD(LD));
  buf or_1 (or_1_out, CAL_R);  // OR_Gate
  buf or_2 (or_2_out, LD);  // OR_Gate
  buf or_3 (or_3_out, CAL_I);  // OR_Gate
  buf or_4 (or_4_out, LD);  // OR_Gate
  Multiplexer #(.width(32), .enable("false")) multiplexer_1 (
    .in0({32{1'b0}}), .in1(RD), .out(multiplexer_1_out), .sel(or_4_out));
  Multiplexer #(.width(5), .enable("false")) multiplexer_2 (
    .in0({5{1'b0}}), .in1(sort_1_rd), .out(multiplexer_2_out), .sel(or_1_out));
  Multiplexer #(.width(32), .enable("false")) multiplexer_3 (
    .in0(multiplexer_1_out), .in1(pc_8), .out(multiplexer_3_out), .sel(jal));
  Multiplexer #(.width(5), .enable("false")) multiplexer_4 (
    .in0(multiplexer_2_out), .in1(sort_1_rt), .out(multiplexer_4_out), .sel(or_5_out));
  or or_5 (or_5_out, or_2_out, or_3_out, lui);
  Multiplexer #(.width(5), .enable("false")) multiplexer_5 (
    .in0(multiplexer_4_out), .in1({5{1'b1}}), .out(des_W), .sel(jal));
  Multiplexer #(.width(32), .enable("false")) multiplexer_6 (
    .in0(multiplexer_3_out), .in1(aluresult), .out(toD), .sel(or_6_out));
  or or_6 (or_6_out, lui, CAL_I, CAL_R);
endmodule

module NPC (
  input  [31:0] oldPC,
  input  Jump,
  input  Jr,
  input  toBranch,
  input  [31:0] ExtResult,
  input  [31:0] ra,
  input  [31:0] instr,
  output [31:0] NPC
);

  wire [31:0] adder_1_out, adder_2_out, multiplexer_1_out, multiplexer_2_out, shifter_1_out;

  Adder #(.width(32)) adder_1 (.a(oldPC), .b(32'h4), .out(adder_1_out));  // open: cin, cout
  Shifter #(.width(32)) shifter_1 (.in(ExtResult), .\dist (5'b00010), .out(shifter_1_out));
  Adder #(.width(32)) adder_2 (.a(oldPC), .b(shifter_1_out), .out(adder_2_out));  // open: cin, cout
  Multiplexer #(.width(32), .enable("false")) multiplexer_1 (
    .in0(adder_1_out), .in1(adder_2_out), .out(multiplexer_1_out), .sel(toBranch));
  Multiplexer #(.width(32), .enable("false")) multiplexer_2 (
    .in0(multiplexer_1_out), .in1({oldPC[31:28], instr[25:0], 2'b00}), .out(multiplexer_2_out), .sel(Jump));
  Multiplexer #(.width(32), .enable("false")) multiplexer_3 (.in0(multiplexer_2_out), .in1(ra), .out(NPC), .sel(Jr));
endmodule

module ALU (
  input  [31:0] A,
  input  [31:0] B,
  input  [3:0] ALUop,
  output [31:0] RES
);

  wire [31:0] A_B, A_B_t, A_B_t_t;

  Subtractor #(.width(32)) subtractor_1 (.a(A), .b(B), .out(A_B_t));  // open: bin, bout
  assign A_B_t_t = A | B;  // OR_Gate or_1, 32 bits wide
  Adder #(.width(32)) adder_1 (.a(A), .b(B), .out(A_B));  // open: cin, cout
  Multiplexer #(.select(4), .width(32), .enable("false")) multiplexer_1 (
    .in0(A_B), .in1(A_B_t), .in2(A_B_t_t), .out(RES), .sel(ALUop));  // open: in3, in4, in5, in6, in7, in8, in9, in10, in11, in12, in13, in14, in15
endmodule

module DM (
  input  [31:0] MemAddr,
  input  MemWrite,
  input  clock,
  input  [1:0] Lsel,
  input  MemRead,
  input  Reset,
  input  [31:0] WD,
  input  [1:0] Ssel,
  output [31:0] RD
);

  wire [7:0] _0_7, _16_23, multiplexer_4_out;
  wire [15:0] multiplexer_3_out;
  wire [15:8] _0_15, _16_31;
  wire [31:0] bit_extender_1_out, bit_extender_2_out, multiplexer_1_out, multiplexer_2_out, multiplexer_6_out;

  RAM #(.addrWidth(5), .dataWidth(32), .bus("separate")) ram_1 (
    .addr(MemAddr[6:2]), .din(multiplexer_6_out), .data({_16_31, _16_23, _0_15, _0_7}), .str(MemWrite),
    .clk(clock), .ld(MemRead), .clr(Reset));  // open: sel
  Multiplexer #(.select(2), .width(32), .enable("false")) multiplexer_1 (
    .in0({_16_31, _16_23, WD[15:0]}), .in2({WD[15:0], _0_15, _0_7}), .out(multiplexer_1_out),
    .sel(MemAddr[1:0]));  // open: in1, in3
  Multiplexer #(.select(2), .width(32), .enable("false")) multiplexer_2 (
    .in0({_16_31, _16_23, _0_15, WD[7:0]}), .in1({_16_31, _16_23, WD[7:0], _0_7}),
    .in2({_16_31, WD[7:0], _0_15, _0_7}), .in3({WD[7:0], _16_23, _0_15, _0_7}), .out(multiplexer_2_out),
    .sel(MemAddr[1:0]));
  Multiplexer #(.select(2), .width(16), .enable("false")) multiplexer_3 (
    .in0({_0_15, _0_7}), .in2({_16_31, _16_23}), .out(multiplexer_3_out), .sel(MemAddr[1:0]));  // open: in1, in3
  Multiplexer #(.select(2), .width(8), .enable("false")) multiplexer_4 (
    .in0(_0_7), .in1(_0_15), .in2(_16_23), .in3(_16_31), .out(multiplexer_4_out), .sel(MemAddr[1:0]));
  assign bit_extender_1_out = {{24{multiplexer_4_out[7]}}, multiplexer_4_out};  // Bit_Extender bit_extender_1
  assign bit_extender_2_out = {{16{multiplexer_3_out[15]}}, multiplexer_3_out};  // Bit_Extender bit_extender_2
  Multiplexer #(.select(2), .width(32), .enable("false")) multiplexer_5 (
    .in0({_16_31, _16_23, _0_15, _0_7}), .in1(bit_extender_1_out), .in2(bit_extender_2_out), .out(RD),
    .sel(Lsel));  // open: in3
  Multiplexer #(.select(2), .width(32), .enable("false")) multiplexer_6 (
    .in0(WD), .in1(multiplexer_2_out), .in2(multiplexer_1_out), .out(multiplexer_6_out), .sel(Ssel));  // open: in3

  // Other names for the same wires on the sheet: _24_31[7:0] = _16_31; _0_15[7:0] = _0_7; _8_15[7:0] = _0_15;
  //   _16_31[7:0] = _16_23; Byte[1:0] = MemAddr[1:0]
endmodule
