// Logisim project bgtz.circ as structural Verilog: 20 circuits, main circuit main
module main (
  input  in_1,
  output [31:0] instr,
  output regwrite,
  output [4:0] regaddr,
  output [31:0] regdata,
  output memwrite,
  output [4:0] memaddr,
  output [31:0] memdata
);

  wire Alusrc, Alusrc2, and_1_out, and_2_out, bigger, branch_op, clk, comparator_1_eq, comparator_1_gt,
       controller_1_branch, controller_1_out_16, equal, flushE, fRtMsel, j_jal, jr, MemRead, MemRead2,
       memread3, MemWrite2, memwrite3, MemWrite_t, not_1_out, RegWrite2, RegWrite3, RegWrite_t, Stall_D,
       Stall_F;
  wire [1:0] ex_mem_1_byte_o, ex_mem_1_lesl_o, ext_op, fRsDsel, fRsEsel, fRtDsel, fRtEsel, lsel, lsel2,
       MemtoReg, MemtoReg2, MemtoReg3, MemtoReg4, Regdst, Regdst2, ssel, ssel2, tuse1_D, tuse2_D;
  wire [2:0] Alu_op, Alu_op2;
  wire [3:0] tnew_E, tnew_M, tnew_W;
  wire [4:0] _11_15rd, _16_20rt, _21_25rs, des_E, des_M, des_W, ex_mem_1_out_19, id_ex_1_rd_o, id_ex_1_rt_o,
       multiplexer_6_out, s1_D, s1_E, s2_D, s2_E, s2_M;
  wire [5:0] func, op;
  wire [15:0] extop_prime;
  wire [31:0] aluresult2, aluresult3, aluresult4, D_CMP_RS, D_CMP_RT, dm_1_rd, E_ALU_A, E_ALU_B, EtoD,
       extresult, extresult1, instr_0, instr_2, instr_3, instr_4, M_DM_WD, memaddr_o, MtoD,
       multiplexer_5_out, npc, pc, pc1, pc2, pc3, pc_41, pc_42, pc_43, pc_81, pc_82, pc_83, pc_84, rd1, rd2,
       readdata4, rs_e, rt_e, writedata, WtoD;

  Clock clock_1 (.out(clk));
  IF if_1 (.npc(npc), .instr(instr), .pc(pc), .in_1(clk), .in_2(in_1), .in_4(Stall_F));
  NPC npc_1 (
    .pc(pc), .instr(instr_0), .extresult(extresult), .npc(npc), .branch_op(branch_op), .j_jal(j_jal),
    .RD1(D_CMP_RS), .jr(jr));
  IF_ID if_id_1 (
    .in_1(clk), .in_2(in_1), .instr_i(instr), .instr_o(instr_0), .pc_i(pc), .pc_o(pc1), .in_5(Stall_D),
    .out_8(pc_41), .out_9(pc_81));
  splitter splitter_1 (
    .instr(instr_0), ._0_15(extop_prime), .func(func), ._11_15rd(_11_15rd), ._16_20rt(_16_20rt),
    ._21_25rs(_21_25rs), .op(op));  // open: _0_25
  EXT ext_1 (.in_2(extop_prime), .out_3(extresult), .in_1(ext_op));
  foward foward_1 (
    .s1_D(s1_D), .s2_D(s2_D), .s1_E(s1_E), .s2_E(s2_E), .des_E(des_E), .tNew_E(tnew_E), .s2_M(s2_M),
    .tNew_M(tnew_M), .des_M(des_M), .tNew_W(tnew_W), .des_W(des_W), .fRsDsel(fRsDsel), .fRtDsel(fRtDsel),
    .fRsEsel(fRsEsel), .fRtEsel(fRtEsel), .fRtMsel(fRtMsel));
  Multiplexer #(.select(2), .width(32), .enable("false")) multiplexer_1 (
    .in0(rd1), .in1(EtoD), .in2(MtoD), .in3({32{1'b0}}), .out(D_CMP_RS), .sel(fRsDsel));
  not not_1 (not_1_out, clk);
  controller controller_1 (
    .RegWrite(RegWrite_t), .MemWrite(MemWrite_t), .MemRead(MemRead), .MemtoReg(MemtoReg), .Alusrc(Alusrc),
    .Alu_op(Alu_op), .Branch(controller_1_branch), .j_jal(j_jal), .Regdst(Regdst), .ext_op(ext_op), .op(op),
    .funct(func), .jr(jr), .Ssel(ssel), .Lsel(lsel), .out_16(controller_1_out_16));
  GRF grf_1 (
    .A1(_21_25rs), .A2(_16_20rt), .A3(regaddr), .WD(regdata), .RD1(rd1), .RD2(rd2), .clk(not_1_out),
    .reset(in_1), .we(regwrite));
  D d_1 (.in_1(instr_0), .s2_D(s2_D), .s1_D(s1_D), .tuse1_D(tuse1_D), .tuse2_D(tuse2_D));
  and and_1 (and_1_out, controller_1_branch, equal);
  and and_2 (and_2_out, bigger, controller_1_out_16);
  Multiplexer #(.select(2), .width(32), .enable("false")) multiplexer_2 (
    .in0(rd2), .in1(EtoD), .in2(MtoD), .in3({32{1'b0}}), .out(D_CMP_RT), .sel(fRtDsel));
  or or_1 (branch_op, and_1_out, and_2_out);
  Comparator #(.width(32)) comparator_1 (
    .a(D_CMP_RS), .b({32{1'b0}}), .gt(comparator_1_gt), .eq(comparator_1_eq));  // open: lt
  Comparator #(.width(32)) comparator_2 (.a(D_CMP_RS), .b(D_CMP_RT), .eq(equal));  // open: gt, lt
  or or_2 (bigger, comparator_1_gt, comparator_1_eq);
  E e_1 (
    .in_1(instr_2), .pc_8(pc_82), .extresult(extresult1), .s2_E(s2_E), .s1_E(s1_E), .toD(EtoD),
    .des_E(des_E), .tnew_E(tnew_E));
  stallU stallu_1 (
    .s1_D(s1_D), .s2_D(s2_D), .tUse1_D(tuse1_D), .tUse2_D(tuse2_D), .des_E(des_E), .tNew_E(tnew_E),
    .tNew_M(tnew_M), .des_M(des_M), .Stall_F(Stall_F), .Stall_D(Stall_D), .flush_E(flushE));
  Multiplexer #(.select(2), .width(32), .enable("false")) multiplexer_3 (
    .in0(rs_e), .in1(MtoD), .in2(WtoD), .in3({32{1'b0}}), .out(E_ALU_A), .sel(fRsEsel));
  M m_1 (.in_1(instr_3), .pc_8(pc_83), .aluresult(aluresult3), .s2_E(s2_M), .toD(MtoD), .des_E(des_M));
  ID_EX id_ex_1 (
    .in_1(clk), .in_2(in_1), .pc_i(pc1), .pc_o(pc2), .RD1_i(D_CMP_RS), .RD1_o(rs_e), .pc_4_i(pc_41),
    .pc_4_o(pc_42), .RD2_i(D_CMP_RT), .RD2_o(rt_e), .pc_8_i(pc_81), .pc_8_o(pc_82), .rs_i(_21_25rs),
    .rt_i(_16_20rt), .rt_o(id_ex_1_rt_o), .rd_i(_11_15rd), .rd_o(id_ex_1_rd_o), .out_31(instr_2),
    .instr_i(instr_0), .in_12(flushE), .RegDst_i(Regdst), .RegDst_o(Regdst2), .MemWrite_i(MemWrite_t),
    .MemWrite_o(MemWrite2), .RegWrite_i(RegWrite_t), .RegWrite_o(RegWrite2), .Alusrc_i(Alusrc),
    .Alusrc_o(Alusrc2), .memread_i(MemRead), .memread_o(MemRead2), .memtoReg_i(MemtoReg),
    .memtoReg_o(MemtoReg2), .Alu_op_i(Alu_op), .Alu_op_o(Alu_op2), .out_41(extresult1),
    .extresult_i(extresult), .byteAB_i(ssel), .byteAB_o(ssel2), .lsel(lsel), .lsel_2(lsel2));  // open: rs_o
  Multiplexer #(.select(2), .width(32), .enable("false")) multiplexer_4 (
    .in0(rt_e), .in1(MtoD), .in2(WtoD), .in3({32{1'b0}}), .out(E_ALU_B), .sel(fRtEsel));
  W w_1 (.in_1(instr_4), .RD(readdata4), .pc_8(pc_84), .aluresult(aluresult4), .toD(WtoD), .des_E(des_W));
  Multiplexer #(.width(32), .enable("false")) multiplexer_5 (
    .in0(E_ALU_B), .in1(extresult1), .out(multiplexer_5_out), .sel(Alusrc2));
  Multiplexer #(.select(2), .width(5), .enable("false")) multiplexer_6 (
    .in0(id_ex_1_rt_o), .in1(id_ex_1_rd_o), .in2({5{1'b1}}), .out(multiplexer_6_out), .sel(Regdst2));  // open: in3
  ALU alu_1 (.RD1(E_ALU_A), .RD2(multiplexer_5_out), .result(aluresult2), .in_3(Alu_op2));  // open: equal
  Multiplexer #(.width(32), .enable("false")) multiplexer_7 (.in0(writedata), .in1(WtoD), .out(M_DM_WD), .sel(fRtMsel));
  EX_MEM ex_mem_1 (
    .aluresult_i(aluresult2), .writedata_i(E_ALU_B), .writereg_i(multiplexer_6_out), .pc_i(pc2),
    .pc_4_i(pc_42), .pc_8_i(pc_82), .instr_i(instr_2), .out_17(aluresult3), .out_18(writedata),
    .out_19(ex_mem_1_out_19), .pc_o(pc3), .pc_4_o(pc_43), .pc_8_o(pc_83), .out_23(instr_3), .in_1(clk),
    .in_2(in_1), .tnew_E(tnew_E), .tnew_M(tnew_M), .memread_i(MemRead2), .memread_o(memread3),
    .memtoReg_i(MemtoReg2), .memtoReg_o(MemtoReg3), .MemWrite_i(MemWrite2), .MemWrite_o(memwrite3),
    .RegWrite_i(RegWrite2), .RegWrite_o(RegWrite3), .byte_i(ssel2), .byte_o(ex_mem_1_byte_o), .lsel(lsel2),
    .lesl_o(ex_mem_1_lesl_o));
  DM dm_1 (
    .MemAddr(aluresult3), .RD(dm_1_rd), .MemWrite(memwrite3), .clock(clk), .Lsel(ex_mem_1_lesl_o),
    .Reset(in_1), .WD(M_DM_WD), .Ssel(ex_mem_1_byte_o));
  MEM_WB mem_wb_1 (
    .writereg_i(ex_mem_1_out_19), .aluresult_i(aluresult3), .writedata_i(writedata), .readdata_i(dm_1_rd),
    .pc_i(pc3), .pc_4_i(pc_43), .pc_8_i(pc_83), .instr_i(instr_3), .memaddr(aluresult3), .memdata(M_DM_WD),
    .memwrite(memwrite3), .out_24(regaddr), .out_17(aluresult4), .out_19(readdata4), .pc_8_o(pc_84),
    .out_23(instr_4), .out_25({memaddr_o[31:7], memaddr, memaddr_o[1:0]}), .out_26(memdata),
    .out_27(memwrite), .in_1(clk), .in_2(in_1), .tnew_M(tnew_M), .tnew_W(tnew_W), .RegWrite_i(RegWrite3),
    .RegWrite_o(regwrite), .memtoReg_i(MemtoReg3), .memtoReg_o(MemtoReg4));  // open: out_18, pc_o, pc_4_o
  Multiplexer #(.select(2), .width(32), .enable("false")) multiplexer_8 (
    .in0(aluresult4), .in1(readdata4), .in2(pc_84), .out(regdata), .sel(MemtoReg4));  // open: in3

  // Other names for the same wires on the sheet: memaddr_o[6:2] = memaddr; memdata_o[31:0] = memdata;
  //   memwrite_o = memwrite; regwrite_o = regwrite; reset = in_1
endmodule

module controller (
  input  [5:0] op,
  input  [5:0] funct,
  output RegWrite,
  output [1:0] Lsel,
  output MemWrite,
  output MemRead,
  output [1:0] MemtoReg,
  output Alusrc,
  output [2:0] Alu_op,
  output Branch,
  output j_jal,
  output jr,
  output [1:0] Regdst,
  output [1:0] ext_op,
  output [1:0] Ssel,
  output out_16
);

  wire addiu, addu, bne, j, lw, nop, ori, subu, sw;

  controllerpart controllerpart_1 (
    .out_3(lw), .out_4(sw), .out_5(ori), .out_6(j), .out_7(Branch), .out_8(ext_op[1]), .out_9(addu),
    .out_10(subu), .out_11(nop), .op(op), .funct(funct), .out_12(jr), .out_13(MemtoReg[1]), .out_14(addiu),
    .out_15(Ssel[0]), .out_16(Ssel[1]), .out_17(Lsel[0]), .out_18(Lsel[1]), .out_19(bne), .out_20(out_16));
  or or_1 (MemRead, lw, Ssel[0], Ssel[1], Lsel[0], Lsel[1]);
  buf or_2 (MemtoReg[0], lw);  // OR_Gate
  or or_3 (MemWrite, sw, Ssel[0], Ssel[1]);
  or or_4 (Alu_op[0], subu, out_16, Branch);
  buf or_5 (Alu_op[1], ori);  // OR_Gate
  or or_6 (j_jal, j, MemtoReg[1]);
  or or_7 (Regdst[0], addu, subu);
  or or_8 (ext_op[0], addiu, Branch, lw, sw, Ssel[0], out_16);
  or or_9 (RegWrite, lw, ext_op[1], addu, subu, ori, addiu, MemtoReg[1]);
  or or_10 (Alusrc, ext_op[1], addiu, ori, lw, Ssel[0], sw);

  assign Alu_op[2] = 1'b0;
  assign Regdst[1] = MemtoReg[1];

  // Other names for the same wires on the sheet: beq = Branch; bgtz = out_16; lui = ext_op[1]; lb = Lsel[0];
  //   lh = Lsel[1]; jal = MemtoReg[1]; sb = Ssel[0]; sh = Ssel[1]
endmodule

module controllerpart (
  input  [5:0] funct,
  input  [5:0] op,
  output out_3,
  output out_4,
  output out_5,
  output out_6,
  output out_7,
  output out_8,
  output out_9,
  output out_10,
  output out_11,
  output out_12,
  output out_13,
  output out_14,
  output out_15,
  output out_16,
  output out_17,
  output out_18,
  output out_19,
  output out_20
);

  wire not_1_out, not_2_out, not_3_out, not_4_out, not_5_out, not_6_out, not_7_out, not_8_out, not_9_out,
       not_10_out, not_11_out, not_12_out, R;

  not not_1 (not_1_out, op[5]);
  not not_2 (not_2_out, op[4]);
  not not_3 (not_3_out, op[2]);
  not not_4 (not_4_out, op[3]);
  not not_5 (not_5_out, op[1]);
  not not_6 (not_6_out, op[0]);
  and and_1 (out_3, op[5], not_2_out, not_4_out, not_3_out, op[1], op[0]);
  and and_2 (out_4, op[5], not_2_out, op[3], not_3_out, op[1], op[0]);
  and and_3 (R, not_1_out, not_2_out, not_4_out, not_3_out, not_5_out, not_6_out);
  and and_4 (out_5, not_1_out, not_2_out, op[3], op[2], not_5_out, op[0]);
  and and_5 (out_6, not_1_out, not_2_out, not_4_out, not_3_out, op[1], not_6_out);
  and and_6 (out_7, not_1_out, not_2_out, not_4_out, op[2], not_5_out, not_6_out);
  and and_7 (out_8, not_1_out, not_2_out, op[3], op[2], op[1], op[0]);
  and and_8 (out_13, not_1_out, not_2_out, not_4_out, not_3_out, op[1], op[0]);
  and and_9 (out_15, op[5], not_2_out, op[3], not_3_out, not_5_out, not_6_out);
  and and_10 (out_14, not_1_out, not_2_out, op[3], not_3_out, not_5_out, op[0]);
  and and_11 (out_16, op[5], not_2_out, op[3], not_3_out, not_5_out, op[0]);
  and and_12 (out_17, op[5], not_2_out, not_4_out, not_3_out, not_5_out, not_6_out);
  and and_13 (out_18, op[5], not_2_out, not_4_out, not_3_out, not_5_out, op[0]);
  and and_14 (out_19, not_1_out, not_2_out, not_4_out, op[2], not_5_out, op[0]);
  and and_15 (out_20, not_1_out, not_2_out, not_4_out, op[2], op[1], op[0]);
  not not_7 (not_7_out, funct[5]);
  not not_8 (not_8_out, funct[4]);
  not not_9 (not_9_out, funct[3]);
  not not_10 (not_10_out, funct[2]);
  not not_11 (not_11_out, funct[1]);
  not not_12 (not_12_out, funct[0]);
  and and_16 (out_9, R, funct[5], not_8_out, not_9_out, not_10_out, not_11_out, funct[0]);
  and and_17 (out_10, R, funct[5], not_8_out, not_9_out, not_10_out, funct[1], funct[0]);
  and and_18 (out_11, R, not_7_out, not_8_out, not_9_out, not_10_out, not_11_out, not_12_out);
  and and_19 (out_12, R, not_7_out, not_8_out, funct[3], not_10_out, not_11_out, not_12_out);

  // Other names for the same wires on the sheet: addiu = out_14; addu = out_9; beq = out_7; bgtz = out_20;
  //   bne = out_19; j = out_6; jal = out_13; jr = out_12; lb = out_17; lh = out_18; lui = out_8; lw = out_3;
  //   nop = out_11; ori = out_5; sb = out_15; sh = out_16; subu = out_10; sw = out_4
endmodule

module ALU (
  input  [31:0] RD1,
  input  [31:0] RD2,
  input  [2:0] in_3,
  output [31:0] result,
  output equal
);

  wire [31:0] adder_1_out, or_1_out, subtractor_1_out;

  Adder #(.width(32)) adder_1 (.a(RD1), .b(RD2), .out(adder_1_out));  // open: cin, cout
  Subtractor #(.width(32)) subtractor_1 (.a(RD1), .b(RD2), .out(subtractor_1_out));  // open: bin, bout
  assign or_1_out = RD1 | RD2;  // OR_Gate or_1, 32 bits wide
  Multiplexer #(.select(3), .width(32), .enable("false")) multiplexer_1 (
    .in0(adder_1_out), .in1(subtractor_1_out), .in2(or_1_out), .out(result), .sel(in_3));  // open: in3, in4, in5, in6, in7
  Comparator #(.width(32)) comparator_1 (.a(result), .b({32{1'b0}}), .eq(equal));  // open: gt, lt
endmodule

module IF_ID (
  input  in_1,
  input  in_2,
  input  [31:0] instr_i,
  input  [31:0] pc_i,
  input  in_5,
  output [31:0] instr_o,
  output [31:0] pc_o,
  output [31:0] out_8,
  output [31:0] out_9
);

  wire clk_prime, not_1_out, not_2_out;

  not not_1 (not_1_out, in_5);
  not not_2 (not_2_out, in_5);
  buf and_1 (clk_prime, in_1);  // AND_Gate
  Register #(.width(32)) register_1 (.D(instr_i), .en(not_1_out), .Q(instr_o), .clk(clk_prime), .clr(in_2));
  Register #(.width(32)) register_2 (.D(pc_i), .en(not_2_out), .Q(pc_o), .clk(clk_prime), .clr(in_2));
  Adder #(.width(32)) adder_1 (.a(pc_o), .b(32'h4), .out(out_8));  // open: cin, cout
  Adder #(.width(32)) adder_2 (.a(pc_o), .b(32'h8), .out(out_9));  // open: cin, cout

  // Other names for the same wires on the sheet: clk = in_1; F_D_stall = in_5; reset = in_2
endmodule

module ID_EX (
  input  in_1,
  input  in_2,
  input  [31:0] pc_i,
  input  [31:0] RD1_i,
  input  [31:0] pc_4_i,
  input  [31:0] RD2_i,
  input  [31:0] pc_8_i,
  input  [4:0] rs_i,
  input  [4:0] rt_i,
  input  [4:0] rd_i,
  input  [31:0] instr_i,
  input  in_12,
  input  [1:0] lsel,
  input  [1:0] byteAB_i,
  input  [1:0] RegDst_i,
  input  MemWrite_i,
  input  RegWrite_i,
  input  Alusrc_i,
  input  memread_i,
  input  [1:0] memtoReg_i,
  input  [2:0] Alu_op_i,
  input  [31:0] extresult_i,
  output [31:0] pc_o,
  output [31:0] RD1_o,
  output [31:0] pc_4_o,
  output [31:0] RD2_o,
  output [31:0] pc_8_o,
  output [4:0] rs_o,
  output [4:0] rt_o,
  output [4:0] rd_o,
  output [31:0] out_31,
  output [1:0] lsel_2,
  output [1:0] byteAB_o,
  output [1:0] RegDst_o,
  output MemWrite_o,
  output RegWrite_o,
  output Alusrc_o,
  output memread_o,
  output [1:0] memtoReg_o,
  output [2:0] Alu_op_o,
  output [31:0] out_41
);

  wire multiplexer_10_out, multiplexer_11_out, multiplexer_12_out, multiplexer_13_out;
  wire [1:0] multiplexer_7_out, multiplexer_8_out, multiplexer_9_out, multiplexer_16_out;
  wire [2:0] multiplexer_14_out;
  wire [4:0] multiplexer_3_out, multiplexer_4_out, multiplexer_5_out;
  wire [31:0] multiplexer_1_out, multiplexer_2_out, multiplexer_6_out, multiplexer_15_out,
       multiplexer_17_out, multiplexer_18_out, multiplexer_19_out;

  Multiplexer #(.width(32), .enable("false")) multiplexer_1 (
    .in0(RD1_i), .in1({32{1'b0}}), .out(multiplexer_1_out), .sel(in_12));
  Multiplexer #(.width(32), .enable("false")) multiplexer_2 (
    .in0(RD2_i), .in1({32{1'b0}}), .out(multiplexer_2_out), .sel(in_12));
  Multiplexer #(.width(5), .enable("false")) multiplexer_3 (
    .in0(rs_i), .in1({5{1'b0}}), .out(multiplexer_3_out), .sel(in_12));
  Multiplexer #(.width(5), .enable("false")) multiplexer_4 (
    .in0(rt_i), .in1({5{1'b0}}), .out(multiplexer_4_out), .sel(in_12));
  Multiplexer #(.width(5), .enable("false")) multiplexer_5 (
    .in0(rd_i), .in1({5{1'b0}}), .out(multiplexer_5_out), .sel(in_12));
  Multiplexer #(.width(32), .enable("false")) multiplexer_6 (
    .in0(instr_i), .in1({32{1'b0}}), .out(multiplexer_6_out), .sel(in_12));
  Multiplexer #(.width(2), .enable("false")) multiplexer_7 (
    .in0(lsel), .in1(2'b00), .out(multiplexer_7_out), .sel(in_12));
  Multiplexer #(.width(2), .enable("false")) multiplexer_8 (
    .in0(byteAB_i), .in1(2'b00), .out(multiplexer_8_out), .sel(in_12));
  Multiplexer #(.width(2), .enable("false")) multiplexer_9 (
    .in0(RegDst_i), .in1(2'b00), .out(multiplexer_9_out), .sel(in_12));
  Multiplexer #(.enable("false")) multiplexer_10 (.in0(MemWrite_i), .in1(1'b0), .out(multiplexer_10_out), .sel(in_12));
  Multiplexer #(.enable("false")) multiplexer_11 (.in0(RegWrite_i), .in1(1'b0), .out(multiplexer_11_out), .sel(in_12));
  Multiplexer #(.enable("false")) multiplexer_12 (.in0(Alusrc_i), .in1(1'b0), .out(multiplexer_12_out), .sel(in_12));
  Multiplexer #(.enable("false")) multiplexer_13 (.in0(memread_i), .in1(1'b0), .out(multiplexer_13_out), .sel(in_12));
  Multiplexer #(.width(3), .enable("false")) multiplexer_14 (
    .in0(Alu_op_i), .in1(3'b000), .out(multiplexer_14_out), .sel(in_12));
  Multiplexer #(.width(32), .enable("false")) multiplexer_15 (
    .in0(extresult_i), .in1({32{1'b0}}), .out(multiplexer_15_out), .sel(in_12));
  Register #(.width(32)) register_1 (.D(multiplexer_1_out), .Q(RD1_o), .clk(in_1), .clr(in_2));  // open: en
  Register #(.width(32)) register_2 (.D(multiplexer_2_out), .Q(RD2_o), .clk(in_1), .clr(in_2));  // open: en
  Register #(.width(5)) register_3 (.D(multiplexer_3_out), .Q(rs_o), .clk(in_1), .clr(in_2));  // open: en
  Register #(.width(5)) register_4 (.D(multiplexer_4_out), .Q(rt_o), .clk(in_1), .clr(in_2));  // open: en
  Register #(.width(5)) register_5 (.D(multiplexer_5_out), .Q(rd_o), .clk(in_1), .clr(in_2));  // open: en
  Register #(.width(32)) register_6 (.D(multiplexer_6_out), .Q(out_31), .clk(in_1), .clr(in_2));  // open: en
  Multiplexer #(.width(2), .enable("false")) multiplexer_16 (
    .in0(memtoReg_i), .in1(2'b00), .out(multiplexer_16_out), .sel(in_12));
  Register #(.width(32)) register_7 (.D(multiplexer_15_out), .Q(out_41), .clk(in_1), .clr(in_2));  // open: en
  Register #(.width(2)) register_8 (.D(multiplexer_7_out), .Q(lsel_2), .clk(in_1), .clr(in_2));  // open: en
  Register #(.width(2)) register_9 (.D(multiplexer_8_out), .Q(byteAB_o), .clk(in_1), .clr(in_2));  // open: en
  Register #(.width(2)) register_10 (.D(multiplexer_9_out), .Q(RegDst_o), .clk(in_1), .clr(in_2));  // open: en
  Register #(.width(1)) register_11 (.D(multiplexer_10_out), .Q(MemWrite_o), .clk(in_1), .clr(in_2));  // open: en
  Register #(.width(1)) register_12 (.D(multiplexer_11_out), .Q(RegWrite_o), .clk(in_1), .clr(in_2));  // open: en
  Register #(.width(1)) register_13 (.D(multiplexer_12_out), .Q(Alusrc_o), .clk(in_1), .clr(in_2));  // open: en
  Register #(.width(1)) register_14 (.D(multiplexer_13_out), .Q(memread_o), .clk(in_1), .clr(in_2));  // open: en
  Register #(.width(2)) register_15 (.D(multiplexer_16_out), .Q(memtoReg_o), .clk(in_1), .clr(in_2));  // open: en
  Register #(.width(3)) register_16 (.D(multiplexer_14_out), .Q(Alu_op_o), .clk(in_1), .clr(in_2));  // open: en
  Multiplexer #(.width(32), .enable("false")) multiplexer_17 (
    .in0(pc_i), .in1({32{1'b0}}), .out(multiplexer_17_out), .sel(in_12));
  Multiplexer #(.width(32), .enable("false")) multiplexer_18 (
    .in0(pc_4_i), .in1({32{1'b0}}), .out(multiplexer_18_out), .sel(in_12));
  Multiplexer #(.width(32), .enable("false")) multiplexer_19 (
    .in0(pc_8_i), .in1({32{1'b0}}), .out(multiplexer_19_out), .sel(in_12));
  Register #(.width(32)) register_17 (.D(multiplexer_17_out), .Q(pc_o), .clk(in_1), .clr(in_2));  // open: en
  Register #(.width(32)) register_18 (.D(multiplexer_18_out), .Q(pc_4_o), .clk(in_1), .clr(in_2));  // open: en
  Register #(.width(32)) register_19 (.D(multiplexer_19_out), .Q(pc_8_o), .clk(in_1), .clr(in_2));  // open: en

  // Other names for the same wires on the sheet: clk = in_1; clk_prime = in_1; flush = in_12; Reset = in_2
endmodule

module EX_MEM (
  input  in_1,
  input  in_2,
  input  [31:0] aluresult_i,
  input  [31:0] writedata_i,
  input  [4:0] writereg_i,
  input  [31:0] pc_i,
  input  [31:0] pc_4_i,
  input  [31:0] pc_8_i,
  input  [31:0] instr_i,
  input  [3:0] tnew_E,
  input  [1:0] lsel,
  input  [1:0] byte_i,
  input  MemWrite_i,
  input  RegWrite_i,
  input  memread_i,
  input  [1:0] memtoReg_i,
  output [31:0] out_17,
  output [31:0] out_18,
  output [4:0] out_19,
  output [31:0] pc_o,
  output [31:0] pc_4_o,
  output [31:0] pc_8_o,
  output [31:0] out_23,
  output [3:0] tnew_M,
  output [1:0] lesl_o,
  output [1:0] byte_o,
  output MemWrite_o,
  output RegWrite_o,
  output memread_o,
  output [1:0] memtoReg_o
);

  wire comparator_1_eq;
  wire [3:0] register_1_q, subtractor_1_out;

  Register #(.width(4)) register_1 (.D(tnew_E), .Q(register_1_q), .clk(in_1), .clr(in_2));  // open: en
  Register #(.width(32)) register_2 (.D(aluresult_i), .Q(out_17), .clk(in_1), .clr(in_2));  // open: en
  Register #(.width(32)) register_3 (.D(writedata_i), .Q(out_18), .clk(in_1), .clr(in_2));  // open: en
  Register #(.width(5)) register_4 (.D(writereg_i), .Q(out_19), .clk(in_1), .clr(in_2));  // open: en
  Register #(.width(32)) register_5 (.D(pc_i), .Q(pc_o), .clk(in_1), .clr(in_2));  // open: en
  Register #(.width(32)) register_6 (.D(pc_4_i), .Q(pc_4_o), .clk(in_1), .clr(in_2));  // open: en
  Register #(.width(32)) register_7 (.D(pc_8_i), .Q(pc_8_o), .clk(in_1), .clr(in_2));  // open: en
  Register #(.width(32)) register_8 (.D(instr_i), .Q(out_23), .clk(in_1), .clr(in_2));  // open: en
  Comparator #(.width(4)) comparator_1 (.a(register_1_q), .b(4'b0000), .eq(comparator_1_eq));  // open: gt, lt
  Subtractor #(.width(4)) subtractor_1 (.a(register_1_q), .b(4'b0001), .out(subtractor_1_out));  // open: bin, bout
  Register #(.width(2)) register_9 (.D(lsel), .Q(lesl_o), .clk(in_1), .clr(in_2));  // open: en
  Register #(.width(2)) register_10 (.D(byte_i), .Q(byte_o), .clk(in_1), .clr(in_2));  // open: en
  Register #(.width(1)) register_11 (.D(MemWrite_i), .Q(MemWrite_o), .clk(in_1), .clr(in_2));  // open: en
  Register #(.width(1)) register_12 (.D(RegWrite_i), .Q(RegWrite_o), .clk(in_1), .clr(in_2));  // open: en
  Register #(.width(1)) register_13 (.D(memread_i), .Q(memread_o), .clk(in_1), .clr(in_2));  // open: en
  Register #(.width(2)) register_14 (.D(memtoReg_i), .Q(memtoReg_o), .clk(in_1), .clr(in_2));  // open: en
  Multiplexer #(.width(4), .enable("false")) multiplexer_1 (
    .in0(subtractor_1_out), .in1(register_1_q), .out(tnew_M), .sel(comparator_1_eq));

  // Other names for the same wires on the sheet: clk = in_1; clk_prime = in_1; Reset = in_2
endmodule

module MEM_WB (
  input  in_1,
  input  in_2,
  input  [31:0] aluresult_i,
  input  [31:0] writedata_i,
  input  [31:0] readdata_i,
  input  [31:0] pc_i,
  input  [31:0] pc_4_i,
  input  [31:0] pc_8_i,
  input  [31:0] instr_i,
  input  [4:0] writereg_i,
  input  [31:0] memaddr,
  input  [31:0] memdata,
  input  memwrite,
  input  [3:0] tnew_M,
  input  RegWrite_i,
  input  [1:0] memtoReg_i,
  output [31:0] out_17,
  output [31:0] out_18,
  output [31:0] out_19,
  output [31:0] pc_o,
  output [31:0] pc_4_o,
  output [31:0] pc_8_o,
  output [31:0] out_23,
  output [4:0] out_24,
  output [31:0] out_25,
  output [31:0] out_26,
  output out_27,
  output [3:0] tnew_W,
  output RegWrite_o,
  output [1:0] memtoReg_o
);

  wire comparator_1_eq;
  wire [3:0] register_1_q, subtractor_1_out;

  Register #(.width(4)) register_1 (.D(tnew_M), .Q(register_1_q), .clk(in_1), .clr(in_2));  // open: en
  Register #(.width(32)) register_2 (.D(aluresult_i), .Q(out_17), .clk(in_1), .clr(in_2));  // open: en
  Register #(.width(32)) register_3 (.D(writedata_i), .Q(out_18), .clk(in_1), .clr(in_2));  // open: en
  Register #(.width(32)) register_4 (.D(readdata_i), .Q(out_19), .clk(in_1), .clr(in_2));  // open: en
  Register #(.width(32)) register_5 (.D(pc_i), .Q(pc_o), .clk(in_1), .clr(in_2));  // open: en
  Register #(.width(32)) register_6 (.D(pc_4_i), .Q(pc_4_o), .clk(in_1), .clr(in_2));  // open: en
  Register #(.width(32)) register_7 (.D(pc_8_i), .Q(pc_8_o), .clk(in_1), .clr(in_2));  // open: en
  Register #(.width(32)) register_8 (.D(instr_i), .Q(out_23), .clk(in_1), .clr(in_2));  // open: en
  Register #(.width(5)) register_9 (.D(writereg_i), .Q(out_24), .clk(in_1), .clr(in_2));  // open: en
  Register #(.width(32)) register_10 (.D(memaddr), .Q(out_25), .clk(in_1), .clr(in_2));  // open: en
  Register #(.width(32)) register_11 (.D(memdata), .Q(out_26), .clk(in_1), .clr(in_2));  // open: en
  Register #(.width(1)) register_12 (.D(memwrite), .Q(out_27), .clk(in_1), .clr(in_2));  // open: en
  Subtractor #(.width(4)) subtractor_1 (.a(register_1_q), .b(4'b0001), .out(subtractor_1_out));  // open: bin, bout
  Comparator #(.width(4)) comparator_1 (.a(register_1_q), .b(4'b0000), .eq(comparator_1_eq));  // open: gt, lt
  Register #(.width(1)) register_13 (.D(RegWrite_i), .Q(RegWrite_o), .clk(in_1), .clr(in_2));  // open: en
  Register #(.width(2)) register_14 (.D(memtoReg_i), .Q(memtoReg_o), .clk(in_1), .clr(in_2));  // open: en
  Multiplexer #(.width(4), .enable("false")) multiplexer_1 (
    .in0(subtractor_1_out), .in1(register_1_q), .out(tnew_W), .sel(comparator_1_eq));

  // Other names for the same wires on the sheet: clk = in_1; clk_prime = in_1; Reset = in_2
endmodule

module splitter (
  input  [31:0] instr,
  output [15:0] _0_15,
  output [25:0] _0_25,
  output [5:0] func,
  output [4:0] _11_15rd,
  output [4:0] _16_20rt,
  output [4:0] _21_25rs,
  output [5:0] op
);


  assign _0_15 = instr[15:0];
  assign _0_25 = instr[25:0];
  assign _11_15rd = instr[15:11];
  assign _16_20rt = instr[20:16];
  assign _21_25rs = instr[25:21];
  assign func = instr[5:0];
  assign op = instr[31:26];
endmodule

module IF (
  input  in_1,
  input  in_2,
  input  [31:0] npc,
  input  in_4,
  output [31:0] instr,
  output [31:0] pc
);

  wire comparator_1_eq, not_1_out;
  wire [31:0] pc_q, subtractor_1_out;

  not not_1 (not_1_out, in_4);
  Register #(.width(32)) u_pc (.D(npc), .en(not_1_out), .Q(pc_q), .clk(in_1), .clr(in_2));
  Comparator #(.width(32)) comparator_1 (.a({32{1'b0}}), .b(pc_q), .eq(comparator_1_eq));  // open: gt, lt
  Multiplexer #(.width(32), .enable("false")) multiplexer_1 (
    .in0(pc_q), .in1(32'h3000), .out(pc), .sel(comparator_1_eq));
  Subtractor #(.width(32)) subtractor_1 (.a(pc), .b(32'h3000), .out(subtractor_1_out));  // open: bin, bout
  ROM #(.addrWidth(10), .dataWidth(32)) rom_1 (.addr(subtractor_1_out[11:2]), .data(instr));  // open: sel

  // Other names for the same wires on the sheet: clook = in_1; F_D_stall = in_4; reset = in_2

  // Notes on the sheet:
  //   contents of rom_1 (hex, n*v repeats v):
  //   35290001 1d200003 21290001 21290001 21290001 ad490000
endmodule

module DM (
  input  [31:0] MemAddr,
  input  MemWrite,
  input  clock,
  input  [1:0] Lsel,
  input  Reset,
  input  [31:0] WD,
  input  [1:0] Ssel,
  output [31:0] RD
);

  wire [7:0] _0_7, _16_23, multiplexer_4_out;
  wire [15:0] multiplexer_3_out;
  wire [15:8] _0_15, _16_31;
  wire [31:0] bit_extender_1_out, bit_extender_2_out, multiplexer_1_out, multiplexer_2_out, multiplexer_6_out;

  RAM #(.addrWidth(5), .dataWidth(32), .bus("separate")) ram_1 (
    .addr(MemAddr[6:2]), .din(multiplexer_6_out), .data({_16_31, _16_23, _0_15, _0_7}), .str(MemWrite),
    .clk(clock), .ld(1'b1), .clr(Reset));  // open: sel
  Multiplexer #(.select(2), .width(32), .enable("false")) multiplexer_1 (
    .in0({_16_31, _16_23, WD[15:0]}), .in2({WD[31:16], _0_15, _0_7}), .out(multiplexer_1_out),
    .sel(MemAddr[1:0]));  // open: in1, in3
  Multiplexer #(.select(2), .width(32), .enable("false")) multiplexer_2 (
    .in0({_16_31, _16_23, _0_15, WD[7:0]}), .in1({_16_31, _16_23, WD[15:8], _0_7}),
    .in2({_16_31, WD[23:16], _0_15, _0_7}), .in3({WD[31:24], _16_23, _0_15, _0_7}), .out(multiplexer_2_out),
    .sel(MemAddr[1:0]));
  Multiplexer #(.select(2), .width(16), .enable("false")) multiplexer_3 (
    .in0({_0_15, _0_7}), .in2({_16_31, _16_23}), .out(multiplexer_3_out), .sel(MemAddr[1:0]));  // open: in1, in3
  assign bit_extender_1_out = {{24{multiplexer_4_out[7]}}, multiplexer_4_out};  // Bit_Extender bit_extender_1
  Multiplexer #(.select(2), .width(8), .enable("false")) multiplexer_4 (
    .in0(_0_7), .in1(_0_15), .in2(_16_23), .in3(_16_31), .out(multiplexer_4_out), .sel(MemAddr[1:0]));
  assign bit_extender_2_out = {{16{multiplexer_3_out[15]}}, multiplexer_3_out};  // Bit_Extender bit_extender_2
  Multiplexer #(.select(2), .width(32), .enable("false")) multiplexer_5 (
    .in0({_16_31, _16_23, _0_15, _0_7}), .in1(bit_extender_1_out), .in2(bit_extender_2_out), .out(RD),
    .sel(Lsel));  // open: in3
  Multiplexer #(.select(2), .width(32), .enable("false")) multiplexer_6 (
    .in0(WD), .in1(multiplexer_2_out), .in2(multiplexer_1_out), .out(multiplexer_6_out), .sel(Ssel));  // open: in3

  // Other names for the same wires on the sheet: _24_31[7:0] = _16_31; _0_15[7:0] = _0_7; _8_15[7:0] = _0_15;
  //   _16_31[7:0] = _16_23; Byte[1:0] = MemAddr[1:0]
endmodule

module NPC (
  input  branch_op,
  input  j_jal,
  input  jr,
  input  [31:0] pc,
  input  [31:0] instr,
  input  [31:0] extresult,
  input  [31:0] RD1,
  output [31:0] npc
);

  wire [31:0] adder_2_out, beq, multiplexer_1_out, multiplexer_2_out, pc_4;

  Shifter #(.width(32)) shifter_1 (.in(extresult), .\dist (5'b00010), .out(beq));
  Adder #(.width(32)) adder_1 (.a(pc), .b(32'h4), .out(pc_4));  // open: cin, cout
  Adder #(.width(32)) adder_2 (.a(pc), .b(beq), .out(adder_2_out));  // open: cin, cout
  Multiplexer #(.width(32), .enable("false")) multiplexer_1 (
    .in0(pc_4), .in1(adder_2_out), .out(multiplexer_1_out), .sel(branch_op));
  Multiplexer #(.width(32), .enable("false")) multiplexer_2 (
    .in0(multiplexer_1_out), .in1({pc[31:28], instr[25:0], 2'b00}), .out(multiplexer_2_out), .sel(j_jal));
  Multiplexer #(.width(32), .enable("false")) multiplexer_3 (.in0(multiplexer_2_out), .in1(RD1), .out(npc), .sel(jr));

  // Other names for the same wires on the sheet: j_jalim[31:2] = {pc[31:28], instr[25:0]}
endmodule

module GRF (
  input  [4:0] A1,
  input  clk,
  input  reset,
  input  we,
  input  [4:0] A2,
  input  [4:0] A3,
  input  [31:0] WD,
  output [31:0] RD1,
  output [31:0] RD2
);

  wire [31:0] I0, I1, I2, I3, I4, I5, I6, I7, I8, I9, I10, I11, I12, I13, I14, I15, I16, I17, I18, I19, I20,
       I21, I22, I23, I24, I25, I26, I27, I28, I29, I30, I31, O0, O1, O2, O3, O4, O5, O6, O7, O8, O9, O10,
       O11, O12, O13, O14, O15, O16, O17, O18, O19, O20, O21, O22, O23, O24, O25, O26, O27, O28, O29, O30,
       O31;

  Demultiplexer #(.select(5), .width(32), .tristate("true")) demultiplexer_1 (
    .out0(I0), .out1(I1), .out2(I2), .out3(I3), .out4(I4), .out5(I5), .out6(I6), .out7(I7), .out8(I8),
    .out9(I9), .out10(I10), .out11(I11), .out12(I12), .out13(I13), .out14(I14), .out15(I15), .out16(I16),
    .out17(I17), .out18(I18), .out19(I19), .out20(I20), .out21(I21), .out22(I22), .out23(I23), .out24(I24),
    .out25(I25), .out26(I26), .out27(I27), .out28(I28), .out29(I29), .out30(I30), .out31(I31), .in(WD),
    .sel(A3));  // open: en
  Multiplexer #(.select(5), .width(32)) multiplexer_1 (
    .in0(O0), .in1(O1), .in2(O2), .in3(O3), .in4(O4), .in5(O5), .in6(O6), .in7(O7), .in8(O8), .in9(O9),
    .in10(O10), .in11(O11), .in12(O12), .in13(O13), .in14(O14), .in15(O15), .in16(O16), .in17(O17),
    .in18(O18), .in19(O19), .in20(O20), .in21(O21), .in22(O22), .in23(O23), .in24(O24), .in25(O25),
    .in26(O26), .in27(O27), .in28(O28), .in29(O29), .in30(O30), .in31(O31), .out(RD2), .sel(A2));  // open: en
  Multiplexer #(.select(5), .width(32)) multiplexer_2 (
    .in0(O0), .in1(O1), .in2(O2), .in3(O3), .in4(O4), .in5(O5), .in6(O6), .in7(O7), .in8(O8), .in9(O9),
    .in10(O10), .in11(O11), .in12(O12), .in13(O13), .in14(O14), .in15(O15), .in16(O16), .in17(O17),
    .in18(O18), .in19(O19), .in20(O20), .in21(O21), .in22(O22), .in23(O23), .in24(O24), .in25(O25),
    .in26(O26), .in27(O27), .in28(O28), .in29(O29), .in30(O30), .in31(O31), .out(RD1), .sel(A1));  // open: en
  Register #(.width(32)) register_1 (.D({32{1'b0}}), .en(we), .Q(O0), .clk(clk), .clr(reset));
  Register #(.width(32)) register_2 (.D(I8), .en(we), .Q(O8), .clk(clk), .clr(reset));
  Register #(.width(32)) register_3 (.D(I16), .en(we), .Q(O16), .clk(clk), .clr(reset));
  Register #(.width(32)) register_4 (.D(I24), .en(we), .Q(O24), .clk(clk), .clr(reset));
  Register #(.width(32)) register_5 (.D(I1), .en(we), .Q(O1), .clk(clk), .clr(reset));
  Register #(.width(32)) register_6 (.D(I9), .en(we), .Q(O9), .clk(clk), .clr(reset));
  Register #(.width(32)) register_7 (.D(I17), .en(we), .Q(O17), .clk(clk), .clr(reset));
  Register #(.width(32)) register_8 (.D(I25), .en(we), .Q(O25), .clk(clk), .clr(reset));
  Register #(.width(32)) register_9 (.D(I2), .en(we), .Q(O2), .clk(clk), .clr(reset));
  Register #(.width(32)) register_10 (.D(I10), .en(we), .Q(O10), .clk(clk), .clr(reset));
  Register #(.width(32)) register_11 (.D(I18), .en(we), .Q(O18), .clk(clk), .clr(reset));
  Register #(.width(32)) register_12 (.D(I26), .en(we), .Q(O26), .clk(clk), .clr(reset));
  Register #(.width(32)) register_13 (.D(I3), .en(we), .Q(O3), .clk(clk), .clr(reset));
  Register #(.width(32)) register_14 (.D(I11), .en(we), .Q(O11), .clk(clk), .clr(reset));
  Register #(.width(32)) register_15 (.D(I19), .en(we), .Q(O19), .clk(clk), .clr(reset));
  Register #(.width(32)) register_16 (.D(I27), .en(we), .Q(O27), .clk(clk), .clr(reset));
  Register #(.width(32)) register_17 (.D(I4), .en(we), .Q(O4), .clk(clk), .clr(reset));
  Register #(.width(32)) register_18 (.D(I12), .en(we), .Q(O12), .clk(clk), .clr(reset));
  Register #(.width(32)) register_19 (.D(I20), .en(we), .Q(O20), .clk(clk), .clr(reset));
  Register #(.width(32)) register_20 (.D(I28), .en(we), .Q(O28), .clk(clk), .clr(reset));
  Register #(.width(32)) register_21 (.D(I5), .en(we), .Q(O5), .clk(clk), .clr(reset));
  Register #(.width(32)) register_22 (.D(I13), .en(we), .Q(O13), .clk(clk), .clr(reset));
  Register #(.width(32)) register_23 (.D(I21), .en(we), .Q(O21), .clk(clk), .clr(reset));
  Register #(.width(32)) register_24 (.D(I29), .en(we), .Q(O29), .clk(clk), .clr(reset));
  Register #(.width(32)) register_25 (.D(I6), .en(we), .Q(O6), .clk(clk), .clr(reset));
  Register #(.width(32)) register_26 (.D(I14), .en(we), .Q(O14), .clk(clk), .clr(reset));
  Register #(.width(32)) register_27 (.D(I22), .en(we), .Q(O22), .clk(clk), .clr(reset));
  Register #(.width(32)) register_28 (.D(I30), .en(we), .Q(O30), .clk(clk), .clr(reset));
  Register #(.width(32)) register_29 (.D(I7), .en(we), .Q(O7), .clk(clk), .clr(reset));
  Register #(.width(32)) register_30 (.D(I15), .en(we), .Q(O15), .clk(clk), .clr(reset));
  Register #(.width(32)) register_31 (.D(I23), .en(we), .Q(O23), .clk(clk), .clr(reset));
  Register #(.width(32)) register_32 (.D(I31), .en(we), .Q(O31), .clk(clk), .clr(reset));
endmodule

module D (
  input  [31:0] in_1,
  output [4:0] s2_D,
  output [4:0] s1_D,
  output [1:0] tuse1_D,
  output [1:0] tuse2_D
);

  wire addiu, addu, beq, bgtz, bne, j, jal, jr, lb, lh, lui, lw, nop, or_1_out, or_2_out, or_3_out, or_4_out,
       or_5_out, ori, s1_D_out, s2_D_out, sb, sh, subu, sw, tuse1_D_out;
  wire [1:0] bit_extender_1_out;
  wire [4:0] splitter_1__16_20rt, splitter_1__21_25rs;
  wire [5:0] splitter_1_func, splitter_1_op;

  splitter splitter_1 (
    .instr(in_1), .func(splitter_1_func), ._16_20rt(splitter_1__16_20rt), ._21_25rs(splitter_1__21_25rs),
    .op(splitter_1_op));  // open: _0_15, _0_25, _11_15rd
  controllerpart controllerpart_1 (
    .out_3(lw), .out_4(sw), .out_5(ori), .out_6(j), .out_7(beq), .out_8(lui), .out_9(addu), .out_10(subu),
    .out_11(nop), .op(splitter_1_op), .funct(splitter_1_func), .out_12(jr), .out_13(jal), .out_14(addiu),
    .out_15(sb), .out_16(sh), .out_17(lb), .out_18(lh), .out_19(bne), .out_20(bgtz));
  or or_1 (or_1_out, lw, sw, sb, sh, lb, lh);
  or or_2 (or_2_out, lw, sw, sb, sh, lb, lh);
  or or_3 (or_3_out, addu, subu, addiu, ori);
  or or_4 (or_4_out, addu, subu, addiu, ori);
  or u_s2_D (s2_D_out, beq, addu, subu, sw, sb, sh, bgtz);
  or u_s1_D (s1_D_out, or_2_out, or_3_out, jr, beq, bgtz);
  or u_tuse1_D (tuse1_D_out, or_1_out, or_4_out);
  assign bit_extender_1_out = {{1{1'b0}}, or_5_out};  // Bit_Extender bit_extender_1
  or or_5 (or_5_out, addu, subu);
  Multiplexer #(.width(5), .enable("false")) multiplexer_1 (
    .in0({5{1'b0}}), .in1(splitter_1__16_20rt), .out(s2_D), .sel(s2_D_out));
  Multiplexer #(.width(5), .enable("false")) multiplexer_2 (
    .in0({5{1'b0}}), .in1(splitter_1__21_25rs), .out(s1_D), .sel(s1_D_out));
  Multiplexer #(.width(2), .enable("false")) multiplexer_3 (.in0(2'b00), .in1(2'b01), .out(tuse1_D), .sel(tuse1_D_out));
  Multiplexer #(.width(2), .enable("false")) multiplexer_4 (
    .in0(bit_extender_1_out), .in1(2'b10), .out(tuse2_D), .sel(sw));
endmodule

module E (
  input  [31:0] in_1,
  input  [31:0] pc_8,
  input  [31:0] extresult,
  output [4:0] des_E,
  output [4:0] s2_E,
  output [4:0] s1_E,
  output [31:0] toD,
  output [3:0] tnew_E
);

  wire addiu, addu, beq, bgtz, bne, j, jal, jr, lb, lh, lui, lw, nop, or_1_out, or_2_out, or_3_out, or_4_out,
       or_5_out, or_6_out, or_7_out, or_8_out, or_9_out, or_10_out, ori, s1_D_out, s2_E_out, sb, sh, subu, sw;
  wire [1:0] bit_extender_1_out, multiplexer_5_out;
  wire [4:0] multiplexer_6_out, multiplexer_7_out, splitter_1__11_15rd, splitter_1__16_20rt,
       splitter_1__21_25rs;
  wire [5:0] splitter_1_func, splitter_1_op;
  wire [31:0] multiplexer_1_out;

  splitter splitter_1 (
    .instr(in_1), .func(splitter_1_func), ._11_15rd(splitter_1__11_15rd), ._16_20rt(splitter_1__16_20rt),
    ._21_25rs(splitter_1__21_25rs), .op(splitter_1_op));  // open: _0_15, _0_25
  controllerpart controllerpart_1 (
    .out_3(lw), .out_4(sw), .out_5(ori), .out_6(j), .out_7(beq), .out_8(lui), .out_9(addu), .out_10(subu),
    .out_11(nop), .op(splitter_1_op), .funct(splitter_1_func), .out_12(jr), .out_13(jal), .out_14(addiu),
    .out_15(sb), .out_16(sh), .out_17(lb), .out_18(lh), .out_19(bne), .out_20(bgtz));
  or or_1 (or_1_out, lw, sw, sb, sh, lb, lh);
  or or_2 (or_2_out, addu, subu, addiu, ori);
  or or_3 (or_3_out, addu, subu);
  or or_4 (or_4_out, sw, sb, sh);
  Multiplexer #(.width(32), .enable("false")) multiplexer_1 (
    .in0({32{1'b0}}), .in1(pc_8), .out(multiplexer_1_out), .sel(jal));
  or u_s2_E (s2_E_out, or_3_out, or_4_out);
  Multiplexer #(.width(5), .enable("false")) multiplexer_2 (
    .in0({5{1'b0}}), .in1(splitter_1__16_20rt), .out(s2_E), .sel(s2_E_out));
  or s1_D (s1_D_out, or_1_out, or_2_out);
  Multiplexer #(.width(32), .enable("false")) multiplexer_3 (
    .in0(multiplexer_1_out), .in1(extresult), .out(toD), .sel(lui));
  or or_5 (or_5_out, lb, lh, lw);
  or or_6 (or_6_out, addu, subu, ori, addiu);
  assign bit_extender_1_out = {{1{1'b0}}, or_6_out};  // Bit_Extender bit_extender_1
  Multiplexer #(.width(5), .enable("false")) multiplexer_4 (
    .in0({5{1'b0}}), .in1(splitter_1__21_25rs), .out(s1_E), .sel(s1_D_out));
  Multiplexer #(.width(2), .enable("false")) multiplexer_5 (
    .in0(bit_extender_1_out), .in1(2'b10), .out(multiplexer_5_out), .sel(or_5_out));
  or or_7 (or_7_out, lb, lh, lw);
  or or_8 (or_8_out, ori, addiu);
  assign tnew_E = {{2{1'b0}}, multiplexer_5_out};  // Bit_Extender bit_extender_2
  or or_9 (or_9_out, addu, subu);
  Multiplexer #(.width(5), .enable("false")) multiplexer_6 (
    .in0({5{1'b0}}), .in1(splitter_1__11_15rd), .out(multiplexer_6_out), .sel(or_9_out));
  or or_10 (or_10_out, or_7_out, or_8_out, lui);
  Multiplexer #(.width(5), .enable("false")) multiplexer_7 (
    .in0(multiplexer_6_out), .in1(splitter_1__16_20rt), .out(multiplexer_7_out), .sel(or_10_out));
  Multiplexer #(.width(5), .enable("false")) multiplexer_8 (
    .in0(multiplexer_7_out), .in1({5{1'b1}}), .out(des_E), .sel(jal));
endmodule

module M (
  input  [31:0] in_1,
  input  [31:0] pc_8,
  input  [31:0] aluresult,
  output [4:0] des_E,
  output [4:0] s2_E,
  output [31:0] toD
);

  wire addiu, addu, beq, bgtz, bne, j, jal, jr, lb, lh, lui, lw, nop, or_1_out, or_2_out, or_3_out, or_4_out,
       or_5_out, ori, s2_E_out, sb, sh, subu, sw;
  wire [4:0] multiplexer_4_out, multiplexer_5_out, splitter_1__11_15rd, splitter_1__16_20rt;
  wire [5:0] splitter_1_func, splitter_1_op;
  wire [31:0] multiplexer_1_out;

  splitter splitter_1 (
    .instr(in_1), .func(splitter_1_func), ._11_15rd(splitter_1__11_15rd), ._16_20rt(splitter_1__16_20rt),
    .op(splitter_1_op));  // open: _0_15, _0_25, _21_25rs
  controllerpart controllerpart_1 (
    .out_3(lw), .out_4(sw), .out_5(ori), .out_6(j), .out_7(beq), .out_8(lui), .out_9(addu), .out_10(subu),
    .out_11(nop), .op(splitter_1_op), .funct(splitter_1_func), .out_12(jr), .out_13(jal), .out_14(addiu),
    .out_15(sb), .out_16(sh), .out_17(lb), .out_18(lh), .out_19(bne), .out_20(bgtz));
  Multiplexer #(.width(32), .enable("false")) multiplexer_1 (
    .in0({32{1'b0}}), .in1(pc_8), .out(multiplexer_1_out), .sel(jal));
  or u_s2_E (s2_E_out, sb, sh, sw);
  Multiplexer #(.width(5), .enable("false")) multiplexer_2 (
    .in0({5{1'b0}}), .in1(splitter_1__16_20rt), .out(s2_E), .sel(s2_E_out));
  Multiplexer #(.width(32), .enable("false")) multiplexer_3 (
    .in0(multiplexer_1_out), .in1(aluresult), .out(toD), .sel(or_1_out));
  or or_1 (or_1_out, lui, ori, addu, subu, addiu);
  or or_2 (or_2_out, addu, subu);
  Multiplexer #(.width(5), .enable("false")) multiplexer_4 (
    .in0({5{1'b0}}), .in1(splitter_1__11_15rd), .out(multiplexer_4_out), .sel(or_2_out));
  or or_3 (or_3_out, lb, lh, lw);
  or or_4 (or_4_out, ori, addiu);
  or or_5 (or_5_out, or_3_out, or_4_out, lui);
  Multiplexer #(.width(5), .enable("false")) multiplexer_5 (
    .in0(multiplexer_4_out), .in1(splitter_1__16_20rt), .out(multiplexer_5_out), .sel(or_5_out));
  Multiplexer #(.width(5), .enable("false")) multiplexer_6 (
    .in0(multiplexer_5_out), .in1({5{1'b1}}), .out(des_E), .sel(jal));
endmodule

module W (
  input  [31:0] in_1,
  input  [31:0] RD,
  input  [31:0] pc_8,
  input  [31:0] aluresult,
  output [4:0] des_E,
  output [31:0] toD
);

  wire addiu, addu, beq, bgtz, bne, j, jal, jr, lb, lh, lui, lw, nop, or_1_out, or_2_out, or_3_out, or_4_out,
       or_5_out, or_6_out, ori, sb, sh, subu, sw;
  wire [4:0] multiplexer_2_out, multiplexer_4_out, rd_t, rt;
  wire [5:0] splitter_1_func, splitter_1_op;
  wire [31:0] multiplexer_1_out, multiplexer_3_out;

  splitter splitter_1 (
    .instr(in_1), .func(splitter_1_func), ._11_15rd(rd_t), ._16_20rt(rt), .op(splitter_1_op));  // open: _0_15, _0_25, _21_25rs
  controllerpart controllerpart_1 (
    .out_3(lw), .out_4(sw), .out_5(ori), .out_6(j), .out_7(beq), .out_8(lui), .out_9(addu), .out_10(subu),
    .out_11(nop), .op(splitter_1_op), .funct(splitter_1_func), .out_12(jr), .out_13(jal), .out_14(addiu),
    .out_15(sb), .out_16(sh), .out_17(lb), .out_18(lh), .out_19(bne), .out_20(bgtz));
  or or_1 (or_1_out, lb, lh, lw);
  Multiplexer #(.width(32), .enable("false")) multiplexer_1 (
    .in0({32{1'b0}}), .in1(RD), .out(multiplexer_1_out), .sel(or_1_out));
  or or_2 (or_2_out, addu, subu);
  or or_3 (or_3_out, lb, lh, lw);
  or or_4 (or_4_out, ori, addiu);
  Multiplexer #(.width(5), .enable("false")) multiplexer_2 (
    .in0({5{1'b0}}), .in1(rd_t), .out(multiplexer_2_out), .sel(or_2_out));
  Multiplexer #(.width(32), .enable("false")) multiplexer_3 (
    .in0(multiplexer_1_out), .in1(pc_8), .out(multiplexer_3_out), .sel(jal));
  Multiplexer #(.width(5), .enable("false")) multiplexer_4 (
    .in0(multiplexer_2_out), .in1(rt), .out(multiplexer_4_out), .sel(or_5_out));
  or or_5 (or_5_out, or_3_out, or_4_out, lui);
  Multiplexer #(.width(32), .enable("false")) multiplexer_5 (
    .in0(multiplexer_3_out), .in1(aluresult), .out(toD), .sel(or_6_out));
  or or_6 (or_6_out, lui, ori, addu, subu, addiu);
  Multiplexer #(.width(5), .enable("false")) multiplexer_6 (
    .in0(multiplexer_4_out), .in1({5{1'b1}}), .out(des_E), .sel(jal));
endmodule

module EXT (
  input  [1:0] in_1,
  input  [15:0] in_2,
  output [31:0] out_3
);

  wire [31:0] bit_extender_1_out, bit_extender_2_out, bit_extender_3_out, shifter_1_out;

  assign bit_extender_1_out = {{16{1'b0}}, in_2};  // Bit_Extender bit_extender_1
  assign bit_extender_2_out = {{16{1'b0}}, in_2};  // Bit_Extender bit_extender_2
  assign bit_extender_3_out = {{16{in_2[15]}}, in_2};  // Bit_Extender bit_extender_3
  Shifter #(.width(32)) shifter_1 (.in(bit_extender_1_out), .\dist (5'b10000), .out(shifter_1_out));
  Multiplexer #(.select(2), .width(32), .enable("false")) multiplexer_1 (
    .in0(bit_extender_2_out), .in1(bit_extender_3_out), .in2(shifter_1_out), .out(out_3), .sel(in_1));  // open: in3
endmodule

module foward (
  input  [4:0] s1_D,
  input  [4:0] s2_D,
  input  [4:0] s1_E,
  input  [4:0] s2_E,
  input  [4:0] des_E,
  input  [3:0] tNew_E,
  input  [4:0] s2_M,
  input  [3:0] tNew_M,
  input  [4:0] des_M,
  input  [3:0] tNew_W,
  input  [4:0] des_W,
  output [1:0] fRsDsel,
  output [1:0] fRtDsel,
  output [1:0] fRsEsel,
  output [1:0] fRtEsel,
  output fRtMsel
);

  wire and_1_out, and_2_out, and_3_out, and_4_out, and_5_out, and_6_out, and_7_out, and_8_out, and_9_out,
       comparator_1_eq, comparator_2_eq, comparator_3_eq, comparator_4_eq, comparator_5_eq, comparator_6_eq,
       comparator_7_eq, comparator_8_eq, comparator_9_eq, comparator_10_eq, comparator_11_eq,
       comparator_12_eq, comparator_13_eq, comparator_14_eq, comparator_15_eq, comparator_16_eq,
       comparator_17_eq, comparator_18_eq, comparator_19_eq, comparator_20_eq, comparator_21_eq,
       comparator_22_eq, comparator_23_eq, comparator_24_eq, comparator_25_eq, comparator_26_eq,
       comparator_27_eq, not_1_out, not_2_out, not_3_out, not_4_out, not_5_out, not_6_out, not_7_out,
       not_8_out, not_9_out;
  wire [1:0] multiplexer_1_out, multiplexer_2_out, multiplexer_5_out, multiplexer_6_out;

  Comparator #(.width(5), .mode("unsigned")) comparator_1 (
    .a(s1_D), .b({5{1'b0}}), .eq(comparator_1_eq));  // open: gt, lt
  not not_1 (not_1_out, comparator_1_eq);
  Comparator #(.width(5), .mode("unsigned")) comparator_2 (.a(s1_D), .b(des_M), .eq(comparator_2_eq));  // open: gt, lt
  Comparator #(.width(4), .mode("unsigned")) comparator_3 (
    .a(tNew_M), .b(4'b0000), .eq(comparator_3_eq));  // open: gt, lt
  Comparator #(.width(5), .mode("unsigned")) comparator_4 (
    .a(s1_D), .b({5{1'b0}}), .eq(comparator_4_eq));  // open: gt, lt
  not not_2 (not_2_out, comparator_4_eq);
  Comparator #(.width(5), .mode("unsigned")) comparator_5 (.a(s1_D), .b(des_E), .eq(comparator_5_eq));  // open: gt, lt
  Comparator #(.width(4), .mode("unsigned")) comparator_6 (
    .a(tNew_E), .b(4'b0000), .eq(comparator_6_eq));  // open: gt, lt
  Comparator #(.width(5), .mode("unsigned")) comparator_7 (
    .a(s2_D), .b({5{1'b0}}), .eq(comparator_7_eq));  // open: gt, lt
  Comparator #(.width(5), .mode("unsigned")) comparator_8 (.a(s2_D), .b(des_M), .eq(comparator_8_eq));  // open: gt, lt
  Comparator #(.width(4), .mode("unsigned")) comparator_9 (
    .a(tNew_M), .b(4'b0000), .eq(comparator_9_eq));  // open: gt, lt
  Comparator #(.width(5), .mode("unsigned")) comparator_10 (
    .a(s2_D), .b({5{1'b0}}), .eq(comparator_10_eq));  // open: gt, lt
  Comparator #(.width(5), .mode("unsigned")) comparator_11 (
    .a(s2_D), .b(des_E), .eq(comparator_11_eq));  // open: gt, lt
  Comparator #(.width(4), .mode("unsigned")) comparator_12 (
    .a(tNew_E), .b(4'b0000), .eq(comparator_12_eq));  // open: gt, lt
  and and_1 (and_1_out, not_1_out, comparator_2_eq, comparator_3_eq);
  and and_2 (and_2_out, not_2_out, comparator_5_eq, comparator_6_eq);
  not not_3 (not_3_out, comparator_7_eq);
  not not_4 (not_4_out, comparator_10_eq);
  Multiplexer #(.width(2)) multiplexer_1 (
    .in0(2'b00), .in1(2'b10), .out(multiplexer_1_out), .sel(and_1_out));  // open: en
  and and_3 (and_3_out, not_3_out, comparator_8_eq, comparator_9_eq);
  and and_4 (and_4_out, not_4_out, comparator_11_eq, comparator_12_eq);
  Multiplexer #(.width(2)) multiplexer_2 (
    .in0(2'b00), .in1(2'b10), .out(multiplexer_2_out), .sel(and_3_out));  // open: en
  Multiplexer #(.width(2)) multiplexer_3 (
    .in0(multiplexer_1_out), .in1(2'b01), .out(fRsDsel), .sel(and_2_out));  // open: en
  Multiplexer #(.width(2)) multiplexer_4 (
    .in0(multiplexer_2_out), .in1(2'b01), .out(fRtDsel), .sel(and_4_out));  // open: en
  Comparator #(.width(5), .mode("unsigned")) comparator_13 (
    .a(s1_E), .b({5{1'b0}}), .eq(comparator_13_eq));  // open: gt, lt
  Comparator #(.width(5), .mode("unsigned")) comparator_14 (
    .a(s1_E), .b(des_W), .eq(comparator_14_eq));  // open: gt, lt
  Comparator #(.width(4), .mode("unsigned")) comparator_15 (
    .a(tNew_W), .b(4'b0000), .eq(comparator_15_eq));  // open: gt, lt
  Comparator #(.width(5), .mode("unsigned")) comparator_16 (
    .a(s1_E), .b({5{1'b0}}), .eq(comparator_16_eq));  // open: gt, lt
  Comparator #(.width(5), .mode("unsigned")) comparator_17 (
    .a(s1_E), .b(des_M), .eq(comparator_17_eq));  // open: gt, lt
  Comparator #(.width(4), .mode("unsigned")) comparator_18 (
    .a(tNew_M), .b(4'b0000), .eq(comparator_18_eq));  // open: gt, lt
  Comparator #(.width(5), .mode("unsigned")) comparator_19 (
    .a(s2_E), .b({5{1'b0}}), .eq(comparator_19_eq));  // open: gt, lt
  Comparator #(.width(5), .mode("unsigned")) comparator_20 (
    .a(s2_E), .b(des_W), .eq(comparator_20_eq));  // open: gt, lt
  Comparator #(.width(4), .mode("unsigned")) comparator_21 (
    .a(tNew_W), .b(4'b0000), .eq(comparator_21_eq));  // open: gt, lt
  Comparator #(.width(5), .mode("unsigned")) comparator_22 (
    .a(s2_E), .b({5{1'b0}}), .eq(comparator_22_eq));  // open: gt, lt
  Comparator #(.width(5), .mode("unsigned")) comparator_23 (
    .a(s2_E), .b(des_M), .eq(comparator_23_eq));  // open: gt, lt
  Comparator #(.width(4), .mode("unsigned")) comparator_24 (
    .a(tNew_M), .b(4'b0000), .eq(comparator_24_eq));  // open: gt, lt
  not not_5 (not_5_out, comparator_13_eq);
  not not_6 (not_6_out, comparator_16_eq);
  not not_7 (not_7_out, comparator_19_eq);
  not not_8 (not_8_out, comparator_22_eq);
  and and_5 (and_5_out, not_5_out, comparator_14_eq, comparator_15_eq);
  and and_6 (and_6_out, not_6_out, comparator_17_eq, comparator_18_eq);
  and and_7 (and_7_out, not_7_out, comparator_20_eq, comparator_21_eq);
  and and_8 (and_8_out, not_8_out, comparator_23_eq, comparator_24_eq);
  Multiplexer #(.width(2)) multiplexer_5 (
    .in0(2'b00), .in1(2'b10), .out(multiplexer_5_out), .sel(and_5_out));  // open: en
  Multiplexer #(.width(2)) multiplexer_6 (
    .in0(2'b00), .in1(2'b10), .out(multiplexer_6_out), .sel(and_7_out));  // open: en
  Multiplexer #(.width(2)) multiplexer_7 (
    .in0(multiplexer_5_out), .in1(2'b01), .out(fRsEsel), .sel(and_6_out));  // open: en
  Multiplexer #(.width(2)) multiplexer_8 (
    .in0(multiplexer_6_out), .in1(2'b01), .out(fRtEsel), .sel(and_8_out));  // open: en
  not not_9 (not_9_out, comparator_25_eq);
  Comparator #(.width(5), .mode("unsigned")) comparator_25 (
    .a(s2_M), .b({5{1'b0}}), .eq(comparator_25_eq));  // open: gt, lt
  Comparator #(.width(5), .mode("unsigned")) comparator_26 (
    .a(s2_M), .b(des_W), .eq(comparator_26_eq));  // open: gt, lt
  Comparator #(.width(4), .mode("unsigned")) comparator_27 (
    .a(tNew_W), .b(4'b0000), .eq(comparator_27_eq));  // open: gt, lt
  and and_9 (and_9_out, not_9_out, comparator_26_eq, comparator_27_eq);
  Multiplexer multiplexer_9 (.in0(1'b0), .in1(1'b1), .out(fRtMsel), .sel(and_9_out));  // open: en
endmodule

module stallU (
  input  [4:0] s1_D,
  input  [4:0] s2_D,
  input  [1:0] tUse1_D,
  input  [1:0] tUse2_D,
  input  [4:0] des_E,
  input  [3:0] tNew_E,
  input  [3:0] tNew_M,
  input  [4:0] des_M,
  output Stall_F,
  output Stall_D,
  output flush_E
);

  wire and_1_out, and_2_out, and_3_out, and_4_out, comparator_1_eq, comparator_2_eq, comparator_3_lt,
       comparator_4_eq, comparator_5_eq, comparator_6_lt, comparator_7_eq, comparator_8_eq, comparator_9_lt,
       comparator_10_eq, comparator_11_eq, comparator_12_lt, not_1_out, not_2_out, not_3_out, not_4_out;
  wire [3:0] tUse1_D_t, tUse2_D_t;

  Comparator #(.width(5), .mode("unsigned")) comparator_1 (
    .a(s1_D), .b({5{1'b0}}), .eq(comparator_1_eq));  // open: gt, lt
  Comparator #(.width(5), .mode("unsigned")) comparator_2 (.a(s1_D), .b(des_E), .eq(comparator_2_eq));  // open: gt, lt
  Comparator #(.width(4), .mode("unsigned")) comparator_3 (
    .a(tUse1_D_t), .b(tNew_E), .lt(comparator_3_lt));  // open: gt, eq
  Comparator #(.width(5), .mode("unsigned")) comparator_4 (
    .a(s2_D), .b({5{1'b0}}), .eq(comparator_4_eq));  // open: gt, lt
  Comparator #(.width(5), .mode("unsigned")) comparator_5 (.a(s2_D), .b(des_E), .eq(comparator_5_eq));  // open: gt, lt
  Comparator #(.width(4), .mode("unsigned")) comparator_6 (
    .a(tUse2_D_t), .b(tNew_E), .lt(comparator_6_lt));  // open: gt, eq
  Comparator #(.width(5), .mode("unsigned")) comparator_7 (
    .a(s1_D), .b({5{1'b0}}), .eq(comparator_7_eq));  // open: gt, lt
  Comparator #(.width(5), .mode("unsigned")) comparator_8 (.a(s1_D), .b(des_M), .eq(comparator_8_eq));  // open: gt, lt
  Comparator #(.width(4), .mode("unsigned")) comparator_9 (
    .a(tUse1_D_t), .b(tNew_M), .lt(comparator_9_lt));  // open: gt, eq
  Comparator #(.width(5), .mode("unsigned")) comparator_10 (
    .a(s2_D), .b({5{1'b0}}), .eq(comparator_10_eq));  // open: gt, lt
  Comparator #(.width(5), .mode("unsigned")) comparator_11 (
    .a(s2_D), .b(des_M), .eq(comparator_11_eq));  // open: gt, lt
  Comparator #(.width(4), .mode("unsigned")) comparator_12 (
    .a(tUse2_D_t), .b(tNew_M), .lt(comparator_12_lt));  // open: gt, eq
  assign tUse1_D_t = {{2{1'b0}}, tUse1_D};  // Bit_Extender bit_extender_1
  not not_1 (not_1_out, comparator_1_eq);
  not not_2 (not_2_out, comparator_4_eq);
  not not_3 (not_3_out, comparator_7_eq);
  not not_4 (not_4_out, comparator_10_eq);
  and and_1 (and_1_out, not_1_out, comparator_2_eq, comparator_3_lt);
  and and_2 (and_2_out, not_2_out, comparator_5_eq, comparator_6_lt);
  and and_3 (and_3_out, not_3_out, comparator_8_eq, comparator_9_lt);
  and and_4 (and_4_out, not_4_out, comparator_11_eq, comparator_12_lt);
  assign tUse2_D_t = {{2{1'b0}}, tUse2_D};  // Bit_Extender bit_extender_2
  or or_1 (flush_E, and_1_out, and_2_out, and_3_out, and_4_out);

  assign Stall_D = flush_E;
  assign Stall_F = flush_E;

  // Other names for the same wires on the sheet: stall_flag = flush_E
endmodule
