// Logisim project trial-8.circ as structural Verilog: 23 circuits, main circuit main
module main (
  input  Reset,
  output [31:0] out_2,
  output Reg_Write,
  output [4:0] RegAddr,
  output [31:0] RegData,
  output MemWrite,
  output [4:0] MemAddr,
  output [31:0] MemData
);

  wire BSEL, BSEL_E, clock, Flush_E, forwardnuit_1_frtmsel, Stall_D, Stall_F, we, we_E, we_M, WM, WM_E, WM_M;
  wire [1:0] A3SEL, A3SEL_E, A3SEL_M, A3SEL_W, cmpop, DMSEL, DMSEL_E, DMSEL_M, extop, forwardnuit_1_frsdsel,
       forwardnuit_1_frsesel, forwardnuit_1_frtdsel, forwardnuit_1_frtesel, NPCOP, tuse1_D, tuse2_D, WD3SEL,
       WD3SEL_E, WD3SEL_M, WD3SEL_W;
  wire [2:0] aluop, aluop_E;
  wire [3:0] tnew_E, tnew_M, tnew_W;
  wire [4:0] Des_E, Des_M, Des_W, rd_D, rd_E, rs_D, rs_E, rt_D, rt_E, S1_D, S1_E, S2_D, S2_E, S2_M, shamt_D,
       shamt_E;
  wire [5:0] Func, Op;
  wire [15:0] I16_D, I16_E;
  wire [25:0] IM26_D, IM26_E;
  wire [31:0] AO_E, AO_M, AO_W, B, EtoD, EXTD_D, EXTD_E, Fwd_ALUA_E, Fwd_ALUB_E, Fwd_RD1_D, Fwd_RD2_D,
       Fwd_WD_M, IR_D, IR_E, IR_M, IR_W, MtoD, NPC, PC4_D, PC4_F, PC8_D, PC8_E, PC8_F, PC8_M, PC8_W, PC_D,
       PC_E, PC_F, PC_M, PC_W, RD1_D, RD1_E, RD2_D, RD2_E, RD_M, RD_W, wd, WD_M, WtoD;

  PC pc_1 (.NPC(NPC), .PC(PC_F), .Stall_F(Stall_F), .colck(clock), .reset(Reset));
  Clock u_clock (.out(clock));
  Adder #(.width(32)) adder_1 (.a(32'h4), .b(PC_F), .out(PC4_F));  // open: cin, cout
  Adder #(.width(32)) adder_2 (.a(32'h8), .b(PC_F), .out(PC8_F));  // open: cin, cout
  ext ext_1 (.Imm16(I16_D), .out_3(EXTD_D), .extop(extop));
  NPC npc_1 (.PC4(PC4_F), .I26(IM26_D), .rs(Fwd_RD1_D), .NPCOP(NPCOP), .D2(Fwd_RD2_D), .cmpop(cmpop), .out_7(NPC));
  ROM #(.addrWidth(10), .dataWidth(32)) rom_1 (.addr(PC_F[11:2]), .data(out_2));  // open: sel
  F_D_Reg f_d_reg_1 (
    .IR(out_2), .PC4(PC4_F), .PC8(PC8_F), .PC(PC_F), .clk(clock), .rst(Reset), .IR_2(IR_D), .PC4_2(PC4_D),
    .PC8_2(PC8_D), .PC_2(PC_D), .Stall_D(Stall_D));
  Controller controller_1 (
    .in_1(Op), .in_2(Func), .cmpop(cmpop), .extop(extop), .BSEL(BSEL), .WM(WM), .DMSEL(DMSEL), .A3SEL(A3SEL),
    .WD3SEL(WD3SEL), .aluop(aluop), .NPCOP(NPCOP), .we(we));
  Splitter splitter_1 (
    .IR(IR_D), .out_2(Op), .out_3(rs_D), .out_4(rt_D), .out_5(rd_D), .out_6(shamt_D), .out_7(Func),
    .out_8(I16_D), .out_9(IM26_D));
  D d_1 (.IR(IR_D), .S1_D(S1_D), .S2_D(S2_D), .tuse_1(tuse1_D), .tuse_2(tuse2_D));
  E e_1 (
    .IR_E(IR_E), .EXTD_E(EXTD_E), .PC8_E(PC8_E), .S1_E(S1_E), .S2_E(S2_E), .DES_E(Des_E), .EtoD(EtoD),
    .tnew_E(tnew_E));
  M m_1 (.IR_M(IR_M), .AO(AO_M), .PC8(PC8_M), .S2_M(S2_M), .Des_M(Des_M), .MtoD(MtoD));
  W w_1 (.IR_W(IR_W), .RD(RD_W), .AO({AO_W[31:7], MemAddr, AO_W[1:0]}), .PC8(PC8_W), .Des_M(Des_W), .WtoD(WtoD));
  RF rf_1 (
    .A1(rs_D), .A2(rt_D), .A3(RegAddr), .WD(RegData), .RD1(RD1_D), .RD2(RD2_D), .clk(clock), .reset(Reset),
    .we(Reg_Write));
  // Probe on forwardnuit_1_frsdsel
  forwardNuit forwardnuit_1 (
    .s1_D(S1_D), .s2_D(S2_D), .s1_E(S1_E), .s2_E(S2_E), .des_E(Des_E), .tNew_E(tnew_E), .s2_M(S2_M),
    .tNew_M(tnew_M), .des_M(Des_M), .tNew_W(tnew_W), .des_W(Des_W), .fRsDsel(forwardnuit_1_frsdsel),
    .fRtDsel(forwardnuit_1_frtdsel), .fRsEsel(forwardnuit_1_frsesel), .fRtEsel(forwardnuit_1_frtesel),
    .fRtMsel(forwardnuit_1_frtmsel));
  Multiplexer #(.select(2), .width(32), .enable("false")) multiplexer_1 (
    .in0(RD1_D), .in1(EtoD), .in2(MtoD), .in3({32{1'b0}}), .out(Fwd_RD1_D), .sel(forwardnuit_1_frsdsel));
  StallUnit stallunit_1 (
    .s1_D(S1_D), .s2_D(S2_D), .tUse1_D(tuse1_D), .tUse2_D(tuse2_D), .des_E(Des_E), .tNew_E(tnew_E),
    .tNew_M(tnew_M), .des_M(Des_M), .Stall_F(Stall_F), .Stall_D(Stall_D), .flush_E(Flush_E));
  D_E_Reg d_e_reg_1 (
    .IR_2(IR_D), .RD1_2(Fwd_RD1_D), .EXTD_2(EXTD_D), .RD2_2(Fwd_RD2_D), .PC8_2(PC8_D), .PC_2(PC_D),
    .Clk(clock), .rst(Reset), .IR_3(IR_E), .RD1_3(RD1_E), .EXTD_3(EXTD_E), .RD2_3(RD2_E), .PC8_3(PC8_E),
    .PC_3(PC_E), .BSEL(BSEL), .BSEL_E(BSEL_E), .aluop(aluop), .aluop_E(aluop_E), .WM(WM), .WM_E(WM_E),
    .A3SEL(A3SEL), .A3SEL_E(A3SEL_E), .WD3SEL(WD3SEL), .WD3SEL_E(WD3SEL_E), .we(we), .we_E(we_E),
    .DMSEL(DMSEL), .DMSEL_E(DMSEL_E), .Flush_E(Flush_E));
  Multiplexer #(.select(2), .width(32), .enable("false")) multiplexer_2 (
    .in0(RD2_D), .in1(EtoD), .in2(MtoD), .in3({32{1'b0}}), .out(Fwd_RD2_D), .sel(forwardnuit_1_frtdsel));
  Splitter splitter_2 (
    .IR(IR_E), .out_3(rs_E), .out_4(rt_E), .out_5(rd_E), .out_6(shamt_E), .out_8(I16_E), .out_9(IM26_E));  // open: out_2, out_7
  // Probe on forwardnuit_1_frsesel
  Multiplexer #(.select(2), .width(32), .enable("false")) multiplexer_3 (
    .in0(RD1_E), .in1(MtoD), .in2(WtoD), .in3({32{1'b0}}), .out(Fwd_ALUA_E), .sel(forwardnuit_1_frsesel));
  ALU alu_1 (.A(Fwd_ALUA_E), .B(B), .aluop(aluop_E), .shamt(shamt_E), .out_5(AO_E));
  Multiplexer #(.width(32), .enable("false")) multiplexer_4 (.in0(Fwd_ALUB_E), .in1(EXTD_E), .out(B), .sel(BSEL_E));
  Multiplexer #(.select(2), .width(32), .enable("false")) multiplexer_5 (
    .in0(RD2_E), .in1(MtoD), .in2(WtoD), .in3({32{1'b0}}), .out(Fwd_ALUB_E), .sel(forwardnuit_1_frtesel));
  E_M_Reg e_m_reg_1 (
    .IR(IR_E), .AO(AO_E), .RD2(Fwd_ALUB_E), .PC8(PC8_E), .PC(PC_E), .out_14(IR_M), .out_15(AO_M),
    .out_16(WD_M), .out_17(PC8_M), .out_18(PC_M), .clk(clock), .rst(Reset), .WM(WM_E), .WM_E(WM_M),
    .A3SEL(A3SEL_E), .A3SEL_E(A3SEL_M), .WD3SEL(WD3SEL_E), .WD3SEL_E(WD3SEL_M), .we(we_E), .we_E(we_M),
    .DMSEL(DMSEL_E), .DMSEL_E(DMSEL_M), .tnew_E(tnew_E), .tnew_M(tnew_M));
  Multiplexer #(.width(32), .enable("false")) multiplexer_6 (
    .in0(WD_M), .in1(WtoD), .out(Fwd_WD_M), .sel(forwardnuit_1_frtmsel));
  DM dm_1 (.A(AO_M), .WD(Fwd_WD_M), .clk(clock), .MemWrite(WM_M), .Reset(Reset), .Sel(DMSEL_M), .RD(RD_M), .out_8(wd));
  M_W_Reg m_w_reg_1 (
    .IR(IR_M), .RD(RD_M), .AO(AO_M), .PC8(PC8_M), .PC(PC_M), .clk(clock), .rst(Reset), .out_14(IR_W),
    .out_15(RD_W), .out_16({AO_W[31:7], MemAddr, AO_W[1:0]}), .out_17(PC8_W), .out_18(PC_W), .A3SEL(A3SEL_M),
    .A3SEL_E(A3SEL_W), .WD3SEL(WD3SEL_M), .WD3SEL_E(WD3SEL_W), .we(we_M), .we_E(Reg_Write), .tnew_E(tnew_M),
    .tnew_M(tnew_W), .WM_W(WM_M), .MemWrite_W(MemWrite), .MemData(wd), .MemData_2(MemData));
  MFA3 mfa3_1 (.IR(IR_W), .A3SEL(A3SEL_W), .A3(RegAddr));
  MFWD3 mfwd3_1 (.AO_W({AO_W[31:7], MemAddr, AO_W[1:0]}), .PC_8W(PC8_W), .WD3SEL(WD3SEL_W), .WD3(RegData), .RD(RD_W));

  // Other names for the same wires on the sheet: A3[4:0] = RegAddr; AO_W[6:2] = MemAddr; IR_F[31:0] = out_2;
  //   WD3[31:0] = RegData; we_W = Reg_Write; WriteMem = MemWrite
endmodule

module IM (
  input  [31:0] PC,
  output [31:0] D
);

  ROM #(.addrWidth(10), .dataWidth(32)) rom_1 (.addr(PC[11:2]), .data(D));  // open: sel

  // Notes on the sheet:
  //   contents of rom_1 (hex, n*v repeats v):
  //   3c090064 3c0a0064 ae290000 8e2b0000 112b0002 0 1494821 1494823 8000c0b 0 1498821 1498823
endmodule

module F_D_Reg (
  input  [31:0] IR,
  input  [31:0] PC4,
  input  [31:0] PC8,
  input  [31:0] PC,
  input  clk,
  input  rst,
  input  Stall_D,
  output [31:0] IR_2,
  output [31:0] PC4_2,
  output [31:0] PC8_2,
  output [31:0] PC_2
);

  wire Stall_D_t;

  not not_1 (Stall_D_t, Stall_D);
  Register #(.width(32)) register_1 (.D(IR), .en(Stall_D_t), .Q(IR_2), .clk(clk), .clr(rst));
  Register #(.width(32)) register_2 (.D(PC4), .en(Stall_D_t), .Q(PC4_2), .clk(clk), .clr(rst));
  Register #(.width(32)) register_3 (.D(PC8), .en(Stall_D_t), .Q(PC8_2), .clk(clk), .clr(rst));
  Register #(.width(32)) register_4 (.D(PC), .en(Stall_D_t), .Q(PC_2), .clk(clk), .clr(rst));
endmodule

module RF (
  input  [4:0] A1,
  input  clk,
  input  reset,
  input  we,
  input  [4:0] A2,
  input  [4:0] A3,
  input  [31:0] WD,
  output [31:0] RD1,
  output [31:0] RD2
);

  wire and_1_out, and_2_out, comparator_1_eq, comparator_2_eq, comparator_3_eq, comparator_4_eq;
  wire [31:0] I0, I1, I2, I3, I4, I5, I6, I7, I8, I9, I10, I11, I12, I13, I14, I15, I16, I17, I18, I19, I20,
       I21, I22, I23, I24, I25, I26, I27, I28, I29, I30, I31, multiplexer_2_out, multiplexer_3_out, O0, O1,
       O2, O3, O4, O5, O6, O7, O8, O9, O10, O11, O12, O13, O14, O15, O16, O17, O18, O19, O20, O21, O22, O23,
       O24, O25, O26, O27, O28, O29, O30, O31, RD1_t, RD2_t;

  Demultiplexer #(.select(5), .width(32), .tristate("true")) demultiplexer_1 (
    .out0(I0), .out1(I1), .out2(I2), .out3(I3), .out4(I4), .out5(I5), .out6(I6), .out7(I7), .out8(I8),
    .out9(I9), .out10(I10), .out11(I11), .out12(I12), .out13(I13), .out14(I14), .out15(I15), .out16(I16),
    .out17(I17), .out18(I18), .out19(I19), .out20(I20), .out21(I21), .out22(I22), .out23(I23), .out24(I24),
    .out25(I25), .out26(I26), .out27(I27), .out28(I28), .out29(I29), .out30(I30), .out31(I31), .in(WD),
    .sel(A3));  // open: en
  Multiplexer #(.select(5), .width(32)) multiplexer_1 (
    .in0(O0), .in1(O1), .in2(O2), .in3(O3), .in4(O4), .in5(O5), .in6(O6), .in7(O7), .in8(O8), .in9(O9),
    .in10(O10), .in11(O11), .in12(O12), .in13(O13), .in14(O14), .in15(O15), .in16(O16), .in17(O17),
    .in18(O18), .in19(O19), .in20(O20), .in21(O21), .in22(O22), .in23(O23), .in24(O24), .in25(O25),
    .in26(O26), .in27(O27), .in28(O28), .in29(O29), .in30(O30), .in31(O31), .out(RD2_t), .sel(A2));  // open: en
  Comparator #(.width(5)) comparator_1 (.a(A1), .b(A3), .eq(comparator_1_eq));  // open: gt, lt
  Comparator #(.width(5)) comparator_2 (.a(A2), .b(A3), .eq(comparator_2_eq));  // open: gt, lt
  Comparator #(.width(5)) comparator_3 (.a(A1), .b({5{1'b0}}), .eq(comparator_3_eq));  // open: gt, lt
  Multiplexer #(.width(32), .enable("false")) multiplexer_2 (
    .in0(RD1_t), .in1(WD), .out(multiplexer_2_out), .sel(and_1_out));
  and and_1 (and_1_out, comparator_1_eq, we);
  Comparator #(.width(5)) comparator_4 (.a(A2), .b({5{1'b0}}), .eq(comparator_4_eq));  // open: gt, lt
  Multiplexer #(.width(32), .enable("false")) multiplexer_3 (
    .in0(RD2_t), .in1(WD), .out(multiplexer_3_out), .sel(and_2_out));
  and and_2 (and_2_out, comparator_2_eq, we);
  Multiplexer #(.width(32), .enable("false")) multiplexer_4 (
    .in0(multiplexer_2_out), .in1({32{1'b0}}), .out(RD1), .sel(comparator_3_eq));
  Multiplexer #(.width(32), .enable("false")) multiplexer_5 (
    .in0(multiplexer_3_out), .in1({32{1'b0}}), .out(RD2), .sel(comparator_4_eq));
  Multiplexer #(.select(5), .width(32)) multiplexer_6 (
    .in0(O0), .in1(O1), .in2(O2), .in3(O3), .in4(O4), .in5(O5), .in6(O6), .in7(O7), .in8(O8), .in9(O9),
    .in10(O10), .in11(O11), .in12(O12), .in13(O13), .in14(O14), .in15(O15), .in16(O16), .in17(O17),
    .in18(O18), .in19(O19), .in20(O20), .in21(O21), .in22(O22), .in23(O23), .in24(O24), .in25(O25),
    .in26(O26), .in27(O27), .in28(O28), .in29(O29), .in30(O30), .in31(O31), .out(RD1_t), .sel(A1));  // open: en
  Register #(.width(32)) register_1 (.D({32{1'b0}}), .en(we), .Q(O0), .clk(clk), .clr(reset));
  Register #(.width(32)) register_2 (.D(I8), .en(we), .Q(O8), .clk(clk), .clr(reset));
  Register #(.width(32)) register_3 (.D(I16), .en(we), .Q(O16), .clk(clk), .clr(reset));
  Register #(.width(32)) register_4 (.D(I24), .en(we), .Q(O24), .clk(clk), .clr(reset));
  Register #(.width(32)) register_5 (.D(I1), .en(we), .Q(O1), .clk(clk), .clr(reset));
  Register #(.width(32)) register_6 (.D(I9), .en(we), .Q(O9), .clk(clk), .clr(reset));
  Register #(.width(32)) register_7 (.D(I17), .en(we), .Q(O17), .clk(clk), .clr(reset));
  Register #(.width(32)) register_8 (.D(I25), .en(we), .Q(O25), .clk(clk), .clr(reset));
  Register #(.width(32)) register_9 (.D(I2), .en(we), .Q(O2), .clk(clk), .clr(reset));
  Register #(.width(32)) register_10 (.D(I10), .en(we), .Q(O10), .clk(clk), .clr(reset));
  Register #(.width(32)) register_11 (.D(I18), .en(we), .Q(O18), .clk(clk), .clr(reset));
  Register #(.width(32)) register_12 (.D(I26), .en(we), .Q(O26), .clk(clk), .clr(reset));
  Register #(.width(32)) register_13 (.D(I3), .en(we), .Q(O3), .clk(clk), .clr(reset));
  Register #(.width(32)) register_14 (.D(I11), .en(we), .Q(O11), .clk(clk), .clr(reset));
  Register #(.width(32)) register_15 (.D(I19), .en(we), .Q(O19), .clk(clk), .clr(reset));
  Register #(.width(32)) register_16 (.D(I27), .en(we), .Q(O27), .clk(clk), .clr(reset));
  Register #(.width(32)) register_17 (.D(I4), .en(we), .Q(O4), .clk(clk), .clr(reset));
  Register #(.width(32)) register_18 (.D(I12), .en(we), .Q(O12), .clk(clk), .clr(reset));
  Register #(.width(32)) register_19 (.D(I20), .en(we), .Q(O20), .clk(clk), .clr(reset));
  Register #(.width(32)) register_20 (.D(I28), .en(we), .Q(O28), .clk(clk), .clr(reset));
  Register #(.width(32)) register_21 (.D(I5), .en(we), .Q(O5), .clk(clk), .clr(reset));
  Register #(.width(32)) register_22 (.D(I13), .en(we), .Q(O13), .clk(clk), .clr(reset));
  Register #(.width(32)) register_23 (.D(I21), .en(we), .Q(O21), .clk(clk), .clr(reset));
  Register #(.width(32)) register_24 (.D(I29), .en(we), .Q(O29), .clk(clk), .clr(reset));
  Register #(.width(32)) register_25 (.D(I6), .en(we), .Q(O6), .clk(clk), .clr(reset));
  Register #(.width(32)) register_26 (.D(I14), .en(we), .Q(O14), .clk(clk), .clr(reset));
  Register #(.width(32)) register_27 (.D(I22), .en(we), .Q(O22), .clk(clk), .clr(reset));
  Register #(.width(32)) register_28 (.D(I30), .en(we), .Q(O30), .clk(clk), .clr(reset));
  Register #(.width(32)) register_29 (.D(I7), .en(we), .Q(O7), .clk(clk), .clr(reset));
  Register #(.width(32)) register_30 (.D(I15), .en(we), .Q(O15), .clk(clk), .clr(reset));
  Register #(.width(32)) register_31 (.D(I23), .en(we), .Q(O23), .clk(clk), .clr(reset));
  Register #(.width(32)) register_32 (.D(I31), .en(we), .Q(O31), .clk(clk), .clr(reset));
endmodule

module D_E_Reg (
  input  [31:0] IR_2,
  input  [31:0] RD1_2,
  input  [31:0] EXTD_2,
  input  [31:0] RD2_2,
  input  [31:0] PC8_2,
  input  [31:0] PC_2,
  input  BSEL,
  input  [2:0] aluop,
  input  WM,
  input  [1:0] A3SEL,
  input  [1:0] WD3SEL,
  input  we,
  input  [1:0] DMSEL,
  input  Clk,
  input  rst,
  input  Flush_E,
  output [31:0] IR_3,
  output [31:0] RD1_3,
  output [31:0] EXTD_3,
  output [31:0] RD2_3,
  output [31:0] PC8_3,
  output [31:0] PC_3,
  output BSEL_E,
  output [2:0] aluop_E,
  output WM_E,
  output [1:0] A3SEL_E,
  output [1:0] WD3SEL_E,
  output we_E,
  output [1:0] DMSEL_E
);

  wire multiplexer_7_out, multiplexer_9_out, multiplexer_12_out;
  wire [1:0] multiplexer_10_out, multiplexer_11_out, multiplexer_13_out;
  wire [2:0] multiplexer_8_out;
  wire [31:0] multiplexer_1_out, multiplexer_2_out, multiplexer_3_out, multiplexer_4_out, multiplexer_5_out,
       multiplexer_6_out;

  Multiplexer #(.width(32), .enable("false")) multiplexer_1 (
    .in0(IR_2), .in1({32{1'b0}}), .out(multiplexer_1_out), .sel(Flush_E));
  Multiplexer #(.width(32), .enable("false")) multiplexer_2 (
    .in0(RD1_2), .in1({32{1'b0}}), .out(multiplexer_2_out), .sel(Flush_E));
  Multiplexer #(.width(32), .enable("false")) multiplexer_3 (
    .in0(EXTD_2), .in1({32{1'b0}}), .out(multiplexer_3_out), .sel(Flush_E));
  Multiplexer #(.width(32), .enable("false")) multiplexer_4 (
    .in0(RD2_2), .in1({32{1'b0}}), .out(multiplexer_4_out), .sel(Flush_E));
  Multiplexer #(.width(32), .enable("false")) multiplexer_5 (
    .in0(PC8_2), .in1({32{1'b0}}), .out(multiplexer_5_out), .sel(Flush_E));
  Multiplexer #(.width(32), .enable("false")) multiplexer_6 (
    .in0(PC_2), .in1({32{1'b0}}), .out(multiplexer_6_out), .sel(Flush_E));
  Multiplexer #(.enable("false")) multiplexer_7 (.in0(BSEL), .in1(1'b0), .out(multiplexer_7_out), .sel(Flush_E));
  Multiplexer #(.width(3), .enable("false")) multiplexer_8 (
    .in0(aluop), .in1(3'b000), .out(multiplexer_8_out), .sel(Flush_E));
  Multiplexer #(.enable("false")) multiplexer_9 (.in0(WM), .in1(1'b0), .out(multiplexer_9_out), .sel(Flush_E));
  Multiplexer #(.width(2), .enable("false")) multiplexer_10 (
    .in0(A3SEL), .in1(2'b00), .out(multiplexer_10_out), .sel(Flush_E));
  Multiplexer #(.width(2), .enable("false")) multiplexer_11 (
    .in0(WD3SEL), .in1(2'b00), .out(multiplexer_11_out), .sel(Flush_E));
  Register #(.width(1)) register_1 (.D(multiplexer_12_out), .Q(we_E), .clk(Clk), .clr(rst));  // open: en
  Multiplexer #(.enable("false")) multiplexer_12 (.in0(we), .in1(1'b0), .out(multiplexer_12_out), .sel(Flush_E));
  Multiplexer #(.width(2), .enable("false")) multiplexer_13 (
    .in0(DMSEL), .in1(2'b00), .out(multiplexer_13_out), .sel(Flush_E));
  Register #(.width(2)) register_2 (.D(multiplexer_13_out), .Q(DMSEL_E), .clk(Clk), .clr(rst));  // open: en
  Register #(.width(32)) register_3 (.D(multiplexer_1_out), .Q(IR_3), .clk(Clk), .clr(rst));  // open: en
  Register #(.width(32)) register_4 (.D(multiplexer_2_out), .Q(RD1_3), .clk(Clk), .clr(rst));  // open: en
  Register #(.width(32)) register_5 (.D(multiplexer_3_out), .Q(EXTD_3), .clk(Clk), .clr(rst));  // open: en
  Register #(.width(32)) register_6 (.D(multiplexer_4_out), .Q(RD2_3), .clk(Clk), .clr(rst));  // open: en
  Register #(.width(32)) register_7 (.D(multiplexer_5_out), .Q(PC8_3), .clk(Clk), .clr(rst));  // open: en
  Register #(.width(32)) register_8 (.D(multiplexer_6_out), .Q(PC_3), .clk(Clk), .clr(rst));  // open: en
  Register #(.width(1)) register_9 (.D(multiplexer_7_out), .Q(BSEL_E), .clk(Clk), .clr(rst));  // open: en
  Register #(.width(3)) register_10 (.D(multiplexer_8_out), .Q(aluop_E), .clk(Clk), .clr(rst));  // open: en
  Register #(.width(1)) register_11 (.D(multiplexer_9_out), .Q(WM_E), .clk(Clk), .clr(rst));  // open: en
  Register #(.width(2)) register_12 (.D(multiplexer_10_out), .Q(A3SEL_E), .clk(Clk), .clr(rst));  // open: en
  Register #(.width(2)) register_13 (.D(multiplexer_11_out), .Q(WD3SEL_E), .clk(Clk), .clr(rst));  // open: en
endmodule

module E_M_Reg (
  input  [31:0] IR,
  input  [31:0] AO,
  input  [31:0] RD2,
  input  [31:0] PC8,
  input  [31:0] PC,
  input  WM,
  input  [1:0] A3SEL,
  input  [1:0] WD3SEL,
  input  we,
  input  [1:0] DMSEL,
  input  [3:0] tnew_E,
  input  clk,
  input  rst,
  output [31:0] out_14,
  output [31:0] out_15,
  output [31:0] out_16,
  output [31:0] out_17,
  output [31:0] out_18,
  output WM_E,
  output [1:0] A3SEL_E,
  output [1:0] WD3SEL_E,
  output we_E,
  output [1:0] DMSEL_E,
  output [3:0] tnew_M
);

  wire comparator_1_lt;
  wire [3:0] multiplexer_1_out, subtractor_1_out;

  Subtractor #(.width(4)) subtractor_1 (.a(tnew_E), .b(4'b0001), .out(subtractor_1_out));  // open: bin, bout
  Register #(.width(32)) register_1 (.D(IR), .Q(out_14), .clk(clk), .clr(rst));  // open: en
  Register #(.width(32)) register_2 (.D(AO), .Q(out_15), .clk(clk), .clr(rst));  // open: en
  Register #(.width(32)) register_3 (.D(RD2), .Q(out_16), .clk(clk), .clr(rst));  // open: en
  Register #(.width(32)) register_4 (.D(PC8), .Q(out_17), .clk(clk), .clr(rst));  // open: en
  Register #(.width(32)) register_5 (.D(PC), .Q(out_18), .clk(clk), .clr(rst));  // open: en
  Register #(.width(1)) register_6 (.D(WM), .Q(WM_E), .clk(clk), .clr(rst));  // open: en
  Register #(.width(2)) register_7 (.D(A3SEL), .Q(A3SEL_E), .clk(clk), .clr(rst));  // open: en
  Register #(.width(2)) register_8 (.D(WD3SEL), .Q(WD3SEL_E), .clk(clk), .clr(rst));  // open: en
  Register #(.width(1)) register_9 (.D(we), .Q(we_E), .clk(clk), .clr(rst));  // open: en
  Register #(.width(2)) register_10 (.D(DMSEL), .Q(DMSEL_E), .clk(clk), .clr(rst));  // open: en
  Comparator #(.width(4)) comparator_1 (.a(subtractor_1_out), .b(4'b0000), .lt(comparator_1_lt));  // open: gt, eq
  Multiplexer #(.width(4), .enable("false")) multiplexer_1 (
    .in0(subtractor_1_out), .in1(4'b0000), .out(multiplexer_1_out), .sel(comparator_1_lt));
  Register #(.width(4)) register_11 (.D(multiplexer_1_out), .Q(tnew_M), .clk(clk), .clr(rst));  // open: en
endmodule

module DM (
  input  [31:0] A,
  input  [31:0] WD,
  input  clk,
  input  MemWrite,
  input  Reset,
  input  [1:0] Sel,
  output [31:0] RD,
  output [31:0] out_8
);

  wire decoder_1_out0, decoder_1_out1, decoder_1_out2, decoder_1_out3, decoder_2_out0, decoder_2_out1;
  wire [7:0] _0_7, _8_15, _16_23, _24_31, multiplexer_2_out;
  wire [15:0] multiplexer_3_out;
  wire [31:0] lb, lh, sb, sh;

  Multiplexer #(.select(2), .width(32), .enable("false")) multiplexer_1 (
    .in0({_24_31, _16_23, _8_15, _0_7}), .in1(lh), .in2(lb), .out(RD), .sel(Sel));  // open: in3
  Multiplexer #(.select(2), .width(8), .enable("false")) multiplexer_2 (
    .in0(_0_7), .in1(_8_15), .in2(_16_23), .in3(_24_31), .out(multiplexer_2_out), .sel(A[1:0]));
  Multiplexer #(.width(16), .enable("false")) multiplexer_3 (
    .in0({_8_15, _0_7}), .in1({_24_31, _16_23}), .out(multiplexer_3_out), .sel(A[1]));
  assign lb = {{24{1'b0}}, multiplexer_2_out};  // Bit_Extender bit_extender_1
  assign lh = {{16{1'b0}}, multiplexer_3_out};  // Bit_Extender bit_extender_2
  Decoder #(.select(2)) decoder_1 (
    .out0(decoder_1_out0), .out1(decoder_1_out1), .out2(decoder_1_out2), .out3(decoder_1_out3), .sel(A[1:0]));  // open: en
  Decoder decoder_2 (.out0(decoder_2_out0), .out1(decoder_2_out1), .sel(A[1]));  // open: en
  Multiplexer #(.select(2), .width(32), .enable("false")) multiplexer_4 (
    .in0(WD), .in1(sh), .in2(sb), .out(out_8), .sel(Sel));  // open: in3
  Multiplexer #(.width(16), .enable("false")) multiplexer_5 (
    .in0({_8_15, _0_7}), .in1(WD[15:0]), .out(sh[15:0]), .sel(decoder_2_out0));
  Multiplexer #(.width(8), .enable("false")) multiplexer_6 (
    .in0(_0_7), .in1(WD[7:0]), .out(sb[7:0]), .sel(decoder_1_out0));
  Multiplexer #(.width(8), .enable("false")) multiplexer_7 (
    .in0(_8_15), .in1(WD[7:0]), .out(sb[15:8]), .sel(decoder_1_out1));
  Multiplexer #(.width(8), .enable("false")) multiplexer_8 (
    .in0(_16_23), .in1(WD[7:0]), .out(sb[23:16]), .sel(decoder_1_out2));
  Multiplexer #(.width(8), .enable("false")) multiplexer_9 (
    .in0(_24_31), .in1(WD[7:0]), .out(sb[31:24]), .sel(decoder_1_out3));
  Multiplexer #(.width(16), .enable("false")) multiplexer_10 (
    .in0({_24_31, _16_23}), .in1(WD[15:0]), .out(sh[31:16]), .sel(decoder_2_out1));
  RAM #(.addrWidth(5), .dataWidth(32), .bus("separate")) ram_1 (
    .addr(A[6:2]), .din(out_8), .data({_24_31, _16_23, _8_15, _0_7}), .str(MemWrite), .clk(clk), .clr(Reset));  // open: sel, ld

  // Other names for the same wires on the sheet: lw[31:0] = {_24_31, _16_23, _8_15, _0_7}; cb[1:0] = A[1:0];
  //   ch = A[1]; A_t[4:0] = A[6:2]; rst = Reset; _0_7s[7:0] = WD[7:0]; _0_15s_prime[15:0] = WD[15:0]; sw[31:0] = WD;
  //   WD_t[31:0] = out_8
endmodule

module M_W_Reg (
  input  [31:0] IR,
  input  [31:0] RD,
  input  [31:0] AO,
  input  [31:0] PC8,
  input  [31:0] PC,
  input  [1:0] A3SEL,
  input  [1:0] WD3SEL,
  input  we,
  input  WM_W,
  input  [31:0] MemData,
  input  [3:0] tnew_E,
  input  clk,
  input  rst,
  output [31:0] out_14,
  output [31:0] out_15,
  output [31:0] out_16,
  output [31:0] out_17,
  output [31:0] out_18,
  output [1:0] A3SEL_E,
  output [1:0] WD3SEL_E,
  output we_E,
  output MemWrite_W,
  output [31:0] MemData_2,
  output [3:0] tnew_M
);

  wire comparator_1_lt;
  wire [3:0] multiplexer_1_out, subtractor_1_out;

  Register #(.width(1)) register_1 (.D(WM_W), .Q(MemWrite_W), .clk(clk), .clr(rst));  // open: en
  Register #(.width(32)) register_2 (.D(MemData), .Q(MemData_2), .clk(clk), .clr(rst));  // open: en
  Subtractor #(.width(4)) subtractor_1 (.a(tnew_E), .b(4'b0001), .out(subtractor_1_out));  // open: bin, bout
  Register #(.width(32)) register_3 (.D(IR), .Q(out_14), .clk(clk), .clr(rst));  // open: en
  Register #(.width(32)) register_4 (.D(RD), .Q(out_15), .clk(clk), .clr(rst));  // open: en
  Register #(.width(32)) register_5 (.D(AO), .Q(out_16), .clk(clk), .clr(rst));  // open: en
  Register #(.width(32)) register_6 (.D(PC8), .Q(out_17), .clk(clk), .clr(rst));  // open: en
  Register #(.width(32)) register_7 (.D(PC), .Q(out_18), .clk(clk), .clr(rst));  // open: en
  Register #(.width(2)) register_8 (.D(A3SEL), .Q(A3SEL_E), .clk(clk), .clr(rst));  // open: en
  Register #(.width(1)) register_9 (.D(we), .Q(we_E), .clk(clk), .clr(rst));  // open: en
  Comparator #(.width(4)) comparator_1 (.a(subtractor_1_out), .b(4'b0000), .lt(comparator_1_lt));  // open: gt, eq
  Multiplexer #(.width(4), .enable("false")) multiplexer_1 (
    .in0(subtractor_1_out), .in1(4'b0000), .out(multiplexer_1_out), .sel(comparator_1_lt));
  Register #(.width(4)) register_10 (.D(multiplexer_1_out), .Q(tnew_M), .clk(clk), .clr(rst));  // open: en
  Register #(.width(2)) register_11 (.D(WD3SEL), .Q(WD3SEL_E), .clk(clk), .clr(rst));  // open: en
endmodule

module MFA3 (
  input  [31:0] IR,
  input  [1:0] A3SEL,
  output [4:0] A3
);

  Multiplexer #(.select(2), .width(5), .enable("false")) multiplexer_1 (
    .in0(IR[15:11]), .in1(IR[20:16]), .in2({5{1'b1}}), .out(A3), .sel(A3SEL));  // open: in3

  // Other names for the same wires on the sheet: IR_W_Rd[4:0] = IR[15:11]; IR_W_Rt[4:0] = IR[20:16]
endmodule

module MFWD3 (
  input  [31:0] AO_W,
  input  [31:0] RD,
  input  [31:0] PC_8W,
  input  [1:0] WD3SEL,
  output [31:0] WD3
);

  Multiplexer #(.select(2), .width(32), .enable("false")) multiplexer_1 (
    .in0(AO_W), .in1(RD), .in2(PC_8W), .out(WD3), .sel(WD3SEL));  // open: in3
endmodule

module Splitter (
  input  [31:0] IR,
  output [5:0] out_2,
  output [4:0] out_3,
  output [4:0] out_4,
  output [4:0] out_5,
  output [4:0] out_6,
  output [5:0] out_7,
  output [15:0] out_8,
  output [25:0] out_9
);


  assign out_2 = IR[31:26];
  assign out_3 = IR[25:21];
  assign out_4 = IR[20:16];
  assign out_5 = IR[15:11];
  assign out_6 = IR[10:6];
  assign out_7 = IR[5:0];
  assign out_8 = IR[15:0];
  assign out_9 = IR[25:0];
endmodule

module Instruct (
  input  [5:0] Opcode,
  input  [5:0] funct,
  output out_3,
  output out_4,
  output out_5,
  output out_6,
  output out_7,
  output out_8,
  output out_9,
  output out_10,
  output out_11,
  output out_12,
  output out_13,
  output out_14,
  output out_15,
  output out_16,
  output out_17,
  output out_18,
  output out_19
);

  wire not_1_out, not_2_out, not_3_out, not_4_out, not_5_out, not_6_out, not_7_out, not_8_out, not_9_out,
       not_10_out, not_11_out, not_12_out, R;

  not not_1 (not_1_out, Opcode[5]);
  not not_2 (not_2_out, Opcode[4]);
  not not_3 (not_3_out, Opcode[3]);
  not not_4 (not_4_out, Opcode[2]);
  not not_5 (not_5_out, Opcode[0]);
  not not_6 (not_6_out, Opcode[1]);
  and sw (out_3, Opcode[5], not_2_out, Opcode[3], not_4_out, Opcode[1], Opcode[0]);
  and lw (out_8, Opcode[5], not_2_out, not_3_out, not_4_out, Opcode[1], Opcode[0]);
  and ori (out_11, not_1_out, not_2_out, Opcode[3], Opcode[2], not_6_out, Opcode[0]);
  and u_R (R, not_1_out, not_2_out, not_3_out, not_4_out, not_6_out, not_5_out);
  and beq (out_14, not_1_out, not_2_out, Opcode[2], not_6_out, not_5_out);
  and j (out_12, not_1_out, not_2_out, not_3_out, not_4_out, Opcode[1], not_5_out);
  and lh (out_6, Opcode[5], not_2_out, not_3_out, not_4_out, not_6_out, Opcode[0]);
  and lb (out_7, Opcode[5], not_2_out, not_3_out, not_4_out, not_6_out, not_5_out);
  and sh (out_4, Opcode[5], not_2_out, Opcode[3], not_4_out, not_6_out, Opcode[0]);
  and sb (out_5, Opcode[5], not_2_out, Opcode[3], not_4_out, not_6_out, not_5_out);
  and jal (out_15, not_1_out, not_2_out, not_3_out, not_4_out, Opcode[1], Opcode[0]);
  and lui (out_16, not_1_out, not_2_out, Opcode[3], Opcode[2], Opcode[1], Opcode[0]);
  and addiu (out_18, not_1_out, not_2_out, Opcode[3], not_4_out, not_6_out, Opcode[0]);
  and blez (out_19, not_1_out, not_2_out, not_3_out, Opcode[2], Opcode[1], Opcode[0]);
  not not_7 (not_7_out, funct[5]);
  not not_8 (not_8_out, funct[4]);
  not not_9 (not_9_out, funct[3]);
  not not_10 (not_10_out, funct[1]);
  not not_11 (not_11_out, funct[2]);
  not not_12 (not_12_out, funct[0]);
  and addu (out_9, funct[5], not_8_out, not_9_out, not_11_out, not_10_out, funct[0], R);
  and subu (out_10, funct[5], not_8_out, not_9_out, not_11_out, funct[1], funct[0], R);
  and jr (out_13, not_7_out, not_8_out, funct[3], not_11_out, not_10_out, not_12_out, R);
  and nop (out_17, not_7_out, not_8_out, not_9_out, not_11_out, not_10_out, not_12_out, R);

  // Other names for the same wires on the sheet: addiu = out_18; addu = out_9; beq = out_14; blez = out_19;
  //   j = out_12; jal = out_15; jr = out_13; lb = out_7; lh = out_6; lui = out_16; lw = out_8; nop = out_17;
  //   ori = out_11; sb = out_5; sh = out_4; subu = out_10; sw = out_3
endmodule

module Controller (
  input  [5:0] in_1,
  input  [5:0] in_2,
  output we,
  output [1:0] cmpop,
  output [1:0] extop,
  output BSEL,
  output WM,
  output [1:0] DMSEL,
  output [1:0] A3SEL,
  output [1:0] WD3SEL,
  output [2:0] aluop,
  output [1:0] NPCOP
);

  wire addiu, addu, beq, blez, j, jal, jr, lb, lh, lui, lw, nop, or_1_out, or_2_out, or_9_out, or_11_out,
       or_12_out, ori, sb, sh, subu, sw;
  wire [0:0] not_2_out, or_4_out;
  wire [1:0] or_6_out, or_13_out;
  wire [2:0] not_1_out;

  Instruct instruct_1 (
    .out_3(sw), .out_4(sh), .out_5(sb), .out_6(lh), .out_7(lb), .out_8(lw), .out_9(addu), .out_10(subu),
    .out_11(ori), .out_12(j), .out_13(jr), .out_14(beq), .out_15(jal), .out_16(lui), .out_17(nop),
    .Opcode(in_1), .funct(in_2), .out_18(addiu), .out_19(blez));
  or or_1 (or_1_out, sw, sh, sb);
  or or_2 (or_2_out, j, jr, beq, jal, blez);
  not not_1 (not_1_out[0], or_2_out);
  or or_3 (not_1_out[2], j, jal);
  or or_4 (or_4_out[0], sw, sh, sb, lw, lh, lb);
  or or_5 (WM, sw, sh, sb);
  or or_6 (or_6_out[0], addu, subu, nop);
  or or_7 (or_6_out[1], lw, addiu, ori, lui);
  or or_8 (or_13_out[1], sw, sh, sb, lb, lw, lh);
  or or_9 (or_9_out, subu, lui, ori);
  not not_2 (not_2_out[0], or_9_out);
  or or_10 (not_1_out[1], blez, beq);
  or or_11 (or_11_out, blez, or_1_out, beq, j, nop);
  BitFinder #(.width(3)) bitfinder_1 (.in({1'b0, beq, blez}), .index(cmpop));  // open: found
  or or_12 (or_12_out, addu, nop, subu);
  BitFinder #(.width(3)) bitfinder_2 (.in({sb, sh, sw}), .index(DMSEL));  // open: found
  BitFinder #(.width(3)) bitfinder_3 (.in({jal, or_6_out}), .index(A3SEL));  // open: found
  or or_13 (or_13_out[0], addiu, addu, subu, ori, nop, lui);
  not not_3 (we, or_11_out);
  BitFinder #(.width(3)) bitfinder_4 (.in({lui, ori, or_4_out[0]}), .index(extop));  // open: found
  not not_4 (BSEL, or_12_out);
  BitFinder #(.width(3)) bitfinder_5 (.in({jal, or_13_out}), .index(WD3SEL));  // open: found
  BitFinder #(.width(7)) bitfinder_6 (.in({2'b00, lui, 1'b0, ori, subu, not_2_out[0]}), .index(aluop));  // open: found
  BitFinder #(.width(4)) bitfinder_7 (.in({jr, not_1_out}), .index(NPCOP));  // open: found

  // Notes on the sheet:
  //   MemWrite
  //   RegWrite
  //   ALUSrc
  //   数据通路
  //   RegDst
  //   MemtoReg
endmodule

module D (
  input  [31:0] IR,
  output [4:0] S1_D,
  output [4:0] S2_D,
  output [1:0] tuse_1,
  output [1:0] tuse_2
);

  wire addiu, addu, B_TYPE, beq, blez, cal_i, cal_R, j, jal, JR, lb, LD, lh, lui, lw, nop, or_6_out,
       or_7_out, or_8_out, or_9_out, ori, sb, sh, str, subu, sw;
  wire [0:0] not_1_out;
  wire [4:0] rd, rs, rt;
  wire [5:0] splitter_1_out_2, splitter_1_out_7;

  Splitter splitter_1 (
    .IR(IR), .out_2(splitter_1_out_2), .out_3(rs), .out_4(rt), .out_5(rd), .out_7(splitter_1_out_7));  // open: out_6, out_8, out_9
  Instruct instruct_1 (
    .out_3(sw), .out_4(sh), .out_5(sb), .out_6(lh), .out_7(lb), .out_8(lw), .out_9(addu), .out_10(subu),
    .out_11(ori), .out_12(j), .out_13(JR), .out_14(beq), .out_15(jal), .out_16(lui), .out_17(nop),
    .Opcode(splitter_1_out_2), .funct(splitter_1_out_7), .out_18(addiu), .out_19(blez));
  or or_1 (str, sw, sh, sb);
  or or_2 (LD, lh, lb, lw);
  or or_3 (cal_R, addu, subu);
  or or_4 (cal_i, ori, addiu);
  or or_5 (B_TYPE, beq, blez);
  not not_1 (not_1_out[0], or_6_out);
  or or_6 (or_6_out, str, cal_R);
  or or_7 (or_7_out, str, LD, cal_R, cal_i, B_TYPE, JR);
  Multiplexer #(.width(5), .enable("false")) multiplexer_1 (.in0({5{1'b0}}), .in1(rt), .out(S2_D), .sel(or_8_out));
  or or_8 (or_8_out, str, cal_R, B_TYPE);
  or or_9 (or_9_out, str, LD, cal_R, cal_i);
  BitFinder #(.width(3)) bitfinder_1 (.in({str, cal_R, not_1_out[0]}), .index(tuse_2));  // open: found
  Multiplexer #(.width(5), .enable("false")) multiplexer_2 (.in0({5{1'b0}}), .in1(rs), .out(S1_D), .sel(or_7_out));
  assign tuse_1 = {{1{1'b0}}, or_9_out};  // Bit_Extender bit_extender_1
endmodule

module E (
  input  [31:0] IR_E,
  input  [31:0] EXTD_E,
  input  [31:0] PC8_E,
  output [4:0] S1_E,
  output [4:0] S2_E,
  output [3:0] tnew_E,
  output [4:0] DES_E,
  output [31:0] EtoD
);

  wire addiu, addu, B_TYPE, beq, blez, cal_i, cal_R, j, Jal, JR, lb, LD, lh, lui, lw, nop, or_3_out,
       or_8_out, or_10_out, or_11_out, or_12_out, ori, sb, sh, str, subu, sw;
  wire [0:0] not_1_out;
  wire [1:0] bitfinder_1_index, bitfinder_2_index, bitfinder_3_index, not_2_out, not_3_out;
  wire [4:0] rd, rs, rt;
  wire [5:0] splitter_1_out_2, splitter_1_out_7;

  Splitter splitter_1 (
    .IR(IR_E), .out_2(splitter_1_out_2), .out_3(rs), .out_4(rt), .out_5(rd), .out_7(splitter_1_out_7));  // open: out_6, out_8, out_9
  Instruct instruct_1 (
    .out_3(sw), .out_4(sh), .out_5(sb), .out_6(lh), .out_7(lb), .out_8(lw), .out_9(addu), .out_10(subu),
    .out_11(ori), .out_12(j), .out_13(JR), .out_14(beq), .out_15(Jal), .out_16(lui), .out_17(nop),
    .Opcode(splitter_1_out_2), .funct(splitter_1_out_7), .out_18(addiu), .out_19(blez));
  or or_1 (cal_i, ori, addiu);
  or or_2 (B_TYPE, beq, blez);
  or or_3 (or_3_out, lui, Jal);
  or or_4 (str, sw, sh, sb);
  or or_5 (LD, lh, lb, lw);
  or or_6 (cal_R, addu, subu);
  not not_1 (not_1_out[0], or_3_out);
  or or_7 (not_2_out[1], lui, LD, cal_i);
  Multiplexer #(.select(2), .width(32), .enable("false")) multiplexer_1 (
    .in0({32{1'b0}}), .in1(EXTD_E), .in2(PC8_E), .out(EtoD), .sel(bitfinder_1_index));  // open: in3
  BitFinder #(.width(3)) bitfinder_1 (.in({Jal, lui, not_1_out[0]}), .index(bitfinder_1_index));  // open: found
  or or_8 (or_8_out, str, cal_R);
  or or_9 (not_3_out[1], cal_R, cal_i);
  or or_10 (or_10_out, not_2_out[1], cal_R, Jal);
  not not_2 (not_2_out[0], or_10_out);
  or or_11 (or_11_out, str, LD, cal_R, cal_i);
  Multiplexer #(.width(5), .enable("false")) multiplexer_2 (.in0({5{1'b0}}), .in1(rt), .out(S2_E), .sel(or_8_out));
  not not_3 (not_3_out[0], or_12_out);
  or or_12 (or_12_out, not_3_out[1], LD);
  BitFinder #(.width(4)) bitfinder_2 (.in({Jal, cal_R, not_2_out}), .index(bitfinder_2_index));  // open: found
  Multiplexer #(.width(5), .enable("false")) multiplexer_3 (.in0({5{1'b0}}), .in1(rs), .out(S1_E), .sel(or_11_out));
  BitFinder #(.width(3)) bitfinder_3 (.in({LD, not_3_out}), .index(bitfinder_3_index));  // open: found
  Multiplexer #(.select(2), .width(5), .enable("false")) multiplexer_4 (
    .in0({5{1'b0}}), .in1(rt), .in2(rd), .in3({5{1'b1}}), .out(DES_E), .sel(bitfinder_2_index));
  // Probe on bitfinder_2_index
  assign tnew_E = {{2{1'b0}}, bitfinder_3_index};  // Bit_Extender bit_extender_1

  // Other names for the same wires on the sheet: PC8[31:0] = PC8_E
endmodule

module M (
  input  [31:0] IR_M,
  input  [31:0] AO,
  input  [31:0] PC8,
  output [4:0] S2_M,
  output [4:0] Des_M,
  output [31:0] MtoD
);

  wire addiu, addu, B_TYPE, beq, blez, cal_i, cal_R, j, Jal, JR, lb, LD, lh, lui, lw, nop, or_8_out,
       or_9_out, ori, sb, sh, str, subu, sw;
  wire [1:0] bitfinder_1_index, bitfinder_2_index, not_1_out, not_2_out;
  wire [4:0] rd, rs, rt;
  wire [5:0] splitter_1_out_2, splitter_1_out_7;

  Splitter splitter_1 (
    .IR(IR_M), .out_2(splitter_1_out_2), .out_3(rs), .out_4(rt), .out_5(rd), .out_7(splitter_1_out_7));  // open: out_6, out_8, out_9
  Instruct instruct_1 (
    .out_3(sw), .out_4(sh), .out_5(sb), .out_6(lh), .out_7(lb), .out_8(lw), .out_9(addu), .out_10(subu),
    .out_11(ori), .out_12(j), .out_13(JR), .out_14(beq), .out_15(Jal), .out_16(lui), .out_17(nop),
    .Opcode(splitter_1_out_2), .funct(splitter_1_out_7), .out_18(addiu), .out_19(blez));
  or or_1 (cal_i, ori, addiu);
  or or_2 (B_TYPE, beq, blez);
  or or_3 (str, sw, sh, sb);
  or or_4 (LD, lh, lb, lw);
  or or_5 (cal_R, addu, subu);
  or or_6 (not_1_out[1], cal_R, lui, cal_i);
  or or_7 (not_2_out[1], LD, cal_i, lui);
  not not_1 (not_1_out[0], or_8_out);
  or or_8 (or_8_out, not_1_out[1], Jal);
  Multiplexer #(.width(5), .enable("false")) multiplexer_1 (.in0({5{1'b0}}), .in1(rt), .out(S2_M), .sel(str));
  not not_2 (not_2_out[0], or_9_out);
  or or_9 (or_9_out, not_2_out[1], cal_R, Jal);
  BitFinder #(.width(3)) bitfinder_1 (.in({Jal, not_1_out}), .index(bitfinder_1_index));  // open: found
  BitFinder #(.width(4)) bitfinder_2 (.in({Jal, cal_R, not_2_out}), .index(bitfinder_2_index));  // open: found
  Multiplexer #(.select(2), .width(32), .enable("false")) multiplexer_2 (
    .in0({32{1'b0}}), .in1(AO), .in2(PC8), .out(MtoD), .sel(bitfinder_1_index));  // open: in3
  Multiplexer #(.select(2), .width(5), .enable("false")) multiplexer_3 (
    .in0({5{1'b0}}), .in1(rt), .in2(rd), .in3({5{1'b1}}), .out(Des_M), .sel(bitfinder_2_index));
endmodule

module W (
  input  [31:0] IR_W,
  input  [31:0] RD,
  input  [31:0] AO,
  input  [31:0] PC8,
  output [4:0] Des_M,
  output [31:0] WtoD
);

  wire addiu, addu, B_TYPE, beq, blez, cal_i, cal_R, j, Jal, JR, lb, LD, lh, lui, lw, nop, or_7_out,
       or_9_out, ori, sb, sh, str, subu, sw;
  wire [1:0] bitfinder_1_index, bitfinder_2_index, not_1_out;
  wire [2:0] not_2_out;
  wire [4:0] rd_t, rs, rt;
  wire [5:0] splitter_1_out_2, splitter_1_out_7;

  Splitter splitter_1 (
    .IR(IR_W), .out_2(splitter_1_out_2), .out_3(rs), .out_4(rt), .out_5(rd_t), .out_7(splitter_1_out_7));  // open: out_6, out_8, out_9
  Instruct instruct_1 (
    .out_3(sw), .out_4(sh), .out_5(sb), .out_6(lh), .out_7(lb), .out_8(lw), .out_9(addu), .out_10(subu),
    .out_11(ori), .out_12(j), .out_13(JR), .out_14(beq), .out_15(Jal), .out_16(lui), .out_17(nop),
    .Opcode(splitter_1_out_2), .funct(splitter_1_out_7), .out_18(addiu), .out_19(blez));
  or or_1 (cal_i, ori, addiu);
  or or_2 (B_TYPE, beq, blez);
  or or_3 (str, sw, sh, sb);
  or or_4 (LD, lh, lb, lw);
  or or_5 (cal_R, addu, subu);
  or or_6 (not_1_out[1], LD, cal_i, lui);
  or or_7 (or_7_out, LD, not_2_out[2], Jal);
  or or_8 (not_2_out[2], cal_R, lui, cal_i);
  not not_1 (not_1_out[0], or_9_out);
  or or_9 (or_9_out, not_1_out[1], cal_R, Jal);
  not not_2 (not_2_out[0], or_7_out);
  Multiplexer #(.select(2), .width(5), .enable("false")) multiplexer_1 (
    .in0({5{1'b0}}), .in1(rt), .in2(rd_t), .in3({5{1'b1}}), .out(Des_M), .sel(bitfinder_1_index));
  BitFinder #(.width(4)) bitfinder_1 (.in({Jal, cal_R, not_1_out}), .index(bitfinder_1_index));  // open: found
  Multiplexer #(.select(2), .width(32), .enable("false")) multiplexer_2 (
    .in0({32{1'b0}}), .in1(RD), .in2(AO), .in3(PC8), .out(WtoD), .sel(bitfinder_2_index));
  BitFinder #(.width(4)) bitfinder_2 (
    .in({Jal, not_2_out[2], LD, not_2_out[0]}), .index(bitfinder_2_index));  // open: found
endmodule

module StallUnit (
  input  [4:0] s1_D,
  input  [4:0] s2_D,
  input  [1:0] tUse1_D,
  input  [1:0] tUse2_D,
  input  [4:0] des_E,
  input  [3:0] tNew_E,
  input  [3:0] tNew_M,
  input  [4:0] des_M,
  output Stall_F,
  output Stall_D,
  output flush_E
);

  wire and_1_out, and_2_out, and_3_out, and_4_out, comparator_1_eq, comparator_2_eq, comparator_3_lt,
       comparator_4_eq, comparator_5_eq, comparator_6_lt, comparator_7_eq, comparator_8_eq, comparator_9_lt,
       comparator_10_eq, comparator_11_eq, comparator_12_lt, not_1_out, not_2_out, not_3_out, not_4_out;
  wire [3:0] tUse1_D_t, tUse2_D_t;

  Comparator #(.width(5), .mode("unsigned")) comparator_1 (
    .a(s1_D), .b({5{1'b0}}), .eq(comparator_1_eq));  // open: gt, lt
  Comparator #(.width(5), .mode("unsigned")) comparator_2 (.a(s1_D), .b(des_E), .eq(comparator_2_eq));  // open: gt, lt
  Comparator #(.width(4), .mode("unsigned")) comparator_3 (
    .a(tUse1_D_t), .b(tNew_E), .lt(comparator_3_lt));  // open: gt, eq
  Comparator #(.width(5), .mode("unsigned")) comparator_4 (
    .a(s2_D), .b({5{1'b0}}), .eq(comparator_4_eq));  // open: gt, lt
  Comparator #(.width(5), .mode("unsigned")) comparator_5 (.a(s2_D), .b(des_E), .eq(comparator_5_eq));  // open: gt, lt
  Comparator #(.width(4), .mode("unsigned")) comparator_6 (
    .a(tUse2_D_t), .b(tNew_E), .lt(comparator_6_lt));  // open: gt, eq
  Comparator #(.width(5), .mode("unsigned")) comparator_7 (
    .a(s1_D), .b({5{1'b0}}), .eq(comparator_7_eq));  // open: gt, lt
  Comparator #(.width(5), .mode("unsigned")) comparator_8 (.a(s1_D), .b(des_M), .eq(comparator_8_eq));  // open: gt, lt
  Comparator #(.width(4), .mode("unsigned")) comparator_9 (
    .a(tUse1_D_t), .b(tNew_M), .lt(comparator_9_lt));  // open: gt, eq
  Comparator #(.width(5), .mode("unsigned")) comparator_10 (
    .a(s2_D), .b({5{1'b0}}), .eq(comparator_10_eq));  // open: gt, lt
  Comparator #(.width(5), .mode("unsigned")) comparator_11 (
    .a(s2_D), .b(des_M), .eq(comparator_11_eq));  // open: gt, lt
  Comparator #(.width(4), .mode("unsigned")) comparator_12 (
    .a(tUse2_D_t), .b(tNew_M), .lt(comparator_12_lt));  // open: gt, eq
  assign tUse1_D_t = {{2{1'b0}}, tUse1_D};  // Bit_Extender bit_extender_1
  not not_1 (not_1_out, comparator_1_eq);
  not not_2 (not_2_out, comparator_4_eq);
  not not_3 (not_3_out, comparator_7_eq);
  not not_4 (not_4_out, comparator_10_eq);
  and and_1 (and_1_out, not_1_out, comparator_2_eq, comparator_3_lt);
  and and_2 (and_2_out, not_2_out, comparator_5_eq, comparator_6_lt);
  and and_3 (and_3_out, not_3_out, comparator_8_eq, comparator_9_lt);
  and and_4 (and_4_out, not_4_out, comparator_11_eq, comparator_12_lt);
  assign tUse2_D_t = {{2{1'b0}}, tUse2_D};  // Bit_Extender bit_extender_2
  or or_1 (flush_E, and_1_out, and_2_out, and_3_out, and_4_out);

  assign Stall_D = flush_E;
  assign Stall_F = flush_E;

  // Other names for the same wires on the sheet: stall_flag = flush_E
endmodule

module forwardNuit (
  input  [4:0] s1_D,
  input  [4:0] s2_D,
  input  [4:0] s1_E,
  input  [4:0] s2_E,
  input  [4:0] des_E,
  input  [3:0] tNew_E,
  input  [4:0] s2_M,
  input  [3:0] tNew_M,
  input  [4:0] des_M,
  input  [3:0] tNew_W,
  input  [4:0] des_W,
  output [1:0] fRsDsel,
  output [1:0] fRtDsel,
  output [1:0] fRsEsel,
  output [1:0] fRtEsel,
  output fRtMsel
);

  wire and_1_out, and_2_out, and_3_out, and_4_out, and_5_out, and_6_out, and_7_out, and_8_out, and_9_out,
       comparator_1_eq, comparator_2_eq, comparator_3_eq, comparator_4_eq, comparator_5_eq, comparator_6_eq,
       comparator_7_eq, comparator_8_eq, comparator_9_eq, comparator_10_eq, comparator_11_eq,
       comparator_12_eq, comparator_13_eq, comparator_14_eq, comparator_15_eq, comparator_16_eq,
       comparator_17_eq, comparator_18_eq, comparator_19_eq, comparator_20_eq, comparator_21_eq,
       comparator_22_eq, comparator_23_eq, comparator_24_eq, comparator_25_eq, comparator_26_eq,
       comparator_27_eq, not_1_out, not_2_out, not_3_out, not_4_out, not_5_out, not_6_out, not_7_out,
       not_8_out, not_9_out;
  wire [1:0] multiplexer_1_out, multiplexer_2_out, multiplexer_5_out, multiplexer_6_out;

  not not_1 (not_1_out, comparator_1_eq);
  Comparator #(.width(5), .mode("unsigned")) comparator_1 (
    .a(s1_D), .b({5{1'b0}}), .eq(comparator_1_eq));  // open: gt, lt
  Comparator #(.width(5), .mode("unsigned")) comparator_2 (.a(s1_D), .b(des_M), .eq(comparator_2_eq));  // open: gt, lt
  Comparator #(.width(4), .mode("unsigned")) comparator_3 (
    .a(tNew_M), .b(4'b0000), .eq(comparator_3_eq));  // open: gt, lt
  Comparator #(.width(5), .mode("unsigned")) comparator_4 (
    .a(s1_D), .b({5{1'b0}}), .eq(comparator_4_eq));  // open: gt, lt
  not not_2 (not_2_out, comparator_4_eq);
  Comparator #(.width(5), .mode("unsigned")) comparator_5 (.a(s1_D), .b(des_E), .eq(comparator_5_eq));  // open: gt, lt
  Comparator #(.width(4), .mode("unsigned")) comparator_6 (
    .a(tNew_E), .b(4'b0000), .eq(comparator_6_eq));  // open: gt, lt
  Comparator #(.width(5), .mode("unsigned")) comparator_7 (
    .a(s2_D), .b({5{1'b0}}), .eq(comparator_7_eq));  // open: gt, lt
  Comparator #(.width(5), .mode("unsigned")) comparator_8 (.a(s2_D), .b(des_M), .eq(comparator_8_eq));  // open: gt, lt
  Comparator #(.width(4), .mode("unsigned")) comparator_9 (
    .a(tNew_M), .b(4'b0000), .eq(comparator_9_eq));  // open: gt, lt
  Comparator #(.width(5), .mode("unsigned")) comparator_10 (
    .a(s2_D), .b({5{1'b0}}), .eq(comparator_10_eq));  // open: gt, lt
  Comparator #(.width(5), .mode("unsigned")) comparator_11 (
    .a(s2_D), .b(des_E), .eq(comparator_11_eq));  // open: gt, lt
  Comparator #(.width(4), .mode("unsigned")) comparator_12 (
    .a(tNew_E), .b(4'b0000), .eq(comparator_12_eq));  // open: gt, lt
  and and_1 (and_1_out, not_1_out, comparator_2_eq, comparator_3_eq);
  and and_2 (and_2_out, not_2_out, comparator_5_eq, comparator_6_eq);
  not not_3 (not_3_out, comparator_7_eq);
  not not_4 (not_4_out, comparator_10_eq);
  Multiplexer #(.width(2)) multiplexer_1 (
    .in0(2'b00), .in1(2'b10), .out(multiplexer_1_out), .sel(and_1_out));  // open: en
  and and_3 (and_3_out, not_3_out, comparator_8_eq, comparator_9_eq);
  and and_4 (and_4_out, not_4_out, comparator_11_eq, comparator_12_eq);
  Multiplexer #(.width(2)) multiplexer_2 (
    .in0(2'b00), .in1(2'b10), .out(multiplexer_2_out), .sel(and_3_out));  // open: en
  Multiplexer #(.width(2)) multiplexer_3 (
    .in0(multiplexer_1_out), .in1(2'b01), .out(fRsDsel), .sel(and_2_out));  // open: en
  Multiplexer #(.width(2)) multiplexer_4 (
    .in0(multiplexer_2_out), .in1(2'b01), .out(fRtDsel), .sel(and_4_out));  // open: en
  Comparator #(.width(5), .mode("unsigned")) comparator_13 (
    .a(s1_E), .b({5{1'b0}}), .eq(comparator_13_eq));  // open: gt, lt
  Comparator #(.width(5), .mode("unsigned")) comparator_14 (
    .a(s1_E), .b(des_W), .eq(comparator_14_eq));  // open: gt, lt
  Comparator #(.width(4), .mode("unsigned")) comparator_15 (
    .a(tNew_W), .b(4'b0000), .eq(comparator_15_eq));  // open: gt, lt
  Comparator #(.width(5), .mode("unsigned")) comparator_16 (
    .a(s1_E), .b({5{1'b0}}), .eq(comparator_16_eq));  // open: gt, lt
  Comparator #(.width(5), .mode("unsigned")) comparator_17 (
    .a(s1_E), .b(des_M), .eq(comparator_17_eq));  // open: gt, lt
  Comparator #(.width(4), .mode("unsigned")) comparator_18 (
    .a(tNew_M), .b(4'b0000), .eq(comparator_18_eq));  // open: gt, lt
  Comparator #(.width(5), .mode("unsigned")) comparator_19 (
    .a(s2_E), .b({5{1'b0}}), .eq(comparator_19_eq));  // open: gt, lt
  Comparator #(.width(5), .mode("unsigned")) comparator_20 (
    .a(s2_E), .b(des_W), .eq(comparator_20_eq));  // open: gt, lt
  Comparator #(.width(4), .mode("unsigned")) comparator_21 (
    .a(tNew_W), .b(4'b0000), .eq(comparator_21_eq));  // open: gt, lt
  Comparator #(.width(5), .mode("unsigned")) comparator_22 (
    .a(s2_E), .b({5{1'b0}}), .eq(comparator_22_eq));  // open: gt, lt
  Comparator #(.width(5), .mode("unsigned")) comparator_23 (
    .a(s2_E), .b(des_M), .eq(comparator_23_eq));  // open: gt, lt
  Comparator #(.width(4), .mode("unsigned")) comparator_24 (
    .a(tNew_M), .b(4'b0000), .eq(comparator_24_eq));  // open: gt, lt
  not not_5 (not_5_out, comparator_13_eq);
  not not_6 (not_6_out, comparator_16_eq);
  not not_7 (not_7_out, comparator_19_eq);
  not not_8 (not_8_out, comparator_22_eq);
  and and_5 (and_5_out, not_5_out, comparator_14_eq, comparator_15_eq);
  and and_6 (and_6_out, not_6_out, comparator_17_eq, comparator_18_eq);
  and and_7 (and_7_out, not_7_out, comparator_20_eq, comparator_21_eq);
  and and_8 (and_8_out, not_8_out, comparator_23_eq, comparator_24_eq);
  Multiplexer #(.width(2)) multiplexer_5 (
    .in0(2'b00), .in1(2'b10), .out(multiplexer_5_out), .sel(and_5_out));  // open: en
  Multiplexer #(.width(2)) multiplexer_6 (
    .in0(2'b00), .in1(2'b10), .out(multiplexer_6_out), .sel(and_7_out));  // open: en
  Multiplexer #(.width(2)) multiplexer_7 (
    .in0(multiplexer_5_out), .in1(2'b01), .out(fRsEsel), .sel(and_6_out));  // open: en
  Multiplexer #(.width(2)) multiplexer_8 (
    .in0(multiplexer_6_out), .in1(2'b01), .out(fRtEsel), .sel(and_8_out));  // open: en
  // Probe on fRsEsel
  Comparator #(.width(5), .mode("unsigned")) comparator_25 (
    .a(s2_M), .b({5{1'b0}}), .eq(comparator_25_eq));  // open: gt, lt
  not not_9 (not_9_out, comparator_25_eq);
  Comparator #(.width(5), .mode("unsigned")) comparator_26 (
    .a(s2_M), .b(des_W), .eq(comparator_26_eq));  // open: gt, lt
  Comparator #(.width(4), .mode("unsigned")) comparator_27 (
    .a(tNew_W), .b(4'b0000), .eq(comparator_27_eq));  // open: gt, lt
  and and_9 (and_9_out, not_9_out, comparator_26_eq, comparator_27_eq);
  Multiplexer multiplexer_9 (.in0(1'b0), .in1(1'b1), .out(fRtMsel), .sel(and_9_out));  // open: en
endmodule

module ALU (
  input  [31:0] A,
  input  [31:0] B,
  input  [2:0] aluop,
  input  [4:0] shamt,
  output [31:0] out_5
);

  wire [31:0] adder_1_out, or_1_out, shifter_1_out, subtractor_1_out;

  Adder #(.width(32)) adder_1 (.a(A), .b(B), .out(adder_1_out));  // open: cin, cout
  Subtractor #(.width(32)) subtractor_1 (.a(A), .b(B), .out(subtractor_1_out));  // open: bin, bout
  assign or_1_out = A | B;  // OR_Gate or_1, 32 bits wide
  Shifter #(.width(32)) shifter_1 (.in(A), .\dist (shamt), .out(shifter_1_out));
  Multiplexer #(.select(3), .width(32), .enable("false")) multiplexer_1 (
    .in0(adder_1_out), .in1(subtractor_1_out), .in2(or_1_out), .in3(shifter_1_out), .in4(B), .out(out_5),
    .sel(aluop));  // open: in5, in6, in7
endmodule

module ext (
  input  [15:0] Imm16,
  input  [1:0] extop,
  output [31:0] out_3
);

  wire [31:0] bit_extender_1_out, bit_extender_2_out;

  assign bit_extender_1_out = {{16{Imm16[15]}}, Imm16};  // Bit_Extender bit_extender_1
  assign bit_extender_2_out = {{16{1'b0}}, Imm16};  // Bit_Extender bit_extender_2
  Multiplexer #(.select(2), .width(32), .enable("false")) multiplexer_1 (
    .in0(bit_extender_1_out), .in1(bit_extender_2_out), .in2({Imm16, {16{1'b0}}}), .out(out_3), .sel(extop));  // open: in3
endmodule

module PC (
  input  [31:0] NPC,
  input  reset,
  input  colck,
  input  Stall_F,
  output [31:0] PC
);

  wire comparator_1_eq, not_1_out;
  wire [31:0] register_1_q;

  not not_1 (not_1_out, Stall_F);
  Register #(.width(32)) register_1 (.D(NPC), .en(not_1_out), .Q(register_1_q), .clk(colck), .clr(reset));
  Comparator #(.width(32)) comparator_1 (.a(register_1_q), .b({32{1'b0}}), .eq(comparator_1_eq));  // open: gt, lt
  Multiplexer #(.width(32), .enable("false")) multiplexer_1 (
    .in0(register_1_q), .in1(32'h3000), .out(PC), .sel(comparator_1_eq));
endmodule

module NPC (
  input  [31:0] PC4,
  input  [25:0] I26,
  input  [31:0] rs,
  input  [1:0] NPCOP,
  input  [31:0] D2,
  input  [1:0] cmpop,
  output [31:0] out_7
);

  wire cmp;
  wire [2:0] or_1_out;
  wire [27:0] PC;
  wire [31:0] adder_1_out, bit_extender_1_out, BPC;
  wire [31:28] JPC;

  Subtractor #(.width(32)) subtractor_1 (.a(PC4), .b(32'h4), .out({JPC, PC}));  // open: bin, bout
  BitSelector #(.width(3)) bitselector_1 (.in(or_1_out), .out(cmp), .sel(cmpop));
  Multiplexer #(.select(2), .width(32), .enable("false")) multiplexer_1 (
    .in0(PC4), .in1(BPC), .in2({JPC, I26, 2'b00}), .in3(rs), .out(out_7), .sel(NPCOP));
  assign bit_extender_1_out = {{14{I26[15]}}, {I26[15:0], 2'b00}};  // Bit_Extender bit_extender_1
  Adder #(.width(32)) adder_1 (.a(bit_extender_1_out), .b({JPC, PC}), .out(adder_1_out));  // open: cin, cout
  Multiplexer #(.width(32), .enable("false")) multiplexer_2 (.in0(PC4), .in1(adder_1_out), .out(BPC), .sel(cmp));
  Comparator #(.width(32)) comparator_1 (.a(rs), .b(D2), .eq(or_1_out[1]), .lt(or_1_out[2]));  // open: gt
  or or_1 (or_1_out[0], or_1_out[2], or_1_out[1]);

  // Other names for the same wires on the sheet: Imm26[25:0] = I26; JPC[27:2] = I26; PC[31:28] = JPC;
  //   jr_rs[31:0] = rs; PC_4[31:0] = PC4
endmodule
