// Logisim project 流水线.circ as structural Verilog
module main (
  input  in_1,
  output [31:0] instr,
  output RegWrite,
  output [4:0] RegAddr,
  output [31:0] RegData,
  output MemWrite,
  output [4:0] MemAddr,
  output [31:0] MemDat
);

  wire ALUSrc, ALUSrc_E, Clk_prime, comparator_1_eq, Flush_E, forwardunit_1_frtmsel, MemRead, MemRead_E,
       MemRead_M, MemWrite_E, MemWrite_M, MemWrite_t, RegWrite_E, RegWrite_M, RegWrite_t, Stall_D, Stall_F;
  wire [1:0] ALUOp, ALUOp_E, controller_1_memread, controller_1_memwrite, EXTOp, forwardunit_1_frsdsel,
       forwardunit_1_frsesel, forwardunit_1_frtdsel, forwardunit_1_frtesel, m_w_reg_1_out_20, MemToReg,
       MemToReg_E, MemToReg_M, RegDst, RegDst_E, RegDst_M, RegDst_W, tuse1_D, tuse2_D;
  wire [2:0] NPCOp;
  wire [3:0] tNew_E, tNew_M, tNew_W;
  wire [4:0] DES_E, DES_M, DES_W, rd_E, rd_t, rs, rt, rt_E, S1_D, S1_E, S1_M, S2_D, S2_E, S2_M, WriteReg_E,
       WriteReg_M;
  wire [5:0] splitter_1_funct, splitter_1_op;
  wire [15:0] splitter_1__15_0;
  wire [23:0] mmu_1_instraddr;
  wire [25:0] splitter_1__25_0;
  wire [31:0] adder_2_out, ALUresult, ALUresult_M, ALUresult_W, d_e_reg_1_pc_o, E__D, EXTresult, EXTResult_E,
       Fwd_ALUA_E, Fwd_ALUB_E, Fwd_RD1_D, Fwd_RD2_D, Fwd_WD_M, instr_D, instr_E, instr_M, instr_W, M__D,
       MemAddr_W, multiplexer_2_out, NPC, PC, PC_4, PC_4_D, PC_4_E, PC_4_M, PC_8_D, PC_8_E, PC_8_M, PC_8_W,
       PC_D, PC_M, RD, RD1, RD1_E, RD2, RD2_E, ReadData_W, W__D, WD_M;

  // Probe on S1_D
  // Probe on S2_D
  // Probe on S1_E
  // Probe on S2_E
  // Probe on NPC
  // Probe on DES_E
  // Probe on tNew_E
  MMU mmu_1 (.NPC(NPC), .instrAddr(mmu_1_instraddr), .out_6(PC), .in_1(Clk_prime), .Reset(in_1), .in_4(Stall_F));
  // Probe on PC
  // Probe on S2_M
  // Probe on tNew_M
  // Probe on DES_M
  // Probe on tNew_W
  // Probe on DES_W
  Clock clock_1 (.out(Clk_prime));
  ROM #(.addrWidth(24), .dataWidth(32)) rom_1 (.addr(mmu_1_instraddr), .data(instr));  // open: sel
  Adder #(.width(32)) adder_1 (.a(PC), .b(32'h4), .out(PC_4));  // open: cin, cout
  Adder #(.width(32)) adder_2 (.a(PC), .b(32'h8), .out(adder_2_out));  // open: cin, cout
  // Probe on instr
  F_D_reg f_d_reg_1 (
    .instr_i(instr), .pc_i(PC), .pc_4_i(PC_4), .pc_8_i(adder_2_out), .instr_o(instr_D), .pc_o(PC_D),
    .pc_4_o(PC_4_D), .pc_8_o(PC_8_D), .in_1(Clk_prime), .in_2(in_1), .in_7(Stall_D));
  D d_1 (.in_1(instr_D), .S1_D(S1_D), .S2_D(S2_D), .tuse1_D(tuse1_D), .tuse2_D(tuse2_D));
  splitter splitter_1 (
    .in_1(instr_D), ._25_0(splitter_1__25_0), ._15_0(splitter_1__15_0), ._25_21(rs), ._20_16(rt),
    ._15_11(rd_t), .funct(splitter_1_funct), .op(splitter_1_op));
  Controller controller_1 (
    .OP(splitter_1_op), .FUNCT(splitter_1_funct), .RegDst(RegDst), .ALUSrc(ALUSrc), .MemtoReg(MemToReg),
    .RegWrite(RegWrite_t), .Beq(NPCOp[0]), .ALUOp(ALUOp), .Jump(NPCOp[1]), .jr(NPCOp[2]), .ExtOp(EXTOp),
    .MemWrite(controller_1_memwrite), .MemRead(controller_1_memread));
  E e_1 (
    .in_1(instr_E), .in_4(PC_8_E), .in_5(EXTResult_E), .S1_E(S1_E), .S2_E(S2_E), .DES_E(DES_E),
    .tNew_E(tNew_E), .E__D(E__D), .RegWrite(RegWrite_E), .writereg_E(WriteReg_E));
  M m_1 (
    .in_1(instr_M), .in_4(PC_8_M), .in_5(ALUresult_M), .S1_M(S1_M), .S2_M(S2_M), .M__D(M__D), .DES_E(DES_M),
    .writereg_E(WriteReg_M), .RegWrite(RegWrite_M));
  W w_1 (
    .in_1(instr_W), .in_4(ReadData_W), .in_5(ALUresult_W), .in_6(PC_8_W), .W__D(W__D), .DES_E(DES_W),
    .writereg_E(RegAddr), .RegWrite(RegWrite));
  Extend extend_1 (.Imm16(splitter_1__15_0), .Imm32(EXTresult), .ExtOp(EXTOp));
  // Probe on EXTOp
  // Probe on S1_D
  // Probe on EXTresult
  GRF grf_1 (
    .A1(rs), .A2(rt), .A3(RegAddr), .WD(RegData), .RD1(RD1), .RD2(RD2), .clk(Clk_prime), .reset(in_1),
    .we(RegWrite));
  // Probe on S2_D
  // Probe on tNew_E
  // Probe on RD2
  and and_1 (MemWrite_t, controller_1_memwrite[0], controller_1_memwrite[1]);
  and and_2 (MemRead, controller_1_memread[0], controller_1_memread[1]);
  StallUnit stallunit_1 (
    .s1_D(S1_D), .s2_D(S2_D), .tUse1_D(tuse1_D), .tUse2_D(tuse2_D), .des_E(DES_E), .tNew_E(tNew_E),
    .tNew_M(tNew_M), .des_M(DES_M), .Stall_F(Stall_F), .Stall_D(Stall_D), .flush_E(Flush_E));
  Comparator #(.width(32), .mode("unsigned")) comparator_1 (
    .a(Fwd_RD1_D), .b(Fwd_RD2_D), .eq(comparator_1_eq));  // open: gt, lt
  // Probe on PC_4
  // Probe on nothing
  NPC npc_1 (
    .imm32(EXTresult), .imm26(splitter_1__25_0), .PC_4(PC_4), .PC(PC), .RegData(Fwd_RD1_D), .NPC(NPC),
    .EQ(comparator_1_eq), .NPCOp(NPCOp));
  // Probe on NPC
  D_E_reg d_e_reg_1 (
    .pc_i(PC_D), .RD1_i(Fwd_RD1_D), .pc_4_i(PC_4_D), .RD2_i(Fwd_RD2_D), .pc_8_i(PC_8_D), .rs_i(rs),
    .EXTresult_i(EXTresult), .rt_i(rt), .rd_i(rd_t), .regdst(RegDst), .memwrite(MemWrite_t),
    .regwrite(RegWrite_t), .alusrc(ALUSrc), .memreacd(MemRead), .memtoreg(MemToReg), .aluctrl(ALUOp),
    .instr_i(instr_D), .pc_o(d_e_reg_1_pc_o), .RD1_o(RD1_E), .pc_4_o(PC_4_E), .RD2_o(RD2_E), .pc_8_o(PC_8_E),
    .EXTresult_o(EXTResult_E), .rt_o(rt_E), .rd_o(rd_E), .out_30(RegDst_E), .out_31(MemWrite_E),
    .out_32(RegWrite_E), .out_33(ALUSrc_E), .out_34(MemRead_E), .out_35(MemToReg_E), .out_36(ALUOp_E),
    .out_37(instr_E), .in_1(Clk_prime), .in_2(in_1), .in_15(Flush_E));  // open: rs_o
  // Probe on RD2_E
  // Probe on RD1_E
  // Probe on EXTResult_E
  // Probe on WriteReg_E
  Multiplexer #(.select(2), .width(5), .enable("false")) multiplexer_1 (
    .in0(rt_E), .in1(rd_E), .in2({5{1'b1}}), .out(WriteReg_E), .sel(RegDst_E));  // open: in3
  Multiplexer #(.width(32), .enable("false")) multiplexer_2 (
    .in0(Fwd_ALUB_E), .in1(EXTResult_E), .out(multiplexer_2_out), .sel(ALUSrc_E));
  forwardUnit forwardunit_1 (
    .s1_D(S1_D), .s2_D(S2_D), .s1_E(S1_E), .s2_E(S2_E), .des_E(DES_E), .tNew_E(tNew_E), .s2_M(S2_M),
    .tNew_M(tNew_M), .des_M(DES_M), .tNew_W(tNew_W), .des_W(DES_W), .fRsDsel(forwardunit_1_frsdsel),
    .fRtDsel(forwardunit_1_frtdsel), .fRsEsel(forwardunit_1_frsesel), .fRtEsel(forwardunit_1_frtesel),
    .fRtMsel(forwardunit_1_frtmsel));
  // Probe on forwardunit_1_frsdsel
  Multiplexer #(.select(2), .width(32), .enable("false")) multiplexer_3 (
    .in0(RD1), .in1(E__D), .in2(M__D), .in3({32{1'b0}}), .out(Fwd_RD1_D), .sel(forwardunit_1_frsdsel));
  // Probe on nothing
  // Probe on ALUOp_E
  ALU alu_1 (.A(Fwd_ALUA_E), .B(multiplexer_2_out), .ALUOp(ALUOp_E), .Result(ALUresult));
  // Probe on ALUresult
  // Probe on Fwd_ALUB_E
  // Probe on forwardunit_1_frtdsel
  Multiplexer #(.select(2), .width(32), .enable("false")) multiplexer_4 (
    .in0(RD2), .in1(E__D), .in2(M__D), .in3({32{1'b0}}), .out(Fwd_RD2_D), .sel(forwardunit_1_frtdsel));
  // Probe on Fwd_ALUA_E
  // Probe on forwardunit_1_frsesel
  // Probe on forwardunit_1_frtesel
  Multiplexer #(.select(2), .width(32), .enable("false")) multiplexer_5 (
    .in0(RD1_E), .in1(M__D), .in2(W__D), .in3({32{1'b0}}), .out(Fwd_ALUA_E), .sel(forwardunit_1_frsesel));
  E_M_reg e_m_reg_1 (
    .memwrite(MemWrite_E), .regwrite(RegWrite_E), .memreacd(MemRead_E), .memtoreg(MemToReg_E),
    .aluresult_i(ALUresult), .writedata_i(Fwd_ALUB_E), .writereg_i(WriteReg_E), .pc_i(d_e_reg_1_pc_o),
    .pc_4_i(PC_4_E), .pc_8_i(PC_8_E), .instr_i(instr_E), .out_16(MemWrite_M), .out_17(RegWrite_M),
    .out_19(MemRead_M), .out_20(MemToReg_M), .out_21(ALUresult_M), .out_22(WD_M), .out_23(WriteReg_M),
    .pc_o(PC_M), .pc_4_o(PC_4_M), .pc_8_o(PC_8_M), .out_27(instr_M), .in_1(Clk_prime), .in_2(in_1),
    .ResDst(RegDst_E), .out_28(RegDst_M), .in_4(tNew_E), .out_18(tNew_M));
  // Probe on forwardunit_1_frtmsel
  // Probe on ALUresult_M
  Multiplexer #(.select(2), .width(32), .enable("false")) multiplexer_6 (
    .in0(RD2_E), .in1(M__D), .in2(W__D), .in3({32{1'b0}}), .out(Fwd_ALUB_E), .sel(forwardunit_1_frtesel));
  Multiplexer #(.width(32), .enable("false")) multiplexer_7 (
    .in0(WD_M), .in1(W__D), .out(Fwd_WD_M), .sel(forwardunit_1_frtmsel));
  RAM #(.addrWidth(10), .dataWidth(32), .bus("separate")) ram_1 (
    .addr(ALUresult_M[11:2]), .din(Fwd_WD_M), .data(RD), .str(MemWrite_M), .clk(Clk_prime), .ld(MemRead_M),
    .clr(in_1));  // open: sel
  // Probe on RD
  M_W_reg m_w_reg_1 (
    .regwrite(RegWrite_M), .memtoreg(MemToReg_M), .aluresult_i(ALUresult_M), .writedata_i(WD_M),
    .writereg_i(WriteReg_M), .readdata_i(RD), .pc_i(PC_M), .pc_4_i(PC_4_M), .pc_8_i(PC_8_M),
    .instr_i(instr_M), .memaddr(ALUresult_M), .memdata(Fwd_WD_M), .memwrite(MemWrite_M), .out_18(RegWrite),
    .out_20(m_w_reg_1_out_20), .out_21(ALUresult_W), .out_23(RegAddr), .out_24(ReadData_W), .pc_8_o(PC_8_W),
    .out_28(instr_W), .out_29({MemAddr_W[31:7], MemAddr, MemAddr_W[1:0]}), .out_30(MemDat),
    .out_31(MemWrite), .in_1(Clk_prime), .in_2(in_1), .out_19(tNew_W), .RegDst(RegDst_M),
    .RegDst_2(RegDst_W), .in_3(tNew_M));  // open: out_22, pc_o, pc_4_o
  // Probe on ALUresult_W
  // Probe on m_w_reg_1_out_20
  Multiplexer #(.select(2), .width(32), .enable("false")) multiplexer_8 (
    .in0(ALUresult_W), .in1(ReadData_W), .in2(PC_8_W), .out(RegData), .sel(m_w_reg_1_out_20));  // open: in3
  // Probe on RegData

  // Other names for the same wires on the sheet: MemAddr_W[6:2] = MemAddr; MemData_W[31:0] = MemDat;
  //   MemWrite_W = MemWrite; RegAddr_W[4:0] = RegAddr; RegData_W[31:0] = RegData; RegWrite_W = RegWrite; reset = in_1

  // Notes on the sheet:
  //   contents of rom_1 (hex, n*v repeats v):
  //   35290001 ad490000 8d4a0000 214a0001
  //   IF
  //   IF/ID
  //   ID
  //   ID/EX
  //   EX
  //   EX/MEM
  //   MEM
  //   MEM/WB
  //   WB
endmodule

module StallUnit (
  input  [4:0] s1_D,
  input  [4:0] s2_D,
  input  [1:0] tUse1_D,
  input  [1:0] tUse2_D,
  input  [4:0] des_E,
  input  [3:0] tNew_E,
  input  [3:0] tNew_M,
  input  [4:0] des_M,
  output Stall_F,
  output Stall_D,
  output flush_E
);

  wire and_1_out, and_2_out, and_3_out, and_4_out, comparator_1_eq, comparator_2_eq, comparator_3_lt,
       comparator_4_eq, comparator_5_eq, comparator_6_lt, comparator_7_eq, comparator_8_eq, comparator_9_lt,
       comparator_10_eq, comparator_11_eq, comparator_12_lt, not_1_out, not_2_out, not_3_out, not_4_out;
  wire [3:0] tUse1_D_t, tUse2_D_t;

  Comparator #(.width(5), .mode("unsigned")) comparator_1 (
    .a(s1_D), .b({5{1'b0}}), .eq(comparator_1_eq));  // open: gt, lt
  Comparator #(.width(5), .mode("unsigned")) comparator_2 (.a(s1_D), .b(des_E), .eq(comparator_2_eq));  // open: gt, lt
  Comparator #(.width(4), .mode("unsigned")) comparator_3 (
    .a(tUse1_D_t), .b(tNew_E), .lt(comparator_3_lt));  // open: gt, eq
  Comparator #(.width(5), .mode("unsigned")) comparator_4 (
    .a(s2_D), .b({5{1'b0}}), .eq(comparator_4_eq));  // open: gt, lt
  Comparator #(.width(5), .mode("unsigned")) comparator_5 (.a(s2_D), .b(des_E), .eq(comparator_5_eq));  // open: gt, lt
  Comparator #(.width(4), .mode("unsigned")) comparator_6 (
    .a(tUse2_D_t), .b(tNew_E), .lt(comparator_6_lt));  // open: gt, eq
  Comparator #(.width(5), .mode("unsigned")) comparator_7 (
    .a(s1_D), .b({5{1'b0}}), .eq(comparator_7_eq));  // open: gt, lt
  Comparator #(.width(5), .mode("unsigned")) comparator_8 (.a(s1_D), .b(des_M), .eq(comparator_8_eq));  // open: gt, lt
  Comparator #(.width(4), .mode("unsigned")) comparator_9 (
    .a(tUse1_D_t), .b(tNew_M), .lt(comparator_9_lt));  // open: gt, eq
  Comparator #(.width(5), .mode("unsigned")) comparator_10 (
    .a(s2_D), .b({5{1'b0}}), .eq(comparator_10_eq));  // open: gt, lt
  Comparator #(.width(5), .mode("unsigned")) comparator_11 (
    .a(s2_D), .b(des_M), .eq(comparator_11_eq));  // open: gt, lt
  Comparator #(.width(4), .mode("unsigned")) comparator_12 (
    .a(tUse2_D_t), .b(tNew_M), .lt(comparator_12_lt));  // open: gt, eq
  assign tUse1_D_t = {{2{1'b0}}, tUse1_D};  // Bit_Extender bit_extender_1
  not not_1 (not_1_out, comparator_1_eq);
  not not_2 (not_2_out, comparator_4_eq);
  not not_3 (not_3_out, comparator_7_eq);
  not not_4 (not_4_out, comparator_10_eq);
  and and_1 (and_1_out, not_1_out, comparator_2_eq, comparator_3_lt);
  and and_2 (and_2_out, not_2_out, comparator_5_eq, comparator_6_lt);
  and and_3 (and_3_out, not_3_out, comparator_8_eq, comparator_9_lt);
  and and_4 (and_4_out, not_4_out, comparator_11_eq, comparator_12_lt);
  assign tUse2_D_t = {{2{1'b0}}, tUse2_D};  // Bit_Extender bit_extender_2
  or or_1 (flush_E, and_1_out, and_2_out, and_3_out, and_4_out);

  assign Stall_D = flush_E;
  assign Stall_F = flush_E;

  // Other names for the same wires on the sheet: stall_flag = flush_E
endmodule

module forwardUnit (
  input  [4:0] s1_D,
  input  [4:0] s2_D,
  input  [4:0] s1_E,
  input  [4:0] s2_E,
  input  [4:0] des_E,
  input  [3:0] tNew_E,
  input  [4:0] s2_M,
  input  [3:0] tNew_M,
  input  [4:0] des_M,
  input  [3:0] tNew_W,
  input  [4:0] des_W,
  output [1:0] fRsDsel,
  output [1:0] fRtDsel,
  output [1:0] fRsEsel,
  output [1:0] fRtEsel,
  output fRtMsel
);

  wire and_1_out, and_2_out, and_3_out, and_4_out, and_5_out, and_6_out, and_7_out, and_8_out, and_9_out,
       comparator_1_eq, comparator_2_eq, comparator_3_eq, comparator_4_eq, comparator_5_eq, comparator_6_eq,
       comparator_7_eq, comparator_8_eq, comparator_9_eq, comparator_10_eq, comparator_11_eq,
       comparator_12_eq, comparator_13_eq, comparator_14_eq, comparator_15_eq, comparator_16_eq,
       comparator_17_eq, comparator_18_eq, comparator_19_eq, comparator_20_eq, comparator_21_eq,
       comparator_22_eq, comparator_23_eq, comparator_24_eq, comparator_25_eq, comparator_26_eq,
       comparator_27_eq, not_1_out, not_2_out, not_3_out, not_4_out, not_5_out, not_6_out, not_7_out,
       not_8_out, not_9_out;
  wire [1:0] multiplexer_1_out, multiplexer_2_out, multiplexer_5_out, multiplexer_6_out;

  not not_1 (not_1_out, comparator_1_eq);
  Comparator #(.width(5), .mode("unsigned")) comparator_1 (
    .a(s1_D), .b({5{1'b0}}), .eq(comparator_1_eq));  // open: gt, lt
  Comparator #(.width(5), .mode("unsigned")) comparator_2 (.a(s1_D), .b(des_M), .eq(comparator_2_eq));  // open: gt, lt
  Comparator #(.width(4), .mode("unsigned")) comparator_3 (
    .a(tNew_M), .b(4'b0000), .eq(comparator_3_eq));  // open: gt, lt
  Comparator #(.width(5), .mode("unsigned")) comparator_4 (
    .a(s1_D), .b({5{1'b0}}), .eq(comparator_4_eq));  // open: gt, lt
  not not_2 (not_2_out, comparator_4_eq);
  Comparator #(.width(5), .mode("unsigned")) comparator_5 (.a(s1_D), .b(des_E), .eq(comparator_5_eq));  // open: gt, lt
  Comparator #(.width(4), .mode("unsigned")) comparator_6 (
    .a(tNew_E), .b(4'b0000), .eq(comparator_6_eq));  // open: gt, lt
  Comparator #(.width(5), .mode("unsigned")) comparator_7 (
    .a(s2_D), .b({5{1'b0}}), .eq(comparator_7_eq));  // open: gt, lt
  Comparator #(.width(5), .mode("unsigned")) comparator_8 (.a(s2_D), .b(des_M), .eq(comparator_8_eq));  // open: gt, lt
  Comparator #(.width(4), .mode("unsigned")) comparator_9 (
    .a(tNew_M), .b(4'b0000), .eq(comparator_9_eq));  // open: gt, lt
  Comparator #(.width(5), .mode("unsigned")) comparator_10 (
    .a(s2_D), .b({5{1'b0}}), .eq(comparator_10_eq));  // open: gt, lt
  Comparator #(.width(5), .mode("unsigned")) comparator_11 (
    .a(s2_D), .b(des_E), .eq(comparator_11_eq));  // open: gt, lt
  Comparator #(.width(4), .mode("unsigned")) comparator_12 (
    .a(tNew_E), .b(4'b0000), .eq(comparator_12_eq));  // open: gt, lt
  and and_1 (and_1_out, not_1_out, comparator_2_eq, comparator_3_eq);
  and and_2 (and_2_out, not_2_out, comparator_5_eq, comparator_6_eq);
  not not_3 (not_3_out, comparator_7_eq);
  not not_4 (not_4_out, comparator_10_eq);
  Multiplexer #(.width(2)) multiplexer_1 (
    .in0(2'b00), .in1(2'b10), .out(multiplexer_1_out), .sel(and_1_out));  // open: en
  and and_3 (and_3_out, not_3_out, comparator_8_eq, comparator_9_eq);
  and and_4 (and_4_out, not_4_out, comparator_11_eq, comparator_12_eq);
  Multiplexer #(.width(2)) multiplexer_2 (
    .in0(2'b00), .in1(2'b10), .out(multiplexer_2_out), .sel(and_3_out));  // open: en
  Multiplexer #(.width(2)) multiplexer_3 (
    .in0(multiplexer_1_out), .in1(2'b01), .out(fRsDsel), .sel(and_2_out));  // open: en
  Multiplexer #(.width(2)) multiplexer_4 (
    .in0(multiplexer_2_out), .in1(2'b01), .out(fRtDsel), .sel(and_4_out));  // open: en
  Comparator #(.width(5), .mode("unsigned")) comparator_13 (
    .a(s1_E), .b({5{1'b0}}), .eq(comparator_13_eq));  // open: gt, lt
  Comparator #(.width(5), .mode("unsigned")) comparator_14 (
    .a(s1_E), .b(des_W), .eq(comparator_14_eq));  // open: gt, lt
  Comparator #(.width(4), .mode("unsigned")) comparator_15 (
    .a(tNew_W), .b(4'b0000), .eq(comparator_15_eq));  // open: gt, lt
  Comparator #(.width(5), .mode("unsigned")) comparator_16 (
    .a(s1_E), .b({5{1'b0}}), .eq(comparator_16_eq));  // open: gt, lt
  Comparator #(.width(5), .mode("unsigned")) comparator_17 (
    .a(s1_E), .b(des_M), .eq(comparator_17_eq));  // open: gt, lt
  Comparator #(.width(4), .mode("unsigned")) comparator_18 (
    .a(tNew_M), .b(4'b0000), .eq(comparator_18_eq));  // open: gt, lt
  Comparator #(.width(5), .mode("unsigned")) comparator_19 (
    .a(s2_E), .b({5{1'b0}}), .eq(comparator_19_eq));  // open: gt, lt
  Comparator #(.width(5), .mode("unsigned")) comparator_20 (
    .a(s2_E), .b(des_W), .eq(comparator_20_eq));  // open: gt, lt
  Comparator #(.width(4), .mode("unsigned")) comparator_21 (
    .a(tNew_W), .b(4'b0000), .eq(comparator_21_eq));  // open: gt, lt
  Comparator #(.width(5), .mode("unsigned")) comparator_22 (
    .a(s2_E), .b({5{1'b0}}), .eq(comparator_22_eq));  // open: gt, lt
  Comparator #(.width(5), .mode("unsigned")) comparator_23 (
    .a(s2_E), .b(des_M), .eq(comparator_23_eq));  // open: gt, lt
  Comparator #(.width(4), .mode("unsigned")) comparator_24 (
    .a(tNew_M), .b(4'b0000), .eq(comparator_24_eq));  // open: gt, lt
  not not_5 (not_5_out, comparator_13_eq);
  not not_6 (not_6_out, comparator_16_eq);
  not not_7 (not_7_out, comparator_19_eq);
  not not_8 (not_8_out, comparator_22_eq);
  and and_5 (and_5_out, not_5_out, comparator_14_eq, comparator_15_eq);
  and and_6 (and_6_out, not_6_out, comparator_17_eq, comparator_18_eq);
  and and_7 (and_7_out, not_7_out, comparator_20_eq, comparator_21_eq);
  and and_8 (and_8_out, not_8_out, comparator_23_eq, comparator_24_eq);
  Multiplexer #(.width(2)) multiplexer_5 (
    .in0(2'b00), .in1(2'b10), .out(multiplexer_5_out), .sel(and_5_out));  // open: en
  Multiplexer #(.width(2)) multiplexer_6 (
    .in0(2'b00), .in1(2'b10), .out(multiplexer_6_out), .sel(and_7_out));  // open: en
  Multiplexer #(.width(2)) multiplexer_7 (
    .in0(multiplexer_5_out), .in1(2'b01), .out(fRsEsel), .sel(and_6_out));  // open: en
  Multiplexer #(.width(2)) multiplexer_8 (
    .in0(multiplexer_6_out), .in1(2'b01), .out(fRtEsel), .sel(and_8_out));  // open: en
  Comparator #(.width(5), .mode("unsigned")) comparator_25 (
    .a(s2_M), .b({5{1'b0}}), .eq(comparator_25_eq));  // open: gt, lt
  not not_9 (not_9_out, comparator_25_eq);
  Comparator #(.width(5), .mode("unsigned")) comparator_26 (
    .a(s2_M), .b(des_W), .eq(comparator_26_eq));  // open: gt, lt
  Comparator #(.width(4), .mode("unsigned")) comparator_27 (
    .a(tNew_W), .b(4'b0000), .eq(comparator_27_eq));  // open: gt, lt
  and and_9 (and_9_out, not_9_out, comparator_26_eq, comparator_27_eq);
  Multiplexer multiplexer_9 (.in0(1'b0), .in1(1'b1), .out(fRtMsel), .sel(and_9_out));  // open: en
endmodule

module M_W_reg (
  input  in_1,
  input  in_2,
  input  [3:0] in_3,
  input  regwrite,
  input  [1:0] memtoreg,
  input  [31:0] aluresult_i,
  input  [31:0] writedata_i,
  input  [4:0] writereg_i,
  input  [31:0] readdata_i,
  input  [31:0] pc_i,
  input  [31:0] pc_4_i,
  input  [31:0] pc_8_i,
  input  [31:0] instr_i,
  input  [31:0] memaddr,
  input  [31:0] memdata,
  input  memwrite,
  input  [1:0] RegDst,
  output out_18,
  output [3:0] out_19,
  output [1:0] out_20,
  output [31:0] out_21,
  output [31:0] out_22,
  output [4:0] out_23,
  output [31:0] out_24,
  output [31:0] pc_o,
  output [31:0] pc_4_o,
  output [31:0] pc_8_o,
  output [31:0] out_28,
  output [31:0] out_29,
  output [31:0] out_30,
  output out_31,
  output [1:0] RegDst_2
);

  wire comparator_1_eq;
  wire [3:0] multiplexer_1_out, subtractor_1_out;

  Register #(.width(1)) register_1 (.D(regwrite), .Q(out_18), .clk(in_1), .clr(in_2));  // open: en
  Register #(.width(2)) register_2 (.D(memtoreg), .Q(out_20), .clk(in_1), .clr(in_2));  // open: en
  Register #(.width(32)) register_3 (.D(aluresult_i), .Q(out_21), .clk(in_1), .clr(in_2));  // open: en
  Register #(.width(32)) register_4 (.D(writedata_i), .Q(out_22), .clk(in_1), .clr(in_2));  // open: en
  Register #(.width(5)) register_5 (.D(writereg_i), .Q(out_23), .clk(in_1), .clr(in_2));  // open: en
  Register #(.width(32)) register_6 (.D(readdata_i), .Q(out_24), .clk(in_1), .clr(in_2));  // open: en
  Register #(.width(32)) register_7 (.D(pc_i), .Q(pc_o), .clk(in_1), .clr(in_2));  // open: en
  Register #(.width(32)) register_8 (.D(pc_4_i), .Q(pc_4_o), .clk(in_1), .clr(in_2));  // open: en
  Register #(.width(32)) register_9 (.D(pc_8_i), .Q(pc_8_o), .clk(in_1), .clr(in_2));  // open: en
  Register #(.width(32)) register_10 (.D(instr_i), .Q(out_28), .clk(in_1), .clr(in_2));  // open: en
  Register #(.width(32)) register_11 (.D(memaddr), .Q(out_29), .clk(in_1), .clr(in_2));  // open: en
  Register #(.width(32)) register_12 (.D(memdata), .Q(out_30), .clk(in_1), .clr(in_2));  // open: en
  Register #(.width(1)) register_13 (.D(memwrite), .Q(out_31), .clk(in_1), .clr(in_2));  // open: en
  Register #(.width(2)) u_RegDst (.D(RegDst), .Q(RegDst_2), .clk(in_1), .clr(in_2));  // open: en
  Comparator #(.width(4), .mode("unsigned")) comparator_1 (
    .a(in_3), .b(4'b0000), .eq(comparator_1_eq));  // open: gt, lt
  Subtractor #(.width(4)) subtractor_1 (.a(in_3), .b(4'b0001), .out(subtractor_1_out));  // open: bin, bout
  Multiplexer #(.width(4), .enable("false")) multiplexer_1 (
    .in0(subtractor_1_out), .in1(4'b0000), .out(multiplexer_1_out), .sel(comparator_1_eq));
  Register #(.width(4)) register_14 (.D(multiplexer_1_out), .Q(out_19), .clk(in_1), .clr(in_2));  // open: en

  // Other names for the same wires on the sheet: clk = in_1; clk_prime = in_1; Reset = in_2
endmodule

module E_M_reg (
  input  in_1,
  input  in_2,
  input  memwrite,
  input  [3:0] in_4,
  input  regwrite,
  input  memreacd,
  input  [1:0] memtoreg,
  input  [31:0] aluresult_i,
  input  [31:0] writedata_i,
  input  [4:0] writereg_i,
  input  [31:0] pc_i,
  input  [31:0] pc_4_i,
  input  [31:0] pc_8_i,
  input  [31:0] instr_i,
  input  [1:0] ResDst,
  output out_16,
  output out_17,
  output [3:0] out_18,
  output out_19,
  output [1:0] out_20,
  output [31:0] out_21,
  output [31:0] out_22,
  output [4:0] out_23,
  output [31:0] pc_o,
  output [31:0] pc_4_o,
  output [31:0] pc_8_o,
  output [31:0] out_27,
  output [1:0] out_28
);

  wire comparator_1_eq;
  wire [3:0] multiplexer_1_out, subtractor_1_out;

  Register #(.width(2)) register_1 (.D(ResDst), .Q(out_28), .clk(in_1), .clr(in_2));  // open: en
  Register #(.width(1)) register_2 (.D(memwrite), .Q(out_16), .clk(in_1), .clr(in_2));  // open: en
  Register #(.width(1)) register_3 (.D(regwrite), .Q(out_17), .clk(in_1), .clr(in_2));  // open: en
  Register #(.width(1)) register_4 (.D(memreacd), .Q(out_19), .clk(in_1), .clr(in_2));  // open: en
  Register #(.width(2)) register_5 (.D(memtoreg), .Q(out_20), .clk(in_1), .clr(in_2));  // open: en
  Register #(.width(32)) register_6 (.D(aluresult_i), .Q(out_21), .clk(in_1), .clr(in_2));  // open: en
  Register #(.width(32)) register_7 (.D(writedata_i), .Q(out_22), .clk(in_1), .clr(in_2));  // open: en
  Register #(.width(5)) register_8 (.D(writereg_i), .Q(out_23), .clk(in_1), .clr(in_2));  // open: en
  Register #(.width(32)) register_9 (.D(pc_i), .Q(pc_o), .clk(in_1), .clr(in_2));  // open: en
  Register #(.width(32)) register_10 (.D(pc_4_i), .Q(pc_4_o), .clk(in_1), .clr(in_2));  // open: en
  Register #(.width(32)) register_11 (.D(pc_8_i), .Q(pc_8_o), .clk(in_1), .clr(in_2));  // open: en
  Register #(.width(32)) register_12 (.D(instr_i), .Q(out_27), .clk(in_1), .clr(in_2));  // open: en
  Comparator #(.width(4), .mode("unsigned")) comparator_1 (
    .a(in_4), .b(4'b0000), .eq(comparator_1_eq));  // open: gt, lt
  Subtractor #(.width(4)) subtractor_1 (.a(in_4), .b(4'b0001), .out(subtractor_1_out));  // open: bin, bout
  Multiplexer #(.width(4), .enable("false")) multiplexer_1 (
    .in0(subtractor_1_out), .in1(4'b0000), .out(multiplexer_1_out), .sel(comparator_1_eq));
  Register #(.width(4)) register_13 (.D(multiplexer_1_out), .Q(out_18), .clk(in_1), .clr(in_2));  // open: en

  // Other names for the same wires on the sheet: clk = in_1; clk_prime = in_1; Reset = in_2
endmodule

module D_E_reg (
  input  in_1,
  input  in_2,
  input  [31:0] pc_i,
  input  [31:0] RD1_i,
  input  [31:0] pc_4_i,
  input  [31:0] RD2_i,
  input  [31:0] pc_8_i,
  input  [4:0] rs_i,
  input  [31:0] EXTresult_i,
  input  [4:0] rt_i,
  input  [4:0] rd_i,
  input  [1:0] regdst,
  input  memwrite,
  input  regwrite,
  input  in_15,
  input  alusrc,
  input  memreacd,
  input  [1:0] memtoreg,
  input  [1:0] aluctrl,
  input  [31:0] instr_i,
  output [31:0] pc_o,
  output [31:0] RD1_o,
  output [31:0] pc_4_o,
  output [31:0] RD2_o,
  output [31:0] pc_8_o,
  output [4:0] rs_o,
  output [31:0] EXTresult_o,
  output [4:0] rt_o,
  output [4:0] rd_o,
  output [1:0] out_30,
  output out_31,
  output out_32,
  output out_33,
  output out_34,
  output [1:0] out_35,
  output [1:0] out_36,
  output [31:0] out_37
);

  wire multiplexer_2_out, multiplexer_3_out, multiplexer_4_out, multiplexer_5_out;
  wire [1:0] multiplexer_1_out, multiplexer_6_out, multiplexer_7_out;
  wire [4:0] multiplexer_10_out, multiplexer_11_out, multiplexer_12_out;
  wire [31:0] multiplexer_8_out, multiplexer_9_out, multiplexer_13_out, multiplexer_14_out,
       multiplexer_15_out, multiplexer_16_out, multiplexer_17_out;

  Multiplexer #(.width(2), .enable("false")) multiplexer_1 (
    .in0(regdst), .in1(2'b00), .out(multiplexer_1_out), .sel(in_15));
  Multiplexer #(.enable("false")) multiplexer_2 (.in0(memwrite), .in1(1'b0), .out(multiplexer_2_out), .sel(in_15));
  Multiplexer #(.enable("false")) multiplexer_3 (.in0(regwrite), .in1(1'b0), .out(multiplexer_3_out), .sel(in_15));
  Multiplexer #(.enable("false")) multiplexer_4 (.in0(alusrc), .in1(1'b0), .out(multiplexer_4_out), .sel(in_15));
  Multiplexer #(.enable("false")) multiplexer_5 (.in0(memreacd), .in1(1'b0), .out(multiplexer_5_out), .sel(in_15));
  Multiplexer #(.width(2), .enable("false")) multiplexer_6 (
    .in0(memtoreg), .in1(2'b00), .out(multiplexer_6_out), .sel(in_15));
  Multiplexer #(.width(2), .enable("false")) multiplexer_7 (
    .in0(aluctrl), .in1(2'b00), .out(multiplexer_7_out), .sel(in_15));
  Register #(.width(2)) register_1 (.D(multiplexer_1_out), .Q(out_30), .clk(in_1), .clr(in_2));  // open: en
  Register #(.width(1)) register_2 (.D(multiplexer_2_out), .Q(out_31), .clk(in_1), .clr(in_2));  // open: en
  Register #(.width(1)) register_3 (.D(multiplexer_3_out), .Q(out_32), .clk(in_1), .clr(in_2));  // open: en
  Register #(.width(1)) register_4 (.D(multiplexer_4_out), .Q(out_33), .clk(in_1), .clr(in_2));  // open: en
  Register #(.width(1)) register_5 (.D(multiplexer_5_out), .Q(out_34), .clk(in_1), .clr(in_2));  // open: en
  Register #(.width(2)) register_6 (.D(multiplexer_6_out), .Q(out_35), .clk(in_1), .clr(in_2));  // open: en
  Register #(.width(2)) register_7 (.D(multiplexer_7_out), .Q(out_36), .clk(in_1), .clr(in_2));  // open: en
  Multiplexer #(.width(32), .enable("false")) multiplexer_8 (
    .in0(RD1_i), .in1({32{1'b0}}), .out(multiplexer_8_out), .sel(in_15));
  Multiplexer #(.width(32), .enable("false")) multiplexer_9 (
    .in0(RD2_i), .in1({32{1'b0}}), .out(multiplexer_9_out), .sel(in_15));
  Multiplexer #(.width(5), .enable("false")) multiplexer_10 (
    .in0(rs_i), .in1({5{1'b0}}), .out(multiplexer_10_out), .sel(in_15));
  Multiplexer #(.width(5), .enable("false")) multiplexer_11 (
    .in0(rt_i), .in1({5{1'b0}}), .out(multiplexer_11_out), .sel(in_15));
  Multiplexer #(.width(5), .enable("false")) multiplexer_12 (
    .in0(rd_i), .in1({5{1'b0}}), .out(multiplexer_12_out), .sel(in_15));
  Register #(.width(32)) register_8 (.D(multiplexer_8_out), .Q(RD1_o), .clk(in_1), .clr(in_2));  // open: en
  Register #(.width(32)) register_9 (.D(multiplexer_9_out), .Q(RD2_o), .clk(in_1), .clr(in_2));  // open: en
  Register #(.width(5)) register_10 (.D(multiplexer_10_out), .Q(rs_o), .clk(in_1), .clr(in_2));  // open: en
  Register #(.width(5)) register_11 (.D(multiplexer_11_out), .Q(rt_o), .clk(in_1), .clr(in_2));  // open: en
  Register #(.width(5)) register_12 (.D(multiplexer_12_out), .Q(rd_o), .clk(in_1), .clr(in_2));  // open: en
  Multiplexer #(.width(32), .enable("false")) multiplexer_13 (
    .in0(instr_i), .in1({32{1'b0}}), .out(multiplexer_13_out), .sel(in_15));
  Register #(.width(32)) register_13 (.D(multiplexer_13_out), .Q(out_37), .clk(in_1), .clr(in_2));  // open: en
  Multiplexer #(.width(32), .enable("false")) multiplexer_14 (
    .in0(pc_i), .in1({32{1'b0}}), .out(multiplexer_14_out), .sel(in_15));
  Multiplexer #(.width(32), .enable("false")) multiplexer_15 (
    .in0(pc_4_i), .in1({32{1'b0}}), .out(multiplexer_15_out), .sel(in_15));
  Multiplexer #(.width(32), .enable("false")) multiplexer_16 (
    .in0(pc_8_i), .in1({32{1'b0}}), .out(multiplexer_16_out), .sel(in_15));
  Multiplexer #(.width(32), .enable("false")) multiplexer_17 (
    .in0(EXTresult_i), .in1({32{1'b0}}), .out(multiplexer_17_out), .sel(in_15));
  Register #(.width(32)) register_14 (.D(multiplexer_14_out), .Q(pc_o), .clk(in_1), .clr(in_2));  // open: en
  Register #(.width(32)) register_15 (.D(multiplexer_15_out), .Q(pc_4_o), .clk(in_1), .clr(in_2));  // open: en
  Register #(.width(32)) register_16 (.D(multiplexer_16_out), .Q(pc_8_o), .clk(in_1), .clr(in_2));  // open: en
  Register #(.width(32)) register_17 (.D(multiplexer_17_out), .Q(EXTresult_o), .clk(in_1), .clr(in_2));  // open: en

  // Other names for the same wires on the sheet: clk = in_1; clk_prime = in_1; flush = in_15; Reset = in_2
endmodule

module F_D_reg (
  input  in_1,
  input  in_2,
  input  [31:0] instr_i,
  input  [31:0] pc_i,
  input  [31:0] pc_4_i,
  input  [31:0] pc_8_i,
  input  in_7,
  output [31:0] instr_o,
  output [31:0] pc_o,
  output [31:0] pc_4_o,
  output [31:0] pc_8_o
);

  wire clk_prime, not_1_out, not_2_out, not_3_out, not_4_out;

  not not_1 (not_1_out, in_7);
  not not_2 (not_2_out, in_7);
  not not_3 (not_3_out, in_7);
  not not_4 (not_4_out, in_7);
  buf and_1 (clk_prime, in_1);  // AND_Gate
  Register #(.width(32)) register_1 (.D(instr_i), .en(not_1_out), .Q(instr_o), .clk(clk_prime), .clr(in_2));
  Register #(.width(32)) register_2 (.D(pc_i), .en(not_2_out), .Q(pc_o), .clk(clk_prime), .clr(in_2));
  Register #(.width(32)) register_3 (.D(pc_4_i), .en(not_3_out), .Q(pc_4_o), .clk(clk_prime), .clr(in_2));
  Register #(.width(32)) register_4 (.D(pc_8_i), .en(not_4_out), .Q(pc_8_o), .clk(clk_prime), .clr(in_2));

  // Other names for the same wires on the sheet: clk = in_1; F_D_stall = in_7; reset = in_2
endmodule

module MMU (
  input  in_1,
  input  Reset,
  input  [31:0] NPC,
  input  in_4,
  output [23:0] instrAddr,
  output [31:0] out_6
);

  wire comparator_1_eq, not_1_out;
  wire [31:0] register_1_q, subtractor_1_out;

  not not_1 (not_1_out, in_4);
  Register #(.width(32)) register_1 (.D(NPC), .en(not_1_out), .Q(register_1_q), .clk(in_1), .clr(Reset));
  Comparator #(.width(32)) comparator_1 (.a(register_1_q), .b({32{1'b0}}), .eq(comparator_1_eq));  // open: gt, lt
  Multiplexer #(.width(32), .enable("false")) multiplexer_1 (
    .in0(register_1_q), .in1(32'h3000), .out(out_6), .sel(comparator_1_eq));
  Subtractor #(.width(32)) subtractor_1 (
    .a(out_6), .b(32'h3000), .out({subtractor_1_out[31:26], instrAddr, subtractor_1_out[1:0]}));  // open: bin, bout

  // Other names for the same wires on the sheet: Clk = in_1; StallF = in_4
endmodule

module splitter (
  input  [31:0] in_1,
  output [5:0] op,
  output [5:0] funct,
  output [25:0] _25_0,
  output [15:0] _15_0,
  output [4:0] _25_21,
  output [4:0] _20_16,
  output [4:0] _15_11
);


  assign _15_0 = in_1[15:0];
  assign _15_11 = in_1[15:11];
  assign _20_16 = in_1[20:16];
  assign _25_0 = in_1[25:0];
  assign _25_21 = in_1[25:21];
  assign funct = in_1[5:0];
  assign op = in_1[31:26];
endmodule

module Extend (
  input  [15:0] Imm16,
  input  [1:0] ExtOp,
  output [31:0] Imm32
);

  wire [31:0] bit_extender_1_out, bit_extender_2_out;

  assign bit_extender_1_out = {{16{1'b0}}, Imm16};  // Bit_Extender bit_extender_1
  assign bit_extender_2_out = {{16{Imm16[15]}}, Imm16};  // Bit_Extender bit_extender_2
  Multiplexer #(.select(2), .width(32), .enable("false")) multiplexer_1 (
    .in0(bit_extender_1_out), .in1(bit_extender_2_out), .in2({Imm16, {16{1'b0}}}), .out(Imm32), .sel(ExtOp));  // open: in3
endmodule

module Controller (
  input  [5:0] OP,
  input  [5:0] FUNCT,
  output [1:0] RegDst,
  output ALUSrc,
  output [1:0] MemtoReg,
  output RegWrite,
  output [1:0] MemWrite,
  output Beq,
  output [1:0] ALUOp,
  output [1:0] MemRead,
  output Jump,
  output jr,
  output [1:0] ExtOp
);

  wire ADD, ADDIU, ADDU, J, JALR, LB, LH, NOP, not_1_out, not_2_out, not_3_out, not_4_out, not_5_out,
       not_6_out, not_7_out, not_8_out, not_9_out, not_10_out, not_11_out, not_12_out, R, SB, SH, SLTI, SUB,
       SW;

  not not_1 (not_1_out, OP[5]);
  not not_2 (not_2_out, OP[4]);
  not not_3 (not_3_out, OP[2]);
  not not_4 (not_4_out, OP[3]);
  not not_5 (not_5_out, OP[0]);
  not not_6 (not_6_out, OP[1]);
  and LW (MemtoReg[0], OP[5], not_2_out, not_4_out, not_3_out, OP[1], OP[0]);
  and u_SW (SW, OP[5], not_2_out, OP[3], not_3_out, OP[1], OP[0]);
  and ORI (ALUOp[0], not_1_out, not_2_out, OP[3], OP[2], not_6_out, OP[0]);
  and u_SLTI (SLTI, not_1_out, not_2_out, OP[3], not_3_out, OP[1], not_5_out);
  and u_ADDIU (ADDIU, not_1_out, not_2_out, OP[3], not_3_out, not_6_out, OP[0]);
  and LUI (ExtOp[1], not_1_out, not_2_out, OP[3], OP[2], OP[1], OP[0]);
  and u_BEQ (Beq, not_1_out, not_2_out, not_4_out, OP[2], not_6_out, not_5_out);
  and u_J (J, not_1_out, not_2_out, not_4_out, not_3_out, OP[1], not_5_out);
  and JAL (MemtoReg[1], not_1_out, not_2_out, not_4_out, not_3_out, OP[1], OP[0]);
  and FUNC (R, not_1_out, not_2_out, not_4_out, not_3_out, not_6_out, not_5_out);
  and u_SB (SB, OP[5], not_2_out, OP[3], not_3_out, not_6_out, not_5_out);
  and u_SH (SH, OP[5], not_2_out, OP[3], not_3_out, not_6_out, OP[0]);
  and u_LB (LB, OP[5], not_2_out, not_4_out, not_3_out, not_6_out, not_5_out);
  and u_LH (LH, OP[5], not_2_out, not_4_out, not_3_out, not_6_out, OP[0]);
  not not_7 (not_7_out, FUNCT[4]);
  not not_8 (not_8_out, FUNCT[5]);
  not not_9 (not_9_out, FUNCT[2]);
  not not_10 (not_10_out, FUNCT[3]);
  not not_11 (not_11_out, FUNCT[1]);
  or or_1 (MemWrite[0], SB, SW);
  not not_12 (not_12_out, FUNCT[0]);
  or or_2 (MemRead[0], MemtoReg[0], LB);
  or u_RegDst (Jump, J, MemtoReg[1]);
  or RegDst_2 (ExtOp[0], ALUOp[1], MemtoReg[0], SW, ADDU);
  and u_ADD (ADD, FUNCT[5], not_7_out, not_10_out, not_9_out, not_11_out, not_12_out, R);
  and u_ADDU (ADDU, FUNCT[5], not_7_out, not_10_out, not_9_out, not_11_out, FUNCT[0], R);
  and u_SUB (SUB, FUNCT[5], not_7_out, not_10_out, not_9_out, FUNCT[1], not_12_out, R);
  and SUBU (ALUOp[1], FUNCT[5], not_7_out, not_10_out, not_9_out, FUNCT[1], FUNCT[0], R);
  and u_JR (jr, not_8_out, not_7_out, FUNCT[3], not_9_out, not_11_out, not_12_out, R);
  and u_JALR (JALR, not_8_out, not_7_out, FUNCT[3], not_9_out, not_11_out, FUNCT[0], R);
  and u_NOP (NOP, not_8_out, not_7_out, not_10_out, not_9_out, not_11_out, not_12_out, R);
  or or_3 (MemWrite[1], SW, SH);
  or or_4 (MemRead[1], MemtoReg[0], LH);
  or RegDst_3 (RegDst[0], ADDU, ALUOp[1]);
  or u_ALUSrc (ALUSrc, SW, MemtoReg[0], ALUOp[0], ADDIU, ExtOp[1]);
  or u_RegWrite (RegWrite, ADDU, ALUOp[1], MemtoReg[0], ALUOp[0], ADDIU, ExtOp[1], MemtoReg[1]);

  assign RegDst[1] = MemtoReg[1];

  // Other names for the same wires on the sheet: ORI = ALUOp[0]; SUBU = ALUOp[1]; LUI = ExtOp[1]; LW = MemtoReg[0];
  //   JAL = MemtoReg[1]
endmodule

module GRF (
  input  [4:0] A1,
  input  clk,
  input  reset,
  input  we,
  input  [4:0] A2,
  input  [4:0] A3,
  input  [31:0] WD,
  output [31:0] RD1,
  output [31:0] RD2
);

  wire and_1_out, and_2_out, comparator_1_eq, comparator_2_eq;
  wire [31:0] I0, I1, I2, I3, I4, I5, I6, I7, I8, I9, I10, I11, I12, I13, I14, I15, I16, I17, I18, I19, I20,
       I21, I22, I23, I24, I25, I26, I27, I28, I29, I30, I31, O0, O1, O2, O3, O4, O5, O6, O7, O8, O9, O10,
       O11, O12, O13, O14, O15, O16, O17, O18, O19, O20, O21, O22, O23, O24, O25, O26, O27, O28, O29, O30,
       O31, RD1_t, RD2_t;

  Demultiplexer #(.select(5), .width(32), .tristate("true")) demultiplexer_1 (
    .out0(I0), .out1(I1), .out2(I2), .out3(I3), .out4(I4), .out5(I5), .out6(I6), .out7(I7), .out8(I8),
    .out9(I9), .out10(I10), .out11(I11), .out12(I12), .out13(I13), .out14(I14), .out15(I15), .out16(I16),
    .out17(I17), .out18(I18), .out19(I19), .out20(I20), .out21(I21), .out22(I22), .out23(I23), .out24(I24),
    .out25(I25), .out26(I26), .out27(I27), .out28(I28), .out29(I29), .out30(I30), .out31(I31), .in(WD),
    .sel(A3));  // open: en
  Multiplexer #(.select(5), .width(32)) multiplexer_1 (
    .in0(O0), .in1(O1), .in2(O2), .in3(O3), .in4(O4), .in5(O5), .in6(O6), .in7(O7), .in8(O8), .in9(O9),
    .in10(O10), .in11(O11), .in12(O12), .in13(O13), .in14(O14), .in15(O15), .in16(O16), .in17(O17),
    .in18(O18), .in19(O19), .in20(O20), .in21(O21), .in22(O22), .in23(O23), .in24(O24), .in25(O25),
    .in26(O26), .in27(O27), .in28(O28), .in29(O29), .in30(O30), .in31(O31), .out(RD2_t), .sel(A2));  // open: en
  Comparator #(.width(5), .mode("unsigned")) comparator_1 (.a(A1), .b(A3), .eq(comparator_1_eq));  // open: gt, lt
  Comparator #(.width(5), .mode("unsigned")) comparator_2 (.a(A2), .b(A3), .eq(comparator_2_eq));  // open: gt, lt
  Multiplexer #(.width(32), .enable("false")) multiplexer_2 (.in0(RD1_t), .in1(WD), .out(RD1), .sel(and_1_out));
  and and_1 (and_1_out, comparator_1_eq, we);
  Multiplexer #(.width(32), .enable("false")) multiplexer_3 (.in0(RD2_t), .in1(WD), .out(RD2), .sel(and_2_out));
  and and_2 (and_2_out, comparator_2_eq, we);
  Multiplexer #(.select(5), .width(32)) multiplexer_4 (
    .in0(O0), .in1(O1), .in2(O2), .in3(O3), .in4(O4), .in5(O5), .in6(O6), .in7(O7), .in8(O8), .in9(O9),
    .in10(O10), .in11(O11), .in12(O12), .in13(O13), .in14(O14), .in15(O15), .in16(O16), .in17(O17),
    .in18(O18), .in19(O19), .in20(O20), .in21(O21), .in22(O22), .in23(O23), .in24(O24), .in25(O25),
    .in26(O26), .in27(O27), .in28(O28), .in29(O29), .in30(O30), .in31(O31), .out(RD1_t), .sel(A1));  // open: en
  Register #(.width(32)) register_1 (.D({32{1'b0}}), .en(we), .Q(O0), .clk(clk), .clr(reset));
  Register #(.width(32)) register_2 (.D(I8), .en(we), .Q(O8), .clk(clk), .clr(reset));
  Register #(.width(32)) register_3 (.D(I16), .en(we), .Q(O16), .clk(clk), .clr(reset));
  Register #(.width(32)) register_4 (.D(I24), .en(we), .Q(O24), .clk(clk), .clr(reset));
  Register #(.width(32)) register_5 (.D(I1), .en(we), .Q(O1), .clk(clk), .clr(reset));
  Register #(.width(32)) register_6 (.D(I9), .en(we), .Q(O9), .clk(clk), .clr(reset));
  Register #(.width(32)) register_7 (.D(I17), .en(we), .Q(O17), .clk(clk), .clr(reset));
  Register #(.width(32)) register_8 (.D(I25), .en(we), .Q(O25), .clk(clk), .clr(reset));
  Register #(.width(32)) register_9 (.D(I2), .en(we), .Q(O2), .clk(clk), .clr(reset));
  Register #(.width(32)) register_10 (.D(I10), .en(we), .Q(O10), .clk(clk), .clr(reset));
  Register #(.width(32)) register_11 (.D(I18), .en(we), .Q(O18), .clk(clk), .clr(reset));
  Register #(.width(32)) register_12 (.D(I26), .en(we), .Q(O26), .clk(clk), .clr(reset));
  Register #(.width(32)) register_13 (.D(I3), .en(we), .Q(O3), .clk(clk), .clr(reset));
  Register #(.width(32)) register_14 (.D(I11), .en(we), .Q(O11), .clk(clk), .clr(reset));
  Register #(.width(32)) register_15 (.D(I19), .en(we), .Q(O19), .clk(clk), .clr(reset));
  Register #(.width(32)) register_16 (.D(I27), .en(we), .Q(O27), .clk(clk), .clr(reset));
  Register #(.width(32)) register_17 (.D(I4), .en(we), .Q(O4), .clk(clk), .clr(reset));
  Register #(.width(32)) register_18 (.D(I12), .en(we), .Q(O12), .clk(clk), .clr(reset));
  Register #(.width(32)) register_19 (.D(I20), .en(we), .Q(O20), .clk(clk), .clr(reset));
  Register #(.width(32)) register_20 (.D(I28), .en(we), .Q(O28), .clk(clk), .clr(reset));
  Register #(.width(32)) register_21 (.D(I5), .en(we), .Q(O5), .clk(clk), .clr(reset));
  Register #(.width(32)) register_22 (.D(I13), .en(we), .Q(O13), .clk(clk), .clr(reset));
  Register #(.width(32)) register_23 (.D(I21), .en(we), .Q(O21), .clk(clk), .clr(reset));
  Register #(.width(32)) register_24 (.D(I29), .en(we), .Q(O29), .clk(clk), .clr(reset));
  Register #(.width(32)) register_25 (.D(I6), .en(we), .Q(O6), .clk(clk), .clr(reset));
  Register #(.width(32)) register_26 (.D(I14), .en(we), .Q(O14), .clk(clk), .clr(reset));
  Register #(.width(32)) register_27 (.D(I22), .en(we), .Q(O22), .clk(clk), .clr(reset));
  Register #(.width(32)) register_28 (.D(I30), .en(we), .Q(O30), .clk(clk), .clr(reset));
  Register #(.width(32)) register_29 (.D(I7), .en(we), .Q(O7), .clk(clk), .clr(reset));
  Register #(.width(32)) register_30 (.D(I15), .en(we), .Q(O15), .clk(clk), .clr(reset));
  Register #(.width(32)) register_31 (.D(I23), .en(we), .Q(O23), .clk(clk), .clr(reset));
  Register #(.width(32)) register_32 (.D(I31), .en(we), .Q(O31), .clk(clk), .clr(reset));
endmodule

module ALU (
  input  [31:0] A,
  input  [31:0] B,
  input  [1:0] ALUOp,
  output [31:0] Result
);

  wire [31:0] adder_1_out, or_1_out, subtractor_1_out;

  Adder #(.width(32)) adder_1 (.a(A), .b(B), .out(adder_1_out));  // open: cin, cout
  Subtractor #(.width(32)) subtractor_1 (.a(A), .b(B), .out(subtractor_1_out));  // open: bin, bout
  assign or_1_out = A | B;  // OR_Gate or_1, 32 bits wide
  Multiplexer #(.select(2), .width(32)) multiplexer_1 (
    .in0(adder_1_out), .in1(or_1_out), .in2(subtractor_1_out), .out(Result), .sel(ALUOp));  // open: in3, en

  // Notes on the sheet:
  //   0 0 add
  //   1 0 sub
  //   0 1 or
  //   alu控制信号 控制输出哪一个结果
endmodule

module D (
  input  [31:0] in_1,
  output [4:0] S1_D,
  output [4:0] S2_D,
  output [1:0] tuse1_D,
  output [1:0] tuse2_D
);

  wire addiu, addu, beq, j, jal, jr, lui, lw, no, ori, S1_D_out, S2_D_2_out, S2_D_out, subu, sw, tuse1_D_out;
  wire [1:0] bit_extender_1_out;
  wire [4:0] splitter_1__20_16, splitter_1__25_21;
  wire [5:0] splitter_1_funct, splitter_1_op;

  splitter splitter_1 (
    .in_1(in_1), ._25_21(splitter_1__25_21), ._20_16(splitter_1__20_16), .funct(splitter_1_funct),
    .op(splitter_1_op));  // open: _25_0, _15_0, _15_11
  UseFunc usefunc_1 (
    .OP(splitter_1_op), .FUNCT(splitter_1_funct), .LW(lw), .SW(sw), .ADDU(addu), .SUBU(subu), .ORI(ori),
    .LUI(lui), .ADDIU(addiu), .BEQ(beq), .J(j), .Jal(jal), .JR(jr), .NOP(no));
  or u_S1_D (S1_D_out, lw, sw, addu, subu, ori, addiu, beq);
  or u_S2_D (S2_D_out, sw, addu, subu, beq);
  or u_tuse1_D (tuse1_D_out, lw, sw, addu, subu, ori, addiu);
  or S2_D_2 (S2_D_2_out, addu, subu);
  Multiplexer #(.width(5), .enable("false")) multiplexer_1 (
    .in0({5{1'b0}}), .in1(splitter_1__25_21), .out(S1_D), .sel(S1_D_out));
  Multiplexer #(.width(5), .enable("false")) multiplexer_2 (
    .in0({5{1'b0}}), .in1(splitter_1__20_16), .out(S2_D), .sel(S2_D_out));
  Multiplexer #(.width(2), .enable("false")) multiplexer_3 (.in0(2'b00), .in1(2'b01), .out(tuse1_D), .sel(tuse1_D_out));
  assign bit_extender_1_out = {{1{1'b0}}, S2_D_2_out};  // Bit_Extender bit_extender_1
  Multiplexer #(.width(2), .enable("false")) multiplexer_4 (
    .in0(bit_extender_1_out), .in1(2'b10), .out(tuse2_D), .sel(sw));
endmodule

module UseFunc (
  input  [5:0] OP,
  input  [5:0] FUNCT,
  output LW,
  output SW,
  output ADDU,
  output SUBU,
  output ORI,
  output LUI,
  output ADDIU,
  output BEQ,
  output J,
  output Jal,
  output JR,
  output NOP
);

  wire ADD, JALR, LB, LH, not_1_out, not_2_out, not_3_out, not_4_out, not_5_out, not_6_out, not_7_out,
       not_8_out, not_9_out, not_10_out, not_11_out, not_12_out, R, SB, SH, SLTI, SUB;

  not not_1 (not_1_out, OP[5]);
  not not_2 (not_2_out, OP[4]);
  not not_3 (not_3_out, OP[2]);
  not not_4 (not_4_out, OP[3]);
  not not_5 (not_5_out, OP[0]);
  not not_6 (not_6_out, OP[1]);
  and u_LW (LW, OP[5], not_2_out, not_4_out, not_3_out, OP[1], OP[0]);
  and u_SW (SW, OP[5], not_2_out, OP[3], not_3_out, OP[1], OP[0]);
  and u_ORI (ORI, not_1_out, not_2_out, OP[3], OP[2], not_6_out, OP[0]);
  and u_SLTI (SLTI, not_1_out, not_2_out, OP[3], not_3_out, OP[1], not_5_out);
  and u_ADDIU (ADDIU, not_1_out, not_2_out, OP[3], not_3_out, not_6_out, OP[0]);
  and u_LUI (LUI, not_1_out, not_2_out, OP[3], OP[2], OP[1], OP[0]);
  and u_BEQ (BEQ, not_1_out, not_2_out, not_4_out, OP[2], not_6_out, not_5_out);
  and u_J (J, not_1_out, not_2_out, not_4_out, not_3_out, OP[1], not_5_out);
  and u_JAL (Jal, not_1_out, not_2_out, not_4_out, not_3_out, OP[1], OP[0]);
  and FUNC (R, not_1_out, not_2_out, not_4_out, not_3_out, not_6_out, not_5_out);
  and u_SB (SB, OP[5], not_2_out, OP[3], not_3_out, not_6_out, not_5_out);
  and u_SH (SH, OP[5], not_2_out, OP[3], not_3_out, not_6_out, OP[0]);
  and u_LB (LB, OP[5], not_2_out, not_4_out, not_3_out, not_6_out, not_5_out);
  and u_LH (LH, OP[5], not_2_out, not_4_out, not_3_out, not_6_out, OP[0]);
  not not_7 (not_7_out, FUNCT[5]);
  not not_8 (not_8_out, FUNCT[4]);
  not not_9 (not_9_out, FUNCT[2]);
  not not_10 (not_10_out, FUNCT[3]);
  not not_11 (not_11_out, FUNCT[1]);
  not not_12 (not_12_out, FUNCT[0]);
  and u_ADD (ADD, FUNCT[5], not_8_out, not_10_out, not_9_out, not_11_out, not_12_out, R);
  and u_ADDU (ADDU, FUNCT[5], not_8_out, not_10_out, not_9_out, not_11_out, FUNCT[0], R);
  and u_SUB (SUB, FUNCT[5], not_8_out, not_10_out, not_9_out, FUNCT[1], not_12_out, R);
  and u_SUBU (SUBU, FUNCT[5], not_8_out, not_10_out, not_9_out, FUNCT[1], FUNCT[0], R);
  and u_JR (JR, not_7_out, not_8_out, FUNCT[3], not_9_out, not_11_out, not_12_out, R);
  and u_JALR (JALR, not_7_out, not_8_out, FUNCT[3], not_9_out, not_11_out, FUNCT[0], R);
  and u_NOP (NOP, not_7_out, not_8_out, not_10_out, not_9_out, not_11_out, not_12_out, R);
endmodule

module NPC (
  input  EQ,
  input  [31:0] imm32,
  input  [25:0] imm26,
  input  [2:0] NPCOp,
  input  [31:0] PC_4,
  input  [31:0] PC,
  input  [31:0] RegData,
  output [31:0] NPC
);

  wire [31:0] adder_1_out, multiplexer_1_out, shifter_1_out;

  Shifter #(.width(32)) shifter_1 (.in(imm32), .\dist (5'b00010), .out(shifter_1_out));
  Adder #(.width(32)) adder_1 (.a(PC), .b(shifter_1_out), .out(adder_1_out));  // open: cin, cout
  Multiplexer #(.width(32), .enable("false")) multiplexer_1 (
    .in0(PC_4), .in1(adder_1_out), .out(multiplexer_1_out), .sel(EQ));
  Multiplexer #(.select(3), .width(32), .enable("false")) multiplexer_2 (
    .in0(PC_4), .in1(multiplexer_1_out), .in2({PC_4[31:28], imm26, 2'b00}), .in4(RegData), .out(NPC),
    .sel(NPCOp));  // open: in3, in5, in6, in7
endmodule

module E (
  input  [31:0] in_1,
  input  [4:0] writereg_E,
  input  RegWrite,
  input  [31:0] in_4,
  input  [31:0] in_5,
  output [4:0] S1_E,
  output [4:0] S2_E,
  output [4:0] DES_E,
  output [3:0] tNew_E,
  output [31:0] E__D
);

  wire addiu, addu, beq, j, jal, jr, lui, lw, no, or_1_out, ori, S1_E_out, S2_E_out, subu, sw;
  wire [3:0] multiplexer_1_out;
  wire [4:0] rd, rt, splitter_1__25_21;
  wire [5:0] splitter_1_funct, splitter_1_op;

  UseFunc usefunc_1 (
    .OP(splitter_1_op), .FUNCT(splitter_1_funct), .LW(lw), .SW(sw), .ADDU(addu), .SUBU(subu), .ORI(ori),
    .LUI(lui), .ADDIU(addiu), .BEQ(beq), .J(j), .Jal(jal), .JR(jr), .NOP(no));
  splitter splitter_1 (
    .in_1(in_1), ._25_21(splitter_1__25_21), ._20_16(rt), ._15_11(rd), .funct(splitter_1_funct),
    .op(splitter_1_op));  // open: _25_0, _15_0
  or or_1 (or_1_out, addu, subu, ori);
  Multiplexer #(.width(4), .enable("false")) multiplexer_1 (
    .in0(4'b0000), .in1(4'b0001), .out(multiplexer_1_out), .sel(or_1_out));
  Multiplexer #(.width(5), .enable("false")) multiplexer_2 (
    .in0({5{1'b0}}), .in1(writereg_E), .out(DES_E), .sel(RegWrite));
  Multiplexer #(.width(4), .enable("false")) multiplexer_3 (
    .in0(multiplexer_1_out), .in1(4'b0010), .out(tNew_E), .sel(lw));
  or u_S1_E (S1_E_out, lw, sw, addu, subu, ori, addiu, beq);
  or u_S2_E (S2_E_out, sw, addu, subu, beq);
  Multiplexer #(.width(32), .enable("false")) multiplexer_4 (.in0(in_4), .in1(in_5), .out(E__D), .sel(lui));
  Multiplexer #(.width(5), .enable("false")) multiplexer_5 (
    .in0({5{1'b0}}), .in1(splitter_1__25_21), .out(S1_E), .sel(S1_E_out));
  Multiplexer #(.width(5), .enable("false")) multiplexer_6 (.in0({5{1'b0}}), .in1(rt), .out(S2_E), .sel(S2_E_out));
endmodule

module M (
  input  [31:0] in_1,
  input  [4:0] writereg_E,
  input  RegWrite,
  input  [31:0] in_4,
  input  [31:0] in_5,
  output [4:0] S1_M,
  output [4:0] S2_M,
  output [4:0] DES_E,
  output [31:0] M__D
);

  wire addiu, addu, beq, j, jal, jr, lui, lw, nop, ori, S1_M_out, S2_M_out, subu, sw;
  wire [4:0] rd, rt, splitter_1__25_21;
  wire [5:0] splitter_1_funct, splitter_1_op;

  UseFunc usefunc_1 (
    .OP(splitter_1_op), .FUNCT(splitter_1_funct), .LW(lw), .SW(sw), .ADDU(addu), .SUBU(subu), .ORI(ori),
    .LUI(lui), .ADDIU(addiu), .BEQ(beq), .J(j), .Jal(jal), .JR(jr), .NOP(nop));
  splitter splitter_1 (
    .in_1(in_1), ._25_21(splitter_1__25_21), ._20_16(rt), ._15_11(rd), .funct(splitter_1_funct),
    .op(splitter_1_op));  // open: _25_0, _15_0
  Multiplexer #(.width(5), .enable("false")) multiplexer_1 (
    .in0({5{1'b0}}), .in1(writereg_E), .out(DES_E), .sel(RegWrite));
  or u_S1_M (S1_M_out, lw, sw, addu, subu, ori, addiu, beq);
  or u_S2_M (S2_M_out, sw, addu, subu, beq);
  Multiplexer #(.width(32), .enable("false")) multiplexer_2 (.in0(in_5), .in1(in_4), .out(M__D), .sel(jal));
  Multiplexer #(.width(5), .enable("false")) multiplexer_3 (
    .in0({5{1'b0}}), .in1(splitter_1__25_21), .out(S1_M), .sel(S1_M_out));
  Multiplexer #(.width(5), .enable("false")) multiplexer_4 (.in0({5{1'b0}}), .in1(rt), .out(S2_M), .sel(S2_M_out));
endmodule

module W (
  input  [31:0] in_1,
  input  [4:0] writereg_E,
  input  RegWrite,
  input  [31:0] in_4,
  input  [31:0] in_5,
  input  [31:0] in_6,
  output [4:0] DES_E,
  output [31:0] W__D
);

  wire addiu, addu, beq, j, jal, jr, lui, lw, no, ori, subu, sw;
  wire [4:0] rd, rt;
  wire [5:0] splitter_1_funct, splitter_1_op;
  wire [31:0] multiplexer_1_out;

  UseFunc usefunc_1 (
    .OP(splitter_1_op), .FUNCT(splitter_1_funct), .LW(lw), .SW(sw), .ADDU(addu), .SUBU(subu), .ORI(ori),
    .LUI(lui), .ADDIU(addiu), .BEQ(beq), .J(j), .Jal(jal), .JR(jr), .NOP(no));
  splitter splitter_1 (
    .in_1(in_1), ._20_16(rt), ._15_11(rd), .funct(splitter_1_funct), .op(splitter_1_op));  // open: _25_0, _15_0, _25_21
  Multiplexer #(.width(32), .enable("false")) multiplexer_1 (.in0(in_5), .in1(in_4), .out(multiplexer_1_out), .sel(lw));
  Multiplexer #(.width(5), .enable("false")) multiplexer_2 (
    .in0({5{1'b0}}), .in1(writereg_E), .out(DES_E), .sel(RegWrite));
  Multiplexer #(.width(32), .enable("false")) multiplexer_3 (
    .in0(multiplexer_1_out), .in1(in_6), .out(W__D), .sel(jal));
endmodule
