// Logisim project 流水线cpu.circ as structural Verilog: 20 circuits, main circuit main
module main (
  input  in_1,
  output [31:0] instr,
  output regwrite,
  output [4:0] regaddr,
  output [31:0] regdata,
  output memwrite,
  output [4:0] memaddr,
  output [31:0] memdata
);

  wire Alusrc, branch_op, byteAB, clk, controller_1_branch, equal, ex_mem_1_byte_o, ex_mem_1_memread_o,
       ex_mem_1_memwrite_o, ex_mem_1_regwrite_o, flushE, fRtMsel, id_ex_1_alusrc_o, id_ex_1_byteab_o,
       id_ex_1_memread_o, id_ex_1_memwrite_o, id_ex_1_regwrite_o, j_jal, jr, MemRead, MemWrite_t, not_1_out,
       RegWrite_t, Stall_D, Stall_F;
  wire [1:0] ex_mem_1_memtoreg_o, ext_op, fRsDsel, fRsEsel, fRtDsel, fRtEsel, id_ex_1_memtoreg_o,
       id_ex_1_regdst_o, mem_wb_1_memtoreg_o, MemtoReg, Regdst, tuse1_D, tuse2_D;
  wire [2:0] Alu_op, id_ex_1_alu_op_o;
  wire [3:0] tnew_E, tnew_M, tnew_W;
  wire [4:0] des_E, des_M, des_W, ex_mem_1_out_18, id_ex_1_rd_o, id_ex_1_rt_o, multiplexer_6_out, s1_D, s1_E,
       s1_M, s2_D, s2_E, s2_M, splitter_1__11_15rd, splitter_1__16_20rt, splitter_1__21_25rs;
  wire [5:0] func, op;
  wire [15:0] splitter_1__0_15;
  wire [31:0] alu_1_result, D_CMP_RS, D_CMP_RT, dm_1_rd, E_ALU_A, E_ALU_B, EtoD, ex_mem_1_out_16,
       ex_mem_1_out_17, ex_mem_1_out_22, ex_mem_1_pc_4_o, ex_mem_1_pc_8_o, ex_mem_1_pc_o, extresult,
       id_ex_1_out_30, id_ex_1_out_39, id_ex_1_pc_4_o, id_ex_1_pc_8_o, id_ex_1_pc_o, if_id_1_out_8,
       if_id_1_out_9, if_id_1_pc_o, instr_0, M_DM_WD, mem_wb_1_out_17, mem_wb_1_out_19, mem_wb_1_out_23,
       mem_wb_1_pc_8_o, memaddr_o, MtoD, multiplexer_5_out, npc, pc, rd1, rd2, rs_e, rt_e, WtoD;

  Clock clock_1 (.out(clk));
  IF if_1 (.npc(npc), .instr(instr), .pc(pc), .in_1(clk), .in_2(in_1), .in_4(Stall_F));
  npc npc_1 (
    .pc(pc), .instr(instr_0), .extresult(extresult), .npc(npc), .branch_op(branch_op), .j_jal(j_jal),
    .RD1(D_CMP_RS), .jr(jr));
  IF_ID if_id_1 (
    .in_1(clk), .in_2(in_1), .instr_i(instr), .instr_o(instr_0), .pc_i(pc), .pc_o(if_id_1_pc_o),
    .in_5(Stall_D), .out_8(if_id_1_out_8), .out_9(if_id_1_out_9));
  splitter splitter_1 (
    .instr(instr_0), ._0_15(splitter_1__0_15), .func(func), ._11_15rd(splitter_1__11_15rd),
    ._16_20rt(splitter_1__16_20rt), ._21_25rs(splitter_1__21_25rs), .op(op));  // open: _0_25
  foward foward_1 (
    .s1_D(s1_D), .s2_D(s2_D), .s1_E(s1_E), .s2_E(s2_E), .des_E(des_E), .tNew_E(tnew_E), .s2_M(s2_M),
    .tNew_M(tnew_M), .des_M(des_M), .tNew_W(tnew_W), .des_W(des_W), .fRsDsel(fRsDsel), .fRtDsel(fRtDsel),
    .fRsEsel(fRsEsel), .fRtEsel(fRtEsel), .fRtMsel(fRtMsel));
  Multiplexer #(.select(2), .width(32), .enable("false")) multiplexer_1 (
    .in0(rd1), .in1(EtoD), .in2(MtoD), .in3({32{1'b0}}), .out(D_CMP_RS), .sel(fRsDsel));
  EXT ext_1 (.in_2(splitter_1__0_15), .out_3(extresult), .in_1(ext_op));
  controller controller_1 (
    .RegWrite(RegWrite_t), .MemWrite(MemWrite_t), .MemRead(MemRead), .MemtoReg(MemtoReg), .Alusrc(Alusrc),
    .Alu_op(Alu_op), .Branch(controller_1_branch), .j_jal(j_jal), .Regdst(Regdst), .ext_op(ext_op), .op(op),
    .funct(func), .jr(jr), .byteAB(byteAB));
  not not_1 (not_1_out, clk);
  D d_1 (.in_1(instr_0), .s2_D(s2_D), .s1_D(s1_D), .tuse1_D(tuse1_D), .tuse2_D(tuse2_D));
  and and_1 (branch_op, controller_1_branch, equal);
  GRF grf_1 (
    .A1(splitter_1__21_25rs), .A2(splitter_1__16_20rt), .A3(regaddr), .WD(regdata), .RD1(rd1), .RD2(rd2),
    .clk(not_1_out), .reset(in_1), .we(regwrite));
  Multiplexer #(.select(2), .width(32), .enable("false")) multiplexer_2 (
    .in0(rd2), .in1(EtoD), .in2(MtoD), .in3({32{1'b0}}), .out(D_CMP_RT), .sel(fRtDsel));
  Comparator #(.width(32)) comparator_1 (.a(D_CMP_RS), .b(D_CMP_RT), .eq(equal));  // open: gt, lt
  Multiplexer #(.select(2), .width(32), .enable("false")) multiplexer_3 (
    .in0(rs_e), .in1(MtoD), .in2(WtoD), .in3({32{1'b0}}), .out(E_ALU_A), .sel(fRsEsel));
  ID_EX id_ex_1 (
    .in_1(clk), .in_2(in_1), .pc_i(if_id_1_pc_o), .pc_o(id_ex_1_pc_o), .RD1_i(D_CMP_RS), .RD1_o(rs_e),
    .pc_4_i(if_id_1_out_8), .pc_4_o(id_ex_1_pc_4_o), .RD2_i(D_CMP_RT), .RD2_o(rt_e), .pc_8_i(if_id_1_out_9),
    .pc_8_o(id_ex_1_pc_8_o), .rs_i(splitter_1__21_25rs), .rt_i(splitter_1__16_20rt), .rt_o(id_ex_1_rt_o),
    .rd_i(splitter_1__11_15rd), .rd_o(id_ex_1_rd_o), .out_30(id_ex_1_out_30), .instr_i(instr_0),
    .in_12(flushE), .RegDst_i(Regdst), .RegDst_o(id_ex_1_regdst_o), .MemWrite_i(MemWrite_t),
    .MemWrite_o(id_ex_1_memwrite_o), .RegWrite_i(RegWrite_t), .RegWrite_o(id_ex_1_regwrite_o),
    .Alusrc_i(Alusrc), .Alusrc_o(id_ex_1_alusrc_o), .memread_i(MemRead), .memread_o(id_ex_1_memread_o),
    .memtoReg_i(MemtoReg), .memtoReg_o(id_ex_1_memtoreg_o), .Alu_op_i(Alu_op), .Alu_op_o(id_ex_1_alu_op_o),
    .out_39(id_ex_1_out_39), .extresult_i(extresult), .byteAB_i(byteAB), .byteAB_o(id_ex_1_byteab_o));  // open: rs_o
  stallU stallu_1 (
    .s1_D(s1_D), .s2_D(s2_D), .tUse1_D(tuse1_D), .tUse2_D(tuse2_D), .des_E(des_E), .tNew_E(tnew_E),
    .tNew_M(tnew_M), .des_M(des_M), .Stall_F(Stall_F), .Stall_D(Stall_D), .flush_E(flushE));
  Multiplexer #(.select(2), .width(32), .enable("false")) multiplexer_4 (
    .in0(rt_e), .in1(MtoD), .in2(WtoD), .in3({32{1'b0}}), .out(E_ALU_B), .sel(fRtEsel));
  Multiplexer #(.width(32), .enable("false")) multiplexer_5 (
    .in0(E_ALU_B), .in1(id_ex_1_out_39), .out(multiplexer_5_out), .sel(id_ex_1_alusrc_o));
  Multiplexer #(.select(2), .width(5), .enable("false")) multiplexer_6 (
    .in0(id_ex_1_rt_o), .in1(id_ex_1_rd_o), .in2({5{1'b1}}), .out(multiplexer_6_out), .sel(id_ex_1_regdst_o));  // open: in3
  E e_1 (
    .in_1(id_ex_1_out_30), .pc_8(id_ex_1_pc_8_o), .extresult(id_ex_1_out_39), .s2_E(s2_E), .s1_E(s1_E),
    .toD(EtoD), .des_E(des_E), .tnew_E(tnew_E));
  Multiplexer #(.width(32), .enable("false")) multiplexer_7 (
    .in0(ex_mem_1_out_17), .in1(WtoD), .out(M_DM_WD), .sel(fRtMsel));
  ALU alu_1 (.RD1(E_ALU_A), .RD2(multiplexer_5_out), .result(alu_1_result), .in_3(id_ex_1_alu_op_o));  // open: equal
  EX_MEM ex_mem_1 (
    .aluresult_i(alu_1_result), .writedata_i(E_ALU_B), .writereg_i(multiplexer_6_out), .pc_i(id_ex_1_pc_o),
    .pc_4_i(id_ex_1_pc_4_o), .pc_8_i(id_ex_1_pc_8_o), .instr_i(id_ex_1_out_30), .out_16(ex_mem_1_out_16),
    .out_17(ex_mem_1_out_17), .out_18(ex_mem_1_out_18), .pc_o(ex_mem_1_pc_o), .pc_4_o(ex_mem_1_pc_4_o),
    .pc_8_o(ex_mem_1_pc_8_o), .out_22(ex_mem_1_out_22), .in_1(clk), .in_2(in_1), .tnew_E(tnew_E),
    .tnew_M(tnew_M), .memread_i(id_ex_1_memread_o), .memread_o(ex_mem_1_memread_o),
    .memtoReg_i(id_ex_1_memtoreg_o), .memtoReg_o(ex_mem_1_memtoreg_o), .MemWrite_i(id_ex_1_memwrite_o),
    .MemWrite_o(ex_mem_1_memwrite_o), .RegWrite_i(id_ex_1_regwrite_o), .RegWrite_o(ex_mem_1_regwrite_o),
    .byte_i(id_ex_1_byteab_o), .byte_o(ex_mem_1_byte_o));
  M m_1 (
    .in_1(ex_mem_1_out_22), .pc_8(ex_mem_1_pc_8_o), .aluresult(ex_mem_1_out_16), .s2_E(s2_M), .s1_E(s1_M),
    .toD(MtoD), .des_E(des_M));
  DM dm_1 (
    .Memaddr(ex_mem_1_out_16), .WD(M_DM_WD), .RD(dm_1_rd), .clk(clk), .in_3(in_1),
    .memwrite(ex_mem_1_memwrite_o), .memread(ex_mem_1_memread_o), .byteable(ex_mem_1_byte_o));
  MEM_WB mem_wb_1 (
    .writereg_i(ex_mem_1_out_18), .aluresult_i(ex_mem_1_out_16), .writedata_i(ex_mem_1_out_17),
    .readdata_i(dm_1_rd), .pc_i(ex_mem_1_pc_o), .pc_4_i(ex_mem_1_pc_4_o), .pc_8_i(ex_mem_1_pc_8_o),
    .instr_i(ex_mem_1_out_22), .memaddr(ex_mem_1_out_16), .memdata(M_DM_WD), .memwrite(ex_mem_1_memwrite_o),
    .out_24(regaddr), .out_17(mem_wb_1_out_17), .out_19(mem_wb_1_out_19), .pc_8_o(mem_wb_1_pc_8_o),
    .out_23(mem_wb_1_out_23), .out_25({memaddr_o[31:7], memaddr, memaddr_o[1:0]}), .out_26(memdata),
    .out_27(memwrite), .in_1(clk), .in_2(in_1), .tnew_M(tnew_M), .tnew_W(tnew_W),
    .RegWrite_i(ex_mem_1_regwrite_o), .RegWrite_o(regwrite), .memtoReg_i(ex_mem_1_memtoreg_o),
    .memtoReg_o(mem_wb_1_memtoreg_o));  // open: out_18, pc_o, pc_4_o
  W w_1 (
    .in_1(mem_wb_1_out_23), .RD(mem_wb_1_out_19), .pc_8(mem_wb_1_pc_8_o), .aluresult(mem_wb_1_out_17),
    .toD(WtoD), .des_E(des_W));
  Multiplexer #(.select(2), .width(32), .enable("false")) multiplexer_8 (
    .in0(mem_wb_1_out_17), .in1(mem_wb_1_out_19), .in2(mem_wb_1_pc_8_o), .out(regdata),
    .sel(mem_wb_1_memtoreg_o));  // open: in3

  // Other names for the same wires on the sheet: memaddr_o[6:2] = memaddr; memdata_o[31:0] = memdata;
  //   memwrite_o = memwrite; regwrite_o = regwrite; reset = in_1
endmodule

module controller (
  input  [5:0] op,
  input  [5:0] funct,
  output RegWrite,
  output MemWrite,
  output MemRead,
  output [1:0] MemtoReg,
  output Alusrc,
  output [2:0] Alu_op,
  output Branch,
  output j_jal,
  output jr,
  output [1:0] Regdst,
  output [1:0] ext_op,
  output byteAB
);

  wire addiu, addu, bne, j, lb, lh, lw, nop, ori, sh, subu, sw;

  useFunc usefunc_1 (
    .out_3(lw), .out_4(sw), .out_5(ori), .out_6(j), .out_7(Branch), .out_8(ext_op[1]), .out_9(addu),
    .out_10(subu), .out_11(nop), .op(op), .funct(funct), .out_12(jr), .out_13(MemtoReg[1]), .out_14(addiu),
    .out_15(byteAB), .out_16(sh), .out_17(lb), .out_18(lh), .out_19(bne));
  or or_1 (MemRead, lw, byteAB, sh, lb, lh);
  buf or_2 (MemtoReg[0], lw);  // OR_Gate
  or or_3 (MemWrite, sw, byteAB, sh);
  or or_4 (Alu_op[0], subu, Branch);
  buf or_5 (Alu_op[1], ori);  // OR_Gate
  or or_6 (j_jal, j, MemtoReg[1]);
  or or_7 (Regdst[0], addu, subu);
  or or_8 (ext_op[0], addiu, Branch, lw, sw, byteAB);
  or or_9 (RegWrite, lw, ext_op[1], addu, subu, ori, addiu, MemtoReg[1]);
  or or_10 (Alusrc, ext_op[1], addiu, ori, lw, byteAB, sw);

  assign Alu_op[2] = 1'b0;
  assign Regdst[1] = MemtoReg[1];

  // Other names for the same wires on the sheet: beq = Branch; lui = ext_op[1]; jal = MemtoReg[1]; sb = byteAB
endmodule

module useFunc (
  input  [5:0] funct,
  input  [5:0] op,
  output out_3,
  output out_4,
  output out_5,
  output out_6,
  output out_7,
  output out_8,
  output out_9,
  output out_10,
  output out_11,
  output out_12,
  output out_13,
  output out_14,
  output out_15,
  output out_16,
  output out_17,
  output out_18,
  output out_19
);

  wire not_1_out, not_2_out, not_3_out, not_4_out, not_5_out, not_6_out, not_7_out, not_8_out, not_9_out,
       not_10_out, not_11_out, not_12_out, R;

  not not_1 (not_1_out, op[5]);
  not not_2 (not_2_out, op[4]);
  not not_3 (not_3_out, op[2]);
  not not_4 (not_4_out, op[3]);
  not not_5 (not_5_out, op[1]);
  not not_6 (not_6_out, op[0]);
  and and_1 (out_3, op[5], not_2_out, not_4_out, not_3_out, op[1], op[0]);
  and and_2 (out_4, op[5], not_2_out, op[3], not_3_out, op[1], op[0]);
  and and_3 (R, not_1_out, not_2_out, not_4_out, not_3_out, not_5_out, not_6_out);
  and and_4 (out_5, not_1_out, not_2_out, op[3], op[2], not_5_out, op[0]);
  and and_5 (out_6, not_1_out, not_2_out, not_4_out, not_3_out, op[1], not_6_out);
  and and_6 (out_7, not_1_out, not_2_out, not_4_out, op[2], not_5_out, not_6_out);
  and and_7 (out_8, not_1_out, not_2_out, op[3], op[2], op[1], op[0]);
  and and_8 (out_13, not_1_out, not_2_out, not_4_out, not_3_out, op[1], op[0]);
  and and_9 (out_15, op[5], not_2_out, op[3], not_3_out, not_5_out, not_6_out);
  and and_10 (out_14, not_1_out, not_2_out, op[3], not_3_out, not_5_out, op[0]);
  and and_11 (out_16, op[5], not_2_out, op[3], not_3_out, not_5_out, op[0]);
  and and_12 (out_17, op[5], not_2_out, not_4_out, not_3_out, not_5_out, not_6_out);
  and and_13 (out_18, op[5], not_2_out, not_4_out, not_3_out, not_5_out, op[0]);
  and and_14 (out_19, not_1_out, not_2_out, not_4_out, op[2], not_5_out, op[0]);
  not not_7 (not_7_out, funct[5]);
  not not_8 (not_8_out, funct[4]);
  not not_9 (not_9_out, funct[2]);
  not not_10 (not_10_out, funct[3]);
  not not_11 (not_11_out, funct[1]);
  not not_12 (not_12_out, funct[0]);
  and and_15 (out_9, R, funct[5], not_8_out, not_10_out, not_9_out, not_11_out, funct[0]);
  and and_16 (out_10, R, funct[5], not_8_out, not_10_out, not_9_out, funct[1], funct[0]);
  and and_17 (out_11, R, not_7_out, not_8_out, not_10_out, not_9_out, not_11_out, not_12_out);
  and and_18 (out_12, R, not_7_out, not_8_out, funct[3], not_9_out, not_11_out, not_12_out);

  // Other names for the same wires on the sheet: addiu = out_14; addu = out_9; beq = out_7; bne = out_19; j = out_6;
  //   jal = out_13; jr = out_12; lb = out_17; lh = out_18; lui = out_8; lw = out_3; nop = out_11; ori = out_5;
  //   sb = out_15; sh = out_16; subu = out_10; sw = out_4
endmodule

module ALU (
  input  [31:0] RD1,
  input  [31:0] RD2,
  input  [2:0] in_3,
  output [31:0] result,
  output equal
);

  wire [31:0] adder_1_out, or_1_out, subtractor_1_out;

  Adder #(.width(32)) adder_1 (.a(RD1), .b(RD2), .out(adder_1_out));  // open: cin, cout
  Subtractor #(.width(32)) subtractor_1 (.a(RD1), .b(RD2), .out(subtractor_1_out));  // open: bin, bout
  assign or_1_out = RD1 | RD2;  // OR_Gate or_1, 32 bits wide
  Multiplexer #(.select(3), .width(32), .enable("false")) multiplexer_1 (
    .in0(adder_1_out), .in1(subtractor_1_out), .in2(or_1_out), .out(result), .sel(in_3));  // open: in3, in4, in5, in6, in7
  Comparator #(.width(32)) comparator_1 (.a(result), .b({32{1'b0}}), .eq(equal));  // open: gt, lt
endmodule

module IF_ID (
  input  in_1,
  input  in_2,
  input  [31:0] instr_i,
  input  [31:0] pc_i,
  input  in_5,
  output [31:0] instr_o,
  output [31:0] pc_o,
  output [31:0] out_8,
  output [31:0] out_9
);

  wire clk_prime, not_1_out, not_2_out;

  not not_1 (not_1_out, in_5);
  not not_2 (not_2_out, in_5);
  buf and_1 (clk_prime, in_1);  // AND_Gate
  Register #(.width(32)) register_1 (.D(instr_i), .en(not_1_out), .Q(instr_o), .clk(clk_prime), .clr(in_2));
  Register #(.width(32)) register_2 (.D(pc_i), .en(not_2_out), .Q(pc_o), .clk(clk_prime), .clr(in_2));
  Adder #(.width(32)) adder_1 (.a(pc_o), .b(32'h4), .out(out_8));  // open: cin, cout
  Adder #(.width(32)) adder_2 (.a(pc_o), .b(32'h8), .out(out_9));  // open: cin, cout

  // Other names for the same wires on the sheet: clk = in_1; F_D_stall = in_5; reset = in_2
endmodule

module ID_EX (
  input  in_1,
  input  in_2,
  input  [31:0] pc_i,
  input  [31:0] RD1_i,
  input  [31:0] pc_4_i,
  input  [31:0] RD2_i,
  input  [31:0] pc_8_i,
  input  [4:0] rs_i,
  input  [4:0] rt_i,
  input  [4:0] rd_i,
  input  [31:0] instr_i,
  input  in_12,
  input  byteAB_i,
  input  [1:0] RegDst_i,
  input  MemWrite_i,
  input  RegWrite_i,
  input  Alusrc_i,
  input  memread_i,
  input  [1:0] memtoReg_i,
  input  [2:0] Alu_op_i,
  input  [31:0] extresult_i,
  output [31:0] pc_o,
  output [31:0] RD1_o,
  output [31:0] pc_4_o,
  output [31:0] RD2_o,
  output [31:0] pc_8_o,
  output [4:0] rs_o,
  output [4:0] rt_o,
  output [4:0] rd_o,
  output [31:0] out_30,
  output byteAB_o,
  output [1:0] RegDst_o,
  output MemWrite_o,
  output RegWrite_o,
  output Alusrc_o,
  output memread_o,
  output [1:0] memtoReg_o,
  output [2:0] Alu_op_o,
  output [31:0] out_39
);

  wire multiplexer_7_out, multiplexer_9_out, multiplexer_10_out, multiplexer_11_out, multiplexer_12_out;
  wire [1:0] multiplexer_8_out, multiplexer_15_out;
  wire [2:0] multiplexer_13_out;
  wire [4:0] multiplexer_3_out, multiplexer_4_out, multiplexer_5_out;
  wire [31:0] multiplexer_1_out, multiplexer_2_out, multiplexer_6_out, multiplexer_14_out,
       multiplexer_16_out, multiplexer_17_out, multiplexer_18_out;

  Multiplexer #(.width(32), .enable("false")) multiplexer_1 (
    .in0(RD1_i), .in1({32{1'b0}}), .out(multiplexer_1_out), .sel(in_12));
  Multiplexer #(.width(32), .enable("false")) multiplexer_2 (
    .in0(RD2_i), .in1({32{1'b0}}), .out(multiplexer_2_out), .sel(in_12));
  Multiplexer #(.width(5), .enable("false")) multiplexer_3 (
    .in0(rs_i), .in1({5{1'b0}}), .out(multiplexer_3_out), .sel(in_12));
  Multiplexer #(.width(5), .enable("false")) multiplexer_4 (
    .in0(rt_i), .in1({5{1'b0}}), .out(multiplexer_4_out), .sel(in_12));
  Multiplexer #(.width(5), .enable("false")) multiplexer_5 (
    .in0(rd_i), .in1({5{1'b0}}), .out(multiplexer_5_out), .sel(in_12));
  Multiplexer #(.width(32), .enable("false")) multiplexer_6 (
    .in0(instr_i), .in1({32{1'b0}}), .out(multiplexer_6_out), .sel(in_12));
  Multiplexer #(.enable("false")) multiplexer_7 (.in0(byteAB_i), .in1(1'b0), .out(multiplexer_7_out), .sel(in_12));
  Multiplexer #(.width(2), .enable("false")) multiplexer_8 (
    .in0(RegDst_i), .in1(2'b00), .out(multiplexer_8_out), .sel(in_12));
  Multiplexer #(.enable("false")) multiplexer_9 (.in0(MemWrite_i), .in1(1'b0), .out(multiplexer_9_out), .sel(in_12));
  Multiplexer #(.enable("false")) multiplexer_10 (.in0(RegWrite_i), .in1(1'b0), .out(multiplexer_10_out), .sel(in_12));
  Multiplexer #(.enable("false")) multiplexer_11 (.in0(Alusrc_i), .in1(1'b0), .out(multiplexer_11_out), .sel(in_12));
  Multiplexer #(.enable("false")) multiplexer_12 (.in0(memread_i), .in1(1'b0), .out(multiplexer_12_out), .sel(in_12));
  Multiplexer #(.width(3), .enable("false")) multiplexer_13 (
    .in0(Alu_op_i), .in1(3'b000), .out(multiplexer_13_out), .sel(in_12));
  Multiplexer #(.width(32), .enable("false")) multiplexer_14 (
    .in0(extresult_i), .in1({32{1'b0}}), .out(multiplexer_14_out), .sel(in_12));
  Register #(.width(32)) register_1 (.D(multiplexer_1_out), .Q(RD1_o), .clk(in_1), .clr(in_2));  // open: en
  Register #(.width(32)) register_2 (.D(multiplexer_2_out), .Q(RD2_o), .clk(in_1), .clr(in_2));  // open: en
  Register #(.width(5)) register_3 (.D(multiplexer_3_out), .Q(rs_o), .clk(in_1), .clr(in_2));  // open: en
  Register #(.width(5)) register_4 (.D(multiplexer_4_out), .Q(rt_o), .clk(in_1), .clr(in_2));  // open: en
  Register #(.width(5)) register_5 (.D(multiplexer_5_out), .Q(rd_o), .clk(in_1), .clr(in_2));  // open: en
  Register #(.width(32)) register_6 (.D(multiplexer_6_out), .Q(out_30), .clk(in_1), .clr(in_2));  // open: en
  Multiplexer #(.width(2), .enable("false")) multiplexer_15 (
    .in0(memtoReg_i), .in1(2'b00), .out(multiplexer_15_out), .sel(in_12));
  Register #(.width(32)) register_7 (.D(multiplexer_14_out), .Q(out_39), .clk(in_1), .clr(in_2));  // open: en
  Register #(.width(1)) register_8 (.D(multiplexer_7_out), .Q(byteAB_o), .clk(in_1), .clr(in_2));  // open: en
  Register #(.width(2)) register_9 (.D(multiplexer_8_out), .Q(RegDst_o), .clk(in_1), .clr(in_2));  // open: en
  Register #(.width(1)) register_10 (.D(multiplexer_9_out), .Q(MemWrite_o), .clk(in_1), .clr(in_2));  // open: en
  Register #(.width(1)) register_11 (.D(multiplexer_10_out), .Q(RegWrite_o), .clk(in_1), .clr(in_2));  // open: en
  Register #(.width(1)) register_12 (.D(multiplexer_11_out), .Q(Alusrc_o), .clk(in_1), .clr(in_2));  // open: en
  Register #(.width(1)) register_13 (.D(multiplexer_12_out), .Q(memread_o), .clk(in_1), .clr(in_2));  // open: en
  Register #(.width(2)) register_14 (.D(multiplexer_15_out), .Q(memtoReg_o), .clk(in_1), .clr(in_2));  // open: en
  Register #(.width(3)) register_15 (.D(multiplexer_13_out), .Q(Alu_op_o), .clk(in_1), .clr(in_2));  // open: en
  Multiplexer #(.width(32), .enable("false")) multiplexer_16 (
    .in0(pc_i), .in1({32{1'b0}}), .out(multiplexer_16_out), .sel(in_12));
  Multiplexer #(.width(32), .enable("false")) multiplexer_17 (
    .in0(pc_4_i), .in1({32{1'b0}}), .out(multiplexer_17_out), .sel(in_12));
  Multiplexer #(.width(32), .enable("false")) multiplexer_18 (
    .in0(pc_8_i), .in1({32{1'b0}}), .out(multiplexer_18_out), .sel(in_12));
  Register #(.width(32)) register_16 (.D(multiplexer_16_out), .Q(pc_o), .clk(in_1), .clr(in_2));  // open: en
  Register #(.width(32)) register_17 (.D(multiplexer_17_out), .Q(pc_4_o), .clk(in_1), .clr(in_2));  // open: en
  Register #(.width(32)) register_18 (.D(multiplexer_18_out), .Q(pc_8_o), .clk(in_1), .clr(in_2));  // open: en

  // Other names for the same wires on the sheet: clk = in_1; clk_prime = in_1; flush = in_12; Reset = in_2
endmodule

module EX_MEM (
  input  in_1,
  input  in_2,
  input  [31:0] aluresult_i,
  input  [31:0] writedata_i,
  input  [4:0] writereg_i,
  input  [31:0] pc_i,
  input  [31:0] pc_4_i,
  input  [31:0] pc_8_i,
  input  [31:0] instr_i,
  input  [3:0] tnew_E,
  input  byte_i,
  input  MemWrite_i,
  input  RegWrite_i,
  input  memread_i,
  input  [1:0] memtoReg_i,
  output [31:0] out_16,
  output [31:0] out_17,
  output [4:0] out_18,
  output [31:0] pc_o,
  output [31:0] pc_4_o,
  output [31:0] pc_8_o,
  output [31:0] out_22,
  output [3:0] tnew_M,
  output byte_o,
  output MemWrite_o,
  output RegWrite_o,
  output memread_o,
  output [1:0] memtoReg_o
);

  wire comparator_1_eq;
  wire [3:0] register_1_q, subtractor_1_out;

  Register #(.width(4)) register_1 (.D(tnew_E), .Q(register_1_q), .clk(in_1), .clr(in_2));  // open: en
  Register #(.width(32)) register_2 (.D(aluresult_i), .Q(out_16), .clk(in_1), .clr(in_2));  // open: en
  Register #(.width(32)) register_3 (.D(writedata_i), .Q(out_17), .clk(in_1), .clr(in_2));  // open: en
  Register #(.width(5)) register_4 (.D(writereg_i), .Q(out_18), .clk(in_1), .clr(in_2));  // open: en
  Register #(.width(32)) register_5 (.D(pc_i), .Q(pc_o), .clk(in_1), .clr(in_2));  // open: en
  Register #(.width(32)) register_6 (.D(pc_4_i), .Q(pc_4_o), .clk(in_1), .clr(in_2));  // open: en
  Register #(.width(32)) register_7 (.D(pc_8_i), .Q(pc_8_o), .clk(in_1), .clr(in_2));  // open: en
  Register #(.width(32)) register_8 (.D(instr_i), .Q(out_22), .clk(in_1), .clr(in_2));  // open: en
  Comparator #(.width(4)) comparator_1 (.a(register_1_q), .b(4'b0000), .eq(comparator_1_eq));  // open: gt, lt
  Subtractor #(.width(4)) subtractor_1 (.a(register_1_q), .b(4'b0001), .out(subtractor_1_out));  // open: bin, bout
  Register #(.width(1)) register_9 (.D(byte_i), .Q(byte_o), .clk(in_1), .clr(in_2));  // open: en
  Register #(.width(1)) register_10 (.D(MemWrite_i), .Q(MemWrite_o), .clk(in_1), .clr(in_2));  // open: en
  Register #(.width(1)) register_11 (.D(RegWrite_i), .Q(RegWrite_o), .clk(in_1), .clr(in_2));  // open: en
  Register #(.width(1)) register_12 (.D(memread_i), .Q(memread_o), .clk(in_1), .clr(in_2));  // open: en
  Register #(.width(2)) register_13 (.D(memtoReg_i), .Q(memtoReg_o), .clk(in_1), .clr(in_2));  // open: en
  Multiplexer #(.width(4), .enable("false")) multiplexer_1 (
    .in0(subtractor_1_out), .in1(register_1_q), .out(tnew_M), .sel(comparator_1_eq));

  // Other names for the same wires on the sheet: clk = in_1; clk_prime = in_1; Reset = in_2
endmodule

module MEM_WB (
  input  in_1,
  input  in_2,
  input  [31:0] aluresult_i,
  input  [31:0] writedata_i,
  input  [31:0] readdata_i,
  input  [31:0] pc_i,
  input  [31:0] pc_4_i,
  input  [31:0] pc_8_i,
  input  [31:0] instr_i,
  input  [4:0] writereg_i,
  input  [31:0] memaddr,
  input  [31:0] memdata,
  input  memwrite,
  input  [3:0] tnew_M,
  input  RegWrite_i,
  input  [1:0] memtoReg_i,
  output [31:0] out_17,
  output [31:0] out_18,
  output [31:0] out_19,
  output [31:0] pc_o,
  output [31:0] pc_4_o,
  output [31:0] pc_8_o,
  output [31:0] out_23,
  output [4:0] out_24,
  output [31:0] out_25,
  output [31:0] out_26,
  output out_27,
  output [3:0] tnew_W,
  output RegWrite_o,
  output [1:0] memtoReg_o
);

  wire comparator_1_eq;
  wire [3:0] register_1_q, subtractor_1_out;

  Register #(.width(4)) register_1 (.D(tnew_M), .Q(register_1_q), .clk(in_1), .clr(in_2));  // open: en
  Register #(.width(32)) register_2 (.D(aluresult_i), .Q(out_17), .clk(in_1), .clr(in_2));  // open: en
  Register #(.width(32)) register_3 (.D(writedata_i), .Q(out_18), .clk(in_1), .clr(in_2));  // open: en
  Register #(.width(32)) register_4 (.D(readdata_i), .Q(out_19), .clk(in_1), .clr(in_2));  // open: en
  Register #(.width(32)) register_5 (.D(pc_i), .Q(pc_o), .clk(in_1), .clr(in_2));  // open: en
  Register #(.width(32)) register_6 (.D(pc_4_i), .Q(pc_4_o), .clk(in_1), .clr(in_2));  // open: en
  Register #(.width(32)) register_7 (.D(pc_8_i), .Q(pc_8_o), .clk(in_1), .clr(in_2));  // open: en
  Register #(.width(32)) register_8 (.D(instr_i), .Q(out_23), .clk(in_1), .clr(in_2));  // open: en
  Register #(.width(5)) register_9 (.D(writereg_i), .Q(out_24), .clk(in_1), .clr(in_2));  // open: en
  Register #(.width(32)) register_10 (.D(memaddr), .Q(out_25), .clk(in_1), .clr(in_2));  // open: en
  Register #(.width(32)) register_11 (.D(memdata), .Q(out_26), .clk(in_1), .clr(in_2));  // open: en
  Register #(.width(1)) register_12 (.D(memwrite), .Q(out_27), .clk(in_1), .clr(in_2));  // open: en
  Subtractor #(.width(4)) subtractor_1 (.a(register_1_q), .b(4'b0001), .out(subtractor_1_out));  // open: bin, bout
  Comparator #(.width(4)) comparator_1 (.a(register_1_q), .b(4'b0000), .eq(comparator_1_eq));  // open: gt, lt
  Register #(.width(1)) register_13 (.D(RegWrite_i), .Q(RegWrite_o), .clk(in_1), .clr(in_2));  // open: en
  Register #(.width(2)) register_14 (.D(memtoReg_i), .Q(memtoReg_o), .clk(in_1), .clr(in_2));  // open: en
  Multiplexer #(.width(4), .enable("false")) multiplexer_1 (
    .in0(subtractor_1_out), .in1(register_1_q), .out(tnew_W), .sel(comparator_1_eq));

  // Other names for the same wires on the sheet: clk = in_1; clk_prime = in_1; Reset = in_2
endmodule

module splitter (
  input  [31:0] instr,
  output [15:0] _0_15,
  output [25:0] _0_25,
  output [5:0] func,
  output [4:0] _11_15rd,
  output [4:0] _16_20rt,
  output [4:0] _21_25rs,
  output [5:0] op
);


  assign _0_15 = instr[15:0];
  assign _0_25 = instr[25:0];
  assign _11_15rd = instr[15:11];
  assign _16_20rt = instr[20:16];
  assign _21_25rs = instr[25:21];
  assign func = instr[5:0];
  assign op = instr[31:26];
endmodule

module IF (
  input  in_1,
  input  in_2,
  input  [31:0] npc,
  input  in_4,
  output [31:0] instr,
  output [31:0] pc
);

  wire comparator_1_eq, not_1_out;
  wire [31:0] pc_q, subtractor_1_out;

  not not_1 (not_1_out, in_4);
  Register #(.width(32)) u_pc (.D(npc), .en(not_1_out), .Q(pc_q), .clk(in_1), .clr(in_2));
  Comparator #(.width(32)) comparator_1 (.a({32{1'b0}}), .b(pc_q), .eq(comparator_1_eq));  // open: gt, lt
  Multiplexer #(.width(32), .enable("false")) multiplexer_1 (
    .in0(pc_q), .in1(32'h3000), .out(pc), .sel(comparator_1_eq));
  Subtractor #(.width(32)) subtractor_1 (.a(pc), .b(32'h3000), .out(subtractor_1_out));  // open: bin, bout
  ROM #(.addrWidth(10), .dataWidth(32)) rom_1 (.addr(subtractor_1_out[11:2]), .data(instr));  // open: sel

  // Other names for the same wires on the sheet: clook = in_1; F_D_stall = in_4; reset = in_2

  // Notes on the sheet:
  //   contents of rom_1 (hex, n*v repeats v):
  //   36100000 36310003 36f70003 ae110000 8e120000 12f20001 36530004 ae130004
endmodule

module DM (
  input  byteable,
  input  clk,
  input  in_3,
  input  [31:0] Memaddr,
  input  [31:0] WD,
  input  memwrite,
  input  memread,
  output [31:0] RD
);

  wire [4:0] bit_extender_1_out, bitselector_1_out, shifter_2_out;
  wire [7:0] \byte ;
  wire [31:0] and_1_out, and_2_out, and_3_out, and_4_out, bit_extender_2_out, multiplexer_1_out,
       multiplexer_2_out, or_1_out, shifter_1_out, shifter_3_out;

  assign bit_extender_1_out = {{3{1'b0}}, Memaddr[1:0]};  // Bit_Extender bit_extender_1
  BitSelector #(.width(32), .group(5)) bitselector_1 (.in(shifter_1_out), .out(bitselector_1_out), .sel(3'b000));
  Shifter #(.width(32), .shift("lr")) shifter_1 (.in(Memaddr), .\dist (5'b00010), .out(shifter_1_out));
  BitSelector #(.width(32), .group(8)) bitselector_2 (.in(WD), .out(\byte ), .sel(Memaddr[1:0]));
  assign bit_extender_2_out = {{24{1'b0}}, \byte };  // Bit_Extender bit_extender_2
  Shifter #(.width(5)) shifter_2 (.in(bit_extender_1_out), .\dist (3'b011), .out(shifter_2_out));
  Shifter #(.width(32)) shifter_3 (.in(bit_extender_2_out), .\dist (shifter_2_out), .out(shifter_3_out));
  assign or_1_out = shifter_3_out | multiplexer_2_out;  // OR_Gate or_1, 32 bits wide
  Multiplexer #(.width(32), .enable("false")) multiplexer_1 (
    .in0(WD), .in1(or_1_out), .out(multiplexer_1_out), .sel(byteable));
  Multiplexer #(.select(2), .width(32), .enable("false")) multiplexer_2 (
    .in0(and_1_out), .in1(and_2_out), .in2(and_3_out), .in3(and_4_out), .out(multiplexer_2_out),
    .sel(Memaddr[1:0]));
  RAM #(.addrWidth(5), .dataWidth(32), .bus("separate")) ram_1 (
    .addr(bitselector_1_out), .din(multiplexer_1_out), .data(RD), .str(memwrite), .clk(clk), .ld(memread),
    .clr(in_3));  // open: sel
  assign and_1_out = RD & 32'hffffff00;  // AND_Gate and_1, 32 bits wide
  assign and_2_out = RD & 32'hffff00ff;  // AND_Gate and_2, 32 bits wide
  assign and_3_out = RD & 32'hff00ffff;  // AND_Gate and_3, 32 bits wide
  assign and_4_out = RD & 32'hffffff;  // AND_Gate and_4, 32 bits wide

  // Other names for the same wires on the sheet: byteaddr[1:0] = Memaddr[1:0]
endmodule

module npc (
  input  branch_op,
  input  j_jal,
  input  jr,
  input  [31:0] pc,
  input  [31:0] instr,
  input  [31:0] extresult,
  input  [31:0] RD1,
  output [31:0] npc
);

  wire [31:0] adder_2_out, beq, multiplexer_1_out, multiplexer_2_out, pc_4;

  Shifter #(.width(32)) shifter_1 (.in(extresult), .\dist (5'b00010), .out(beq));
  Adder #(.width(32)) adder_1 (.a(pc), .b(32'h4), .out(pc_4));  // open: cin, cout
  Adder #(.width(32)) adder_2 (.a(pc), .b(beq), .out(adder_2_out));  // open: cin, cout
  Multiplexer #(.width(32), .enable("false")) multiplexer_1 (
    .in0(pc_4), .in1(adder_2_out), .out(multiplexer_1_out), .sel(branch_op));
  Multiplexer #(.width(32), .enable("false")) multiplexer_2 (
    .in0(multiplexer_1_out), .in1({pc[31:28], instr[25:0], 2'b00}), .out(multiplexer_2_out), .sel(j_jal));
  Multiplexer #(.width(32), .enable("false")) multiplexer_3 (.in0(multiplexer_2_out), .in1(RD1), .out(npc), .sel(jr));

  // Other names for the same wires on the sheet: j_jalim[31:2] = {pc[31:28], instr[25:0]}
endmodule

module GRF (
  input  [4:0] A1,
  input  clk,
  input  reset,
  input  we,
  input  [4:0] A2,
  input  [4:0] A3,
  input  [31:0] WD,
  output [31:0] RD1,
  output [31:0] RD2
);

  wire [31:0] I0, I1, I2, I3, I4, I5, I6, I7, I8, I9, I10, I11, I12, I13, I14, I15, I16, I17, I18, I19, I20,
       I21, I22, I23, I24, I25, I26, I27, I28, I29, I30, I31, O0, O1, O2, O3, O4, O5, O6, O7, O8, O9, O10,
       O11, O12, O13, O14, O15, O16, O17, O18, O19, O20, O21, O22, O23, O24, O25, O26, O27, O28, O29, O30,
       O31;

  Demultiplexer #(.select(5), .width(32), .tristate("true")) demultiplexer_1 (
    .out0(I0), .out1(I1), .out2(I2), .out3(I3), .out4(I4), .out5(I5), .out6(I6), .out7(I7), .out8(I8),
    .out9(I9), .out10(I10), .out11(I11), .out12(I12), .out13(I13), .out14(I14), .out15(I15), .out16(I16),
    .out17(I17), .out18(I18), .out19(I19), .out20(I20), .out21(I21), .out22(I22), .out23(I23), .out24(I24),
    .out25(I25), .out26(I26), .out27(I27), .out28(I28), .out29(I29), .out30(I30), .out31(I31), .in(WD),
    .sel(A3));  // open: en
  Multiplexer #(.select(5), .width(32)) multiplexer_1 (
    .in0(O0), .in1(O1), .in2(O2), .in3(O3), .in4(O4), .in5(O5), .in6(O6), .in7(O7), .in8(O8), .in9(O9),
    .in10(O10), .in11(O11), .in12(O12), .in13(O13), .in14(O14), .in15(O15), .in16(O16), .in17(O17),
    .in18(O18), .in19(O19), .in20(O20), .in21(O21), .in22(O22), .in23(O23), .in24(O24), .in25(O25),
    .in26(O26), .in27(O27), .in28(O28), .in29(O29), .in30(O30), .in31(O31), .out(RD2), .sel(A2));  // open: en
  Multiplexer #(.select(5), .width(32)) multiplexer_2 (
    .in0(O0), .in1(O1), .in2(O2), .in3(O3), .in4(O4), .in5(O5), .in6(O6), .in7(O7), .in8(O8), .in9(O9),
    .in10(O10), .in11(O11), .in12(O12), .in13(O13), .in14(O14), .in15(O15), .in16(O16), .in17(O17),
    .in18(O18), .in19(O19), .in20(O20), .in21(O21), .in22(O22), .in23(O23), .in24(O24), .in25(O25),
    .in26(O26), .in27(O27), .in28(O28), .in29(O29), .in30(O30), .in31(O31), .out(RD1), .sel(A1));  // open: en
  Register #(.width(32)) register_1 (.D({32{1'b0}}), .en(we), .Q(O0), .clk(clk), .clr(reset));
  Register #(.width(32)) register_2 (.D(I8), .en(we), .Q(O8), .clk(clk), .clr(reset));
  Register #(.width(32)) register_3 (.D(I16), .en(we), .Q(O16), .clk(clk), .clr(reset));
  Register #(.width(32)) register_4 (.D(I24), .en(we), .Q(O24), .clk(clk), .clr(reset));
  Register #(.width(32)) register_5 (.D(I1), .en(we), .Q(O1), .clk(clk), .clr(reset));
  Register #(.width(32)) register_6 (.D(I9), .en(we), .Q(O9), .clk(clk), .clr(reset));
  Register #(.width(32)) register_7 (.D(I17), .en(we), .Q(O17), .clk(clk), .clr(reset));
  Register #(.width(32)) register_8 (.D(I25), .en(we), .Q(O25), .clk(clk), .clr(reset));
  Register #(.width(32)) register_9 (.D(I2), .en(we), .Q(O2), .clk(clk), .clr(reset));
  Register #(.width(32)) register_10 (.D(I10), .en(we), .Q(O10), .clk(clk), .clr(reset));
  Register #(.width(32)) register_11 (.D(I18), .en(we), .Q(O18), .clk(clk), .clr(reset));
  Register #(.width(32)) register_12 (.D(I26), .en(we), .Q(O26), .clk(clk), .clr(reset));
  Register #(.width(32)) register_13 (.D(I3), .en(we), .Q(O3), .clk(clk), .clr(reset));
  Register #(.width(32)) register_14 (.D(I11), .en(we), .Q(O11), .clk(clk), .clr(reset));
  Register #(.width(32)) register_15 (.D(I19), .en(we), .Q(O19), .clk(clk), .clr(reset));
  Register #(.width(32)) register_16 (.D(I27), .en(we), .Q(O27), .clk(clk), .clr(reset));
  Register #(.width(32)) register_17 (.D(I4), .en(we), .Q(O4), .clk(clk), .clr(reset));
  Register #(.width(32)) register_18 (.D(I12), .en(we), .Q(O12), .clk(clk), .clr(reset));
  Register #(.width(32)) register_19 (.D(I20), .en(we), .Q(O20), .clk(clk), .clr(reset));
  Register #(.width(32)) register_20 (.D(I28), .en(we), .Q(O28), .clk(clk), .clr(reset));
  Register #(.width(32)) register_21 (.D(I5), .en(we), .Q(O5), .clk(clk), .clr(reset));
  Register #(.width(32)) register_22 (.D(I13), .en(we), .Q(O13), .clk(clk), .clr(reset));
  Register #(.width(32)) register_23 (.D(I21), .en(we), .Q(O21), .clk(clk), .clr(reset));
  Register #(.width(32)) register_24 (.D(I29), .en(we), .Q(O29), .clk(clk), .clr(reset));
  Register #(.width(32)) register_25 (.D(I6), .en(we), .Q(O6), .clk(clk), .clr(reset));
  Register #(.width(32)) register_26 (.D(I14), .en(we), .Q(O14), .clk(clk), .clr(reset));
  Register #(.width(32)) register_27 (.D(I22), .en(we), .Q(O22), .clk(clk), .clr(reset));
  Register #(.width(32)) register_28 (.D(I30), .en(we), .Q(O30), .clk(clk), .clr(reset));
  Register #(.width(32)) register_29 (.D(I7), .en(we), .Q(O7), .clk(clk), .clr(reset));
  Register #(.width(32)) register_30 (.D(I15), .en(we), .Q(O15), .clk(clk), .clr(reset));
  Register #(.width(32)) register_31 (.D(I23), .en(we), .Q(O23), .clk(clk), .clr(reset));
  Register #(.width(32)) register_32 (.D(I31), .en(we), .Q(O31), .clk(clk), .clr(reset));
endmodule

module D (
  input  [31:0] in_1,
  output [4:0] s2_D,
  output [4:0] s1_D,
  output [1:0] tuse1_D,
  output [1:0] tuse2_D
);

  wire addiu, addu, beq, bne, j, jal, jr, lb, lh, lui, lw, nop, or_1_out, or_2_out, or_3_out, or_4_out,
       or_5_out, or_6_out, or_7_out, ori, s1_D_out, s2_D_out, sb, sh, subu, sw, tuse1_D_out;
  wire [1:0] bit_extender_1_out;
  wire [4:0] multiplexer_5_out, multiplexer_6_out, splitter_1__11_15rd, splitter_1__16_20rt,
       splitter_1__21_25rs;
  wire [5:0] splitter_1_func, splitter_1_op;

  splitter splitter_1 (
    .instr(in_1), .func(splitter_1_func), ._11_15rd(splitter_1__11_15rd), ._16_20rt(splitter_1__16_20rt),
    ._21_25rs(splitter_1__21_25rs), .op(splitter_1_op));  // open: _0_15, _0_25
  useFunc usefunc_1 (
    .out_3(lw), .out_4(sw), .out_5(ori), .out_6(j), .out_7(beq), .out_8(lui), .out_9(addu), .out_10(subu),
    .out_11(nop), .op(splitter_1_op), .funct(splitter_1_func), .out_12(jr), .out_13(jal), .out_14(addiu),
    .out_15(sb), .out_16(sh), .out_17(lb), .out_18(lh), .out_19(bne));
  or or_1 (or_1_out, lw, sw, sb, sh, lb, lh);
  or or_2 (or_2_out, lw, sw, sb, sh, lb, lh);
  or or_3 (or_3_out, addu, subu, addiu, ori);
  or or_4 (or_4_out, addu, subu, addiu, ori);
  or u_s2_D (s2_D_out, beq, addu, subu, sw, sb, sh);
  or u_s1_D (s1_D_out, or_2_out, or_3_out, jr, beq);
  or u_tuse1_D (tuse1_D_out, or_1_out, or_4_out);
  assign bit_extender_1_out = {{1{1'b0}}, or_5_out};  // Bit_Extender bit_extender_1
  or or_5 (or_5_out, addu, subu);
  or or_6 (or_6_out, addu, subu);
  Multiplexer #(.width(5), .enable("false")) multiplexer_1 (
    .in0({5{1'b0}}), .in1(splitter_1__16_20rt), .out(s2_D), .sel(s2_D_out));
  Multiplexer #(.width(5), .enable("false")) multiplexer_2 (
    .in0({5{1'b0}}), .in1(splitter_1__21_25rs), .out(s1_D), .sel(s1_D_out));
  Multiplexer #(.width(2), .enable("false")) multiplexer_3 (.in0(2'b00), .in1(2'b01), .out(tuse1_D), .sel(tuse1_D_out));
  Multiplexer #(.width(2), .enable("false")) multiplexer_4 (
    .in0(bit_extender_1_out), .in1(2'b10), .out(tuse2_D), .sel(sw));
  Multiplexer #(.width(5), .enable("false")) multiplexer_5 (
    .in0({5{1'b0}}), .in1(splitter_1__11_15rd), .out(multiplexer_5_out), .sel(or_6_out));
  Multiplexer #(.width(5), .enable("false")) multiplexer_6 (
    .in0(multiplexer_5_out), .in1(splitter_1__16_20rt), .out(multiplexer_6_out), .sel(or_7_out));
  or or_7 (or_7_out, sw, ori, lui);
endmodule

module E (
  input  [31:0] in_1,
  input  [31:0] pc_8,
  input  [31:0] extresult,
  output [4:0] des_E,
  output [4:0] s2_E,
  output [4:0] s1_E,
  output [31:0] toD,
  output [3:0] tnew_E
);

  wire addiu, addu, beq, bne, j, jal, jr, lb, lh, lui, lw, nop, or_1_out, or_2_out, or_3_out, or_4_out,
       or_5_out, or_6_out, or_7_out, or_8_out, or_9_out, or_10_out, ori, s1_D_out, s2_E_out, sb, sh, subu, sw;
  wire [1:0] bit_extender_1_out, multiplexer_5_out;
  wire [4:0] multiplexer_6_out, multiplexer_7_out, splitter_1__11_15rd, splitter_1__16_20rt,
       splitter_1__21_25rs;
  wire [5:0] splitter_1_func, splitter_1_op;
  wire [31:0] multiplexer_1_out;

  splitter splitter_1 (
    .instr(in_1), .func(splitter_1_func), ._11_15rd(splitter_1__11_15rd), ._16_20rt(splitter_1__16_20rt),
    ._21_25rs(splitter_1__21_25rs), .op(splitter_1_op));  // open: _0_15, _0_25
  useFunc usefunc_1 (
    .out_3(lw), .out_4(sw), .out_5(ori), .out_6(j), .out_7(beq), .out_8(lui), .out_9(addu), .out_10(subu),
    .out_11(nop), .op(splitter_1_op), .funct(splitter_1_func), .out_12(jr), .out_13(jal), .out_14(addiu),
    .out_15(sb), .out_16(sh), .out_17(lb), .out_18(lh), .out_19(bne));
  or or_1 (or_1_out, lw, sw, sb, sh, lb, lh);
  or or_2 (or_2_out, addu, subu, addiu, ori);
  or or_3 (or_3_out, addu, subu);
  or or_4 (or_4_out, sw, sb, sh);
  Multiplexer #(.width(32), .enable("false")) multiplexer_1 (
    .in0({32{1'b0}}), .in1(pc_8), .out(multiplexer_1_out), .sel(jal));
  or u_s2_E (s2_E_out, or_3_out, or_4_out);
  Multiplexer #(.width(5), .enable("false")) multiplexer_2 (
    .in0({5{1'b0}}), .in1(splitter_1__16_20rt), .out(s2_E), .sel(s2_E_out));
  or s1_D (s1_D_out, or_1_out, or_2_out, jr);
  Multiplexer #(.width(32), .enable("false")) multiplexer_3 (
    .in0(multiplexer_1_out), .in1(extresult), .out(toD), .sel(lui));
  or or_5 (or_5_out, lb, lh, lw);
  assign bit_extender_1_out = {{1{1'b0}}, or_6_out};  // Bit_Extender bit_extender_1
  or or_6 (or_6_out, addu, subu, ori, addiu);
  Multiplexer #(.width(5), .enable("false")) multiplexer_4 (
    .in0({5{1'b0}}), .in1(splitter_1__21_25rs), .out(s1_E), .sel(s1_D_out));
  Multiplexer #(.width(2), .enable("false")) multiplexer_5 (
    .in0(bit_extender_1_out), .in1(2'b10), .out(multiplexer_5_out), .sel(or_5_out));
  or or_7 (or_7_out, lb, lh, lw);
  or or_8 (or_8_out, ori, addiu);
  assign tnew_E = {{2{1'b0}}, multiplexer_5_out};  // Bit_Extender bit_extender_2
  or or_9 (or_9_out, addu, subu);
  Multiplexer #(.width(5), .enable("false")) multiplexer_6 (
    .in0({5{1'b0}}), .in1(splitter_1__11_15rd), .out(multiplexer_6_out), .sel(or_9_out));
  or or_10 (or_10_out, or_7_out, or_8_out, lui);
  Multiplexer #(.width(5), .enable("false")) multiplexer_7 (
    .in0(multiplexer_6_out), .in1(splitter_1__16_20rt), .out(multiplexer_7_out), .sel(or_10_out));
  Multiplexer #(.width(5), .enable("false")) multiplexer_8 (
    .in0(multiplexer_7_out), .in1({5{1'b1}}), .out(des_E), .sel(jal));
endmodule

module M (
  input  [31:0] in_1,
  input  [31:0] pc_8,
  input  [31:0] aluresult,
  output [4:0] des_E,
  output [4:0] s2_E,
  output [4:0] s1_E,
  output [31:0] toD
);

  wire addiu, addu, beq, bne, j, jal, jr, lb, lh, lui, lw, nop, or_1_out, or_2_out, or_3_out, or_4_out,
       or_5_out, ori, s2_E_out, sb, sh, subu, sw;
  wire [4:0] multiplexer_4_out, multiplexer_5_out, splitter_1__11_15rd, splitter_1__16_20rt;
  wire [5:0] splitter_1_func, splitter_1_op;
  wire [31:0] multiplexer_1_out;

  splitter splitter_1 (
    .instr(in_1), .func(splitter_1_func), ._11_15rd(splitter_1__11_15rd), ._16_20rt(splitter_1__16_20rt),
    .op(splitter_1_op));  // open: _0_15, _0_25, _21_25rs
  useFunc usefunc_1 (
    .out_3(lw), .out_4(sw), .out_5(ori), .out_6(j), .out_7(beq), .out_8(lui), .out_9(addu), .out_10(subu),
    .out_11(nop), .op(splitter_1_op), .funct(splitter_1_func), .out_12(jr), .out_13(jal), .out_14(addiu),
    .out_15(sb), .out_16(sh), .out_17(lb), .out_18(lh), .out_19(bne));
  Multiplexer #(.width(32), .enable("false")) multiplexer_1 (
    .in0({32{1'b0}}), .in1(pc_8), .out(multiplexer_1_out), .sel(jal));
  or u_s2_E (s2_E_out, beq, addu, subu, sw);
  Multiplexer #(.width(5), .enable("false")) multiplexer_2 (
    .in0({5{1'b0}}), .in1(splitter_1__16_20rt), .out(s2_E), .sel(s2_E_out));
  Multiplexer #(.width(32), .enable("false")) multiplexer_3 (
    .in0(multiplexer_1_out), .in1(aluresult), .out(toD), .sel(or_1_out));
  or or_1 (or_1_out, lui, ori, addu, subu, addiu);
  or or_2 (or_2_out, addu, subu);
  Multiplexer #(.width(5), .enable("false")) multiplexer_4 (
    .in0({5{1'b0}}), .in1(splitter_1__11_15rd), .out(multiplexer_4_out), .sel(or_2_out));
  or or_3 (or_3_out, lb, lh, lw);
  or or_4 (or_4_out, ori, addiu);
  or or_5 (or_5_out, or_3_out, or_4_out, lui);
  Multiplexer #(.width(5), .enable("false")) multiplexer_5 (
    .in0(multiplexer_4_out), .in1(splitter_1__16_20rt), .out(multiplexer_5_out), .sel(or_5_out));
  Multiplexer #(.width(5), .enable("false")) multiplexer_6 (
    .in0(multiplexer_5_out), .in1({5{1'b1}}), .out(des_E), .sel(jal));

  assign s1_E = {5{1'b0}};
endmodule

module W (
  input  [31:0] in_1,
  input  [31:0] RD,
  input  [31:0] pc_8,
  input  [31:0] aluresult,
  output [4:0] des_E,
  output [31:0] toD
);

  wire addiu, addu, beq, bne, j, jal, jr, lb, lh, lui, lw, nop, or_1_out, or_2_out, or_3_out, or_4_out,
       or_5_out, or_6_out, ori, sb, sh, subu, sw;
  wire [4:0] multiplexer_4_out, multiplexer_5_out, splitter_1__11_15rd, splitter_1__16_20rt,
       splitter_1__21_25rs;
  wire [5:0] splitter_1_func, splitter_1_op;
  wire [31:0] multiplexer_1_out, multiplexer_2_out;

  splitter splitter_1 (
    .instr(in_1), .func(splitter_1_func), ._11_15rd(splitter_1__11_15rd), ._16_20rt(splitter_1__16_20rt),
    ._21_25rs(splitter_1__21_25rs), .op(splitter_1_op));  // open: _0_15, _0_25
  useFunc usefunc_1 (
    .out_3(lw), .out_4(sw), .out_5(ori), .out_6(j), .out_7(beq), .out_8(lui), .out_9(addu), .out_10(subu),
    .out_11(nop), .op(splitter_1_op), .funct(splitter_1_func), .out_12(jr), .out_13(jal), .out_14(addiu),
    .out_15(sb), .out_16(sh), .out_17(lb), .out_18(lh), .out_19(bne));
  or or_1 (or_1_out, lb, lh, lw);
  Multiplexer #(.width(32), .enable("false")) multiplexer_1 (
    .in0({32{1'b0}}), .in1(RD), .out(multiplexer_1_out), .sel(or_1_out));
  Multiplexer #(.width(32), .enable("false")) multiplexer_2 (
    .in0(multiplexer_1_out), .in1(pc_8), .out(multiplexer_2_out), .sel(jal));
  Multiplexer #(.width(32), .enable("false")) multiplexer_3 (
    .in0(multiplexer_2_out), .in1(aluresult), .out(toD), .sel(or_2_out));
  or or_2 (or_2_out, lui, ori, addu, subu, addiu);
  or or_3 (or_3_out, addu, subu);
  Multiplexer #(.width(5), .enable("false")) multiplexer_4 (
    .in0({5{1'b0}}), .in1(splitter_1__11_15rd), .out(multiplexer_4_out), .sel(or_3_out));
  or or_4 (or_4_out, lb, lh, lw);
  or or_5 (or_5_out, ori, addiu);
  or or_6 (or_6_out, or_4_out, or_5_out, lui);
  Multiplexer #(.width(5), .enable("false")) multiplexer_5 (
    .in0(multiplexer_4_out), .in1(splitter_1__16_20rt), .out(multiplexer_5_out), .sel(or_6_out));
  Multiplexer #(.width(5), .enable("false")) multiplexer_6 (
    .in0(multiplexer_5_out), .in1({5{1'b1}}), .out(des_E), .sel(jal));
endmodule

module EXT (
  input  [1:0] in_1,
  input  [15:0] in_2,
  output [31:0] out_3
);

  wire [31:0] bit_extender_1_out, bit_extender_2_out, bit_extender_3_out, shifter_1_out;

  assign bit_extender_1_out = {{16{1'b0}}, in_2};  // Bit_Extender bit_extender_1
  assign bit_extender_2_out = {{16{1'b0}}, in_2};  // Bit_Extender bit_extender_2
  assign bit_extender_3_out = {{16{in_2[15]}}, in_2};  // Bit_Extender bit_extender_3
  Shifter #(.width(32)) shifter_1 (.in(bit_extender_1_out), .\dist (5'b10000), .out(shifter_1_out));
  Multiplexer #(.select(2), .width(32), .enable("false")) multiplexer_1 (
    .in0(bit_extender_2_out), .in1(bit_extender_3_out), .in2(shifter_1_out), .out(out_3), .sel(in_1));  // open: in3
endmodule

module foward (
  input  [4:0] s1_D,
  input  [4:0] s2_D,
  input  [4:0] s1_E,
  input  [4:0] s2_E,
  input  [4:0] des_E,
  input  [3:0] tNew_E,
  input  [4:0] s2_M,
  input  [3:0] tNew_M,
  input  [4:0] des_M,
  input  [3:0] tNew_W,
  input  [4:0] des_W,
  output [1:0] fRsDsel,
  output [1:0] fRtDsel,
  output [1:0] fRsEsel,
  output [1:0] fRtEsel,
  output fRtMsel
);

  wire and_1_out, and_2_out, and_3_out, and_4_out, and_5_out, and_6_out, and_7_out, and_8_out, and_9_out,
       comparator_1_eq, comparator_2_eq, comparator_3_eq, comparator_4_eq, comparator_5_eq, comparator_6_eq,
       comparator_7_eq, comparator_8_eq, comparator_9_eq, comparator_10_eq, comparator_11_eq,
       comparator_12_eq, comparator_13_eq, comparator_14_eq, comparator_15_eq, comparator_16_eq,
       comparator_17_eq, comparator_18_eq, comparator_19_eq, comparator_20_eq, comparator_21_eq,
       comparator_22_eq, comparator_23_eq, comparator_24_eq, comparator_25_eq, comparator_26_eq,
       comparator_27_eq, not_1_out, not_2_out, not_3_out, not_4_out, not_5_out, not_6_out, not_7_out,
       not_8_out, not_9_out;
  wire [1:0] multiplexer_1_out, multiplexer_2_out, multiplexer_5_out, multiplexer_6_out;

  Comparator #(.width(5), .mode("unsigned")) comparator_1 (
    .a(s1_D), .b({5{1'b0}}), .eq(comparator_1_eq));  // open: gt, lt
  not not_1 (not_1_out, comparator_1_eq);
  Comparator #(.width(5), .mode("unsigned")) comparator_2 (.a(s1_D), .b(des_M), .eq(comparator_2_eq));  // open: gt, lt
  Comparator #(.width(4), .mode("unsigned")) comparator_3 (
    .a(tNew_M), .b(4'b0000), .eq(comparator_3_eq));  // open: gt, lt
  Comparator #(.width(5), .mode("unsigned")) comparator_4 (
    .a(s1_D), .b({5{1'b0}}), .eq(comparator_4_eq));  // open: gt, lt
  not not_2 (not_2_out, comparator_4_eq);
  Comparator #(.width(5), .mode("unsigned")) comparator_5 (.a(s1_D), .b(des_E), .eq(comparator_5_eq));  // open: gt, lt
  Comparator #(.width(4), .mode("unsigned")) comparator_6 (
    .a(tNew_E), .b(4'b0000), .eq(comparator_6_eq));  // open: gt, lt
  Comparator #(.width(5), .mode("unsigned")) comparator_7 (
    .a(s2_D), .b({5{1'b0}}), .eq(comparator_7_eq));  // open: gt, lt
  Comparator #(.width(5), .mode("unsigned")) comparator_8 (.a(s2_D), .b(des_M), .eq(comparator_8_eq));  // open: gt, lt
  Comparator #(.width(4), .mode("unsigned")) comparator_9 (
    .a(tNew_M), .b(4'b0000), .eq(comparator_9_eq));  // open: gt, lt
  Comparator #(.width(5), .mode("unsigned")) comparator_10 (
    .a(s2_D), .b({5{1'b0}}), .eq(comparator_10_eq));  // open: gt, lt
  Comparator #(.width(5), .mode("unsigned")) comparator_11 (
    .a(s2_D), .b(des_E), .eq(comparator_11_eq));  // open: gt, lt
  Comparator #(.width(4), .mode("unsigned")) comparator_12 (
    .a(tNew_E), .b(4'b0000), .eq(comparator_12_eq));  // open: gt, lt
  and and_1 (and_1_out, not_1_out, comparator_2_eq, comparator_3_eq);
  and and_2 (and_2_out, not_2_out, comparator_5_eq, comparator_6_eq);
  not not_3 (not_3_out, comparator_7_eq);
  not not_4 (not_4_out, comparator_10_eq);
  Multiplexer #(.width(2)) multiplexer_1 (
    .in0(2'b00), .in1(2'b10), .out(multiplexer_1_out), .sel(and_1_out));  // open: en
  and and_3 (and_3_out, not_3_out, comparator_8_eq, comparator_9_eq);
  and and_4 (and_4_out, not_4_out, comparator_11_eq, comparator_12_eq);
  Multiplexer #(.width(2)) multiplexer_2 (
    .in0(2'b00), .in1(2'b10), .out(multiplexer_2_out), .sel(and_3_out));  // open: en
  Multiplexer #(.width(2)) multiplexer_3 (
    .in0(multiplexer_1_out), .in1(2'b01), .out(fRsDsel), .sel(and_2_out));  // open: en
  Multiplexer #(.width(2)) multiplexer_4 (
    .in0(multiplexer_2_out), .in1(2'b01), .out(fRtDsel), .sel(and_4_out));  // open: en
  Comparator #(.width(5), .mode("unsigned")) comparator_13 (
    .a(s1_E), .b({5{1'b0}}), .eq(comparator_13_eq));  // open: gt, lt
  Comparator #(.width(5), .mode("unsigned")) comparator_14 (
    .a(s1_E), .b(des_W), .eq(comparator_14_eq));  // open: gt, lt
  Comparator #(.width(4), .mode("unsigned")) comparator_15 (
    .a(tNew_W), .b(4'b0000), .eq(comparator_15_eq));  // open: gt, lt
  Comparator #(.width(5), .mode("unsigned")) comparator_16 (
    .a(s1_E), .b({5{1'b0}}), .eq(comparator_16_eq));  // open: gt, lt
  Comparator #(.width(5), .mode("unsigned")) comparator_17 (
    .a(s1_E), .b(des_M), .eq(comparator_17_eq));  // open: gt, lt
  Comparator #(.width(4), .mode("unsigned")) comparator_18 (
    .a(tNew_M), .b(4'b0000), .eq(comparator_18_eq));  // open: gt, lt
  Comparator #(.width(5), .mode("unsigned")) comparator_19 (
    .a(s2_E), .b({5{1'b0}}), .eq(comparator_19_eq));  // open: gt, lt
  Comparator #(.width(5), .mode("unsigned")) comparator_20 (
    .a(s2_E), .b(des_W), .eq(comparator_20_eq));  // open: gt, lt
  Comparator #(.width(4), .mode("unsigned")) comparator_21 (
    .a(tNew_W), .b(4'b0000), .eq(comparator_21_eq));  // open: gt, lt
  Comparator #(.width(5), .mode("unsigned")) comparator_22 (
    .a(s2_E), .b({5{1'b0}}), .eq(comparator_22_eq));  // open: gt, lt
  Comparator #(.width(5), .mode("unsigned")) comparator_23 (
    .a(s2_E), .b(des_M), .eq(comparator_23_eq));  // open: gt, lt
  Comparator #(.width(4), .mode("unsigned")) comparator_24 (
    .a(tNew_M), .b(4'b0000), .eq(comparator_24_eq));  // open: gt, lt
  not not_5 (not_5_out, comparator_13_eq);
  not not_6 (not_6_out, comparator_16_eq);
  not not_7 (not_7_out, comparator_19_eq);
  not not_8 (not_8_out, comparator_22_eq);
  and and_5 (and_5_out, not_5_out, comparator_14_eq, comparator_15_eq);
  and and_6 (and_6_out, not_6_out, comparator_17_eq, comparator_18_eq);
  and and_7 (and_7_out, not_7_out, comparator_20_eq, comparator_21_eq);
  and and_8 (and_8_out, not_8_out, comparator_23_eq, comparator_24_eq);
  Multiplexer #(.width(2)) multiplexer_5 (
    .in0(2'b00), .in1(2'b10), .out(multiplexer_5_out), .sel(and_5_out));  // open: en
  Multiplexer #(.width(2)) multiplexer_6 (
    .in0(2'b00), .in1(2'b10), .out(multiplexer_6_out), .sel(and_7_out));  // open: en
  Multiplexer #(.width(2)) multiplexer_7 (
    .in0(multiplexer_5_out), .in1(2'b01), .out(fRsEsel), .sel(and_6_out));  // open: en
  Multiplexer #(.width(2)) multiplexer_8 (
    .in0(multiplexer_6_out), .in1(2'b01), .out(fRtEsel), .sel(and_8_out));  // open: en
  Comparator #(.width(5), .mode("unsigned")) comparator_25 (
    .a(s2_M), .b({5{1'b0}}), .eq(comparator_25_eq));  // open: gt, lt
  not not_9 (not_9_out, comparator_25_eq);
  Comparator #(.width(5), .mode("unsigned")) comparator_26 (
    .a(s2_M), .b(des_W), .eq(comparator_26_eq));  // open: gt, lt
  Comparator #(.width(4), .mode("unsigned")) comparator_27 (
    .a(tNew_W), .b(4'b0000), .eq(comparator_27_eq));  // open: gt, lt
  and and_9 (and_9_out, not_9_out, comparator_26_eq, comparator_27_eq);
  Multiplexer multiplexer_9 (.in0(1'b0), .in1(1'b1), .out(fRtMsel), .sel(and_9_out));  // open: en
endmodule

module stallU (
  input  [4:0] s1_D,
  input  [4:0] s2_D,
  input  [1:0] tUse1_D,
  input  [1:0] tUse2_D,
  input  [4:0] des_E,
  input  [3:0] tNew_E,
  input  [3:0] tNew_M,
  input  [4:0] des_M,
  output Stall_F,
  output Stall_D,
  output flush_E
);

  wire and_1_out, and_2_out, and_3_out, and_4_out, comparator_1_eq, comparator_2_eq, comparator_3_lt,
       comparator_4_eq, comparator_5_eq, comparator_6_lt, comparator_7_eq, comparator_8_eq, comparator_9_lt,
       comparator_10_eq, comparator_11_eq, comparator_12_lt, not_1_out, not_2_out, not_3_out, not_4_out;
  wire [3:0] tUse1_D_t, tUse2_D_t;

  Comparator #(.width(5), .mode("unsigned")) comparator_1 (
    .a(s1_D), .b({5{1'b0}}), .eq(comparator_1_eq));  // open: gt, lt
  Comparator #(.width(5), .mode("unsigned")) comparator_2 (.a(s1_D), .b(des_E), .eq(comparator_2_eq));  // open: gt, lt
  Comparator #(.width(4), .mode("unsigned")) comparator_3 (
    .a(tUse1_D_t), .b(tNew_E), .lt(comparator_3_lt));  // open: gt, eq
  Comparator #(.width(5), .mode("unsigned")) comparator_4 (
    .a(s2_D), .b({5{1'b0}}), .eq(comparator_4_eq));  // open: gt, lt
  Comparator #(.width(5), .mode("unsigned")) comparator_5 (.a(s2_D), .b(des_E), .eq(comparator_5_eq));  // open: gt, lt
  Comparator #(.width(4), .mode("unsigned")) comparator_6 (
    .a(tUse2_D_t), .b(tNew_E), .lt(comparator_6_lt));  // open: gt, eq
  Comparator #(.width(5), .mode("unsigned")) comparator_7 (
    .a(s1_D), .b({5{1'b0}}), .eq(comparator_7_eq));  // open: gt, lt
  Comparator #(.width(5), .mode("unsigned")) comparator_8 (.a(s1_D), .b(des_M), .eq(comparator_8_eq));  // open: gt, lt
  Comparator #(.width(4), .mode("unsigned")) comparator_9 (
    .a(tUse1_D_t), .b(tNew_M), .lt(comparator_9_lt));  // open: gt, eq
  Comparator #(.width(5), .mode("unsigned")) comparator_10 (
    .a(s2_D), .b({5{1'b0}}), .eq(comparator_10_eq));  // open: gt, lt
  Comparator #(.width(5), .mode("unsigned")) comparator_11 (
    .a(s2_D), .b(des_M), .eq(comparator_11_eq));  // open: gt, lt
  Comparator #(.width(4), .mode("unsigned")) comparator_12 (
    .a(tUse2_D_t), .b(tNew_M), .lt(comparator_12_lt));  // open: gt, eq
  assign tUse1_D_t = {{2{1'b0}}, tUse1_D};  // Bit_Extender bit_extender_1
  not not_1 (not_1_out, comparator_1_eq);
  not not_2 (not_2_out, comparator_4_eq);
  not not_3 (not_3_out, comparator_7_eq);
  not not_4 (not_4_out, comparator_10_eq);
  and and_1 (and_1_out, not_1_out, comparator_2_eq, comparator_3_lt);
  and and_2 (and_2_out, not_2_out, comparator_5_eq, comparator_6_lt);
  and and_3 (and_3_out, not_3_out, comparator_8_eq, comparator_9_lt);
  and and_4 (and_4_out, not_4_out, comparator_11_eq, comparator_12_lt);
  assign tUse2_D_t = {{2{1'b0}}, tUse2_D};  // Bit_Extender bit_extender_2
  or or_1 (flush_E, and_1_out, and_2_out, and_3_out, and_4_out);

  assign Stall_D = flush_E;
  assign Stall_F = flush_E;

  // Other names for the same wires on the sheet: stall_flag = flush_E
endmodule
