// Logisim project Cache(1).circ as structural Verilog: 12 circuits, main circuit Cache
module Cache (
  input  [31:0] Addr,
  input  [31:0] Datai,
  input  MemWrite,
  input  Clk,
  input  MemRead,
  input  Reset,
  output [15:0] All,
  output [15:0] Hit,
  output [31:0] Datao,
  output Stop
);

  wire and_1_out, and_2_out, and_3_out, and_4_out, and_5_out, and_6_out, decoder_1_out0, decoder_1_out1,
       decoder_1_out2, decoder_1_out3, Hit1, Hit2, Hit3, Hit4, Hit_t, or_1_out, or_3_out;
  wire [31:0] G1__1_2, G1__2_2, G1__3_2, G1__4_2, G2__1_2, G2__2_2, G2__3_2, G2__4_2, G3__1_2, G3__2_2,
       G3__3_2, G3__4_2, G4__1_2, G4__2_2, G4__3_2, G4__4_2, multiplexer_1_out, multiplexer_2_out,
       multiplexer_3_out, rb1, rb2, rb3, rb4;

  Decoder #(.select(2), .enable("false")) decoder_1 (
    .out0(decoder_1_out0), .out1(decoder_1_out1), .out2(decoder_1_out2), .out3(decoder_1_out3),
    .sel(Addr[5:4]));
  or or_1 (or_1_out, MemRead, MemWrite);
  and and_1 (and_1_out, or_1_out, decoder_1_out0);
  and and_2 (and_2_out, or_1_out, decoder_1_out1);
  and and_3 (and_3_out, or_1_out, decoder_1_out2);
  and and_4 (and_4_out, or_1_out, decoder_1_out3);
  Counter_part #(.width(16), .max('hffff)) counter_1 (
    .count(and_5_out), .Q(All), .clk(Clk), .clr(Reset));  // open: load, D, carry
  and and_5 (and_5_out, MemRead, ~Stop);  // AND_Gate
  Group G1 (
    ._4(rb4), ._3(rb3), ._2(rb2), ._1(rb1), .MemRead(MemRead), .MemWrite(MemWrite), ._4_2(G1__4_2),
    ._3_2(G1__3_2), ._2_2(G1__2_2), ._1_2(G1__1_2), .Hit(Hit1), .Tag(Addr[11:6]), .Clk(Clk),
    .GroupEn(and_1_out), .Stop(Stop), .Reset(Reset));
  Group G2 (
    ._4(rb4), ._3(rb3), ._2(rb2), ._1(rb1), .MemRead(MemRead), .MemWrite(MemWrite), ._4_2(G2__4_2),
    ._3_2(G2__3_2), ._2_2(G2__2_2), ._1_2(G2__1_2), .Hit(Hit2), .Tag(Addr[11:6]), .Clk(Clk),
    .GroupEn(and_2_out), .Stop(Stop), .Reset(Reset));
  Group G3 (
    ._4(rb4), ._3(rb3), ._2(rb2), ._1(rb1), .MemRead(MemRead), .MemWrite(MemWrite), ._4_2(G3__4_2),
    ._3_2(G3__3_2), ._2_2(G3__2_2), ._1_2(G3__1_2), .Hit(Hit3), .Tag(Addr[11:6]), .Clk(Clk),
    .GroupEn(and_3_out), .Stop(Stop), .Reset(Reset));
  Group G4 (
    ._4(rb4), ._3(rb3), ._2(rb2), ._1(rb1), .MemRead(MemRead), .MemWrite(MemWrite), ._4_2(G4__4_2),
    ._3_2(G4__3_2), ._2_2(G4__2_2), ._1_2(G4__1_2), .Hit(Hit4), .Tag(Addr[11:6]), .Clk(Clk),
    .GroupEn(and_4_out), .Stop(Stop), .Reset(Reset));
  and and_6 (and_6_out, MemRead, ~Stop, Hit_t);  // AND_Gate
  Counter_part #(.width(16), .max('hffff)) counter_2 (
    .count(and_6_out), .Q(Hit), .clk(Clk), .clr(Reset));  // open: load, D, carry
  Multiplexer #(.select(4), .width(32), .enable("false")) multiplexer_1 (
    .in0(G1__1_2), .in1(G1__2_2), .in2(G1__3_2), .in3(G1__4_2), .in4(G2__1_2), .in5(G2__2_2), .in6(G2__3_2),
    .in7(G2__4_2), .in8(G3__1_2), .in9(G3__2_2), .in10(G3__3_2), .in11(G3__4_2), .in12(G4__1_2),
    .in13(G4__2_2), .in14(G4__3_2), .in15(G4__4_2), .out(multiplexer_1_out), .sel(Addr[5:2]));
  RAM ram_1 (
    .MuxBlock(Addr[3:2]), .MemWrite(MemWrite), .MemRead(MemRead), .Hit(Hit_t), .Tag(Addr[11:6]),
    .MuxGroup(Addr[5:4]), .MemData(Datai), .Clk(Clk), .Reset(Reset), ._4(rb4), ._3(rb3), ._2(rb2),
    .out_13(Stop), ._1(rb1));
  Multiplexer #(.select(2), .width(32), .enable("false")) multiplexer_2 (
    .in0(rb1), .in1(rb2), .in2(rb3), .in3(rb4), .out(multiplexer_2_out), .sel(Addr[3:2]));
  or or_2 (Hit_t, Hit1, Hit2, Hit3, Hit4);
  Multiplexer #(.width(32), .enable("false")) multiplexer_3 (
    .in0(multiplexer_2_out), .in1(multiplexer_1_out), .out(multiplexer_3_out), .sel(Hit_t));
  or or_3 (or_3_out, MemWrite, Stop);
  Multiplexer #(.width(32), .enable("false")) multiplexer_4 (
    .in0(multiplexer_3_out), .in1({32{1'b0}}), .out(Datao), .sel(or_3_out));

  // Other names for the same wires on the sheet: MuxBlock[1:0] = Addr[3:2]; MuxGroup[1:0] = Addr[5:4];
  //   Tag[5:0] = Addr[11:6]; Data[31:0] = Datai
endmodule

module Group (
  input  [5:0] Tag,
  input  Clk,
  input  GroupEn,
  input  Stop,
  input  Reset,
  input  [31:0] _4,
  input  [31:0] _3,
  input  [31:0] _2,
  input  [31:0] _1,
  input  MemRead,
  input  MemWrite,
  output [31:0] _4_2,
  output [31:0] _3_2,
  output [31:0] _2_2,
  output [31:0] _1_2,
  output Hit
);

  wire BE1, BE2, BE3, BE4, Block1_2_out_9, Block1_3_out_9, Block1_4_out_9, Block1_out_9, comparator_1_eq,
       comparator_2_eq, comparator_3_eq, comparator_4_eq, GE, Hit1, Hit2, Hit3, Hit4, not_1_out, or_3_out;
  wire [1:0] BCode;
  wire [5:0] Block1_2_out_10, Block1_3_out_10, Block1_4_out_10, Block1_out_10;
  wire [15:0] cnt1, cnt2, cnt3, cnt4, Hitcode;
  wire [31:0] _1B1, _1B2, _1B3, _1B4, _2B1, _2B2, _2B3, _2B4, _3B1, _3B2, _3B3, _3B4, _4B1, _4B2, _4B3, _4B4;

  not not_1 (not_1_out, Stop);
  and and_1 (GE, GroupEn, not_1_out);
  LRU lru_1 (
    ._1(cnt1), .in_2(cnt2), .in_3(cnt3), ._4(cnt4), .Hit1(Hit1), .in_6(Hit2), .in_7(Hit3), .Hit4(Hit4),
    .MemRead(MemRead), .MemWrite(MemWrite), .GroupEn(GE), ._1_2(BE1), ._2(BE2), ._3(BE3), ._4_2(BE4));
  Comparator #(.width(6), .mode("unsigned")) comparator_1 (
    .a(Block1_3_out_10), .b(Tag), .eq(comparator_1_eq));  // open: gt, lt
  Comparator #(.width(6), .mode("unsigned")) comparator_2 (
    .a(Block1_4_out_10), .b(Tag), .eq(comparator_2_eq));  // open: gt, lt
  Block Block1 (
    .in_6(Reset), .in_7(Clk), .in_8(BE1), .in_1(Tag), .in_2(_4), .in_3(_3), .in_4(_2), .in_5(_1),
    .out_9(Block1_out_9), .out_10(Block1_out_10), .out_11(_4B1), .out_12(_3B1), .out_13(_2B1), .out_14(_1B1));
  Comparator #(.width(6), .mode("unsigned")) comparator_3 (
    .a(Block1_out_10), .b(Tag), .eq(comparator_3_eq));  // open: gt, lt
  and and_2 (Hit1, comparator_3_eq, Block1_out_9);
  Block Block1_2 (
    .in_6(Reset), .in_7(Clk), .in_8(BE2), .in_1(Tag), .in_2(_4), .in_3(_3), .in_4(_2), .in_5(_1),
    .out_9(Block1_2_out_9), .out_10(Block1_2_out_10), .out_11(_4B2), .out_12(_3B2), .out_13(_2B2),
    .out_14(_1B2));
  Comparator #(.width(6), .mode("unsigned")) comparator_4 (
    .a(Block1_2_out_10), .b(Tag), .eq(comparator_4_eq));  // open: gt, lt
  and and_3 (Hit2, comparator_4_eq, Block1_2_out_9);
  Block Block1_3 (
    .in_6(Reset), .in_7(Clk), .in_8(BE3), .in_1(Tag), .in_2(_4), .in_3(_3), .in_4(_2), .in_5(_1),
    .out_9(Block1_3_out_9), .out_10(Block1_3_out_10), .out_11(_4B3), .out_12(_3B3), .out_13(_2B3),
    .out_14(_1B3));
  and and_4 (Hit3, comparator_1_eq, Block1_3_out_9);
  Block Block1_4 (
    .in_6(Reset), .in_7(Clk), .in_8(BE4), .in_1(Tag), .in_2(_4), .in_3(_3), .in_4(_2), .in_5(_1),
    .out_9(Block1_4_out_9), .out_10(Block1_4_out_10), .out_11(_4B4), .out_12(_3B4), .out_13(_2B4),
    .out_14(_1B4));
  and and_5 (Hit4, comparator_2_eq, Block1_4_out_9);
  Multiplexer #(.select(2), .width(32), .enable("false")) multiplexer_1 (
    .in0(_2B1), .in1(_2B2), .in2(_2B3), .in3(_2B4), .out(_2_2), .sel(BCode));
  Multiplexer #(.select(2), .width(32), .enable("false")) multiplexer_2 (
    .in0(_1B1), .in1(_1B2), .in2(_1B3), .in3(_1B4), .out(_1_2), .sel(BCode));
  Multiplexer #(.select(2), .width(32), .enable("false")) multiplexer_3 (
    .in0(_4B1), .in1(_4B2), .in2(_4B3), .in3(_4B4), .out(_4_2), .sel(BCode));
  Multiplexer #(.select(2), .width(32), .enable("false")) multiplexer_4 (
    .in0(_3B1), .in1(_3B2), .in2(_3B3), .in3(_3B4), .out(_3_2), .sel(BCode));
  or or_1 (BCode[0], Hit2, Hit4);
  or or_2 (BCode[1], Hit3, Hit4);
  Multiplexer #(.select(2), .width(16), .enable("false")) multiplexer_5 (
    .in0(cnt1), .in1(cnt2), .in2(cnt3), .in3(cnt4), .out(Hitcode), .sel(BCode));
  or or_3 (or_3_out, Hit1, Hit2, Hit3, Hit4);
  and and_6 (Hit, or_3_out, GroupEn);
  Counter counter_1 (.\output (cnt1), .in_1(Clk), .in_2(Reset), .BlockEn(BE1), .Hit(Hit1), .MemRead(MemRead), .GE(GE));
  Counter counter_2 (.\output (cnt2), .in_1(Clk), .in_2(Reset), .BlockEn(BE2), .Hit(Hit2), .MemRead(MemRead), .GE(GE));
  Counter counter_3 (.\output (cnt3), .in_1(Clk), .in_2(Reset), .BlockEn(BE3), .Hit(Hit3), .MemRead(MemRead), .GE(GE));
  Counter counter_4 (.\output (cnt4), .in_1(Clk), .in_2(Reset), .BlockEn(BE4), .Hit(Hit4), .MemRead(MemRead), .GE(GE));

  // Other names for the same wires on the sheet: _1in[31:0] = _1; _2in[31:0] = _2; _3in[31:0] = _3; _4in[31:0] = _4

  // Notes on the sheet:
  //   模块的GE满足EN有效stop无效
  //   Hit满足EN有效，与stop无关
endmodule

module Block (
  input  [5:0] in_1,
  input  [31:0] in_2,
  input  [31:0] in_3,
  input  [31:0] in_4,
  input  [31:0] in_5,
  input  in_6,
  input  in_7,
  input  in_8,
  output out_9,
  output [5:0] out_10,
  output [31:0] out_11,
  output [31:0] out_12,
  output [31:0] out_13,
  output [31:0] out_14
);

  Register #(.width(1)) register_1 (.D(1'b1), .en(in_8), .Q(out_9), .clk(in_7), .clr(in_6));
  Register #(.width(6)) register_2 (.D(in_1), .en(in_8), .Q(out_10), .clk(in_7), .clr(in_6));
  Register #(.width(32)) register_3 (.D(in_2), .en(in_8), .Q(out_11), .clk(in_7), .clr(in_6));
  Register #(.width(32)) register_4 (.D(in_3), .en(in_8), .Q(out_12), .clk(in_7), .clr(in_6));
  Register #(.width(32)) register_5 (.D(in_4), .en(in_8), .Q(out_13), .clk(in_7), .clr(in_6));
  Register #(.width(32)) register_6 (.D(in_5), .en(in_8), .Q(out_14), .clk(in_7), .clr(in_6));

  // Other names for the same wires on the sheet: Clk = in_7; En = in_8; Reset = in_6
endmodule

module Counter (
  input  in_1,
  input  in_2,
  input  Hit,
  input  MemRead,
  input  BlockEn,
  input  GE,
  output [15:0] \output 
);

  wire and_1_out, and_2_out, and_4_out, count, not_1_out, not_2_out, set0;

  not not_1 (not_1_out, Hit);
  not not_2 (not_2_out, set0);
  and and_1 (and_1_out, Hit, MemRead);
  and and_2 (and_2_out, not_1_out, MemRead, BlockEn);
  and and_3 (count, not_2_out, MemRead, GE);
  or or_1 (set0, and_1_out, and_2_out);
  and and_4 (and_4_out, set0, GE);
  Counter_part #(.width(16), .max('hffff)) counter_1 (
    .load(and_4_out), .D({16{1'b0}}), .count(count), .Q(\output ), .clk(in_1), .clr(in_2));  // open: carry

  // Other names for the same wires on the sheet: Clk = in_1; Reset = in_2

  // Notes on the sheet:
  //   命中块时清零
  //   未命中但是LRU选择替换时清零
  //   读数&Group使能&不清零
endmodule

module LRU (
  input  [15:0] _1,
  input  [15:0] in_2,
  input  [15:0] in_3,
  input  [15:0] _4,
  input  Hit1,
  input  in_6,
  input  in_7,
  input  Hit4,
  input  MemRead,
  input  MemWrite,
  input  GroupEn,
  output _1_2,
  output _2,
  output _3,
  output _4_2
);

  wire _1cmp, _2cmp, _3cmp, _4cmp, multiplexer_1_out, multiplexer_2_out, multiplexer_3_out,
       multiplexer_4_out, not_1_out, not_2_out, or_1_out, or_2_out;
  wire [1:0] op;

  sort sort_1 (
    .in_1(_1), .in_2(in_2), .in_3(in_3), .in_4(_4), .out_5(_1cmp), .out_6(_2cmp), .out_7(_3cmp), .out_8(_4cmp));
  or or_1 (or_1_out, Hit1, in_6, in_7, Hit4);
  or or_2 (or_2_out, Hit1, in_6, in_7, Hit4);
  and and_1 (op[0], or_1_out, MemWrite);
  not not_1 (not_1_out, or_2_out);
  not not_2 (not_2_out, MemWrite);
  and and_2 (op[1], not_1_out, not_2_out);
  Multiplexer #(.select(2), .enable("false")) multiplexer_1 (
    .in0(1'b0), .in1(Hit1), .in2(_1cmp), .out(multiplexer_1_out), .sel(op));  // open: in3
  Multiplexer #(.select(2), .enable("false")) multiplexer_2 (
    .in0(1'b0), .in1(in_6), .in2(_2cmp), .out(multiplexer_2_out), .sel(op));  // open: in3
  Multiplexer #(.select(2), .enable("false")) multiplexer_3 (
    .in0(1'b0), .in1(in_7), .in2(_3cmp), .out(multiplexer_3_out), .sel(op));  // open: in3
  Multiplexer #(.select(2), .enable("false")) multiplexer_4 (
    .in0(1'b0), .in1(Hit4), .in2(_4cmp), .out(multiplexer_4_out), .sel(op));  // open: in3
  and and_3 (_1_2, GroupEn, multiplexer_1_out);
  and and_4 (_2, GroupEn, multiplexer_2_out);
  and and_5 (_3, GroupEn, multiplexer_3_out);
  and and_6 (_4_2, GroupEn, multiplexer_4_out);

  // Other names for the same wires on the sheet: _1in = Hit1; _2in = in_6; _3in = in_7; _4in = Hit4; en = GroupEn
endmodule

module RAM (
  input  [1:0] MuxBlock,
  input  MemWrite,
  input  MemRead,
  input  Hit,
  input  [5:0] Tag,
  input  [1:0] MuxGroup,
  input  [31:0] MemData,
  input  Clk,
  input  Reset,
  output [31:0] _4,
  output [31:0] _3,
  output [31:0] _2,
  output out_13,
  output [31:0] _1
);

  wire _1_t, _2_t, _3_t, _4_t, and_1_out, and_2_out, counter_1_carry, not_1_out, not_2_out;
  wire [9:0] adder_1_out, adder_2_out, adder_3_out, adder_4_out, multiplexer_1_out;
  wire [31:0] ram_1_data, ram_2_data, ram_3_data, ram_4_data;

  and and_1 (and_1_out, MemRead, not_1_out);
  not not_1 (not_1_out, Hit);
  Counter_part #(.width(3), .max('h5)) counter_1 (
    .count(and_1_out), .carry(counter_1_carry), .clk(Clk), .clr(Reset));  // open: load, D, Q
  and and_2 (and_2_out, MemRead, Hit);
  and and_3 (out_13, and_1_out, not_2_out);
  not not_2 (not_2_out, counter_1_carry);
  Demultiplexer #(.select(2)) demultiplexer_1 (
    .out0(_1_t), .out1(_2_t), .out2(_3_t), .out3(_4_t), .in(MemWrite), .sel(MuxBlock));  // open: en
  Multiplexer #(.width(10), .enable("false")) multiplexer_1 (
    .in0({Tag, MuxGroup, 2'b00}), .in1({10{1'b0}}), .out(multiplexer_1_out), .sel(and_2_out));
  Adder #(.width(10)) adder_1 (.a(10'h3), .b(multiplexer_1_out), .out(adder_1_out));  // open: cin, cout
  Adder #(.width(10)) adder_2 (.a(10'h2), .b(multiplexer_1_out), .out(adder_2_out));  // open: cin, cout
  Adder #(.width(10)) adder_3 (.a(10'h1), .b(multiplexer_1_out), .out(adder_3_out));  // open: cin, cout
  Adder #(.width(10)) adder_4 (.a({10{1'b0}}), .b(multiplexer_1_out), .out(adder_4_out));  // open: cin, cout
  RAM_part #(.addrWidth(10), .dataWidth(32), .bus("separate")) ram_1 (
    .addr(adder_1_out), .din(MemData), .data(ram_1_data), .str(_4_t), .clk(Clk), .clr(Reset));  // open: sel, ld
  RAM_part #(.addrWidth(10), .dataWidth(32), .bus("separate")) ram_2 (
    .addr(adder_2_out), .din(MemData), .data(ram_2_data), .str(_3_t), .clk(Clk), .clr(Reset));  // open: sel, ld
  RAM_part #(.addrWidth(10), .dataWidth(32), .bus("separate")) ram_3 (
    .addr(adder_3_out), .din(MemData), .data(ram_3_data), .str(_2_t), .clk(Clk), .clr(Reset));  // open: sel, ld
  RAM_part #(.addrWidth(10), .dataWidth(32), .bus("separate")) ram_4 (
    .addr(adder_4_out), .din(MemData), .data(ram_4_data), .str(_1_t), .clk(Clk), .clr(Reset));  // open: sel, ld
  Multiplexer #(.width(32), .enable("false")) multiplexer_2 (.in0(ram_1_data), .in1(MemData), .out(_4), .sel(_4_t));
  Multiplexer #(.width(32), .enable("false")) multiplexer_3 (.in0(ram_2_data), .in1(MemData), .out(_3), .sel(_3_t));
  Multiplexer #(.width(32), .enable("false")) multiplexer_4 (.in0(ram_3_data), .in1(MemData), .out(_2), .sel(_2_t));
  Multiplexer #(.width(32), .enable("false")) multiplexer_5 (.in0(ram_4_data), .in1(MemData), .out(_1), .sel(_1_t));

  // Other names for the same wires on the sheet: Data[31:0] = MemData
endmodule

module compar (
  input  [15:0] in_1,
  input  [15:0] in_2,
  output [15:0] out_3,
  output [15:0] out_4
);

  wire comparator_1_gt, comparator_1_lt;

  Comparator #(.width(16), .mode("unsigned")) comparator_1 (
    .a(in_1), .b(in_2), .gt(comparator_1_gt), .lt(comparator_1_lt));  // open: eq
  Multiplexer #(.width(16)) multiplexer_1 (.in0(in_2), .in1(in_1), .out(out_4), .sel(comparator_1_lt));  // open: en
  Multiplexer #(.width(16)) multiplexer_2 (.in0(in_2), .in1(in_1), .out(out_3), .sel(comparator_1_gt));  // open: en
endmodule

module sort (
  input  [15:0] in_1,
  input  [15:0] in_2,
  input  [15:0] in_3,
  input  [15:0] in_4,
  output out_5,
  output out_6,
  output out_7,
  output out_8
);

  wire comparator_1_lt, comparator_2_lt, comparator_3_lt;
  wire [2:0] multiplexer_1_out, multiplexer_2_out, multiplexer_3_out;
  wire [15:0] compar_1_out_3, compar_2_out_3;

  compar compar_1 (.in_1(in_1), .in_2(in_2), .out_3(compar_1_out_3));  // open: out_4
  Comparator #(.width(16), .mode("unsigned")) comparator_1 (.a(in_1), .b(in_2), .lt(comparator_1_lt));  // open: gt, eq
  compar compar_2 (.in_1(in_3), .in_2(in_4), .out_3(compar_2_out_3));  // open: out_4
  Comparator #(.width(16), .mode("unsigned")) comparator_2 (.a(in_3), .b(in_4), .lt(comparator_2_lt));  // open: gt, eq
  Multiplexer #(.width(3), .enable("false")) multiplexer_1 (
    .in0(3'b001), .in1(3'b010), .out(multiplexer_1_out), .sel(comparator_1_lt));
  Multiplexer #(.width(3), .enable("false")) multiplexer_2 (
    .in0(3'b011), .in1(3'b100), .out(multiplexer_2_out), .sel(comparator_2_lt));
  Comparator #(.width(16), .mode("unsigned")) comparator_3 (
    .a(compar_1_out_3), .b(compar_2_out_3), .lt(comparator_3_lt));  // open: gt, eq
  Multiplexer #(.width(3), .enable("false")) multiplexer_3 (
    .in0(multiplexer_1_out), .in1(multiplexer_2_out), .out(multiplexer_3_out), .sel(comparator_3_lt));
  Decoder #(.select(3), .enable("false")) decoder_1 (
    .out1(out_5), .out2(out_6), .out3(out_7), .out4(out_8), .sel(multiplexer_3_out));  // open: out0, out5, out6, out7

  // Other names for the same wires on the sheet: _1in[15:0] = in_1; _2in[15:0] = in_2; _3in[15:0] = in_3;
  //   _4in[15:0] = in_4
endmodule

module CounterLRU (
  input  in_1,
  input  in_2,
  input  [15:0] in_3,
  input  Hit,
  input  MemRead,
  input  BlockEn,
  input  GE,
  output [15:0] \output 
);

  wire and_1_out, and_2_out, and_4_out, comparator_1_lt, count, not_1_out, set0;

  Comparator #(.width(16), .mode("unsigned")) comparator_1 (
    .a(\output ), .b(in_3), .lt(comparator_1_lt));  // open: gt, eq
  not not_1 (not_1_out, Hit);
  and and_1 (and_1_out, Hit, MemRead);
  and and_2 (and_2_out, not_1_out, MemRead, BlockEn);
  and and_3 (count, ~set0, MemRead, GE, comparator_1_lt);  // AND_Gate
  or or_1 (set0, and_1_out, and_2_out);
  and and_4 (and_4_out, set0, GE);
  Counter_part #(.width(16), .max('hffff)) counter_1 (
    .load(and_4_out), .D({16{1'b0}}), .count(count), .Q(\output ), .clk(in_1), .clr(in_2));  // open: carry

  // Other names for the same wires on the sheet: Clk = in_1; Hitcnt[15:0] = in_3; Reset = in_2

  // Notes on the sheet:
  //   命中块时清零
  //   未命中但是LRU选择替换时清零
  //   读数&Group使能&不清零&小于命中块计数
endmodule

module CounterFIFO (
  input  in_1,
  input  in_2,
  input  Hit,
  input  MemRead,
  input  BlockEn,
  input  GE,
  output [15:0] \output 
);

  wire and_3_out, count, not_1_out, not_2_out, set0;

  not not_1 (not_1_out, Hit);
  not not_2 (not_2_out, set0);
  and and_1 (set0, not_1_out, MemRead, BlockEn);
  and and_2 (count, not_2_out, MemRead, GE);
  and and_3 (and_3_out, set0, GE);
  Counter_part #(.width(16), .max('hffff)) counter_1 (
    .load(and_3_out), .D({16{1'b0}}), .count(count), .Q(\output ), .clk(in_1), .clr(in_2));  // open: carry

  // Other names for the same wires on the sheet: Clk = in_1; Reset = in_2

  // Notes on the sheet:
  //   未命中但是LRU选择替换时清零
  //   读数&Group使能&不清零
endmodule

module CounterLFU (
  input  in_1,
  input  in_2,
  input  Hit,
  input  MemRead,
  input  BlockEn,
  input  GE,
  output [15:0] \output 
);

  wire and_3_out, count, not_1_out, set0;

  not not_1 (not_1_out, Hit);
  and and_1 (count, ~set0, Hit, MemRead, GE);  // AND_Gate
  and and_2 (set0, not_1_out, MemRead, BlockEn);
  and and_3 (and_3_out, set0, GE);
  Counter_part #(.width(16), .max('hffff)) counter_1 (
    .load(and_3_out), .D({16{1'b0}}), .count(count), .Q(\output ), .clk(in_1), .clr(in_2));  // open: carry

  // Other names for the same wires on the sheet: Clk = in_1; Reset = in_2

  // Notes on the sheet:
  //   命中块&不清零&读数&组使能
  //   未命中但是LRU选择替换时清零
endmodule

module LFUsort (
  input  [15:0] in_1,
  input  [15:0] in_2,
  input  [15:0] in_3,
  input  [15:0] in_4,
  output out_5,
  output out_6,
  output out_7,
  output out_8
);

  wire comparator_1_gt, comparator_2_gt, comparator_3_gt;
  wire [2:0] multiplexer_1_out, multiplexer_2_out, multiplexer_3_out;
  wire [15:0] compar_1_out_4, compar_2_out_4;

  compar compar_1 (.in_1(in_1), .in_2(in_2), .out_4(compar_1_out_4));  // open: out_3
  Comparator #(.width(16), .mode("unsigned")) comparator_1 (.a(in_1), .b(in_2), .gt(comparator_1_gt));  // open: eq, lt
  compar compar_2 (.in_1(in_3), .in_2(in_4), .out_4(compar_2_out_4));  // open: out_3
  Comparator #(.width(16), .mode("unsigned")) comparator_2 (.a(in_3), .b(in_4), .gt(comparator_2_gt));  // open: eq, lt
  Multiplexer #(.width(3), .enable("false")) multiplexer_1 (
    .in0(3'b001), .in1(3'b010), .out(multiplexer_1_out), .sel(comparator_1_gt));
  Multiplexer #(.width(3), .enable("false")) multiplexer_2 (
    .in0(3'b011), .in1(3'b100), .out(multiplexer_2_out), .sel(comparator_2_gt));
  Comparator #(.width(16), .mode("unsigned")) comparator_3 (
    .a(compar_1_out_4), .b(compar_2_out_4), .gt(comparator_3_gt));  // open: eq, lt
  Multiplexer #(.width(3), .enable("false")) multiplexer_3 (
    .in0(multiplexer_1_out), .in1(multiplexer_2_out), .out(multiplexer_3_out), .sel(comparator_3_gt));
  Decoder #(.select(3), .enable("false")) decoder_1 (
    .out1(out_5), .out2(out_6), .out3(out_7), .out4(out_8), .sel(multiplexer_3_out));  // open: out0, out5, out6, out7

  // Other names for the same wires on the sheet: _1in[15:0] = in_1; _2in[15:0] = in_2; _3in[15:0] = in_3;
  //   _4in[15:0] = in_4
endmodule
