// Logisim project Cache11.circ as structural Verilog
module LRU (
  input  [15:0] counter1,
  input  [15:0] counter2,
  input  [15:0] counter3,
  input  [15:0] counter4,
  input  hit1,
  input  hit2,
  input  hit3,
  input  hit4,
  input  MemRead,
  input  MemWrite,
  input  En,
  output ifnew1,
  output ifnew2,
  output ifnew3,
  output ifnew4
);

  wire comparator_1_lt, comparator_2_lt, comparator_3_lt, hitted_2_out, hitted_3_out, hitted_4_out,
       hitted_and_notwrite, hitted_and_write, hitted_out, not_1_out, not_2_out, not_3_out, not_4_out,
       not_5_out, not_6_out, not_7_out, not_8_out, nothitted_and_notwrite, nothitted_and_write, s1, s2, s3,
       s4;
  wire [1:0] CONTROL, multiplexer_1_out, multiplexer_4_out, multiplexer_5_out, multiplexer_6_out,
       multiplexer_7_out, multiplexer_8_out;
  wire [15:0] multiplexer_2_out, multiplexer_3_out;

  or hitted (hitted_out, hit1, hit2, hit3, hit4);
  or hitted_2 (hitted_2_out, hit1, hit2, hit3, hit4);
  or hitted_3 (hitted_3_out, hit1, hit2, hit3, hit4);
  not not_1 (not_1_out, hitted_4_out);
  or hitted_4 (hitted_4_out, hit1, hit2, hit3, hit4);
  not not_2 (not_2_out, MemWrite);
  and and_1 (hitted_and_write, hitted_out, MemWrite);
  and and_2 (hitted_and_notwrite, hitted_2_out, not_3_out);
  not not_3 (not_3_out, MemWrite);
  not not_4 (not_4_out, hitted_3_out);
  and and_3 (nothitted_and_write, not_4_out, MemWrite);
  and and_4 (nothitted_and_notwrite, not_1_out, not_2_out);
  Multiplexer #(.width(2)) multiplexer_1 (
    .in0(2'b01), .in1(2'b00), .out(multiplexer_1_out), .sel(not_5_out));  // open: en
  Comparator #(.width(16), .mode("unsigned")) comparator_1 (
    .a(counter1), .b(counter2), .lt(comparator_1_lt));  // open: gt, eq
  not not_5 (not_5_out, comparator_1_lt);
  Multiplexer #(.width(16)) multiplexer_2 (
    .in0(counter2), .in1(counter1), .out(multiplexer_2_out), .sel(not_5_out));  // open: en
  Comparator #(.width(16), .mode("unsigned")) comparator_2 (
    .a(multiplexer_2_out), .b(counter3), .lt(comparator_2_lt));  // open: gt, eq
  Multiplexer #(.width(16)) multiplexer_3 (
    .in0(counter3), .in1(multiplexer_2_out), .out(multiplexer_3_out), .sel(not_6_out));  // open: en
  Multiplexer #(.width(2)) multiplexer_4 (
    .in0(2'b10), .in1(multiplexer_1_out), .out(multiplexer_4_out), .sel(not_6_out));  // open: en
  Multiplexer #(.width(2)) multiplexer_5 (
    .in0(2'b00), .in1(2'b01), .out(multiplexer_5_out), .sel(hitted_and_notwrite));  // open: en
  not not_6 (not_6_out, comparator_2_lt);
  Comparator #(.width(16), .mode("unsigned")) comparator_3 (
    .a(multiplexer_3_out), .b(counter4), .lt(comparator_3_lt));  // open: gt, eq
  Multiplexer #(.width(2)) multiplexer_6 (
    .in0(2'b11), .in1(multiplexer_4_out), .out(multiplexer_6_out), .sel(not_7_out));  // open: en
  not not_7 (not_7_out, comparator_3_lt);
  Decoder #(.select(2)) decoder_1 (.out0(s1), .out1(s2), .out2(s3), .out3(s4), .sel(multiplexer_6_out));  // open: en
  Multiplexer #(.width(2)) multiplexer_7 (
    .in0(multiplexer_5_out), .in1(2'b01), .out(multiplexer_7_out), .sel(nothitted_and_write));  // open: en
  Multiplexer #(.width(2)) multiplexer_8 (
    .in0(multiplexer_7_out), .in1(2'b10), .out(multiplexer_8_out), .sel(nothitted_and_notwrite));  // open: en
  not not_8 (not_8_out, En);
  Multiplexer #(.width(2)) multiplexer_9 (
    .in0(multiplexer_8_out), .in1(2'b11), .out(CONTROL), .sel(not_8_out));  // open: en
  Multiplexer #(.select(2)) multiplexer_10 (
    .in0(hit1), .in1(1'b0), .in2(s1), .in3(1'b0), .out(ifnew1), .sel(CONTROL));  // open: en
  Multiplexer #(.select(2)) multiplexer_11 (
    .in0(hit2), .in1(1'b0), .in2(s2), .in3(1'b0), .out(ifnew2), .sel(CONTROL));  // open: en
  Multiplexer #(.select(2)) multiplexer_12 (
    .in0(hit3), .in1(1'b0), .in2(s3), .in3(1'b0), .out(ifnew3), .sel(CONTROL));  // open: en
  Multiplexer #(.select(2)) multiplexer_13 (
    .in0(hit4), .in1(1'b0), .in2(s4), .in3(1'b0), .out(ifnew4), .sel(CONTROL));  // open: en

  // Other names for the same wires on the sheet: c1[15:0] = counter1; c2[15:0] = counter2; c3[15:0] = counter3;
  //   c4[15:0] = counter4
endmodule

module Block1 (
  input  [31:0] datain1,
  input  [31:0] datain2,
  input  [31:0] datain3,
  input  [31:0] datain4,
  input  Reset,
  input  Clk,
  input  En,
  input  [5:0] Tagin,
  output [31:0] dataout1,
  output [31:0] dataout1_2,
  output [31:0] dataout1_3,
  output [31:0] dataout1_4,
  output [5:0] Tagout,
  output sig
);

  Register #(.width(1)) register_1 (.D(1'b1), .en(En), .Q(sig), .clk(Clk), .clr(Reset));
  Register #(.width(32)) register_2 (.D(datain1), .en(En), .Q(dataout1), .clk(Clk), .clr(Reset));
  Register #(.width(6)) register_3 (.D(Tagin), .en(En), .Q(Tagout), .clk(Clk), .clr(Reset));
  Register #(.width(32)) register_4 (.D(datain2), .en(En), .Q(dataout1_2), .clk(Clk), .clr(Reset));
  Register #(.width(32)) register_5 (.D(datain3), .en(En), .Q(dataout1_3), .clk(Clk), .clr(Reset));
  Register #(.width(32)) register_6 (.D(datain4), .en(En), .Q(dataout1_4), .clk(Clk), .clr(Reset));
endmodule

module Block2 (
  input  [31:0] datain1,
  input  [31:0] datain2,
  input  [31:0] datain3,
  input  [31:0] datain4,
  input  Reset,
  input  Clk,
  input  En,
  input  [5:0] Tagin,
  output [31:0] dataout1,
  output [31:0] dataout1_2,
  output [31:0] dataout1_3,
  output [31:0] dataout1_4,
  output [5:0] Tagout,
  output sig
);

  Register #(.width(1)) register_1 (.D(1'b1), .en(En), .Q(sig), .clk(Clk), .clr(Reset));
  Register #(.width(32)) register_2 (.D(datain1), .en(En), .Q(dataout1), .clk(Clk), .clr(Reset));
  Register #(.width(6)) register_3 (.D(Tagin), .en(En), .Q(Tagout), .clk(Clk), .clr(Reset));
  Register #(.width(32)) register_4 (.D(datain2), .en(En), .Q(dataout1_2), .clk(Clk), .clr(Reset));
  Register #(.width(32)) register_5 (.D(datain3), .en(En), .Q(dataout1_3), .clk(Clk), .clr(Reset));
  Register #(.width(32)) register_6 (.D(datain4), .en(En), .Q(dataout1_4), .clk(Clk), .clr(Reset));
endmodule

module Block3 (
  input  [31:0] datain1,
  input  [31:0] datain2,
  input  [31:0] datain3,
  input  [31:0] datain4,
  input  Reset,
  input  Clk,
  input  En,
  input  [5:0] Tagin,
  output [31:0] dataout1,
  output [31:0] dataout1_2,
  output [31:0] dataout1_3,
  output [31:0] dataout1_4,
  output [5:0] Tagout,
  output sig
);

  Register #(.width(1)) register_1 (.D(1'b1), .en(En), .Q(sig), .clk(Clk), .clr(Reset));
  Register #(.width(32)) register_2 (.D(datain1), .en(En), .Q(dataout1), .clk(Clk), .clr(Reset));
  Register #(.width(6)) register_3 (.D(Tagin), .en(En), .Q(Tagout), .clk(Clk), .clr(Reset));
  Register #(.width(32)) register_4 (.D(datain2), .en(En), .Q(dataout1_2), .clk(Clk), .clr(Reset));
  Register #(.width(32)) register_5 (.D(datain3), .en(En), .Q(dataout1_3), .clk(Clk), .clr(Reset));
  Register #(.width(32)) register_6 (.D(datain4), .en(En), .Q(dataout1_4), .clk(Clk), .clr(Reset));
endmodule

module Block4 (
  input  [31:0] datain1,
  input  [31:0] datain2,
  input  [31:0] datain3,
  input  [31:0] datain4,
  input  Reset,
  input  Clk,
  input  En,
  input  [5:0] Tagin,
  output [31:0] dataout1,
  output [31:0] dataout1_2,
  output [31:0] dataout1_3,
  output [31:0] dataout1_4,
  output [5:0] Tagout,
  output sig
);

  Register #(.width(1)) register_1 (.D(1'b1), .en(En), .Q(sig), .clk(Clk), .clr(Reset));
  Register #(.width(32)) register_2 (.D(datain1), .en(En), .Q(dataout1), .clk(Clk), .clr(Reset));
  Register #(.width(6)) register_3 (.D(Tagin), .en(En), .Q(Tagout), .clk(Clk), .clr(Reset));
  Register #(.width(32)) register_4 (.D(datain2), .en(En), .Q(dataout1_2), .clk(Clk), .clr(Reset));
  Register #(.width(32)) register_5 (.D(datain3), .en(En), .Q(dataout1_3), .clk(Clk), .clr(Reset));
  Register #(.width(32)) register_6 (.D(datain4), .en(En), .Q(dataout1_4), .clk(Clk), .clr(Reset));
endmodule

module Counter1 (
  input  en,
  input  MemRead,
  input  clk,
  input  reset,
  input  hit,
  input  newflag,
  output [15:0] out_7
);

  wire and_1_out, and_2_out, and_3_out, and_4_out, and_5_out, not_1_out, or_1_out;

  and and_1 (and_1_out, hit, MemRead);
  and and_2 (and_2_out, en, or_1_out);
  and and_3 (and_3_out, MemRead, en);
  or or_1 (or_1_out, and_1_out, and_5_out);
  not not_1 (not_1_out, hit);
  Counter #(.width(16), .max('hffff)) counter_1 (
    .load(and_2_out), .D({16{1'b0}}), .count(and_4_out), .Q(out_7), .clk(clk), .clr(reset));  // open: carry
  and and_4 (and_4_out, and_3_out, ~or_1_out);  // AND_Gate
  and and_5 (and_5_out, not_1_out, MemRead, newflag);

  // Other names for the same wires on the sheet: counteren = newflag
endmodule

module Group1 (
  input  [5:0] tag,
  input  clk,
  input  Reset,
  input  en,
  input  stop,
  input  MemWrite,
  input  MemRead,
  input  [31:0] datain1,
  input  [31:0] datain2,
  input  [31:0] datain3,
  input  [31:0] datain4,
  output hit,
  output [31:0] out_13,
  output [31:0] out_14,
  output [31:0] out_15,
  output [31:0] out_16
);

  wire comparator_1_eq, comparator_2_eq, comparator_3_eq, comparator_4_eq, en_t, hit1, hit2, hit3, hit4,
       new1, new2, new3, new4, not_1_out, or_1_out, v1, v2, v3, v4;
  wire [1:0] control, multiplexer_1_out, multiplexer_2_out;
  wire [5:0] tagout1, tagout2, tagout3, tagout4;
  wire [15:0] counter1, counter2, counter3, counter4;
  wire [31:0] block1_1_dataout1, block1_1_dataout1_2, block1_1_dataout1_3, block1_1_dataout1_4,
       block2_1_dataout1, block2_1_dataout1_2, block2_1_dataout1_3, block2_1_dataout1_4, block3_1_dataout1,
       block3_1_dataout1_2, block3_1_dataout1_3, block3_1_dataout1_4, block4_1_dataout1, block4_1_dataout1_2,
       block4_1_dataout1_3, block4_1_dataout1_4;

  not not_1 (not_1_out, stop);
  and and_1 (en_t, en, not_1_out);
  Comparator #(.width(6), .mode("unsigned")) comparator_1 (.a(tag), .b(tagout1), .eq(comparator_1_eq));  // open: gt, lt
  Comparator #(.width(6), .mode("unsigned")) comparator_2 (.a(tag), .b(tagout2), .eq(comparator_2_eq));  // open: gt, lt
  Comparator #(.width(6), .mode("unsigned")) comparator_3 (.a(tag), .b(tagout3), .eq(comparator_3_eq));  // open: gt, lt
  Comparator #(.width(6), .mode("unsigned")) comparator_4 (.a(tag), .b(tagout4), .eq(comparator_4_eq));  // open: gt, lt
  and and_2 (hit1, v1, comparator_1_eq);
  and and_3 (hit2, v2, comparator_2_eq);
  and and_4 (hit3, v3, comparator_3_eq);
  and and_5 (hit4, v4, comparator_4_eq);
  Counter1 counter1_1 (
    .MemRead(MemRead), .clk(clk), .reset(Reset), .hit(hit1), .out_7(counter1), .en(en_t), .newflag(new1));
  Multiplexer #(.width(2), .enable("false")) multiplexer_1 (
    .in0(2'b00), .in1(2'b01), .out(multiplexer_1_out), .sel(hit2));
  or or_1 (or_1_out, hit1, hit2, hit3, hit4);
  and and_6 (hit, en, or_1_out);
  Multiplexer #(.width(2), .enable("false")) multiplexer_2 (
    .in0(multiplexer_1_out), .in1(2'b10), .out(multiplexer_2_out), .sel(hit3));
  LRU lru_1 (
    .counter1(counter1), .counter2(counter2), .counter3(counter3), .counter4(counter4), .hit1(hit1),
    .hit2(hit2), .hit3(hit3), .hit4(hit4), .MemRead(MemRead), .MemWrite(MemWrite), .En(en_t), .ifnew1(new1),
    .ifnew2(new2), .ifnew3(new3), .ifnew4(new4));
  Multiplexer #(.width(2), .enable("false")) multiplexer_3 (
    .in0(multiplexer_2_out), .in1(2'b11), .out(control), .sel(hit4));
  Counter1 counter1_2 (
    .MemRead(MemRead), .clk(clk), .reset(Reset), .hit(hit2), .out_7(counter2), .en(en_t), .newflag(new2));
  Counter1 counter1_3 (
    .MemRead(MemRead), .clk(clk), .reset(Reset), .hit(hit3), .out_7(counter3), .en(en_t), .newflag(new3));
  Block1 block1_1 (
    .Reset(Reset), .Clk(clk), .En(new1), .Tagin(tag), .Tagout(tagout1), .sig(v1), .datain1(datain1),
    .datain2(datain2), .datain3(datain3), .datain4(datain4), .dataout1(block1_1_dataout1),
    .dataout1_2(block1_1_dataout1_2), .dataout1_3(block1_1_dataout1_3), .dataout1_4(block1_1_dataout1_4));
  Block2 block2_1 (
    .Reset(Reset), .Clk(clk), .En(new2), .Tagin(tag), .Tagout(tagout2), .sig(v2), .datain1(datain1),
    .datain2(datain2), .datain3(datain3), .datain4(datain4), .dataout1(block2_1_dataout1),
    .dataout1_2(block2_1_dataout1_2), .dataout1_3(block2_1_dataout1_3), .dataout1_4(block2_1_dataout1_4));
  Block3 block3_1 (
    .Reset(Reset), .Clk(clk), .En(new3), .Tagin(tag), .Tagout(tagout3), .sig(v3), .datain1(datain1),
    .datain2(datain2), .datain3(datain3), .datain4(datain4), .dataout1(block3_1_dataout1),
    .dataout1_2(block3_1_dataout1_2), .dataout1_3(block3_1_dataout1_3), .dataout1_4(block3_1_dataout1_4));
  Counter1 counter1_4 (
    .MemRead(MemRead), .clk(clk), .reset(Reset), .hit(hit4), .out_7(counter4), .en(en_t), .newflag(new4));
  Block4 block4_1 (
    .Reset(Reset), .Clk(clk), .En(new4), .Tagin(tag), .Tagout(tagout4), .sig(v4), .datain1(datain1),
    .datain2(datain2), .datain3(datain3), .datain4(datain4), .dataout1(block4_1_dataout1),
    .dataout1_2(block4_1_dataout1_2), .dataout1_3(block4_1_dataout1_3), .dataout1_4(block4_1_dataout1_4));
  Multiplexer #(.select(2), .width(32), .enable("false")) multiplexer_4 (
    .in0(block1_1_dataout1), .in1(block2_1_dataout1), .in2(block3_1_dataout1), .in3(block4_1_dataout1),
    .out(out_13), .sel(control));
  Multiplexer #(.select(2), .width(32), .enable("false")) multiplexer_5 (
    .in0(block1_1_dataout1_2), .in1(block2_1_dataout1_2), .in2(block3_1_dataout1_2),
    .in3(block4_1_dataout1_2), .out(out_14), .sel(control));
  Multiplexer #(.select(2), .width(32), .enable("false")) multiplexer_6 (
    .in0(block1_1_dataout1_3), .in1(block2_1_dataout1_3), .in2(block3_1_dataout1_3),
    .in3(block4_1_dataout1_3), .out(out_15), .sel(control));
  Multiplexer #(.select(2), .width(32), .enable("false")) multiplexer_7 (
    .in0(block1_1_dataout1_4), .in1(block2_1_dataout1_4), .in2(block3_1_dataout1_4),
    .in3(block4_1_dataout1_4), .out(out_16), .sel(control));

  // Other names for the same wires on the sheet: dataout1[31:0] = out_13; dataout2[31:0] = out_14;
  //   dataout3[31:0] = out_15; dataout4[31:0] = out_16; re_en = en
endmodule

module Cache (
  input  [31:0] Addr,
  input  [31:0] WriteData,
  input  ld,
  input  str,
  input  clk,
  input  reset,
  output [31:0] out_7,
  output [15:0] all,
  output [15:0] hit,
  output stop
);

  wire and_1_out, and_2_out, cache_on, decoder_1_out0, decoder_1_out1, decoder_1_out2, decoder_1_out3, en1,
       en2, en3, en4, hit1, hit2, hit3, hit4, hit_t, not_1_out, or_1_out;
  wire [31:0] bout1, bout2, bout3, bout4, Group1_out_13, Group1_out_14, Group1_out_15, Group1_out_16,
       Group2_out_13, Group2_out_14, Group2_out_15, Group2_out_16, Group3_out_13, Group3_out_14,
       Group3_out_15, Group3_out_16, Group4_out_13, Group4_out_14, Group4_out_15, Group4_out_16,
       multiplexer_2_out, multiplexer_3_out, multiplexer_4_out, multiplexer_5_out, multiplexer_6_out,
       multiplexer_8_out, Out;

  Multiplexer #(.width(32), .enable("false")) multiplexer_1 (.in0(Out), .in1({32{1'b0}}), .out(out_7), .sel(or_1_out));
  or or_1 (or_1_out, str, stop);
  or or_2 (cache_on, ld, str);
  and and_1 (and_1_out, ld, ~stop);  // AND_Gate
  and and_2 (and_2_out, ld, ~stop, hit_t);  // AND_Gate
  Group1 Group1 (
    .tag(Addr[11:6]), .clk(clk), .en(en1), .Reset(reset), .stop(stop), .MemWrite(str), .MemRead(ld),
    .datain1(bout1), .datain2(bout2), .datain3(bout3), .datain4(bout4), .hit(hit1), .out_13(Group1_out_13),
    .out_14(Group1_out_14), .out_15(Group1_out_15), .out_16(Group1_out_16));
  Group1 Group2 (
    .tag(Addr[11:6]), .clk(clk), .en(en2), .Reset(reset), .stop(stop), .MemWrite(str), .MemRead(ld),
    .datain1(bout1), .datain2(bout2), .datain3(bout3), .datain4(bout4), .hit(hit2), .out_13(Group2_out_13),
    .out_14(Group2_out_14), .out_15(Group2_out_15), .out_16(Group2_out_16));
  Group1 Group3 (
    .tag(Addr[11:6]), .clk(clk), .en(en3), .Reset(reset), .stop(stop), .MemWrite(str), .MemRead(ld),
    .datain1(bout1), .datain2(bout2), .datain3(bout3), .datain4(bout4), .hit(hit3), .out_13(Group3_out_13),
    .out_14(Group3_out_14), .out_15(Group3_out_15), .out_16(Group3_out_16));
  Group1 Group4 (
    .tag(Addr[11:6]), .clk(clk), .en(en4), .Reset(reset), .stop(stop), .MemWrite(str), .MemRead(ld),
    .datain1(bout1), .datain2(bout2), .datain3(bout3), .datain4(bout4), .hit(hit4), .out_13(Group4_out_13),
    .out_14(Group4_out_14), .out_15(Group4_out_15), .out_16(Group4_out_16));
  or or_3 (hit_t, hit1, hit2, hit3, hit4);
  Counter #(.width(16), .max('hffff)) counter_1 (
    .count(and_1_out), .Q(all), .clk(clk), .clr(reset));  // open: load, D, carry
  Counter #(.width(16), .max('hffff)) counter_2 (
    .count(and_2_out), .Q(hit), .clk(clk), .clr(reset));  // open: load, D, carry
  Multiplexer #(.select(2), .width(32)) multiplexer_2 (
    .in0(Group1_out_13), .in1(Group1_out_14), .in2(Group1_out_15), .in3(Group1_out_16),
    .out(multiplexer_2_out), .sel(Addr[3:2]));  // open: en
  Multiplexer #(.select(2), .width(32)) multiplexer_3 (
    .in0(Group2_out_13), .in1(Group2_out_14), .in2(Group2_out_15), .in3(Group2_out_16),
    .out(multiplexer_3_out), .sel(Addr[3:2]));  // open: en
  Multiplexer #(.select(2), .width(32)) multiplexer_4 (
    .in0(Group3_out_13), .in1(Group3_out_14), .in2(Group3_out_15), .in3(Group3_out_16),
    .out(multiplexer_4_out), .sel(Addr[3:2]));  // open: en
  Multiplexer #(.select(2), .width(32)) multiplexer_5 (
    .in0(Group4_out_13), .in1(Group4_out_14), .in2(Group4_out_15), .in3(Group4_out_16),
    .out(multiplexer_5_out), .sel(Addr[3:2]));  // open: en
  Multiplexer #(.select(2), .width(32)) multiplexer_6 (
    .in0(multiplexer_2_out), .in1(multiplexer_3_out), .in2(multiplexer_4_out), .in3(multiplexer_5_out),
    .out(multiplexer_6_out), .sel(Addr[5:4]));  // open: en
  Decoder #(.select(2)) decoder_1 (
    .out0(decoder_1_out0), .out1(decoder_1_out1), .out2(decoder_1_out2), .out3(decoder_1_out3),
    .sel(Addr[5:4]));  // open: en
  Multiplexer #(.width(32), .enable("false")) multiplexer_7 (
    .in0(multiplexer_6_out), .in1(multiplexer_8_out), .out(Out), .sel(not_1_out));
  Multiplexer #(.select(2), .width(32)) multiplexer_8 (
    .in0(bout1), .in1(bout2), .in2(bout3), .in3(bout4), .out(multiplexer_8_out), .sel(Addr[3:2]));  // open: en
  not not_1 (not_1_out, hit_t);
  and and_3 (en1, decoder_1_out0, cache_on);
  and and_4 (en2, decoder_1_out1, cache_on);
  and and_5 (en3, decoder_1_out2, cache_on);
  and and_6 (en4, decoder_1_out3, cache_on);
  RAM ram_1 (
    .MuxBlock(Addr[3:2]), .MemWrite(str), .MemRead(ld), .Hit(hit_t), .Tag(Addr[11:6]), .MuxGroup(Addr[5:4]),
    .MemData(WriteData), .Clk(clk), .Reset(reset), ._4(bout4), ._3(bout3), ._2(bout2), .out_13(stop),
    ._1(bout1));

  // Other names for the same wires on the sheet: MuxBlock[1:0] = Addr[3:2]; MuxGroup[1:0] = Addr[5:4];
  //   tag[5:0] = Addr[11:6]; Data[31:0] = WriteData; MemRead = ld; MemWrite = str
endmodule

module RAM (
  input  [1:0] MuxBlock,
  input  MemWrite,
  input  MemRead,
  input  Hit,
  input  [5:0] Tag,
  input  [1:0] MuxGroup,
  input  [31:0] MemData,
  input  Clk,
  input  Reset,
  output [31:0] _4,
  output [31:0] _3,
  output [31:0] _2,
  output out_13,
  output [31:0] _1
);

  wire _1_t, _2_t, _3_t, _4_t, and_1_out, and_2_out, counter_1_carry, not_1_out, not_2_out;
  wire [9:0] adder_1_out, adder_2_out, adder_3_out, adder_4_out, multiplexer_1_out;
  wire [31:0] ram_1_data, ram_2_data, ram_3_data, ram_4_data;

  and and_1 (and_1_out, MemRead, not_1_out);
  not not_1 (not_1_out, Hit);
  Counter #(.width(3), .max('h5)) counter_1 (
    .count(and_1_out), .carry(counter_1_carry), .clk(Clk), .clr(Reset));  // open: load, D, Q
  and and_2 (and_2_out, MemRead, Hit);
  and and_3 (out_13, and_1_out, not_2_out);
  not not_2 (not_2_out, counter_1_carry);
  Demultiplexer #(.select(2)) demultiplexer_1 (
    .out0(_1_t), .out1(_2_t), .out2(_3_t), .out3(_4_t), .in(MemWrite), .sel(MuxBlock));  // open: en
  Multiplexer #(.width(10), .enable("false")) multiplexer_1 (
    .in0({Tag, MuxGroup, 2'b00}), .in1({10{1'b0}}), .out(multiplexer_1_out), .sel(and_2_out));
  Adder #(.width(10)) adder_1 (.a(10'h3), .b(multiplexer_1_out), .out(adder_1_out));  // open: cin, cout
  Adder #(.width(10)) adder_2 (.a(10'h2), .b(multiplexer_1_out), .out(adder_2_out));  // open: cin, cout
  Adder #(.width(10)) adder_3 (.a(10'h1), .b(multiplexer_1_out), .out(adder_3_out));  // open: cin, cout
  Adder #(.width(10)) adder_4 (.a({10{1'b0}}), .b(multiplexer_1_out), .out(adder_4_out));  // open: cin, cout
  RAM_part #(.addrWidth(10), .dataWidth(32), .bus("separate")) ram_1 (
    .addr(adder_1_out), .din(MemData), .data(ram_1_data), .str(_4_t), .clk(Clk), .clr(Reset));  // open: sel, ld
  RAM_part #(.addrWidth(10), .dataWidth(32), .bus("separate")) ram_2 (
    .addr(adder_2_out), .din(MemData), .data(ram_2_data), .str(_3_t), .clk(Clk), .clr(Reset));  // open: sel, ld
  RAM_part #(.addrWidth(10), .dataWidth(32), .bus("separate")) ram_3 (
    .addr(adder_3_out), .din(MemData), .data(ram_3_data), .str(_2_t), .clk(Clk), .clr(Reset));  // open: sel, ld
  RAM_part #(.addrWidth(10), .dataWidth(32), .bus("separate")) ram_4 (
    .addr(adder_4_out), .din(MemData), .data(ram_4_data), .str(_1_t), .clk(Clk), .clr(Reset));  // open: sel, ld
  Multiplexer #(.width(32), .enable("false")) multiplexer_2 (.in0(ram_1_data), .in1(MemData), .out(_4), .sel(_4_t));
  Multiplexer #(.width(32), .enable("false")) multiplexer_3 (.in0(ram_2_data), .in1(MemData), .out(_3), .sel(_3_t));
  Multiplexer #(.width(32), .enable("false")) multiplexer_4 (.in0(ram_3_data), .in1(MemData), .out(_2), .sel(_2_t));
  Multiplexer #(.width(32), .enable("false")) multiplexer_5 (.in0(ram_4_data), .in1(MemData), .out(_1), .sel(_1_t));

  // Other names for the same wires on the sheet: Data[31:0] = MemData
endmodule
