// Logisim project LRU.circ as structural Verilog: 1 circuit, main circuit LRU
module LRU (
  input  [15:0] cal1,
  input  [15:0] cal2,
  input  [15:0] cal3,
  input  [15:0] cal4,
  input  hit1,
  input  hit2,
  input  hit3,
  input  hit4,
  input  memread,
  input  memwrite,
  input  clock,
  output block1,
  output block2,
  output block3,
  output block4
);

  wire and_1_out, and_2_out, and_3_out, and_4_out, and_5_out, and_6_out, and_7_out, and_8_out,
       comparator_1_eq, comparator_1_gt, comparator_2_eq, comparator_2_gt, comparator_3_eq, comparator_3_gt,
       comparator_4_gt, comparator_5_eq, comparator_5_gt, comparator_6_eq, comparator_6_gt, comparator_7_gt,
       comparator_8_gt, comparator_9_eq, comparator_9_gt, comparator_10_gt, comparator_11_gt,
       comparator_12_gt, hit, not_1_out, not_2_out, not_3_out, not_4_out, not_5_out, not_6_out, not_7_out,
       not_8_out, or_2_out, or_3_out, or_4_out, or_5_out, or_6_out, or_7_out, or_8_out, or_9_out, or_10_out,
       or_11_out, or_12_out, or_13_out, or_14_out, or_15_out, or_16_out, or_17_out;

  or or_1 (hit, hit1, hit2, hit3, hit4);
  Comparator #(.width(16)) comparator_1 (.a(cal1), .b(cal2), .gt(comparator_1_gt), .eq(comparator_1_eq));  // open: lt
  Comparator #(.width(16)) comparator_2 (.a(cal1), .b(cal3), .gt(comparator_2_gt), .eq(comparator_2_eq));  // open: lt
  Comparator #(.width(16)) comparator_3 (.a(cal1), .b(cal4), .gt(comparator_3_gt), .eq(comparator_3_eq));  // open: lt
  Comparator #(.width(16)) comparator_4 (.a(cal2), .b(cal1), .gt(comparator_4_gt));  // open: eq, lt
  Comparator #(.width(16)) comparator_5 (.a(cal2), .b(cal3), .gt(comparator_5_gt), .eq(comparator_5_eq));  // open: lt
  Comparator #(.width(16)) comparator_6 (.a(cal2), .b(cal4), .gt(comparator_6_gt), .eq(comparator_6_eq));  // open: lt
  Comparator #(.width(16)) comparator_7 (.a(cal3), .b(cal1), .gt(comparator_7_gt));  // open: eq, lt
  Comparator #(.width(16)) comparator_8 (.a(cal3), .b(cal2), .gt(comparator_8_gt));  // open: eq, lt
  Comparator #(.width(16)) comparator_9 (.a(cal3), .b(cal4), .gt(comparator_9_gt), .eq(comparator_9_eq));  // open: lt
  Comparator #(.width(16)) comparator_10 (.a(cal4), .b(cal1), .gt(comparator_10_gt));  // open: eq, lt
  Comparator #(.width(16)) comparator_11 (.a(cal4), .b(cal2), .gt(comparator_11_gt));  // open: eq, lt
  Comparator #(.width(16)) comparator_12 (.a(cal4), .b(cal3), .gt(comparator_12_gt));  // open: eq, lt
  or or_2 (or_2_out, comparator_1_gt, comparator_1_eq);
  or or_3 (or_3_out, comparator_2_gt, comparator_2_eq);
  or or_4 (or_4_out, comparator_3_gt, comparator_3_eq);
  not not_1 (not_1_out, hit);
  not not_2 (not_2_out, memwrite);
  buf or_5 (or_5_out, comparator_4_gt);  // OR_Gate
  or or_6 (or_6_out, comparator_5_gt, comparator_5_eq);
  or or_7 (or_7_out, comparator_6_gt, comparator_6_eq);
  not not_3 (not_3_out, hit);
  not not_4 (not_4_out, memwrite);
  buf or_8 (or_8_out, comparator_7_gt);  // OR_Gate
  buf or_9 (or_9_out, comparator_8_gt);  // OR_Gate
  or or_10 (or_10_out, comparator_9_gt, comparator_9_eq);
  not not_5 (not_5_out, hit);
  not not_6 (not_6_out, memwrite);
  buf or_11 (or_11_out, comparator_10_gt);  // OR_Gate
  buf or_12 (or_12_out, comparator_11_gt);  // OR_Gate
  buf or_13 (or_13_out, comparator_12_gt);  // OR_Gate
  not not_7 (not_7_out, hit);
  not not_8 (not_8_out, memwrite);
  and and_1 (and_1_out, or_2_out, or_3_out, or_4_out, not_1_out, not_2_out);
  and and_2 (and_2_out, hit1, memwrite);
  and and_3 (and_3_out, or_5_out, or_6_out, or_7_out, not_3_out, not_4_out);
  and and_4 (and_4_out, hit2, memwrite);
  and and_5 (and_5_out, or_8_out, or_9_out, or_10_out, not_5_out, not_6_out);
  and and_6 (and_6_out, hit3, memwrite);
  and and_7 (and_7_out, or_11_out, or_12_out, or_13_out, not_7_out, not_8_out);
  and and_8 (and_8_out, hit4, memwrite);
  or or_14 (or_14_out, and_1_out, and_2_out);
  or or_15 (or_15_out, and_3_out, and_4_out);
  or or_16 (or_16_out, and_5_out, and_6_out);
  or or_17 (or_17_out, and_7_out, and_8_out);
  and and_9 (block1, or_14_out, clock);
  and and_10 (block2, or_15_out, clock);
  and and_11 (block3, or_16_out, clock);
  and and_12 (block4, or_17_out, clock);
endmodule
