// Logisim project RAM(1).circ as structural Verilog: 9 circuits, main circuit Cache
module Cache (
  input  [31:0] Addresss,
  input  [31:0] Data,
  input  Str,
  input  Clk,
  input  Ld,
  input  Clr,
  output [15:0] HitTimes,
  output [15:0] AllTimes,
  output [31:0] DataOut,
  output Stop
);

  wire and_5_out, and_6_out, and_7_out, decoder_1_out0, decoder_1_out1, decoder_1_out2, decoder_1_out3, En1,
       En2, En3, En4, hit, hit1, hit2, hit3, hit4, not_1_out, not_2_out, not_3_out, or_1_out, or_2_out;
  wire [31:0] cachegroup_1_output1, cachegroup_1_output2, cachegroup_1_output3, cachegroup_1_output4,
       cachegroup_2_output1, cachegroup_2_output2, cachegroup_2_output3, cachegroup_2_output4,
       cachegroup_3_output1, cachegroup_3_output2, cachegroup_3_output3, cachegroup_3_output4,
       cachegroup_4_output1, cachegroup_4_output2, cachegroup_4_output3, cachegroup_4_output4,
       multiplexer_1_out, multiplexer_2_out, multiplexer_3_out, multiplexer_4_out, multiplexer_5_out,
       multiplexer_6_out, multiplexer_7_out, R1, R2, R3, R4;

  CacheGroup cachegroup_1 (
    .Write1(R1), .Write2(R2), .Write3(R3), .Write4(R4), .MemRead(Ld), .MemWrite(Str),
    .output1(cachegroup_1_output1), .output2(cachegroup_1_output2), .output3(cachegroup_1_output3),
    .output4(cachegroup_1_output4), .hit(hit1), .Tag(Addresss[11:6]), .Clk(Clk), .En(En1), .Stop(Stop),
    .Reset(Clr));
  CacheGroup cachegroup_2 (
    .Write1(R1), .Write2(R2), .Write3(R3), .Write4(R4), .MemRead(Ld), .MemWrite(Str),
    .output1(cachegroup_2_output1), .output2(cachegroup_2_output2), .output3(cachegroup_2_output3),
    .output4(cachegroup_2_output4), .hit(hit2), .Tag(Addresss[11:6]), .Clk(Clk), .En(En2), .Stop(Stop),
    .Reset(Clr));
  CacheGroup cachegroup_3 (
    .Write1(R1), .Write2(R2), .Write3(R3), .Write4(R4), .MemRead(Ld), .MemWrite(Str),
    .output1(cachegroup_3_output1), .output2(cachegroup_3_output2), .output3(cachegroup_3_output3),
    .output4(cachegroup_3_output4), .hit(hit3), .Tag(Addresss[11:6]), .Clk(Clk), .En(En3), .Stop(Stop),
    .Reset(Clr));
  CacheGroup cachegroup_4 (
    .Write1(R1), .Write2(R2), .Write3(R3), .Write4(R4), .MemRead(Ld), .MemWrite(Str),
    .output1(cachegroup_4_output1), .output2(cachegroup_4_output2), .output3(cachegroup_4_output3),
    .output4(cachegroup_4_output4), .hit(hit4), .Tag(Addresss[11:6]), .Clk(Clk), .En(En4), .Stop(Stop),
    .Reset(Clr));
  Multiplexer #(.select(2), .width(32)) multiplexer_1 (
    .in0(cachegroup_1_output1), .in1(cachegroup_1_output2), .in2(cachegroup_1_output3),
    .in3(cachegroup_1_output4), .out(multiplexer_1_out), .sel(Addresss[3:2]));  // open: en
  Multiplexer #(.select(2), .width(32)) multiplexer_2 (
    .in0(cachegroup_2_output1), .in1(cachegroup_2_output2), .in2(cachegroup_2_output3),
    .in3(cachegroup_2_output4), .out(multiplexer_2_out), .sel(Addresss[3:2]));  // open: en
  Multiplexer #(.select(2), .width(32)) multiplexer_3 (
    .in0(cachegroup_3_output1), .in1(cachegroup_3_output2), .in2(cachegroup_3_output3),
    .in3(cachegroup_3_output4), .out(multiplexer_3_out), .sel(Addresss[3:2]));  // open: en
  Multiplexer #(.select(2), .width(32)) multiplexer_4 (
    .in0(cachegroup_4_output1), .in1(cachegroup_4_output2), .in2(cachegroup_4_output3),
    .in3(cachegroup_4_output4), .out(multiplexer_4_out), .sel(Addresss[3:2]));  // open: en
  Multiplexer #(.select(2), .width(32)) multiplexer_5 (
    .in0(R1), .in1(R2), .in2(R3), .in3(R4), .out(multiplexer_5_out), .sel(Addresss[3:2]));  // open: en
  Multiplexer #(.select(2), .width(32)) multiplexer_6 (
    .in0(multiplexer_1_out), .in1(multiplexer_2_out), .in2(multiplexer_3_out), .in3(multiplexer_4_out),
    .out(multiplexer_6_out), .sel(Addresss[5:4]));  // open: en
  Multiplexer #(.width(32)) multiplexer_7 (
    .in0(multiplexer_6_out), .in1(multiplexer_5_out), .out(multiplexer_7_out), .sel(not_1_out));  // open: en
  not not_1 (not_1_out, hit);
  Decoder #(.select(2)) decoder_1 (
    .out0(decoder_1_out0), .out1(decoder_1_out1), .out2(decoder_1_out2), .out3(decoder_1_out3),
    .sel(Addresss[5:4]));  // open: en
  or or_1 (or_1_out, Stop, Str);
  or or_2 (or_2_out, Str, Ld);
  Multiplexer #(.width(32)) multiplexer_8 (
    .in0(multiplexer_7_out), .in1({32{1'b0}}), .out(DataOut), .sel(or_1_out));  // open: en
  or or_3 (hit, hit1, hit2, hit3, hit4);
  and and_1 (En1, or_2_out, decoder_1_out0);
  and and_2 (En2, decoder_1_out1, or_2_out);
  and and_3 (En3, or_2_out, decoder_1_out2);
  and and_4 (En4, or_2_out, decoder_1_out3);
  and and_5 (and_5_out, hit, Ld);
  not not_2 (not_2_out, Stop);
  RAM ram_1 (
    .MuxBlock(Addresss[3:2]), .MemWrite(Str), .MemRead(Ld), .Hit(hit), .Tag(Addresss[11:6]),
    .MuxGroup(Addresss[5:4]), .MemData(Data), .Clk(Clk), .Reset(Clr), ._4(R4), ._3(R3), ._2(R2),
    .out_13(Stop), ._1(R1));
  and and_6 (and_6_out, and_5_out, not_2_out);
  not not_3 (not_3_out, Stop);
  and and_7 (and_7_out, not_3_out, Ld);
  Counter_part #(.width(16), .max('hffff)) counter_1 (
    .count(and_6_out), .Q(HitTimes), .clk(Clk), .clr(Clr));  // open: load, D, carry
  Counter_part #(.width(16), .max('hffff)) counter_2 (
    .count(and_7_out), .Q(AllTimes), .clk(Clk), .clr(Clr));  // open: load, D, carry
  // OR_Gate or_4 is placed but not wired

  // Other names for the same wires on the sheet: Addinblock[1:0] = Addresss[3:2]; set[1:0] = Addresss[5:4];
  //   blockAdd[5:0] = Addresss[11:6]; WriteData[31:0] = Data
endmodule

module RAM (
  input  [1:0] MuxBlock,
  input  MemWrite,
  input  MemRead,
  input  Hit,
  input  [5:0] Tag,
  input  [1:0] MuxGroup,
  input  [31:0] MemData,
  input  Clk,
  input  Reset,
  output [31:0] _4,
  output [31:0] _3,
  output [31:0] _2,
  output out_13,
  output [31:0] _1
);

  wire _1_t, _2_t, _3_t, _4_t, and_1_out, and_2_out, counter_1_carry, not_1_out, not_2_out;
  wire [9:0] adder_1_out, adder_2_out, adder_3_out, adder_4_out, multiplexer_1_out;
  wire [31:0] ram_1_data, ram_2_data, ram_3_data, ram_4_data;

  and and_1 (and_1_out, MemRead, not_1_out);
  not not_1 (not_1_out, Hit);
  Counter_part #(.width(3), .max('h5)) counter_1 (
    .count(and_1_out), .carry(counter_1_carry), .clk(Clk), .clr(Reset));  // open: load, D, Q
  and and_2 (and_2_out, MemRead, Hit);
  and and_3 (out_13, and_1_out, not_2_out);
  not not_2 (not_2_out, counter_1_carry);
  Demultiplexer #(.select(2)) demultiplexer_1 (
    .out0(_1_t), .out1(_2_t), .out2(_3_t), .out3(_4_t), .in(MemWrite), .sel(MuxBlock));  // open: en
  Multiplexer #(.width(10), .enable("false")) multiplexer_1 (
    .in0({Tag, MuxGroup, 2'b00}), .in1({10{1'b0}}), .out(multiplexer_1_out), .sel(and_2_out));
  Adder #(.width(10)) adder_1 (.a(10'h3), .b(multiplexer_1_out), .out(adder_1_out));  // open: cin, cout
  Adder #(.width(10)) adder_2 (.a(10'h2), .b(multiplexer_1_out), .out(adder_2_out));  // open: cin, cout
  Adder #(.width(10)) adder_3 (.a(10'h1), .b(multiplexer_1_out), .out(adder_3_out));  // open: cin, cout
  Adder #(.width(10)) adder_4 (.a({10{1'b0}}), .b(multiplexer_1_out), .out(adder_4_out));  // open: cin, cout
  RAM_part #(.addrWidth(10), .dataWidth(32), .bus("separate")) ram_1 (
    .addr(adder_1_out), .din(MemData), .data(ram_1_data), .str(_4_t), .clk(Clk), .clr(Reset));  // open: sel, ld
  RAM_part #(.addrWidth(10), .dataWidth(32), .bus("separate")) ram_2 (
    .addr(adder_2_out), .din(MemData), .data(ram_2_data), .str(_3_t), .clk(Clk), .clr(Reset));  // open: sel, ld
  RAM_part #(.addrWidth(10), .dataWidth(32), .bus("separate")) ram_3 (
    .addr(adder_3_out), .din(MemData), .data(ram_3_data), .str(_2_t), .clk(Clk), .clr(Reset));  // open: sel, ld
  RAM_part #(.addrWidth(10), .dataWidth(32), .bus("separate")) ram_4 (
    .addr(adder_4_out), .din(MemData), .data(ram_4_data), .str(_1_t), .clk(Clk), .clr(Reset));  // open: sel, ld
  Multiplexer #(.width(32), .enable("false")) multiplexer_2 (.in0(ram_1_data), .in1(MemData), .out(_4), .sel(_4_t));
  Multiplexer #(.width(32), .enable("false")) multiplexer_3 (.in0(ram_2_data), .in1(MemData), .out(_3), .sel(_3_t));
  Multiplexer #(.width(32), .enable("false")) multiplexer_4 (.in0(ram_3_data), .in1(MemData), .out(_2), .sel(_2_t));
  Multiplexer #(.width(32), .enable("false")) multiplexer_5 (.in0(ram_4_data), .in1(MemData), .out(_1), .sel(_1_t));

  // Other names for the same wires on the sheet: Data[31:0] = MemData
endmodule

module CacheBlock1 (
  input  Reset,
  input  Clk,
  input  Enable,
  input  [31:0] Blcok1,
  input  [31:0] Blcok2,
  input  [5:0] Tag,
  input  [31:0] Blcok4,
  input  [31:0] Blcok3,
  output V,
  output [31:0] Blcok1_2,
  output [31:0] Blcok2_2,
  output [5:0] Tag_2,
  output [31:0] Blcok4_2,
  output [31:0] Blcok3_2
);

  Register #(.width(1)) register_1 (.D(1'b1), .en(Enable), .Q(V), .clk(Clk), .clr(Reset));
  Register #(.width(32)) register_2 (.D(Blcok3), .en(Enable), .Q(Blcok3_2), .clk(Clk), .clr(Reset));
  Register #(.width(6)) register_3 (.D(Tag), .en(Enable), .Q(Tag_2), .clk(Clk), .clr(Reset));
  Register #(.width(32)) register_4 (.D(Blcok4), .en(Enable), .Q(Blcok4_2), .clk(Clk), .clr(Reset));
  Register #(.width(32)) register_5 (.D(Blcok1), .en(Enable), .Q(Blcok1_2), .clk(Clk), .clr(Reset));
  Register #(.width(32)) register_6 (.D(Blcok2), .en(Enable), .Q(Blcok2_2), .clk(Clk), .clr(Reset));

  // Other names for the same wires on the sheet: En = Enable
endmodule

module CacheBlock2 (
  input  Reset,
  input  Clk,
  input  Enable,
  input  [31:0] Blcok1,
  input  [31:0] Blcok2,
  input  [5:0] Tag,
  input  [31:0] Blcok4,
  input  [31:0] Blcok3,
  output V,
  output [31:0] Blcok1_2,
  output [31:0] Blcok2_2,
  output [5:0] Tag_2,
  output [31:0] Blcok4_2,
  output [31:0] Blcok3_2
);

  Register #(.width(1)) register_1 (.D(1'b1), .en(Enable), .Q(V), .clk(Clk), .clr(Reset));
  Register #(.width(32)) register_2 (.D(Blcok3), .en(Enable), .Q(Blcok3_2), .clk(Clk), .clr(Reset));
  Register #(.width(6)) register_3 (.D(Tag), .en(Enable), .Q(Tag_2), .clk(Clk), .clr(Reset));
  Register #(.width(32)) register_4 (.D(Blcok4), .en(Enable), .Q(Blcok4_2), .clk(Clk), .clr(Reset));
  Register #(.width(32)) register_5 (.D(Blcok1), .en(Enable), .Q(Blcok1_2), .clk(Clk), .clr(Reset));
  Register #(.width(32)) register_6 (.D(Blcok2), .en(Enable), .Q(Blcok2_2), .clk(Clk), .clr(Reset));

  // Other names for the same wires on the sheet: En = Enable
endmodule

module CacheBlock3 (
  input  Reset,
  input  Clk,
  input  Enable,
  input  [31:0] Blcok1,
  input  [31:0] Blcok2,
  input  [5:0] Tag,
  input  [31:0] Blcok4,
  input  [31:0] Blcok3,
  output V,
  output [31:0] Blcok1_2,
  output [31:0] Blcok2_2,
  output [5:0] Tag_2,
  output [31:0] Blcok4_2,
  output [31:0] Blcok3_2
);

  Register #(.width(1)) register_1 (.D(1'b1), .en(Enable), .Q(V), .clk(Clk), .clr(Reset));
  Register #(.width(32)) register_2 (.D(Blcok3), .en(Enable), .Q(Blcok3_2), .clk(Clk), .clr(Reset));
  Register #(.width(6)) register_3 (.D(Tag), .en(Enable), .Q(Tag_2), .clk(Clk), .clr(Reset));
  Register #(.width(32)) register_4 (.D(Blcok4), .en(Enable), .Q(Blcok4_2), .clk(Clk), .clr(Reset));
  Register #(.width(32)) register_5 (.D(Blcok1), .en(Enable), .Q(Blcok1_2), .clk(Clk), .clr(Reset));
  Register #(.width(32)) register_6 (.D(Blcok2), .en(Enable), .Q(Blcok2_2), .clk(Clk), .clr(Reset));

  // Other names for the same wires on the sheet: En = Enable
endmodule

module CacheBlock4 (
  input  Reset,
  input  Clk,
  input  Enable,
  input  [31:0] Blcok1,
  input  [31:0] Blcok2,
  input  [5:0] Tag,
  input  [31:0] Blcok4,
  input  [31:0] Blcok3,
  output V,
  output [31:0] Blcok1_2,
  output [31:0] Blcok2_2,
  output [5:0] Tag_2,
  output [31:0] Blcok4_2,
  output [31:0] Blcok3_2
);

  Register #(.width(1)) register_1 (.D(1'b1), .en(Enable), .Q(V), .clk(Clk), .clr(Reset));
  Register #(.width(32)) register_2 (.D(Blcok3), .en(Enable), .Q(Blcok3_2), .clk(Clk), .clr(Reset));
  Register #(.width(6)) register_3 (.D(Tag), .en(Enable), .Q(Tag_2), .clk(Clk), .clr(Reset));
  Register #(.width(32)) register_4 (.D(Blcok4), .en(Enable), .Q(Blcok4_2), .clk(Clk), .clr(Reset));
  Register #(.width(32)) register_5 (.D(Blcok1), .en(Enable), .Q(Blcok1_2), .clk(Clk), .clr(Reset));
  Register #(.width(32)) register_6 (.D(Blcok2), .en(Enable), .Q(Blcok2_2), .clk(Clk), .clr(Reset));

  // Other names for the same wires on the sheet: En = Enable
endmodule

module Counter (
  input  En,
  input  hit,
  input  MemRead,
  input  Clk,
  input  GroupEn,
  input  Reset,
  output [15:0] out_7
);

  wire and_1_out, and_2_out, and_3_out, and_4_out, not_1_out, not_2_out, or_1_out;

  not not_1 (not_1_out, hit);
  and and_1 (and_1_out, hit, MemRead);
  and and_2 (and_2_out, En, MemRead, not_1_out);
  or or_1 (or_1_out, and_1_out, and_2_out);
  not not_2 (not_2_out, or_1_out);
  and and_3 (and_3_out, not_2_out, MemRead, GroupEn);
  and and_4 (and_4_out, GroupEn, or_1_out);
  Counter_part #(.width(16), .max('hffff)) counter_1 (
    .load(and_4_out), .D({16{1'b0}}), .count(and_3_out), .Q(out_7), .clk(Clk), .clr(Reset));  // open: carry
endmodule

module LRU (
  input  [15:0] blockCount1,
  input  [15:0] blockCount2,
  input  [15:0] blockCount3,
  input  [15:0] blockCount4,
  input  hit1,
  input  hit2,
  input  hit3,
  input  hit4,
  input  MemRead,
  input  MemWrite,
  input  En,
  output En1,
  output En2,
  output En3,
  output En4
);

  wire and_1_out, and_2_out, and_3_out, and_4_out, and_5_out, and_6_out, and_7_out, and_8_out, and_9_out,
       and_10_out, and_11_out, and_12_out, comparator_1_eq, comparator_1_gt, comparator_2_eq,
       comparator_2_gt, comparator_3_eq, comparator_3_gt, comparator_4_gt, comparator_5_eq, comparator_5_gt,
       comparator_6_eq, comparator_6_gt, comparator_7_gt, comparator_8_gt, comparator_9_eq, comparator_9_gt,
       comparator_10_gt, comparator_11_gt, comparator_12_gt, hit, not_1_out, not_2_out, not_3_out, not_4_out,
       not_5_out, not_6_out, not_7_out, not_8_out, or_2_out, or_3_out, or_4_out, or_5_out, or_6_out,
       or_7_out, or_8_out, or_9_out, or_10_out, or_11_out, or_12_out, or_13_out, or_14_out, or_15_out,
       or_16_out, or_17_out;

  or or_1 (hit, hit1, hit2, hit3, hit4);
  Comparator #(.width(16), .mode("unsigned")) comparator_1 (
    .a(blockCount1), .b(blockCount2), .gt(comparator_1_gt), .eq(comparator_1_eq));  // open: lt
  Comparator #(.width(16), .mode("unsigned")) comparator_2 (
    .a(blockCount1), .b(blockCount3), .gt(comparator_2_gt), .eq(comparator_2_eq));  // open: lt
  Comparator #(.width(16), .mode("unsigned")) comparator_3 (
    .a(blockCount1), .b(blockCount4), .gt(comparator_3_gt), .eq(comparator_3_eq));  // open: lt
  Comparator #(.width(16), .mode("unsigned")) comparator_4 (
    .a(blockCount2), .b(blockCount1), .gt(comparator_4_gt));  // open: eq, lt
  Comparator #(.width(16), .mode("unsigned")) comparator_5 (
    .a(blockCount2), .b(blockCount3), .gt(comparator_5_gt), .eq(comparator_5_eq));  // open: lt
  Comparator #(.width(16), .mode("unsigned")) comparator_6 (
    .a(blockCount2), .b(blockCount4), .gt(comparator_6_gt), .eq(comparator_6_eq));  // open: lt
  Comparator #(.width(16), .mode("unsigned")) comparator_7 (
    .a(blockCount3), .b(blockCount2), .gt(comparator_7_gt));  // open: eq, lt
  Comparator #(.width(16), .mode("unsigned")) comparator_8 (
    .a(blockCount3), .b(blockCount1), .gt(comparator_8_gt));  // open: eq, lt
  Comparator #(.width(16), .mode("unsigned")) comparator_9 (
    .a(blockCount3), .b(blockCount4), .gt(comparator_9_gt), .eq(comparator_9_eq));  // open: lt
  Comparator #(.width(16), .mode("unsigned")) comparator_10 (
    .a(blockCount4), .b(blockCount2), .gt(comparator_10_gt));  // open: eq, lt
  Comparator #(.width(16), .mode("unsigned")) comparator_11 (
    .a(blockCount4), .b(blockCount3), .gt(comparator_11_gt));  // open: eq, lt
  Comparator #(.width(16), .mode("unsigned")) comparator_12 (
    .a(blockCount4), .b(blockCount1), .gt(comparator_12_gt));  // open: eq, lt
  or or_2 (or_2_out, comparator_1_gt, comparator_1_eq);
  or or_3 (or_3_out, comparator_2_gt, comparator_2_eq);
  or or_4 (or_4_out, comparator_3_gt, comparator_3_eq);
  buf or_5 (or_5_out, comparator_4_gt);  // OR_Gate
  or or_6 (or_6_out, comparator_5_gt, comparator_5_eq);
  or or_7 (or_7_out, comparator_6_gt, comparator_6_eq);
  buf or_8 (or_8_out, comparator_7_gt);  // OR_Gate
  buf or_9 (or_9_out, comparator_8_gt);  // OR_Gate
  or or_10 (or_10_out, comparator_9_gt, comparator_9_eq);
  buf or_11 (or_11_out, comparator_10_gt);  // OR_Gate
  buf or_12 (or_12_out, comparator_11_gt);  // OR_Gate
  buf or_13 (or_13_out, comparator_12_gt);  // OR_Gate
  and and_1 (and_1_out, or_2_out, or_3_out, or_4_out);
  and and_2 (and_2_out, hit1, MemWrite);
  and and_3 (and_3_out, or_5_out, or_6_out, or_7_out);
  and and_4 (and_4_out, hit2, MemWrite);
  and and_5 (and_5_out, or_8_out, or_9_out, or_10_out);
  and and_6 (and_6_out, hit3, MemWrite);
  and and_7 (and_7_out, or_11_out, or_12_out, or_13_out);
  and and_8 (and_8_out, hit4, MemWrite);
  not not_1 (not_1_out, hit);
  not not_2 (not_2_out, MemWrite);
  not not_3 (not_3_out, hit);
  not not_4 (not_4_out, MemWrite);
  not not_5 (not_5_out, hit);
  not not_6 (not_6_out, MemWrite);
  not not_7 (not_7_out, hit);
  not not_8 (not_8_out, MemWrite);
  and and_9 (and_9_out, and_1_out, not_1_out, not_2_out);
  and and_10 (and_10_out, and_3_out, not_3_out, not_4_out);
  and and_11 (and_11_out, and_5_out, not_5_out, not_6_out);
  and and_12 (and_12_out, and_7_out, not_7_out, not_8_out);
  or or_14 (or_14_out, and_9_out, and_2_out);
  or or_15 (or_15_out, and_10_out, and_4_out);
  or or_16 (or_16_out, and_11_out, and_6_out);
  or or_17 (or_17_out, and_12_out, and_8_out);
  and and_13 (En1, or_14_out, En);
  and and_14 (En2, or_15_out, En);
  and and_15 (En3, or_16_out, En);
  and and_16 (En4, or_17_out, En);

  // Other names for the same wires on the sheet: Count1[15:0] = blockCount1; Count2[15:0] = blockCount2;
  //   Count3[15:0] = blockCount3; Count4[15:0] = blockCount4
endmodule

// Write1
module CacheGroup (
  input  [5:0] Tag,
  input  Clk,
  input  En,
  input  Reset,
  input  Stop,
  input  [31:0] Write1,
  input  [31:0] Write2,
  input  [31:0] Write3,
  input  [31:0] Write4,
  input  MemRead,
  input  MemWrite,
  output [31:0] output1,
  output [31:0] output2,
  output [31:0] output3,
  output [31:0] output4,
  output hit
);

  wire comparator_1_eq, comparator_2_eq, comparator_3_eq, comparator_4_eq, En1, En2, En3, En4, En_t, hit1,
       hit2, hit3, hit4, not_1_out, or_1_out, v1, v2, v3, v4;
  wire [2:0] BlockSel, multiplexer_1_out, multiplexer_2_out;
  wire [5:0] Tag1, Tag2, Tag3, Tag4;
  wire [15:0] count1, count2, count3, count4;
  wire [31:0] Read11, Read12, Read13, Read14, Read21, Read22, Read23, Read24, Read31, Read32, Read33, Read34,
       Read41, Read42, Read43, Read44, Writ3;

  and and_1 (En_t, En, not_1_out);
  not not_1 (not_1_out, Stop);
  Comparator #(.width(6)) comparator_1 (.a(Tag), .b(Tag1), .eq(comparator_1_eq));  // open: gt, lt
  Comparator #(.width(6)) comparator_2 (.a(Tag), .b(Tag2), .eq(comparator_2_eq));  // open: gt, lt
  Comparator #(.width(6)) comparator_3 (.a(Tag), .b(Tag3), .eq(comparator_3_eq));  // open: gt, lt
  Comparator #(.width(6)) comparator_4 (.a(Tag), .b(Tag4), .eq(comparator_4_eq));  // open: gt, lt
  and and_2 (hit1, comparator_1_eq, v1);
  and and_3 (hit2, comparator_2_eq, v2);
  and and_4 (hit3, comparator_3_eq, v3);
  and and_5 (hit4, comparator_4_eq, v4);
  LRU lru_1 (
    .blockCount1(count1), .blockCount2(count2), .En1(En1), .blockCount3(count3), .blockCount4(count4),
    .hit1(hit1), .hit2(hit2), .En2(En2), .hit3(hit3), .hit4(hit4), .MemRead(MemRead), .MemWrite(MemWrite),
    .En(En_t), .En3(En3), .En4(En4));
  CacheBlock1 cacheblock1_1 (
    .Reset(Reset), .Clk(Clk), .Enable(En1), .Blcok3(Write3), .Blcok4(Write4), .Tag(Tag), .Blcok1(Write1),
    .Blcok2(Write2), .V(v1), .Blcok3_2(Read13), .Blcok4_2(Read14), .Tag_2(Tag1), .Blcok1_2(Read11),
    .Blcok2_2(Read12));
  CacheBlock2 cacheblock2_1 (
    .Reset(Reset), .Clk(Clk), .Enable(En2), .Blcok3(Write3), .Blcok4(Write4), .Tag(Tag), .Blcok1(Write1),
    .Blcok2(Write2), .V(v2), .Blcok3_2(Read23), .Blcok4_2(Read24), .Tag_2(Tag2), .Blcok1_2(Read21),
    .Blcok2_2(Read22));
  CacheBlock3 cacheblock3_1 (
    .Reset(Reset), .Clk(Clk), .Enable(En3), .Blcok3(Writ3), .Blcok4(Write4), .Tag(Tag), .Blcok1(Write1),
    .Blcok2(Write2), .V(v3), .Blcok3_2(Read33), .Blcok4_2(Read34), .Tag_2(Tag3), .Blcok1_2(Read31),
    .Blcok2_2(Read32));
  CacheBlock4 cacheblock4_1 (
    .Reset(Reset), .Clk(Clk), .Enable(En4), .Blcok3(Write3), .Blcok4(Write4), .Tag(Tag), .Blcok1(Write1),
    .Blcok2(Write2), .V(v4), .Blcok3_2(Read43), .Blcok4_2(Read44), .Tag_2(Tag4), .Blcok1_2(Read41),
    .Blcok2_2(Read42));
  Counter counter_1 (.MemRead(MemRead), .Reset(Reset), .out_7(count1), .Clk(Clk), .hit(hit1), .En(En1), .GroupEn(En_t));
  Counter counter_2 (.MemRead(MemRead), .Reset(Reset), .out_7(count2), .Clk(Clk), .hit(hit2), .En(En2), .GroupEn(En_t));
  Counter counter_3 (.MemRead(MemRead), .Reset(Reset), .out_7(count3), .Clk(Clk), .hit(hit3), .En(En3), .GroupEn(En_t));
  Counter counter_4 (.MemRead(MemRead), .Reset(Reset), .out_7(count4), .Clk(Clk), .hit(hit4), .En(En4), .GroupEn(En_t));
  Multiplexer #(.width(3)) multiplexer_1 (.in0(3'b000), .in1(3'b001), .out(multiplexer_1_out), .sel(hit2));  // open: en
  Multiplexer #(.width(3)) multiplexer_2 (
    .in0(multiplexer_1_out), .in1(3'b010), .out(multiplexer_2_out), .sel(hit3));  // open: en
  Multiplexer #(.width(3)) multiplexer_3 (
    .in0(multiplexer_2_out), .in1(3'b011), .out(BlockSel), .sel(hit4));  // open: en
  Multiplexer #(.select(3), .width(32)) multiplexer_4 (
    .in0(Read11), .in1(Read21), .in2(Read31), .in3(Read41), .sel(BlockSel));  // open: in4, in5, in6, in7, out, en
  Multiplexer #(.select(3), .width(32)) multiplexer_5 (
    .in0(Read12), .in1(Read22), .in2(Read32), .in3(Read42), .sel(BlockSel));  // open: in4, in5, in6, in7, out, en
  Multiplexer #(.select(3), .width(32)) multiplexer_6 (
    .in0(Read13), .in1(Read23), .in2(Read33), .in3(Read43), .sel(BlockSel));  // open: in4, in5, in6, in7, out, en
  Multiplexer #(.select(3), .width(32)) multiplexer_7 (
    .in0(Read14), .in1(Read24), .in2(Read34), .in3(Read44), .sel(BlockSel));  // open: in4, in5, in6, in7, out, en
  or or_1 (or_1_out, hit1, hit2, hit3, hit4);
  and and_6 (hit, En, or_1_out);
  // AND_Gate and_7 is placed but not wired

  // Other names for the same wires on the sheet: Enin = En
endmodule
