// Logisim project cache 1.circ as structural Verilog: 6 circuits, main circuit Cache
module LRU (
  input  [15:0] in_1,
  input  [15:0] in_2,
  input  [15:0] in_3,
  input  [15:0] in_4,
  input  in_5,
  input  in_6,
  input  in_7,
  input  in_8,
  input  in_9,
  input  in_10,
  input  in_11,
  output Enable1,
  output Enable2,
  output Enable3,
  output Enable4
);

  wire comparator_1_gt, comparator_2_gt, comparator_7_eq, comparator_8_eq, comparator_9_eq, comparator_10_eq,
       comparator_11_gt, Enable1_1, Enable1_2, Enable2_1, Enable2_2, Enable3_1, Enable3_2, Enable4_1,
       Enable4_2, Hit, \new , not_1_out, not_2_out, or_2_out, or_3_out, or_4_out, or_5_out;
  wire [1:0] ans;
  wire [3:0] comparator_3_eq;
  wire [15:0] max, multiplexer_1_out, multiplexer_2_out;

  and and_1 (Enable1_1, in_5, in_10);
  and and_2 (Enable2_1, in_6, in_10);
  and and_3 (Enable3_1, in_7, in_10);
  and and_4 (Enable4_1, in_8, in_10);
  or or_1 (Hit, in_5, in_6, in_7, in_8);
  Comparator #(.width(16), .mode("unsigned")) comparator_1 (.a(in_1), .b(in_2), .gt(comparator_1_gt));  // open: eq, lt
  Comparator #(.width(16), .mode("unsigned")) comparator_2 (.a(in_3), .b(in_4), .gt(comparator_2_gt));  // open: eq, lt
  not not_1 (not_1_out, Hit);
  Comparator #(.width(16), .mode("unsigned")) comparator_3 (
    .a(in_1), .b(max), .eq(comparator_3_eq[0]));  // open: gt, lt
  Comparator #(.width(16), .mode("unsigned")) comparator_4 (
    .a(in_2), .b(max), .eq(comparator_3_eq[1]));  // open: gt, lt
  Comparator #(.width(16), .mode("unsigned")) comparator_5 (
    .a(in_3), .b(max), .eq(comparator_3_eq[2]));  // open: gt, lt
  Comparator #(.width(16), .mode("unsigned")) comparator_6 (
    .a(in_4), .b(max), .eq(comparator_3_eq[3]));  // open: gt, lt
  Multiplexer #(.width(16), .enable("false")) multiplexer_1 (
    .in0(in_2), .in1(in_1), .out(multiplexer_1_out), .sel(comparator_1_gt));
  Multiplexer #(.width(16), .enable("false")) multiplexer_2 (
    .in0(in_4), .in1(in_3), .out(multiplexer_2_out), .sel(comparator_2_gt));
  not not_2 (not_2_out, in_10);
  Comparator #(.width(2), .mode("unsigned")) comparator_7 (.a(2'b00), .b(ans), .eq(comparator_7_eq));  // open: gt, lt
  Comparator #(.width(2), .mode("unsigned")) comparator_8 (.a(2'b01), .b(ans), .eq(comparator_8_eq));  // open: gt, lt
  Comparator #(.width(2), .mode("unsigned")) comparator_9 (.a(2'b10), .b(ans), .eq(comparator_9_eq));  // open: gt, lt
  Comparator #(.width(2), .mode("unsigned")) comparator_10 (.a(2'b11), .b(ans), .eq(comparator_10_eq));  // open: gt, lt
  Comparator #(.width(16), .mode("unsigned")) comparator_11 (
    .a(multiplexer_1_out), .b(multiplexer_2_out), .gt(comparator_11_gt));  // open: eq, lt
  and and_5 (\new , not_2_out, not_1_out);
  and and_6 (Enable1_2, \new , comparator_7_eq);
  and and_7 (Enable2_2, \new , comparator_8_eq);
  and and_8 (Enable3_2, \new , comparator_9_eq);
  and and_9 (Enable4_2, \new , comparator_10_eq);
  Multiplexer #(.width(16), .enable("false")) multiplexer_3 (
    .in0(multiplexer_2_out), .in1(multiplexer_1_out), .out(max), .sel(comparator_11_gt));
  BitFinder #(.width(4)) bitfinder_1 (.in(comparator_3_eq), .index(ans));  // open: found
  or or_2 (or_2_out, Enable1_1, Enable1_2);
  or or_3 (or_3_out, Enable2_1, Enable2_2);
  or or_4 (or_4_out, Enable3_1, Enable3_2);
  or or_5 (or_5_out, Enable4_1, Enable4_2);
  and and_10 (Enable1, in_11, or_2_out);
  and and_11 (Enable2, in_11, or_3_out);
  and and_12 (Enable3, in_11, or_4_out);
  and and_13 (Enable4, in_11, or_5_out);

  // Other names for the same wires on the sheet: cnt1[15:0] = in_1; cnt2[15:0] = in_2; cnt3[15:0] = in_3;
  //   cnt4[15:0] = in_4; Enable = in_11; Hit1 = in_5; Hit2 = in_6; Hit3 = in_7; Hit4 = in_8; MemRead = in_9;
  //   MemWrite = in_10
endmodule

module Cache (
  input  [31:0] Addr,
  input  [31:0] Data_in,
  input  in_3,
  input  in_4,
  input  in_5,
  input  in_6,
  output [31:0] out_7,
  output out_8,
  output [15:0] out_9,
  output [15:0] out_10
);

  wire and_5_out, and_6_out, decoder_1_out0, decoder_1_out1, decoder_1_out2, decoder_1_out3, Enable1,
       Enable2, Enable3, Enable4, flag, Hit, Hit1, Hit2, Hit3, Hit4, not_1_out, not_2_out, not_3_out,
       or_1_out;
  wire [31:0] Bout1, Bout2, Bout3, Bout4, Data_out, group1_out_12, group1_out_13, group1_out_14,
       group1_out_15, group2_out_12, group2_out_13, group2_out_14, group2_out_15, group3_out_12,
       group3_out_13, group3_out_14, group3_out_15, group4_out_12, group4_out_13, group4_out_14,
       group4_out_15, multiplexer_2_out, multiplexer_3_out, multiplexer_4_out, multiplexer_5_out,
       multiplexer_6_out, multiplexer_7_out;

  or or_1 (or_1_out, in_4, out_8);
  Decoder #(.select(2), .enable("false")) decoder_1 (
    .out0(decoder_1_out0), .out1(decoder_1_out1), .out2(decoder_1_out2), .out3(decoder_1_out3),
    .sel(Addr[5:4]));
  or or_2 (Hit, Hit1, Hit2, Hit3, Hit4);
  Multiplexer #(.width(32), .enable("false")) multiplexer_1 (
    .in0(Data_out), .in1({32{1'b0}}), .out(out_7), .sel(or_1_out));
  or or_3 (flag, in_3, in_4);
  and and_1 (Enable1, decoder_1_out0, flag);
  and and_2 (Enable2, decoder_1_out1, flag);
  and and_3 (Enable3, decoder_1_out2, flag);
  and and_4 (Enable4, decoder_1_out3, flag);
  not not_1 (not_1_out, out_8);
  Counter #(.width(16), .max('hffff)) counter_1 (
    .count(and_5_out), .Q(out_9), .clk(in_5), .clr(in_6));  // open: load, D, carry
  and and_5 (and_5_out, in_3, not_1_out);
  group group1 (
    .in_1(Addr[11:6]), .in_2(in_5), .in_3(in_6), .in_4(Enable1), .in_5(out_8), .in_6(in_4), .in_7(in_3),
    .in_8(Bout1), .in_9(Bout2), .in_10(Bout3), .in_11(Bout4), .out_12(group1_out_12), .out_13(group1_out_13),
    .out_14(group1_out_14), .out_15(group1_out_15), .out_16(Hit1));
  group group2 (
    .in_1(Addr[11:6]), .in_2(in_5), .in_3(in_6), .in_4(Enable2), .in_5(out_8), .in_6(in_4), .in_7(in_3),
    .in_8(Bout1), .in_9(Bout2), .in_10(Bout3), .in_11(Bout4), .out_12(group2_out_12), .out_13(group2_out_13),
    .out_14(group2_out_14), .out_15(group2_out_15), .out_16(Hit2));
  group group3 (
    .in_1(Addr[11:6]), .in_2(in_5), .in_3(in_6), .in_4(Enable3), .in_5(out_8), .in_6(in_4), .in_7(in_3),
    .in_8(Bout1), .in_9(Bout2), .in_10(Bout3), .in_11(Bout4), .out_12(group3_out_12), .out_13(group3_out_13),
    .out_14(group3_out_14), .out_15(group3_out_15), .out_16(Hit3));
  group group4 (
    .in_1(Addr[11:6]), .in_2(in_5), .in_3(in_6), .in_4(Enable4), .in_5(out_8), .in_6(in_4), .in_7(in_3),
    .in_8(Bout1), .in_9(Bout2), .in_10(Bout3), .in_11(Bout4), .out_12(group4_out_12), .out_13(group4_out_13),
    .out_14(group4_out_14), .out_15(group4_out_15), .out_16(Hit4));
  not not_2 (not_2_out, out_8);
  Counter #(.width(16), .max('hffff)) counter_2 (
    .count(and_6_out), .Q(out_10), .clk(in_5), .clr(in_6));  // open: load, D, carry
  and and_6 (and_6_out, in_3, not_2_out, Hit);
  Multiplexer #(.select(2), .width(32)) multiplexer_2 (
    .in0(group1_out_12), .in1(group1_out_13), .in2(group1_out_14), .in3(group1_out_15),
    .out(multiplexer_2_out), .sel(Addr[3:2]));  // open: en
  Multiplexer #(.select(2), .width(32)) multiplexer_3 (
    .in0(group2_out_12), .in1(group2_out_13), .in2(group2_out_14), .in3(group2_out_15),
    .out(multiplexer_3_out), .sel(Addr[3:2]));  // open: en
  Multiplexer #(.select(2), .width(32)) multiplexer_4 (
    .in0(group3_out_12), .in1(group3_out_13), .in2(group3_out_14), .in3(group3_out_15),
    .out(multiplexer_4_out), .sel(Addr[3:2]));  // open: en
  Multiplexer #(.select(2), .width(32)) multiplexer_5 (
    .in0(group4_out_12), .in1(group4_out_13), .in2(group4_out_14), .in3(group4_out_15),
    .out(multiplexer_5_out), .sel(Addr[3:2]));  // open: en
  Multiplexer #(.select(2), .width(32)) multiplexer_6 (
    .in0(multiplexer_2_out), .in1(multiplexer_3_out), .in2(multiplexer_4_out), .in3(multiplexer_5_out),
    .out(multiplexer_6_out), .sel(Addr[5:4]));  // open: en
  Multiplexer #(.select(2), .width(32)) multiplexer_7 (
    .in0(Bout1), .in1(Bout2), .in2(Bout3), .in3(Bout4), .out(multiplexer_7_out), .sel(Addr[3:2]));  // open: en
  Multiplexer #(.width(32), .enable("false")) multiplexer_8 (
    .in0(multiplexer_6_out), .in1(multiplexer_7_out), .out(Data_out), .sel(not_3_out));
  not not_3 (not_3_out, Hit);
  RAM ram_1 (
    .MuxBlock(Addr[3:2]), .MemWrite(in_4), .MemRead(in_3), .Hit(Hit), .Tag(Addr[11:6]), .MuxGroup(Addr[5:4]),
    .MemData(Data_in), .Clk(in_5), .Reset(in_6), ._4(Bout4), ._3(Bout3), ._2(Bout2), .out_13(out_8),
    ._1(Bout1));

  // Other names for the same wires on the sheet: MuxBlock[1:0] = Addr[3:2]; MuxGroup[1:0] = Addr[5:4];
  //   Tag[5:0] = Addr[11:6]; Clock = in_5; HitTimes[15:0] = out_10; MemRead = in_3; MemWrite = in_4;
  //   ReadTimes[15:0] = out_9; Reset = in_6; Stop = out_8
endmodule

module RAM (
  input  [1:0] MuxBlock,
  input  MemWrite,
  input  MemRead,
  input  Hit,
  input  [5:0] Tag,
  input  [1:0] MuxGroup,
  input  [31:0] MemData,
  input  Clk,
  input  Reset,
  output [31:0] _4,
  output [31:0] _3,
  output [31:0] _2,
  output out_13,
  output [31:0] _1
);

  wire _1_t, _2_t, _3_t, _4_t, and_1_out, and_2_out, counter_1_carry, not_1_out, not_2_out;
  wire [9:0] adder_1_out, adder_2_out, adder_3_out, adder_4_out, multiplexer_1_out;
  wire [31:0] ram_1_data, ram_2_data, ram_3_data, ram_4_data;

  and and_1 (and_1_out, MemRead, not_1_out);
  not not_1 (not_1_out, Hit);
  Counter #(.width(3), .max('h5)) counter_1 (
    .count(and_1_out), .carry(counter_1_carry), .clk(Clk), .clr(Reset));  // open: load, D, Q
  and and_2 (and_2_out, MemRead, Hit);
  and and_3 (out_13, and_1_out, not_2_out);
  not not_2 (not_2_out, counter_1_carry);
  Demultiplexer #(.select(2)) demultiplexer_1 (
    .out0(_1_t), .out1(_2_t), .out2(_3_t), .out3(_4_t), .in(MemWrite), .sel(MuxBlock));  // open: en
  Multiplexer #(.width(10), .enable("false")) multiplexer_1 (
    .in0({Tag, MuxGroup, 2'b00}), .in1({10{1'b0}}), .out(multiplexer_1_out), .sel(and_2_out));
  Adder #(.width(10)) adder_1 (.a(10'h3), .b(multiplexer_1_out), .out(adder_1_out));  // open: cin, cout
  Adder #(.width(10)) adder_2 (.a(10'h2), .b(multiplexer_1_out), .out(adder_2_out));  // open: cin, cout
  Adder #(.width(10)) adder_3 (.a(10'h1), .b(multiplexer_1_out), .out(adder_3_out));  // open: cin, cout
  Adder #(.width(10)) adder_4 (.a({10{1'b0}}), .b(multiplexer_1_out), .out(adder_4_out));  // open: cin, cout
  RAM_part #(.addrWidth(10), .dataWidth(32), .bus("separate")) ram_1 (
    .addr(adder_1_out), .din(MemData), .data(ram_1_data), .str(_4_t), .clk(Clk), .clr(Reset));  // open: sel, ld
  RAM_part #(.addrWidth(10), .dataWidth(32), .bus("separate")) ram_2 (
    .addr(adder_2_out), .din(MemData), .data(ram_2_data), .str(_3_t), .clk(Clk), .clr(Reset));  // open: sel, ld
  RAM_part #(.addrWidth(10), .dataWidth(32), .bus("separate")) ram_3 (
    .addr(adder_3_out), .din(MemData), .data(ram_3_data), .str(_2_t), .clk(Clk), .clr(Reset));  // open: sel, ld
  RAM_part #(.addrWidth(10), .dataWidth(32), .bus("separate")) ram_4 (
    .addr(adder_4_out), .din(MemData), .data(ram_4_data), .str(_1_t), .clk(Clk), .clr(Reset));  // open: sel, ld
  Multiplexer #(.width(32), .enable("false")) multiplexer_2 (.in0(ram_1_data), .in1(MemData), .out(_4), .sel(_4_t));
  Multiplexer #(.width(32), .enable("false")) multiplexer_3 (.in0(ram_2_data), .in1(MemData), .out(_3), .sel(_3_t));
  Multiplexer #(.width(32), .enable("false")) multiplexer_4 (.in0(ram_3_data), .in1(MemData), .out(_2), .sel(_2_t));
  Multiplexer #(.width(32), .enable("false")) multiplexer_5 (.in0(ram_4_data), .in1(MemData), .out(_1), .sel(_1_t));

  // Other names for the same wires on the sheet: Data[31:0] = MemData
endmodule

module block (
  input  in_1,
  input  in_2,
  input  in_3,
  input  [5:0] in_4,
  input  [31:0] in_5,
  input  [31:0] in_6,
  input  [31:0] in_7,
  input  [31:0] in_8,
  output [31:0] out_9,
  output [31:0] out_10,
  output [31:0] out_11,
  output [31:0] out_12,
  output out_13,
  output [5:0] out_14
);

  Register #(.width(32)) register_1 (.D(in_5), .en(in_3), .Q(out_9), .clk(in_2), .clr(in_1));
  Register #(.width(32)) register_2 (.D(in_6), .en(in_3), .Q(out_10), .clk(in_2), .clr(in_1));
  Register #(.width(32)) register_3 (.D(in_7), .en(in_3), .Q(out_11), .clk(in_2), .clr(in_1));
  Register #(.width(32)) register_4 (.D(in_8), .en(in_3), .Q(out_12), .clk(in_2), .clr(in_1));
  Register #(.width(1)) register_5 (.D(1'b1), .en(in_3), .Q(out_13), .clk(in_2), .clr(in_1));
  Register #(.width(6)) register_6 (.D(in_4), .en(in_3), .Q(out_14), .clk(in_2), .clr(in_1));

  // Other names for the same wires on the sheet: Clock = in_2; Data1_in[31:0] = in_5; Data1_out[31:0] = out_9;
  //   Data2_in[31:0] = in_6; Data2_out[31:0] = out_10; Data3_in[31:0] = in_7; Data3_out[31:0] = out_11;
  //   Data4_in[31:0] = in_8; Data4_out[31:0] = out_12; Enable = in_3; Reset = in_1; Tag_in[5:0] = in_4;
  //   Tag_out[5:0] = out_14; V = out_13
endmodule

module group (
  input  [5:0] in_1,
  input  in_2,
  input  in_3,
  input  in_4,
  input  in_5,
  input  in_6,
  input  in_7,
  input  [31:0] in_8,
  input  [31:0] in_9,
  input  [31:0] in_10,
  input  [31:0] in_11,
  output [31:0] out_12,
  output [31:0] out_13,
  output [31:0] out_14,
  output [31:0] out_15,
  output out_16
);

  wire and_1_out, comparator_1_eq, comparator_2_eq, comparator_3_eq, comparator_4_eq, Enable1, Enable2,
       Enable3, Enable4, Hit1, Hit2, Hit3, Hit4, lru_1_enable1, lru_1_enable2, lru_1_enable3, lru_1_enable4,
       not_1_out, not_2_out, or_1_out, v1, v2, v3, v4;
  wire [1:0] Ans;
  wire [5:0] Tag1_out, Tag2_out, Tag3_out, Tag4_out;
  wire [15:0] cnt1, cnt2, cnt3, cnt4;
  wire [31:0] block_1_out_9, block_1_out_10, block_1_out_11, block_1_out_12, block_2_out_9, block_2_out_10,
       block_2_out_11, block_2_out_12, block_3_out_9, block_3_out_10, block_3_out_11, block_3_out_12,
       block_4_out_9, block_4_out_10, block_4_out_11, block_4_out_12;

  block block_1 (
    .in_1(in_3), .in_3(Enable1), .in_4(in_1), .in_5(in_8), .in_6(in_9), .in_7(in_10), .in_8(in_11),
    .out_9(block_1_out_9), .out_10(block_1_out_10), .out_11(block_1_out_11), .out_12(block_1_out_12),
    .out_13(v1), .in_2(in_2), .out_14(Tag1_out));
  block block_2 (
    .in_1(in_3), .in_3(Enable2), .in_4(in_1), .in_5(in_8), .in_6(in_9), .in_7(in_10), .in_8(in_11),
    .out_9(block_2_out_9), .out_10(block_2_out_10), .out_11(block_2_out_11), .out_12(block_2_out_12),
    .out_13(v2), .in_2(in_2), .out_14(Tag2_out));
  block block_3 (
    .in_1(in_3), .in_3(Enable3), .in_4(in_1), .in_5(in_8), .in_6(in_9), .in_7(in_10), .in_8(in_11),
    .out_9(block_3_out_9), .out_10(block_3_out_10), .out_11(block_3_out_11), .out_12(block_3_out_12),
    .out_13(v3), .in_2(in_2), .out_14(Tag3_out));
  block block_4 (
    .in_1(in_3), .in_3(Enable4), .in_4(in_1), .in_5(in_8), .in_6(in_9), .in_7(in_10), .in_8(in_11),
    .out_9(block_4_out_9), .out_10(block_4_out_10), .out_11(block_4_out_11), .out_12(block_4_out_12),
    .out_13(v4), .in_2(in_2), .out_14(Tag4_out));
  not not_1 (not_1_out, in_5);
  and and_1 (and_1_out, in_4, not_1_out);
  LRU lru_1 (
    .in_1(cnt1), .in_2(cnt2), .in_3(cnt3), .in_4(cnt4), .in_5(Hit1), .in_6(Hit2), .in_7(Hit3), .in_8(Hit4),
    .in_9(in_7), .in_10(in_6), .in_11(and_1_out), .Enable1(lru_1_enable1), .Enable2(lru_1_enable2),
    .Enable3(lru_1_enable3), .Enable4(lru_1_enable4));
  not not_2 (not_2_out, in_5);
  and and_2 (Enable1, lru_1_enable1, not_2_out);
  and and_3 (Enable2, lru_1_enable2, not_2_out);
  and and_4 (Enable3, lru_1_enable3, not_2_out);
  and and_5 (Enable4, lru_1_enable4, not_2_out);
  counter counter_1 (
    .in_1(in_7), .in_2(in_6), .in_3(Hit4), .in_4(in_2), .in_5(in_3), .cnt_out(cnt4), .in_6(in_4),
    .in_7(in_5), .in_8(Enable4));
  Multiplexer #(.select(2), .width(32), .enable("false")) multiplexer_1 (
    .in0(block_1_out_9), .in1(block_2_out_9), .in2(block_3_out_9), .in3(block_4_out_9), .out(out_12),
    .sel(Ans));
  Multiplexer #(.select(2), .width(32), .enable("false")) multiplexer_2 (
    .in0(block_1_out_10), .in1(block_2_out_10), .in2(block_3_out_10), .in3(block_4_out_10), .out(out_13),
    .sel(Ans));
  Multiplexer #(.select(2), .width(32), .enable("false")) multiplexer_3 (
    .in0(block_1_out_11), .in1(block_2_out_11), .in2(block_3_out_11), .in3(block_4_out_11), .out(out_14),
    .sel(Ans));
  Multiplexer #(.select(2), .width(32), .enable("false")) multiplexer_4 (
    .in0(block_1_out_12), .in1(block_2_out_12), .in2(block_3_out_12), .in3(block_4_out_12), .out(out_15),
    .sel(Ans));
  or or_1 (or_1_out, Hit1, Hit2, Hit3, Hit4);
  counter counter_2 (
    .in_1(in_7), .in_2(in_6), .in_3(Hit1), .in_4(in_2), .in_5(in_3), .cnt_out(cnt1), .in_6(in_4),
    .in_7(in_5), .in_8(Enable1));
  counter counter_3 (
    .in_1(in_7), .in_2(in_6), .in_3(Hit2), .in_4(in_2), .in_5(in_3), .cnt_out(cnt2), .in_6(in_4),
    .in_7(in_5), .in_8(Enable2));
  counter counter_4 (
    .in_1(in_7), .in_2(in_6), .in_3(Hit3), .in_4(in_2), .in_5(in_3), .cnt_out(cnt3), .in_6(in_4),
    .in_7(in_5), .in_8(Enable3));
  Comparator #(.width(6), .mode("unsigned")) comparator_1 (
    .a(in_1), .b(Tag1_out), .eq(comparator_1_eq));  // open: gt, lt
  Comparator #(.width(6), .mode("unsigned")) comparator_2 (
    .a(in_1), .b(Tag2_out), .eq(comparator_2_eq));  // open: gt, lt
  Comparator #(.width(6), .mode("unsigned")) comparator_3 (
    .a(in_1), .b(Tag3_out), .eq(comparator_3_eq));  // open: gt, lt
  Comparator #(.width(6), .mode("unsigned")) comparator_4 (
    .a(in_1), .b(Tag4_out), .eq(comparator_4_eq));  // open: gt, lt
  and and_6 (out_16, in_4, or_1_out);
  BitFinder #(.width(4)) bitfinder_1 (.in({Hit4, Hit3, Hit2, Hit1}), .index(Ans));  // open: found
  and and_7 (Hit1, in_4, comparator_1_eq, v1);
  and and_8 (Hit2, in_4, comparator_2_eq, v2);
  and and_9 (Hit3, in_4, comparator_3_eq, v3);
  and and_10 (Hit4, in_4, comparator_4_eq, v4);

  // Other names for the same wires on the sheet: Clock = in_2; Data1_in[31:0] = in_8; Data1_out[31:0] = out_12;
  //   Data2_in[31:0] = in_9; Data2_out[31:0] = out_13; Data3_in[31:0] = in_10; Data3_out[31:0] = out_14;
  //   Data4_in[31:0] = in_11; Data4_out[31:0] = out_15; Enable = in_4; Hit = out_16; MemRead = in_7; MemWrite = in_6;
  //   Reset = in_3; Stop = in_5; Tag_in[5:0] = in_1
endmodule

module counter (
  input  in_1,
  input  in_2,
  input  in_3,
  input  in_4,
  input  in_5,
  input  in_6,
  input  in_7,
  input  in_8,
  output [15:0] cnt_out
);

  wire Add1, and_2_out, and_4_out, and_5_out, and_6_out, not_1_out, not_2_out, not_3_out, not_4_out,
       or_1_out, or_2_out, Zero;

  or or_1 (or_1_out, in_3, in_8);
  not not_1 (not_1_out, in_3);
  not not_2 (not_2_out, in_8);
  and and_1 (Zero, or_1_out, in_1, in_6);
  and and_2 (and_2_out, not_1_out, not_2_out);
  and and_3 (Add1, and_2_out, in_1, in_6);
  not not_3 (not_3_out, in_3);
  and and_4 (and_4_out, not_3_out, in_1, in_8);
  and and_5 (and_5_out, Add1, not_4_out);
  not not_4 (not_4_out, Zero);
  buf and_6 (and_6_out, and_5_out);  // AND_Gate
  or or_2 (or_2_out, and_4_out, Zero);
  Counter #(.width(16), .max('hffff)) counter_1 (
    .load(or_2_out), .D({16{1'b0}}), .count(and_6_out), .Q(cnt_out), .clk(in_4), .clr(in_5));  // open: carry

  // Other names for the same wires on the sheet: Clock = in_4; Enable = in_6; Enable_block = in_8; Hit = in_3;
  //   MemRead = in_1; MemWrite = in_2; Reset = in_5; Stop = in_7
endmodule
