// Logisim project p5.circ as structural Verilog: 6 circuits, main circuit LRU
module LRU (
  input  [15:0] cal1,
  input  [15:0] cal2,
  input  [15:0] cal3,
  input  [15:0] cal4,
  input  hit1,
  input  hit2,
  input  hit3,
  input  hit4,
  input  memread,
  input  memwrite,
  input  clock,
  output block1,
  output block2,
  output block3,
  output block4
);

  wire and_1_out, and_2_out, and_3_out, and_4_out, and_5_out, and_6_out, and_7_out, and_8_out,
       comparator_1_eq, comparator_1_gt, comparator_2_eq, comparator_2_gt, comparator_3_eq, comparator_3_gt,
       comparator_4_gt, comparator_5_eq, comparator_5_gt, comparator_6_eq, comparator_6_gt, comparator_7_gt,
       comparator_8_gt, comparator_9_eq, comparator_9_gt, comparator_10_gt, comparator_11_gt,
       comparator_12_gt, hit, not_1_out, not_2_out, not_3_out, not_4_out, not_5_out, not_6_out, not_7_out,
       not_8_out, or_2_out, or_3_out, or_4_out, or_5_out, or_6_out, or_7_out, or_8_out, or_9_out, or_10_out,
       or_11_out, or_12_out, or_13_out, or_14_out, or_15_out, or_16_out, or_17_out;

  or or_1 (hit, hit1, hit2, hit3, hit4);
  Comparator #(.width(16), .mode("unsigned")) comparator_1 (
    .a(cal1), .b(cal2), .gt(comparator_1_gt), .eq(comparator_1_eq));  // open: lt
  Comparator #(.width(16), .mode("unsigned")) comparator_2 (
    .a(cal1), .b(cal3), .gt(comparator_2_gt), .eq(comparator_2_eq));  // open: lt
  Comparator #(.width(16), .mode("unsigned")) comparator_3 (
    .a(cal1), .b(cal4), .gt(comparator_3_gt), .eq(comparator_3_eq));  // open: lt
  Comparator #(.width(16), .mode("unsigned")) comparator_4 (.a(cal2), .b(cal1), .gt(comparator_4_gt));  // open: eq, lt
  Comparator #(.width(16), .mode("unsigned")) comparator_5 (
    .a(cal2), .b(cal3), .gt(comparator_5_gt), .eq(comparator_5_eq));  // open: lt
  Comparator #(.width(16), .mode("unsigned")) comparator_6 (
    .a(cal2), .b(cal4), .gt(comparator_6_gt), .eq(comparator_6_eq));  // open: lt
  Comparator #(.width(16), .mode("unsigned")) comparator_7 (.a(cal3), .b(cal1), .gt(comparator_7_gt));  // open: eq, lt
  Comparator #(.width(16), .mode("unsigned")) comparator_8 (.a(cal3), .b(cal2), .gt(comparator_8_gt));  // open: eq, lt
  Comparator #(.width(16), .mode("unsigned")) comparator_9 (
    .a(cal3), .b(cal4), .gt(comparator_9_gt), .eq(comparator_9_eq));  // open: lt
  Comparator #(.width(16), .mode("unsigned")) comparator_10 (
    .a(cal4), .b(cal1), .gt(comparator_10_gt));  // open: eq, lt
  Comparator #(.width(16), .mode("unsigned")) comparator_11 (
    .a(cal4), .b(cal2), .gt(comparator_11_gt));  // open: eq, lt
  Comparator #(.width(16), .mode("unsigned")) comparator_12 (
    .a(cal4), .b(cal3), .gt(comparator_12_gt));  // open: eq, lt
  or or_2 (or_2_out, comparator_1_gt, comparator_1_eq);
  or or_3 (or_3_out, comparator_2_gt, comparator_2_eq);
  or or_4 (or_4_out, comparator_3_gt, comparator_3_eq);
  not not_1 (not_1_out, hit);
  not not_2 (not_2_out, memwrite);
  buf or_5 (or_5_out, comparator_4_gt);  // OR_Gate
  or or_6 (or_6_out, comparator_5_gt, comparator_5_eq);
  or or_7 (or_7_out, comparator_6_gt, comparator_6_eq);
  not not_3 (not_3_out, hit);
  not not_4 (not_4_out, memwrite);
  buf or_8 (or_8_out, comparator_7_gt);  // OR_Gate
  buf or_9 (or_9_out, comparator_8_gt);  // OR_Gate
  or or_10 (or_10_out, comparator_9_gt, comparator_9_eq);
  not not_5 (not_5_out, hit);
  not not_6 (not_6_out, memwrite);
  buf or_11 (or_11_out, comparator_10_gt);  // OR_Gate
  buf or_12 (or_12_out, comparator_11_gt);  // OR_Gate
  buf or_13 (or_13_out, comparator_12_gt);  // OR_Gate
  not not_7 (not_7_out, hit);
  not not_8 (not_8_out, memwrite);
  and and_1 (and_1_out, or_2_out, or_3_out, or_4_out, not_1_out, not_2_out);
  and and_2 (and_2_out, hit1, memwrite);
  and and_3 (and_3_out, or_5_out, or_6_out, or_7_out, not_3_out, not_4_out);
  and and_4 (and_4_out, hit2, memwrite);
  and and_5 (and_5_out, or_8_out, or_9_out, or_10_out, not_5_out, not_6_out);
  and and_6 (and_6_out, hit3, memwrite);
  and and_7 (and_7_out, or_11_out, or_12_out, or_13_out, not_7_out, not_8_out);
  and and_8 (and_8_out, hit4, memwrite);
  or or_14 (or_14_out, and_1_out, and_2_out);
  or or_15 (or_15_out, and_3_out, and_4_out);
  or or_16 (or_16_out, and_5_out, and_6_out);
  or or_17 (or_17_out, and_7_out, and_8_out);
  and and_9 (block1, or_14_out, clock);
  and and_10 (block2, or_15_out, clock);
  and and_11 (block3, or_16_out, clock);
  and and_12 (block4, or_17_out, clock);
endmodule

module RAM (
  input  [1:0] MuxBlock,
  input  MemWrite,
  input  MemRead,
  input  Hit,
  input  [5:0] Tag,
  input  [1:0] MuxGroup,
  input  [31:0] MemData,
  input  Clk,
  input  Reset,
  output [31:0] _4,
  output [31:0] _3,
  output [31:0] _2,
  output out_13,
  output [31:0] _1
);

  wire _1_t, _2_t, _3_t, _4_t, and_1_out, and_2_out, counter_1_carry, not_1_out, not_2_out;
  wire [9:0] adder_1_out, adder_2_out, adder_3_out, adder_4_out, multiplexer_1_out;
  wire [31:0] ram_1_data, ram_2_data, ram_3_data, ram_4_data;

  and and_1 (and_1_out, MemRead, not_1_out);
  not not_1 (not_1_out, Hit);
  Counter #(.width(3), .max('h5)) counter_1 (
    .count(and_1_out), .carry(counter_1_carry), .clk(Clk), .clr(Reset));  // open: load, D, Q
  and and_2 (and_2_out, MemRead, Hit);
  and and_3 (out_13, and_1_out, not_2_out);
  not not_2 (not_2_out, counter_1_carry);
  Demultiplexer #(.select(2)) demultiplexer_1 (
    .out0(_1_t), .out1(_2_t), .out2(_3_t), .out3(_4_t), .in(MemWrite), .sel(MuxBlock));  // open: en
  Multiplexer #(.width(10), .enable("false")) multiplexer_1 (
    .in0({Tag, MuxGroup, 2'b00}), .in1({10{1'b0}}), .out(multiplexer_1_out), .sel(and_2_out));
  Adder #(.width(10)) adder_1 (.a(10'h3), .b(multiplexer_1_out), .out(adder_1_out));  // open: cin, cout
  Adder #(.width(10)) adder_2 (.a(10'h2), .b(multiplexer_1_out), .out(adder_2_out));  // open: cin, cout
  Adder #(.width(10)) adder_3 (.a(10'h1), .b(multiplexer_1_out), .out(adder_3_out));  // open: cin, cout
  Adder #(.width(10)) adder_4 (.a({10{1'b0}}), .b(multiplexer_1_out), .out(adder_4_out));  // open: cin, cout
  RAM_part #(.addrWidth(10), .dataWidth(32), .bus("separate")) ram_1 (
    .addr(adder_1_out), .din(MemData), .data(ram_1_data), .str(_4_t), .clk(Clk), .clr(Reset));  // open: sel, ld
  RAM_part #(.addrWidth(10), .dataWidth(32), .bus("separate")) ram_2 (
    .addr(adder_2_out), .din(MemData), .data(ram_2_data), .str(_3_t), .clk(Clk), .clr(Reset));  // open: sel, ld
  RAM_part #(.addrWidth(10), .dataWidth(32), .bus("separate")) ram_3 (
    .addr(adder_3_out), .din(MemData), .data(ram_3_data), .str(_2_t), .clk(Clk), .clr(Reset));  // open: sel, ld
  RAM_part #(.addrWidth(10), .dataWidth(32), .bus("separate")) ram_4 (
    .addr(adder_4_out), .din(MemData), .data(ram_4_data), .str(_1_t), .clk(Clk), .clr(Reset));  // open: sel, ld
  Multiplexer #(.width(32), .enable("false")) multiplexer_2 (.in0(ram_1_data), .in1(MemData), .out(_4), .sel(_4_t));
  Multiplexer #(.width(32), .enable("false")) multiplexer_3 (.in0(ram_2_data), .in1(MemData), .out(_3), .sel(_3_t));
  Multiplexer #(.width(32), .enable("false")) multiplexer_4 (.in0(ram_3_data), .in1(MemData), .out(_2), .sel(_2_t));
  Multiplexer #(.width(32), .enable("false")) multiplexer_5 (.in0(ram_4_data), .in1(MemData), .out(_1), .sel(_1_t));

  // Other names for the same wires on the sheet: Data[31:0] = MemData
endmodule

module Cache (
  input  [31:0] addr,
  input  [31:0] Data,
  input  mr,
  input  mw,
  input  clk,
  input  reset,
  output [31:0] out_7,
  output [15:0] all,
  output [15:0] hit,
  output stop
);

  wire and_1_out, and_2_out, decoder_1_out0, decoder_1_out1, decoder_1_out2, decoder_1_out3, en1, en2, en3,
       en4, hit1, hit2, hit3, hit4, hit_t, not_1_out, or_2_out, read_or_write;
  wire [31:0] bout1, bout2, bout3, bout4, cachegroup_1_output1, cachegroup_1_output2, cachegroup_1_output3,
       cachegroup_1_output4, cachegroup_2_output1, cachegroup_2_output2, cachegroup_2_output3,
       cachegroup_2_output4, cachegroup_3_output1, cachegroup_3_output2, cachegroup_3_output3,
       cachegroup_3_output4, cachegroup_4_output1, cachegroup_4_output2, cachegroup_4_output3,
       cachegroup_4_output4, multiplexer_2_out, multiplexer_3_out, multiplexer_4_out, multiplexer_5_out,
       multiplexer_6_out, multiplexer_7_out, Out;

  Multiplexer #(.width(32), .enable("false")) multiplexer_1 (.in0(Out), .in1({32{1'b0}}), .out(out_7), .sel(or_2_out));
  or or_1 (read_or_write, mr, mw);
  or or_2 (or_2_out, mw, stop);
  and and_1 (and_1_out, mr, ~stop);  // AND_Gate
  and and_2 (and_2_out, mr, ~stop, hit_t);  // AND_Gate
  Decoder #(.select(2)) decoder_1 (
    .out0(decoder_1_out0), .out1(decoder_1_out1), .out2(decoder_1_out2), .out3(decoder_1_out3),
    .sel(addr[5:4]));  // open: en
  or or_3 (hit_t, hit1, hit2, hit3, hit4);
  Counter #(.width(16), .max('hffff)) counter_1 (
    .count(and_1_out), .Q(all), .clk(clk), .clr(reset));  // open: load, D, carry
  Counter #(.width(16), .max('hffff)) counter_2 (
    .count(and_2_out), .Q(hit), .clk(clk), .clr(reset));  // open: load, D, carry
  and and_3 (en1, decoder_1_out0, read_or_write);
  and and_4 (en2, decoder_1_out1, read_or_write);
  and and_5 (en3, decoder_1_out2, read_or_write);
  and and_6 (en4, decoder_1_out3, read_or_write);
  CacheGroup cachegroup_1 (
    .data1(bout1), .data2(bout2), .data3(bout3), .data4(bout4), .MemRead(mr), .MemWrite(mw),
    .Tag(addr[11:6]), .Clk(clk), .en(en1), .stop(stop), .reset(reset), .output1(cachegroup_1_output1),
    .output2(cachegroup_1_output2), .output3(cachegroup_1_output3), .output4(cachegroup_1_output4), .hit(hit1));
  CacheGroup cachegroup_2 (
    .data1(bout1), .data2(bout2), .data3(bout3), .data4(bout4), .MemRead(mr), .MemWrite(mw),
    .Tag(addr[11:6]), .Clk(clk), .en(en2), .stop(stop), .reset(reset), .output1(cachegroup_2_output1),
    .output2(cachegroup_2_output2), .output3(cachegroup_2_output3), .output4(cachegroup_2_output4), .hit(hit2));
  CacheGroup cachegroup_3 (
    .data1(bout1), .data2(bout2), .data3(bout3), .data4(bout4), .MemRead(mr), .MemWrite(mw),
    .Tag(addr[11:6]), .Clk(clk), .en(en3), .stop(stop), .reset(reset), .output1(cachegroup_3_output1),
    .output2(cachegroup_3_output2), .output3(cachegroup_3_output3), .output4(cachegroup_3_output4), .hit(hit3));
  CacheGroup cachegroup_4 (
    .data1(bout1), .data2(bout2), .data3(bout3), .data4(bout4), .MemRead(mr), .MemWrite(mw),
    .Tag(addr[11:6]), .Clk(clk), .en(en4), .stop(stop), .reset(reset), .output1(cachegroup_4_output1),
    .output2(cachegroup_4_output2), .output3(cachegroup_4_output3), .output4(cachegroup_4_output4), .hit(hit4));
  Multiplexer #(.select(2), .width(32)) multiplexer_2 (
    .in0(cachegroup_1_output1), .in1(cachegroup_1_output2), .in2(cachegroup_1_output3),
    .in3(cachegroup_1_output4), .out(multiplexer_2_out), .sel(addr[3:2]));  // open: en
  Multiplexer #(.select(2), .width(32)) multiplexer_3 (
    .in0(cachegroup_2_output1), .in1(cachegroup_2_output2), .in2(cachegroup_2_output3),
    .in3(cachegroup_2_output4), .out(multiplexer_3_out), .sel(addr[3:2]));  // open: en
  Multiplexer #(.select(2), .width(32)) multiplexer_4 (
    .in0(cachegroup_3_output1), .in1(cachegroup_3_output2), .in2(cachegroup_3_output3),
    .in3(cachegroup_3_output4), .out(multiplexer_4_out), .sel(addr[3:2]));  // open: en
  Multiplexer #(.select(2), .width(32)) multiplexer_5 (
    .in0(cachegroup_4_output1), .in1(cachegroup_4_output2), .in2(cachegroup_4_output3),
    .in3(cachegroup_4_output4), .out(multiplexer_5_out), .sel(addr[3:2]));  // open: en
  RAM ram_1 (
    .MuxBlock(addr[3:2]), .MemWrite(mw), .MemRead(mr), .Hit(hit_t), .Tag(addr[11:6]), .MuxGroup(addr[5:4]),
    .MemData(Data), .Clk(clk), .Reset(reset), ._4(bout4), ._3(bout3), ._2(bout2), .out_13(stop), ._1(bout1));
  Multiplexer #(.select(2), .width(32)) multiplexer_6 (
    .in0(multiplexer_2_out), .in1(multiplexer_3_out), .in2(multiplexer_4_out), .in3(multiplexer_5_out),
    .out(multiplexer_6_out), .sel(addr[5:4]));  // open: en
  Multiplexer #(.select(2), .width(32)) multiplexer_7 (
    .in0(bout1), .in1(bout2), .in2(bout3), .in3(bout4), .out(multiplexer_7_out), .sel(addr[3:2]));  // open: en
  Multiplexer #(.width(32), .enable("false")) multiplexer_8 (
    .in0(multiplexer_6_out), .in1(multiplexer_7_out), .out(Out), .sel(not_1_out));
  not not_1 (not_1_out, hit_t);

  // Other names for the same wires on the sheet: MuxBlock[1:0] = addr[3:2]; MuxGroup[1:0] = addr[5:4];
  //   tag[5:0] = addr[11:6]; MemRead = mr; MemWrite = mw
endmodule

module CacheBlock (
  input  Reset,
  input  Clk,
  input  Enable,
  input  [31:0] Blcok4,
  input  [31:0] Blcok3,
  input  [31:0] Blcok2,
  input  [31:0] Blcok1,
  input  [5:0] Tag,
  output [31:0] Blcok4_2,
  output [31:0] Blcok3_2,
  output [31:0] Blcok2_2,
  output [31:0] Blcok1_2,
  output v,
  output [5:0] Tag_2
);

  Register #(.width(1)) register_1 (.D(1'b1), .en(Enable), .Q(v), .clk(Clk), .clr(Reset));
  Register #(.width(6)) register_2 (.D(Tag), .en(Enable), .Q(Tag_2), .clk(Clk), .clr(Reset));
  Register #(.width(32)) register_3 (.D(Blcok1), .en(Enable), .Q(Blcok1_2), .clk(Clk), .clr(Reset));
  Register #(.width(32)) register_4 (.D(Blcok2), .en(Enable), .Q(Blcok2_2), .clk(Clk), .clr(Reset));
  Register #(.width(32)) register_5 (.D(Blcok3), .en(Enable), .Q(Blcok3_2), .clk(Clk), .clr(Reset));
  Register #(.width(32)) register_6 (.D(Blcok4), .en(Enable), .Q(Blcok4_2), .clk(Clk), .clr(Reset));

  // Other names for the same wires on the sheet: En = Enable
endmodule

module CacheGroup (
  input  [5:0] Tag,
  input  Clk,
  input  en,
  input  stop,
  input  reset,
  input  [31:0] data1,
  input  [31:0] data2,
  input  [31:0] data3,
  input  [31:0] data4,
  input  MemRead,
  input  MemWrite,
  output [31:0] output1,
  output [31:0] output2,
  output [31:0] output3,
  output [31:0] output4,
  output hit
);

  wire comparator_1_eq, comparator_2_eq, comparator_3_eq, comparator_4_eq, En1, En2, En3, En4, En_t, hit1,
       hit2, hit3, hit4, not_1_out, or_1_out, v1, v2, v3, v4;
  wire [2:0] BlockSel, multiplexer_1_out, multiplexer_2_out;
  wire [5:0] Tag1, Tag2, Tag3, Tag4;
  wire [15:0] count1, count2, count3, count4;
  wire [31:0] Read11, Read12, Read13, Read14, Read21, Read22, Read23, Read24, Read31, Read32, Read33, Read34,
       Read41, Read42, Read43, Read44;

  Multiplexer #(.width(3)) multiplexer_1 (.in0(3'b000), .in1(3'b001), .out(multiplexer_1_out), .sel(hit2));  // open: en
  Multiplexer #(.width(3)) multiplexer_2 (
    .in0(multiplexer_1_out), .in1(3'b010), .out(multiplexer_2_out), .sel(hit3));  // open: en
  Comparator #(.width(6), .mode("unsigned")) comparator_1 (.a(Tag), .b(Tag1), .eq(comparator_1_eq));  // open: gt, lt
  Comparator #(.width(6), .mode("unsigned")) comparator_2 (.a(Tag), .b(Tag2), .eq(comparator_2_eq));  // open: gt, lt
  Comparator #(.width(6), .mode("unsigned")) comparator_3 (.a(Tag), .b(Tag3), .eq(comparator_3_eq));  // open: gt, lt
  Comparator #(.width(6), .mode("unsigned")) comparator_4 (.a(Tag), .b(Tag4), .eq(comparator_4_eq));  // open: gt, lt
  Multiplexer #(.width(3)) multiplexer_3 (
    .in0(multiplexer_2_out), .in1(3'b011), .out(BlockSel), .sel(hit4));  // open: en
  and and_1 (hit1, comparator_1_eq, v1);
  and and_2 (hit2, comparator_2_eq, v2);
  and and_3 (hit3, comparator_3_eq, v3);
  and and_4 (hit4, comparator_4_eq, v4);
  LRU lru_1 (
    .cal1(count1), .cal2(count2), .cal3(count3), .cal4(count4), .hit1(hit1), .hit2(hit2), .hit3(hit3),
    .hit4(hit4), .memread(MemRead), .memwrite(MemWrite), .clock(En_t), .block1(En1), .block2(En2),
    .block3(En3), .block4(En4));
  not not_1 (not_1_out, stop);
  CacheBlock cacheblock_1 (
    .Reset(reset), .Clk(Clk), .Enable(En1), .Tag(Tag), .Tag_2(Tag1), .v(v1), .Blcok1(data1),
    .Blcok1_2(Read11), .Blcok2(data2), .Blcok2_2(Read12), .Blcok3(data3), .Blcok3_2(Read13), .Blcok4(data4),
    .Blcok4_2(Read14));
  CacheBlock cacheblock_2 (
    .Reset(reset), .Clk(Clk), .Enable(En2), .Tag(Tag), .Tag_2(Tag2), .v(v2), .Blcok1(data1),
    .Blcok1_2(Read21), .Blcok2(data2), .Blcok2_2(Read22), .Blcok3(data3), .Blcok3_2(Read23), .Blcok4(data4),
    .Blcok4_2(Read24));
  CacheBlock cacheblock_3 (
    .Reset(reset), .Clk(Clk), .Enable(En3), .Tag(Tag), .Tag_2(Tag3), .v(v3), .Blcok1(data1),
    .Blcok1_2(Read31), .Blcok2(data2), .Blcok2_2(Read32), .Blcok3(data3), .Blcok3_2(Read33), .Blcok4(data4),
    .Blcok4_2(Read34));
  CacheBlock cacheblock_4 (
    .Reset(reset), .Clk(Clk), .Enable(En4), .Tag(Tag), .Tag_2(Tag4), .v(v4), .Blcok1(data1),
    .Blcok1_2(Read41), .Blcok2(data2), .Blcok2_2(Read42), .Blcok3(data3), .Blcok3_2(Read43), .Blcok4(data4),
    .Blcok4_2(Read44));
  and and_5 (En_t, en, not_1_out);
  counter counter_1 (.En(En1), .hit(hit1), .memread(MemRead), .groupen(En_t), .Clk(Clk), .Reset(reset), .out_7(count1));
  counter counter_2 (.En(En2), .hit(hit2), .memread(MemRead), .groupen(En_t), .Clk(Clk), .Reset(reset), .out_7(count2));
  counter counter_3 (.En(En3), .hit(hit3), .memread(MemRead), .groupen(En_t), .Clk(Clk), .Reset(reset), .out_7(count3));
  counter counter_4 (.En(En4), .hit(hit4), .memread(MemRead), .groupen(En_t), .Clk(Clk), .Reset(reset), .out_7(count4));
  Multiplexer #(.select(3), .width(32)) multiplexer_4 (
    .in0(Read11), .in1(Read21), .in2(Read31), .in3(Read41), .out(output1), .sel(BlockSel));  // open: in4, in5, in6, in7, en
  Multiplexer #(.select(3), .width(32)) multiplexer_5 (
    .in0(Read12), .in1(Read22), .in2(Read32), .in3(Read42), .out(output2), .sel(BlockSel));  // open: in4, in5, in6, in7, en
  or or_1 (or_1_out, hit1, hit2, hit3, hit4);
  Multiplexer #(.select(3), .width(32)) multiplexer_6 (
    .in0(Read13), .in1(Read23), .in2(Read33), .in3(Read43), .out(output3), .sel(BlockSel));  // open: in4, in5, in6, in7, en
  Multiplexer #(.select(3), .width(32)) multiplexer_7 (
    .in0(Read14), .in1(Read24), .in2(Read34), .in3(Read44), .out(output4), .sel(BlockSel));  // open: in4, in5, in6, in7, en
  and and_6 (hit, en, or_1_out);

  // Other names for the same wires on the sheet: Enin = en
endmodule

module counter (
  input  En,
  input  hit,
  input  memread,
  input  groupen,
  input  Clk,
  input  Reset,
  output [15:0] out_7
);

  wire and_1_out, and_2_out, and_3_out, and_4_out, not_1_out, not_2_out, or_1_out;

  not not_1 (not_1_out, hit);
  and and_1 (and_1_out, hit, memread);
  and and_2 (and_2_out, En, memread, not_1_out);
  or or_1 (or_1_out, and_1_out, and_2_out);
  not not_2 (not_2_out, or_1_out);
  and and_3 (and_3_out, not_2_out, memread, groupen);
  and and_4 (and_4_out, groupen, or_1_out);
  Counter #(.width(16), .max('hffff)) counter_1 (
    .load(and_4_out), .D({16{1'b0}}), .count(and_3_out), .Q(out_7), .clk(Clk), .clr(Reset));  // open: carry
endmodule
