// Logisim project REVIEW.circ as structural Verilog: 3 circuits, main circuit main
module main (
  input  in_1,
  output [1:0] out_2
);

  wire clock_1_out;
  wire [2:0] register_1_q, \转移逻辑_1_out_3 ;

  \转移逻辑  \u_转移逻辑_1  (.in_1(register_1_q), .\input (in_1), .out_3(\转移逻辑_1_out_3 ));
  Clock clock_1 (.out(clock_1_out));
  Register #(.width(3)) register_1 (.D(\转移逻辑_1_out_3 ), .Q(register_1_q), .clk(clock_1_out));  // open: en, clr
  \输出逻辑  \u_输出逻辑_1  (.in_1(register_1_q), .out_2(out_2));
endmodule

module \转移逻辑  (
  input  [2:0] in_1,
  input  \input ,
  output [2:0] out_3
);

  wire and_1_out, and_2_out, and_3_out, and_4_out, and_5_out, and_6_out, and_7_out, not_1_out, not_2_out,
       not_3_out, not_4_out, not_5_out, not_6_out, not_7_out, not_8_out, not_9_out, not_10_out;

  and and_1 (and_1_out, in_1[1], \input );
  and and_2 (and_2_out, in_1[1], in_1[0]);
  not not_1 (not_1_out, in_1[2]);
  not not_2 (not_2_out, in_1[1]);
  not not_3 (not_3_out, in_1[2]);
  not not_4 (not_4_out, in_1[1]);
  not not_5 (not_5_out, in_1[0]);
  not not_6 (not_6_out, \input );
  not not_7 (not_7_out, in_1[2]);
  not not_8 (not_8_out, in_1[0]);
  not not_9 (not_9_out, \input );
  not not_10 (not_10_out, in_1[2]);
  or or_1 (out_3[2], and_1_out, and_2_out);
  and and_3 (and_3_out, not_1_out, not_2_out, \input );
  and and_4 (and_4_out, not_3_out, not_4_out, in_1[0]);
  and and_5 (and_5_out, in_1[1], not_5_out, not_6_out);
  and and_6 (and_6_out, not_7_out, not_8_out, not_9_out);
  and and_7 (and_7_out, not_10_out, in_1[0], \input );
  or or_2 (out_3[1], and_3_out, and_4_out, and_5_out);
  or or_3 (out_3[0], and_6_out, and_7_out);
endmodule

module \输出逻辑  (
  input  [2:0] in_1,
  output [1:0] out_2
);

  wire not_1_out;

  and and_1 (out_2[1], in_1[2], in_1[0]);
  not not_1 (not_1_out, in_1[0]);
  and and_2 (out_2[0], in_1[2], not_1_out);
endmodule
