// Logisim project p3 final - 副本.circ as structural Verilog: 4 circuits, main circuit main
module main (
  input  in_1,
  output [31:0] out_2,
  output out_3,
  output [4:0] out_4,
  output [31:0] out_5,
  output out_6,
  output [4:0] out_7,
  output [31:0] out_8
);

  wire ALUsrc, and_1_out, and_2_out, blez, Branch, Clk_prime, comparator_1_eq, judgeblez, Jump, lb, MemRead,
       MemtoReg, or_1_out, or_2_out, Regdst, sb, zero;
  wire [2:0] ALUOp;
  wire [31:0] adder_1_out, adder_2_out, adder_3_out, bit_extender_1_out, bit_extender_2_out,
       bit_extender_3_out, bit_extender_4_out, bit_extender_5_out, grf_1_rd1, grf_1_rd2, multiplexer_1_out,
       multiplexer_2_out, multiplexer_3_out, multiplexer_5_out, multiplexer_7_out, ram_1_data, register_1_q,
       res, shifter_1_out, shifter_2_out;

  Comparator #(.width(32)) comparator_1 (.a({32{1'b0}}), .b(register_1_q), .eq(comparator_1_eq));  // open: gt, lt
  Register #(.width(32)) register_1 (.D(multiplexer_3_out), .Q(register_1_q), .clk(Clk_prime), .clr(in_1));  // open: en
  assign bit_extender_1_out = {{16{out_2[15]}}, out_2[15:0]};  // Bit_Extender bit_extender_1
  Multiplexer #(.width(32), .enable("false")) multiplexer_1 (
    .in0(register_1_q), .in1(adder_1_out), .out(multiplexer_1_out), .sel(comparator_1_eq));
  Adder #(.width(32)) adder_1 (.a(32'h3000), .b(register_1_q), .out(adder_1_out));  // open: cin, cout
  Adder #(.width(32)) adder_2 (.a(multiplexer_1_out), .b(32'h4), .out(adder_2_out));  // open: cin, cout
  Shifter #(.width(32)) shifter_1 (.in(bit_extender_1_out), .\dist (5'b00010), .out(shifter_1_out));
  Clock clock_1 (.out(Clk_prime));
  ROM #(.addrWidth(5), .dataWidth(32)) rom_1 (.addr(multiplexer_1_out[6:2]), .data(out_2));  // open: sel
  assign bit_extender_2_out = {{6{out_2[25]}}, out_2[25:0]};  // Bit_Extender bit_extender_2
  Adder #(.width(32)) adder_3 (.a(adder_2_out), .b(shifter_1_out), .out(adder_3_out));  // open: cin, cout
  control control_1 (
    .func(out_2[5:0]), .op(out_2[31:26]), .Jump(Jump), .Branch(Branch), .MemtoReg(MemtoReg),
    .MemWrite(out_6), .MemRead(MemRead), .ALUop(ALUOp), .ALUsrc(ALUsrc), .RegWrite(out_3), .Regdst(Regdst),
    .judgeblez(judgeblez), .sb(sb), .lb(lb));
  Multiplexer #(.width(32)) multiplexer_2 (
    .in0(adder_2_out), .in1(adder_3_out), .out(multiplexer_2_out), .sel(and_1_out));  // open: en
  and and_1 (and_1_out, Branch, or_1_out);
  or or_1 (or_1_out, zero, and_2_out);
  or or_2 (or_2_out, zero, blez);
  Shifter #(.width(32)) shifter_2 (.in(bit_extender_2_out), .\dist (5'b00010), .out(shifter_2_out));
  Multiplexer #(.width(32)) multiplexer_3 (
    .in0(multiplexer_2_out), .in1(shifter_2_out), .out(multiplexer_3_out), .sel(Jump));  // open: en
  and and_2 (and_2_out, or_2_out, judgeblez);
  Multiplexer #(.width(5)) multiplexer_4 (
    .in0(out_2[20:16]), .in1(out_2[15:11]), .out(out_4), .sel(Regdst));  // open: en
  assign bit_extender_3_out = {{16{out_2[15]}}, out_2[15:0]};  // Bit_Extender bit_extender_3
  GRF grf_1 (
    .A1(out_2[25:21]), .A2(out_2[20:16]), .A3(out_4), .WD(out_5), .clk(Clk_prime), .reset(in_1), .we(out_3),
    .RD1(grf_1_rd1), .RD2(grf_1_rd2));
  Multiplexer #(.width(32)) multiplexer_5 (
    .in0(grf_1_rd2), .in1(bit_extender_3_out), .out(multiplexer_5_out), .sel(ALUsrc));  // open: en
  assign bit_extender_4_out = {{24{grf_1_rd2[7]}}, grf_1_rd2[7:0]};  // Bit_Extender bit_extender_4
  ALU alu_1 (
    .in_1(grf_1_rd1), .in_2(multiplexer_5_out), .in_3(ALUOp), .out_4(zero), .out_5(blez),
    .out_6({res[31:7], out_7, res[1:0]}));
  Multiplexer #(.width(32), .enable("false")) multiplexer_6 (
    .in0(grf_1_rd2), .in1(bit_extender_4_out), .out(out_8), .sel(sb));
  RAM #(.addrWidth(5), .dataWidth(32), .bus("separate")) ram_1 (
    .addr(out_7), .din(out_8), .data(ram_1_data), .str(out_6), .clk(Clk_prime), .ld(MemRead));  // open: sel, clr
  assign bit_extender_5_out = {{24{ram_1_data[7]}}, ram_1_data[7:0]};  // Bit_Extender bit_extender_5
  Multiplexer #(.width(32), .enable("false")) multiplexer_7 (
    .in0(ram_1_data), .in1(bit_extender_5_out), .out(multiplexer_7_out), .sel(lb));
  Multiplexer #(.width(32), .enable("false")) multiplexer_8 (
    .in0({res[31:7], out_7, res[1:0]}), .in1(multiplexer_7_out), .out(out_5), .sel(MemtoReg));

  // Other names for the same wires on the sheet: add26[25:0] = out_2[25:0]; func[5:0] = out_2[5:0];
  //   imm16[15:0] = out_2[15:0]; Instr[31:0] = out_2; MemWrite = out_6; op[5:0] = out_2[31:26];
  //   Rd[4:0] = out_2[15:11]; RegAddr[4:0] = out_4; RegWrite = out_3; MemAddr[4:0] = out_7; res[6:2] = out_7;
  //   reset = in_1; Rs[4:0] = out_2[25:21]; Rt[4:0] = out_2[20:16]; RegData[31:0] = out_5; wd[31:0] = out_5;
  //   MemData[31:0] = out_8; x[31:0] = out_8

  // Notes on the sheet:
  //   contents of rom_1 (hex, n*v repeats v):
  //   35290403 a1490000 814b0000
endmodule

module control (
  input  [5:0] func,
  input  [5:0] op,
  output Jump,
  output Branch,
  output MemtoReg,
  output MemWrite,
  output MemRead,
  output [2:0] ALUop,
  output ALUsrc,
  output RegWrite,
  output Regdst,
  output judgeblez,
  output sb,
  output lb
);

  wire addi, addu, beq, j, lw, not_1_out, not_2_out, not_3_out, not_4_out, not_5_out, not_6_out, not_7_out,
       not_8_out, not_9_out, not_10_out, not_11_out, not_12_out, subu, sw;

  not not_1 (not_1_out, func[5]);
  not not_2 (not_2_out, func[4]);
  not not_3 (not_3_out, func[3]);
  not not_4 (not_4_out, func[2]);
  not not_5 (not_5_out, func[1]);
  not not_6 (not_6_out, func[0]);
  not not_7 (not_7_out, op[5]);
  not not_8 (not_8_out, op[4]);
  not not_9 (not_9_out, op[3]);
  not not_10 (not_10_out, op[2]);
  not not_11 (not_11_out, op[1]);
  not not_12 (not_12_out, op[0]);
  and u_addu (addu, func[5], not_2_out, not_3_out, not_4_out, not_5_out, func[0], not_7_out, not_8_out, not_9_out, not_10_out, not_11_out, not_12_out);
  and u_subu (subu, func[5], not_2_out, not_3_out, not_4_out, func[1], func[0], not_7_out, not_8_out, not_9_out, not_10_out, not_11_out, not_12_out);
  and ori (ALUop[1], not_7_out, not_8_out, op[3], op[2], not_11_out, op[0]);
  and u_lw (lw, op[5], not_8_out, not_9_out, not_10_out, op[1], op[0]);
  and u_sw (sw, op[5], not_8_out, op[3], not_10_out, op[1], op[0]);
  and u_beq (beq, not_7_out, not_8_out, not_9_out, op[2], not_11_out, not_12_out);
  and u_j (j, not_7_out, not_8_out, not_9_out, not_10_out, op[1], not_12_out);
  and u_addi (addi, not_7_out, not_8_out, op[3], not_10_out, not_11_out, not_12_out);
  and blez (judgeblez, not_7_out, not_8_out, not_9_out, op[2], op[1], not_12_out);
  and u_sb (sb, op[5], not_8_out, op[3], not_10_out, not_11_out, not_12_out);
  and u_lb (lb, op[5], not_8_out, not_9_out, not_10_out, not_11_out, not_12_out);
  buf or_1 (Jump, j);  // OR_Gate
  or or_2 (Branch, beq, judgeblez);
  or or_3 (MemtoReg, lw, lb);
  or or_4 (MemWrite, sw, sb);
  or or_5 (MemRead, lw, lb);
  or or_6 (ALUop[0], subu, beq, judgeblez);
  buf or_7 (ALUop[2], 1'b0);  // OR_Gate
  or or_8 (ALUsrc, sb, sw, lw, ALUop[1], lb, addi);
  or or_9 (RegWrite, lb, ALUop[1], addu, subu, lw, addi);
  or or_10 (Regdst, addu, subu);

  // Other names for the same wires on the sheet: ori = ALUop[1]; blez = judgeblez
endmodule

module ALU (
  input  [31:0] in_1,
  input  [31:0] in_2,
  input  [2:0] in_3,
  output out_4,
  output out_5,
  output [31:0] out_6
);

  wire comparator_1_lt;
  wire [31:0] adder_1_out, or_1_out, subtractor_1_out, undriven;

  Adder #(.width(32)) adder_1 (.a(in_1), .b(in_2), .out(adder_1_out));  // open: cin, cout
  Subtractor #(.width(32)) subtractor_1 (.a(in_1), .b(in_2), .out(subtractor_1_out));  // open: bin, bout
  assign or_1_out = in_1 | in_2;  // OR_Gate or_1, 32 bits wide
  Multiplexer #(.select(3), .width(32)) multiplexer_1 (
    .in0(adder_1_out), .in1(subtractor_1_out), .in2(or_1_out), .in4(undriven), .out(out_6), .sel(in_3));  // open: in3, in5, in6, in7, en
  Comparator #(.width(32)) comparator_1 (.a(out_6), .b({32{1'b0}}), .eq(out_4), .lt(comparator_1_lt));  // open: gt
  or or_2 (out_5, out_4, comparator_1_lt);
endmodule

module GRF (
  input  [4:0] A1,
  input  clk,
  input  reset,
  input  we,
  input  [4:0] A2,
  input  [4:0] A3,
  input  [31:0] WD,
  output [31:0] RD1,
  output [31:0] RD2
);

  wire [31:0] I0, I1, I2, I3, I4, I5, I6, I7, I8, I9, I10, I11, I12, I13, I14, I15, I16, I17, I18, I19, I20,
       I21, I22, I23, I24, I25, I26, I27, I28, I29, I30, I31, O0, O1, O2, O3, O4, O5, O6, O7, O8, O9, O10,
       O11, O12, O13, O14, O15, O16, O17, O18, O19, O20, O21, O22, O23, O24, O25, O26, O27, O28, O29, O30,
       O31;

  Demultiplexer #(.select(5), .width(32), .tristate("true")) demultiplexer_1 (
    .out0(I0), .out1(I1), .out2(I2), .out3(I3), .out4(I4), .out5(I5), .out6(I6), .out7(I7), .out8(I8),
    .out9(I9), .out10(I10), .out11(I11), .out12(I12), .out13(I13), .out14(I14), .out15(I15), .out16(I16),
    .out17(I17), .out18(I18), .out19(I19), .out20(I20), .out21(I21), .out22(I22), .out23(I23), .out24(I24),
    .out25(I25), .out26(I26), .out27(I27), .out28(I28), .out29(I29), .out30(I30), .out31(I31), .in(WD),
    .sel(A3));  // open: en
  Multiplexer #(.select(5), .width(32)) multiplexer_1 (
    .in0(O0), .in1(O1), .in2(O2), .in3(O3), .in4(O4), .in5(O5), .in6(O6), .in7(O7), .in8(O8), .in9(O9),
    .in10(O10), .in11(O11), .in12(O12), .in13(O13), .in14(O14), .in15(O15), .in16(O16), .in17(O17),
    .in18(O18), .in19(O19), .in20(O20), .in21(O21), .in22(O22), .in23(O23), .in24(O24), .in25(O25),
    .in26(O26), .in27(O27), .in28(O28), .in29(O29), .in30(O30), .in31(O31), .out(RD2), .sel(A2));  // open: en
  Multiplexer #(.select(5), .width(32)) multiplexer_2 (
    .in0(O0), .in1(O1), .in2(O2), .in3(O3), .in4(O4), .in5(O5), .in6(O6), .in7(O7), .in8(O8), .in9(O9),
    .in10(O10), .in11(O11), .in12(O12), .in13(O13), .in14(O14), .in15(O15), .in16(O16), .in17(O17),
    .in18(O18), .in19(O19), .in20(O20), .in21(O21), .in22(O22), .in23(O23), .in24(O24), .in25(O25),
    .in26(O26), .in27(O27), .in28(O28), .in29(O29), .in30(O30), .in31(O31), .out(RD1), .sel(A1));  // open: en
  Register #(.width(32)) register_1 (.D({32{1'b0}}), .en(we), .Q(O0), .clk(clk), .clr(reset));
  Register #(.width(32)) register_2 (.D(I8), .en(we), .Q(O8), .clk(clk), .clr(reset));
  Register #(.width(32)) register_3 (.D(I16), .en(we), .Q(O16), .clk(clk), .clr(reset));
  Register #(.width(32)) register_4 (.D(I24), .en(we), .Q(O24), .clk(clk), .clr(reset));
  Register #(.width(32)) register_5 (.D(I1), .en(we), .Q(O1), .clk(clk), .clr(reset));
  Register #(.width(32)) register_6 (.D(I9), .en(we), .Q(O9), .clk(clk), .clr(reset));
  Register #(.width(32)) register_7 (.D(I17), .en(we), .Q(O17), .clk(clk), .clr(reset));
  Register #(.width(32)) register_8 (.D(I25), .en(we), .Q(O25), .clk(clk), .clr(reset));
  Register #(.width(32)) register_9 (.D(I2), .en(we), .Q(O2), .clk(clk), .clr(reset));
  Register #(.width(32)) register_10 (.D(I10), .en(we), .Q(O10), .clk(clk), .clr(reset));
  Register #(.width(32)) register_11 (.D(I18), .en(we), .Q(O18), .clk(clk), .clr(reset));
  Register #(.width(32)) register_12 (.D(I26), .en(we), .Q(O26), .clk(clk), .clr(reset));
  Register #(.width(32)) register_13 (.D(I3), .en(we), .Q(O3), .clk(clk), .clr(reset));
  Register #(.width(32)) register_14 (.D(I11), .en(we), .Q(O11), .clk(clk), .clr(reset));
  Register #(.width(32)) register_15 (.D(I19), .en(we), .Q(O19), .clk(clk), .clr(reset));
  Register #(.width(32)) register_16 (.D(I27), .en(we), .Q(O27), .clk(clk), .clr(reset));
  Register #(.width(32)) register_17 (.D(I4), .en(we), .Q(O4), .clk(clk), .clr(reset));
  Register #(.width(32)) register_18 (.D(I12), .en(we), .Q(O12), .clk(clk), .clr(reset));
  Register #(.width(32)) register_19 (.D(I20), .en(we), .Q(O20), .clk(clk), .clr(reset));
  Register #(.width(32)) register_20 (.D(I28), .en(we), .Q(O28), .clk(clk), .clr(reset));
  Register #(.width(32)) register_21 (.D(I5), .en(we), .Q(O5), .clk(clk), .clr(reset));
  Register #(.width(32)) register_22 (.D(I13), .en(we), .Q(O13), .clk(clk), .clr(reset));
  Register #(.width(32)) register_23 (.D(I21), .en(we), .Q(O21), .clk(clk), .clr(reset));
  Register #(.width(32)) register_24 (.D(I29), .en(we), .Q(O29), .clk(clk), .clr(reset));
  Register #(.width(32)) register_25 (.D(I6), .en(we), .Q(O6), .clk(clk), .clr(reset));
  Register #(.width(32)) register_26 (.D(I14), .en(we), .Q(O14), .clk(clk), .clr(reset));
  Register #(.width(32)) register_27 (.D(I22), .en(we), .Q(O22), .clk(clk), .clr(reset));
  Register #(.width(32)) register_28 (.D(I30), .en(we), .Q(O30), .clk(clk), .clr(reset));
  Register #(.width(32)) register_29 (.D(I7), .en(we), .Q(O7), .clk(clk), .clr(reset));
  Register #(.width(32)) register_30 (.D(I15), .en(we), .Q(O15), .clk(clk), .clr(reset));
  Register #(.width(32)) register_31 (.D(I23), .en(we), .Q(O23), .clk(clk), .clr(reset));
  Register #(.width(32)) register_32 (.D(I31), .en(we), .Q(O31), .clk(clk), .clr(reset));
endmodule
