// Logisim project single_circle - 副本.circ as structural Verilog: 7 circuits, main circuit main
module main (
  input  Reset,
  output [31:0] out_2,
  output out_3,
  output [4:0] out_4,
  output [31:0] out_5,
  output out_6,
  output [4:0] out_7,
  output [31:0] out_8
);

  wire alusrc, and_1_out, branch, Clk_prime, jump, memtoreg, not_1_out, regdst, zero;
  wire [1:0] exotp;
  wire [3:0] aluctrl;
  wire [4:0] bit_extender_1_out, bit_extender_2_out;
  wire [9:0] bit_extender_3_out, shifter_2_out;
  wire [15:0] adder_1_out, adder_2_out, adder_3_out, multiplexer_1_out, multiplexer_2_out, PC_q;
  wire [31:0] ext_1_immout, grf_1_rd1, multiplexer_5_out, ram_1_data, x;

  Register #(.width(16)) PC (.D(multiplexer_1_out), .Q(PC_q), .clk(Clk_prime), .clr(Reset));  // open: en
  Multiplexer #(.width(16)) multiplexer_1 (
    .in0(multiplexer_2_out), .in1(out_2[15:0]), .out(multiplexer_1_out), .sel(jump));  // open: en
  Clock clock_1 (.out(Clk_prime));
  Adder #(.width(16)) adder_1 (.a(16'h3000), .b(PC_q), .out(adder_1_out));  // open: cin, cout
  Bit_Extender #(.in_width(16), .out_width(5)) bit_extender_1 (.in(adder_1_out), .out(bit_extender_1_out));
  Adder #(.width(16)) adder_2 (.a(adder_1_out), .b(16'h1), .out(adder_2_out));  // open: cin, cout
  ROM #(.addrWidth(5), .dataWidth(32)) rom_1 (.addr(bit_extender_1_out), .data(out_2));  // open: sel
  Adder #(.width(16)) adder_3 (.a(out_2[15:0]), .b(adder_2_out), .out(adder_3_out));  // open: cin, cout
  Bit_Extender #(.in_width(32), .out_width(5)) bit_extender_2 (.in(x), .out(bit_extender_2_out));
  Multiplexer #(.width(16)) multiplexer_2 (
    .in0(adder_2_out), .in1(adder_3_out), .out(multiplexer_2_out), .sel(and_1_out));  // open: en
  and and_1 (and_1_out, branch, zero);
  Bit_Extender #(.in_width(32), .out_width(10)) bit_extender_3 (.in(x), .out(bit_extender_3_out));
  Shifter #(.width(5), .shift("lr")) shifter_1 (.in(bit_extender_2_out), .\dist (3'b010), .out(out_7));
  Multiplexer #(.width(5)) multiplexer_3 (
    .in0(out_2[20:16]), .in1(out_2[15:11]), .out(out_4), .sel(regdst));  // open: en
  Shifter #(.width(10), .shift("lr")) shifter_2 (.in(bit_extender_3_out), .\dist (4'b0010), .out(shifter_2_out));
  RAM #(.addrWidth(10), .dataWidth(32), .bus("separate")) ram_1 (
    .addr(shifter_2_out), .din(out_8), .data(ram_1_data), .str(out_6), .clk(Clk_prime), .ld(not_1_out));  // open: sel, clr
  not not_1 (not_1_out, out_6);
  Controller controller_1 (
    .Op(out_2[31:26]), .funct(out_2[5:0]), .jump(jump), .ExtOp(exotp), .MemtoReg(memtoreg), .MemWrite(out_6),
    .Branch(branch), .ALUCtrl(aluctrl), .isImm(alusrc), .RegDst(regdst), .RegWrite(out_3), .RT(out_2[20:16]));
  GRF grf_1 (
    .A1(out_2[25:21]), .A2(out_2[20:16]), .A3(out_4), .WD(out_5), .clk(Clk_prime), .we(out_3),
    .RD1(grf_1_rd1), .RD2(out_8));  // open: reset
  ext ext_1 (.ExtOp(exotp), .Imm(out_2[15:0]), .Immout(ext_1_immout));
  Multiplexer #(.width(32)) multiplexer_4 (.in0(x), .in1(ram_1_data), .out(out_5), .sel(memtoreg));  // open: en
  Multiplexer #(.width(32)) multiplexer_5 (
    .in0(out_8), .in1(ext_1_immout), .out(multiplexer_5_out), .sel(alusrc));  // open: en
  ALU ALU (.Op1(grf_1_rd1), .Op2(multiplexer_5_out), .Sel(aluctrl), .Result(x), .Zero(zero));

  // Other names for the same wires on the sheet: _5_0[5:0] = out_2[5:0]; _15_0[15:0] = out_2[15:0];
  //   Instr[31:0] = out_2; _15_11[4:0] = out_2[15:11]; _20_16[4:0] = out_2[20:16]; _25_21[4:0] = out_2[25:21];
  //   _31_26[5:0] = out_2[31:26]; MemAddr[4:0] = out_7; MemData[31:0] = out_8; MemWrite = out_6; RegAddr[4:0] = out_4;
  //   RegData[31:0] = out_5; RegWrite = out_3

  // Notes on the sheet:
  //   contents of rom_1 (hex, n*v repeats v):
  //   24010008 8c090004 ac010004
endmodule

module ALU (
  input  [31:0] Op1,
  input  [31:0] Op2,
  input  [3:0] Sel,
  output [31:0] Result,
  output Zero
);

  wire bitselector_1_out, comparator_1_eq, comparator_1_lt, comparator_2_lt, comparator_3_gt, not_1_out,
       not_3_out;
  wire [4:0] bit_extender_3_out;
  wire [31:0] _0, _1, _2, _3, _4, _5, _6, _7, _8, _9, _10, _11, _12, _13, _14, _15;

  BitSelector #(.width(32)) bitselector_1 (.in(Op1), .out(bitselector_1_out), .sel({5{1'b1}}));
  not not_1 (not_1_out, bitselector_1_out);
  Adder #(.width(32)) adder_1 (.a(Op1), .b(Op2), .out(_2));  // open: cin, cout
  Subtractor #(.width(32)) subtractor_1 (.a(Op1), .b(Op2), .out(_3));  // open: bin, bout
  assign _4 = Op1 & Op2;  // AND_Gate and_1, 32 bits wide
  assign _5 = Op1 | Op2;  // OR_Gate or_1, 32 bits wide
  assign _6 = Op1 ^ Op2;  // XOR_Gate xor_1, 32 bits wide
  assign _1 = {{31{1'b0}}, bitselector_1_out};  // Bit_Extender bit_extender_1
  assign _0 = {{31{1'b0}}, not_1_out};  // Bit_Extender bit_extender_2
  Bit_Extender #(.in_width(32), .out_width(5)) bit_extender_3 (.in(Op2), .out(bit_extender_3_out));
  assign _7 = ~_5;  // NOT_Gate not_2, 32 bits wide
  Comparator #(.width(32)) comparator_1 (.a(Op1), .b(Op2), .eq(comparator_1_eq), .lt(comparator_1_lt));  // open: gt
  Comparator #(.width(32), .mode("unsigned")) comparator_2 (.a(Op1), .b(Op2), .lt(comparator_2_lt));  // open: gt, eq
  Comparator #(.width(32)) comparator_3 (.a(Op1), .b({32{1'b0}}), .gt(comparator_3_gt));  // open: eq, lt
  not not_3 (not_3_out, comparator_3_gt);
  Shifter #(.width(32), .shift("lr")) shifter_1 (.in(Op1), .\dist (bit_extender_3_out), .out(_8));
  Shifter #(.width(32), .shift("ar")) shifter_2 (.in(Op1), .\dist (bit_extender_3_out), .out(_9));
  Shifter #(.width(32)) shifter_3 (.in(Op1), .\dist (bit_extender_3_out), .out(_10));
  assign _11 = {{31{1'b0}}, comparator_1_eq};  // Bit_Extender bit_extender_4
  assign _12 = {{31{1'b0}}, comparator_1_lt};  // Bit_Extender bit_extender_5
  assign _13 = {{31{1'b0}}, comparator_2_lt};  // Bit_Extender bit_extender_6
  assign _14 = {{31{1'b0}}, comparator_3_gt};  // Bit_Extender bit_extender_7
  assign _15 = {{31{1'b0}}, not_3_out};  // Bit_Extender bit_extender_8
  Multiplexer #(.select(4), .width(32)) multiplexer_1 (
    .in0(_0), .in1(_1), .in2(_2), .in3(_3), .in4(_4), .in5(_5), .in6(_6), .in7(_7), .in8(_8), .in9(_9),
    .in10(_10), .in11(_11), .in12(_12), .in13(_13), .in14(_14), .in15(_15), .out(Result), .sel(Sel));  // open: en
  Comparator #(.width(32), .mode("unsigned")) comparator_4 (.a(Result), .b({32{1'b0}}), .eq(Zero));  // open: gt, lt
endmodule

module ALUDecd (
  input  [5:0] OpCode,
  input  [5:0] Funct,
  input  [4:0] RT,
  output [3:0] ALUCtrl
);

  wire nor_1_out;
  wire [3:0] bit_extender_1_out, multiplexer_1_out, multiplexer_2_out, multiplexer_3_out, multiplexer_4_out,
       multiplexer_5_out, multiplexer_6_out, multiplexer_7_out;

  Multiplexer #(.select(3), .width(4)) multiplexer_1 (
    .in0(4'b1010), .in1(4'b0000), .in2(4'b1000), .in3(4'b1001), .in4(4'b1010), .in5(4'b0000), .in6(4'b1000),
    .in7(4'b1001), .out(multiplexer_1_out), .sel(Funct[2:0]));  // open: en
  Multiplexer #(.select(3), .width(4)) multiplexer_2 (
    .in0(4'b0010), .in1(4'b0010), .in2(4'b0011), .in3(4'b0011), .in4(4'b0100), .in5(4'b0101), .in6(4'b0110),
    .in7(4'b0111), .out(multiplexer_2_out), .sel(Funct[2:0]));  // open: en
  Multiplexer #(.select(3), .width(4)) multiplexer_3 (
    .in2(4'b1100), .in3(4'b1101), .out(multiplexer_3_out), .sel(Funct[2:0]));  // open: in0, in1, in4, in5, in6, in7, en
  assign bit_extender_1_out = {{3{1'b0}}, RT[0]};  // Bit_Extender bit_extender_1
  nor nor_1 (nor_1_out, RT[1], RT[2], RT[3], RT[4]);
  Multiplexer #(.width(4)) multiplexer_4 (
    .in1(bit_extender_1_out), .out(multiplexer_4_out), .sel(nor_1_out));  // open: in0, en
  Multiplexer #(.select(3), .width(4)) multiplexer_5 (
    .in0(multiplexer_1_out), .in4(multiplexer_2_out), .in5(multiplexer_3_out), .out(multiplexer_5_out),
    .sel(Funct[5:3]));  // open: in1, in2, in3, in6, in7, en
  Multiplexer #(.select(4), .width(4)) multiplexer_6 (
    .in0(multiplexer_5_out), .in1(multiplexer_4_out), .in2(4'b0000), .in3(4'b0000), .in4(4'b0011),
    .in5(4'b1011), .in6(4'b1110), .in7(4'b1111), .in8(4'b0010), .in9(4'b0010), .in10(4'b1100),
    .in11(4'b1101), .in12(4'b0100), .in13(4'b0101), .in14(4'b0110), .in15(4'b0101), .out(multiplexer_6_out),
    .sel(OpCode[3:0]));  // open: en
  Multiplexer #(.select(4), .width(4)) multiplexer_7 (
    .in3(4'b0010), .in11(4'b0010), .out(multiplexer_7_out), .sel(OpCode[3:0]));  // open: in0, in1, in2, in4, in5, in6, in7, in8, in9, in10, in12, in13, in14, in15, en
  Multiplexer #(.select(2), .width(4)) multiplexer_8 (
    .in0(multiplexer_6_out), .in2(multiplexer_7_out), .out(ALUCtrl), .sel(OpCode[5:4]));  // open: in1, in3, en
endmodule

module ext (
  input  [1:0] ExtOp,
  input  [15:0] Imm,
  output [31:0] Immout
);

  wire [31:0] bit_extender_1_out, bit_extender_2_out, shifter_1_out;

  assign bit_extender_1_out = {{16{Imm[15]}}, Imm};  // Bit_Extender bit_extender_1
  assign bit_extender_2_out = {{16{1'b0}}, Imm};  // Bit_Extender bit_extender_2
  Shifter #(.width(32)) shifter_1 (.in(bit_extender_1_out), .\dist (5'b00010), .out(shifter_1_out));
  Multiplexer #(.select(2), .width(32)) multiplexer_1 (
    .in0(bit_extender_1_out), .in1(bit_extender_2_out), .in2({Imm, {16{1'b0}}}), .in3(shifter_1_out),
    .out(Immout), .sel(ExtOp));  // open: en
endmodule

module Controller (
  input  [5:0] Op,
  input  [5:0] funct,
  input  [4:0] RT,
  output jump,
  output [1:0] ExtOp,
  output MemtoReg,
  output MemWrite,
  output Branch,
  output [3:0] ALUCtrl,
  output isImm,
  output RegDst,
  output RegWrite
);

  wire add_u, addi_u, \and , andi, beq, bgez, bgtz, blez, bltz, bne, Br, nop, \nor , nor_1_out, nor_2_out,
       nor_4_out, not_7_out, not_8_out, not_15_out, \or , or_1_out, ori, Reg, sllv, slt, slti, sltiu, sltu,
       srav, srlv, sub_u, \xor , xori;
  wire [5:0] and_19_out, bit_extender_1_out;
  wire [10:0] mid, not_11_out;

  not not_1 (mid[10], Op[5]);
  not not_2 (mid[6], Op[3]);
  not not_3 (mid[2], Op[1]);
  not not_4 (mid[4], Op[2]);
  not not_5 (mid[8], Op[4]);
  not not_6 (mid[0], Op[0]);
  and and_1 (addi_u, mid[2], mid[4], Op[3], mid[8], mid[10]);
  and and_2 (slti, mid[0], Op[1], mid[4], Op[3], mid[8], mid[10]);
  and and_3 (andi, mid[0], mid[2], Op[2], Op[3], mid[8], mid[10]);
  and and_4 (xori, mid[0], Op[1], Op[2], Op[3], mid[8], mid[10]);
  and and_5 (jump, mid[0], Op[1], mid[4], mid[6], mid[8], mid[10]);
  and and_6 (sltiu, Op[0], Op[1], mid[4], Op[3], mid[8], mid[10]);
  and and_7 (ori, Op[0], mid[2], Op[2], Op[3], mid[8], mid[10]);
  and and_8 (ExtOp[1], Op[0], Op[1], Op[2], Op[3], mid[8], mid[10]);
  not not_7 (not_7_out, RT[0]);
  nor nor_1 (nor_1_out, RT[0], RT[1], RT[2], RT[3], RT[4]);
  nor nor_2 (nor_2_out, not_7_out, RT[1], RT[2], RT[3], RT[4]);
  and and_9 (bltz, nor_1_out, Br);
  and and_10 (beq, mid[0], mid[2], Op[2], mid[6], mid[8], mid[10]);
  and and_11 (blez, mid[0], Op[1], Op[2], mid[6], mid[8], mid[10]);
  and and_12 (MemtoReg, Op[0], Op[1], mid[4], mid[6], mid[8], Op[5]);
  and and_13 (Reg, mid[0], mid[2], mid[4], mid[6], mid[8], mid[10]);
  and and_14 (bgez, Br, nor_2_out);
  and and_15 (bne, Op[0], mid[2], Op[2], mid[6], mid[8], mid[10]);
  and and_16 (bgtz, Op[0], Op[1], Op[2], mid[6], mid[8], mid[10]);
  and and_17 (MemWrite, Op[0], Op[1], mid[4], Op[3], mid[8], Op[5]);
  and and_18 (Br, Op[0], mid[2], mid[4], mid[6], mid[8], mid[10]);
  assign bit_extender_1_out = {{5{Reg}}, Reg};  // Bit_Extender bit_extender_1
  not not_8 (not_8_out, Reg);
  not not_9 (not_11_out[8], and_19_out[4]);
  not not_10 (not_11_out[10], and_19_out[5]);
  assign and_19_out = bit_extender_1_out & funct;  // AND_Gate and_19, 6 bits wide
  nor nor_3 (nop, funct[0], funct[1], funct[2], funct[3], funct[4], funct[5], not_8_out);
  not not_11 (not_11_out[0], and_19_out[0]);
  not not_12 (not_11_out[4], and_19_out[2]);
  not not_13 (not_11_out[2], and_19_out[1]);
  not not_14 (not_11_out[6], and_19_out[3]);
  and and_20 (sllv, not_11_out[0], not_11_out[2], and_19_out[2], not_11_out[6], not_11_out[8], not_11_out[10]);
  and and_21 (srlv, not_11_out[0], and_19_out[1], and_19_out[2], not_11_out[6], not_11_out[8], not_11_out[10]);
  and and_22 (add_u, not_11_out[2], not_11_out[4], not_11_out[6], not_11_out[8], and_19_out[5]);
  and and_23 (sub_u, and_19_out[1], not_11_out[4], not_11_out[6], not_11_out[8], and_19_out[5]);
  and and_24 (\and , not_11_out[0], not_11_out[2], and_19_out[2], not_11_out[6], not_11_out[8], and_19_out[5]);
  and and_25 (\xor , not_11_out[0], and_19_out[1], and_19_out[2], not_11_out[6], not_11_out[8], and_19_out[5]);
  and and_26 (slt, not_11_out[0], and_19_out[1], not_11_out[4], and_19_out[3], not_11_out[8], and_19_out[5]);
  and and_27 (srav, and_19_out[0], and_19_out[1], and_19_out[2], not_11_out[6], not_11_out[8], not_11_out[10]);
  and and_28 (\or , and_19_out[0], not_11_out[2], and_19_out[2], not_11_out[6], not_11_out[8], and_19_out[5]);
  and and_29 (\nor , and_19_out[0], and_19_out[1], and_19_out[2], not_11_out[6], not_11_out[8], and_19_out[5]);
  and and_30 (sltu, and_19_out[0], and_19_out[1], not_11_out[4], and_19_out[3], not_11_out[8], and_19_out[5]);
  not not_15 (not_15_out, nop);
  or or_1 (or_1_out, MemtoReg, isImm, Reg);
  nor nor_4 (nor_4_out, nop, MemWrite);
  or or_2 (ExtOp[0], sltiu, andi, ori, xori);
  or or_3 (Branch, beq, bne, blez, bgtz, Br);
  ALUDecd aludecd_1 (.OpCode(Op), .Funct(funct), .RT(RT), .ALUCtrl(ALUCtrl));
  or or_4 (isImm, MemtoReg, addi_u, slti, sltiu, andi, ori, xori, ExtOp[1], MemWrite);
  and and_31 (RegDst, Reg, not_15_out);
  and and_32 (RegWrite, or_1_out, nor_4_out);

  // Other names for the same wires on the sheet: mid (some bits) = Op; lui = ExtOp[1]; j = jump; lw = MemtoReg;
  //   sw = MemWrite
endmodule

module test (
  output [31:0] out_1,
  output out_2,
  output [4:0] out_3,
  output [31:0] out_4,
  output out_5,
  output [4:0] out_6,
  output [31:0] out_7
);

  wire comparator_1_gt;
  wire [7:0] counter_1_q;

  Counter counter_1 (.Q(counter_1_q));  // open: load, D, count, carry, clk, clr
  Comparator comparator_1 (.a(8'h4), .b(counter_1_q), .gt(comparator_1_gt));  // open: eq, lt
  main main_1 (
    .Reset(comparator_1_gt), .out_2(out_1), .out_3(out_2), .out_4(out_3), .out_5(out_4), .out_6(out_5),
    .out_7(out_6), .out_8(out_7));
endmodule

module GRF (
  input  [4:0] A1,
  input  clk,
  input  reset,
  input  we,
  input  [4:0] A2,
  input  [4:0] A3,
  input  [31:0] WD,
  output [31:0] RD1,
  output [31:0] RD2
);

  wire [31:0] I0, I1, I2, I3, I4, I5, I6, I7, I8, I9, I10, I11, I12, I13, I14, I15, I16, I17, I18, I19, I20,
       I21, I22, I23, I24, I25, I26, I27, I28, I29, I30, I31, O0, O1, O2, O3, O4, O5, O6, O7, O8, O9, O10,
       O11, O12, O13, O14, O15, O16, O17, O18, O19, O20, O21, O22, O23, O24, O25, O26, O27, O28, O29, O30,
       O31;

  Demultiplexer #(.select(5), .width(32), .tristate("true")) demultiplexer_1 (
    .out0(I0), .out1(I1), .out2(I2), .out3(I3), .out4(I4), .out5(I5), .out6(I6), .out7(I7), .out8(I8),
    .out9(I9), .out10(I10), .out11(I11), .out12(I12), .out13(I13), .out14(I14), .out15(I15), .out16(I16),
    .out17(I17), .out18(I18), .out19(I19), .out20(I20), .out21(I21), .out22(I22), .out23(I23), .out24(I24),
    .out25(I25), .out26(I26), .out27(I27), .out28(I28), .out29(I29), .out30(I30), .out31(I31), .in(WD),
    .sel(A3));  // open: en
  Multiplexer #(.select(5), .width(32)) multiplexer_1 (
    .in0(O0), .in1(O1), .in2(O2), .in3(O3), .in4(O4), .in5(O5), .in6(O6), .in7(O7), .in8(O8), .in9(O9),
    .in10(O10), .in11(O11), .in12(O12), .in13(O13), .in14(O14), .in15(O15), .in16(O16), .in17(O17),
    .in18(O18), .in19(O19), .in20(O20), .in21(O21), .in22(O22), .in23(O23), .in24(O24), .in25(O25),
    .in26(O26), .in27(O27), .in28(O28), .in29(O29), .in30(O30), .in31(O31), .out(RD2), .sel(A2));  // open: en
  Multiplexer #(.select(5), .width(32)) multiplexer_2 (
    .in0(O0), .in1(O1), .in2(O2), .in3(O3), .in4(O4), .in5(O5), .in6(O6), .in7(O7), .in8(O8), .in9(O9),
    .in10(O10), .in11(O11), .in12(O12), .in13(O13), .in14(O14), .in15(O15), .in16(O16), .in17(O17),
    .in18(O18), .in19(O19), .in20(O20), .in21(O21), .in22(O22), .in23(O23), .in24(O24), .in25(O25),
    .in26(O26), .in27(O27), .in28(O28), .in29(O29), .in30(O30), .in31(O31), .out(RD1), .sel(A1));  // open: en
  Register #(.width(32)) register_1 (.D({32{1'b0}}), .en(we), .Q(O0), .clk(clk), .clr(reset));
  Register #(.width(32)) register_2 (.D(I8), .en(we), .Q(O8), .clk(clk), .clr(reset));
  Register #(.width(32)) register_3 (.D(I16), .en(we), .Q(O16), .clk(clk), .clr(reset));
  Register #(.width(32)) register_4 (.D(I24), .en(we), .Q(O24), .clk(clk), .clr(reset));
  Register #(.width(32)) register_5 (.D(I1), .en(we), .Q(O1), .clk(clk), .clr(reset));
  Register #(.width(32)) register_6 (.D(I9), .en(we), .Q(O9), .clk(clk), .clr(reset));
  Register #(.width(32)) register_7 (.D(I17), .en(we), .Q(O17), .clk(clk), .clr(reset));
  Register #(.width(32)) register_8 (.D(I25), .en(we), .Q(O25), .clk(clk), .clr(reset));
  Register #(.width(32)) register_9 (.D(I2), .en(we), .Q(O2), .clk(clk), .clr(reset));
  Register #(.width(32)) register_10 (.D(I10), .en(we), .Q(O10), .clk(clk), .clr(reset));
  Register #(.width(32)) register_11 (.D(I18), .en(we), .Q(O18), .clk(clk), .clr(reset));
  Register #(.width(32)) register_12 (.D(I26), .en(we), .Q(O26), .clk(clk), .clr(reset));
  Register #(.width(32)) register_13 (.D(I3), .en(we), .Q(O3), .clk(clk), .clr(reset));
  Register #(.width(32)) register_14 (.D(I11), .en(we), .Q(O11), .clk(clk), .clr(reset));
  Register #(.width(32)) register_15 (.D(I19), .en(we), .Q(O19), .clk(clk), .clr(reset));
  Register #(.width(32)) register_16 (.D(I27), .en(we), .Q(O27), .clk(clk), .clr(reset));
  Register #(.width(32)) register_17 (.D(I4), .en(we), .Q(O4), .clk(clk), .clr(reset));
  Register #(.width(32)) register_18 (.D(I12), .en(we), .Q(O12), .clk(clk), .clr(reset));
  Register #(.width(32)) register_19 (.D(I20), .en(we), .Q(O20), .clk(clk), .clr(reset));
  Register #(.width(32)) register_20 (.D(I28), .en(we), .Q(O28), .clk(clk), .clr(reset));
  Register #(.width(32)) register_21 (.D(I5), .en(we), .Q(O5), .clk(clk), .clr(reset));
  Register #(.width(32)) register_22 (.D(I13), .en(we), .Q(O13), .clk(clk), .clr(reset));
  Register #(.width(32)) register_23 (.D(I21), .en(we), .Q(O21), .clk(clk), .clr(reset));
  Register #(.width(32)) register_24 (.D(I29), .en(we), .Q(O29), .clk(clk), .clr(reset));
  Register #(.width(32)) register_25 (.D(I6), .en(we), .Q(O6), .clk(clk), .clr(reset));
  Register #(.width(32)) register_26 (.D(I14), .en(we), .Q(O14), .clk(clk), .clr(reset));
  Register #(.width(32)) register_27 (.D(I22), .en(we), .Q(O22), .clk(clk), .clr(reset));
  Register #(.width(32)) register_28 (.D(I30), .en(we), .Q(O30), .clk(clk), .clr(reset));
  Register #(.width(32)) register_29 (.D(I7), .en(we), .Q(O7), .clk(clk), .clr(reset));
  Register #(.width(32)) register_30 (.D(I15), .en(we), .Q(O15), .clk(clk), .clr(reset));
  Register #(.width(32)) register_31 (.D(I23), .en(we), .Q(O23), .clk(clk), .clr(reset));
  Register #(.width(32)) register_32 (.D(I31), .en(we), .Q(O31), .clk(clk), .clr(reset));
endmodule
