// Logisim project test3.circ as structural Verilog: 3 circuits, main circuit 状态转移
module \状态转移  (
  input  [1:0] n2,
  input  \input ,
  output [1:0] out_3
);

  wire and_1_out, and_2_out, and_3_out, and_4_out, and_5_out, and_6_out, not_1_out, not_2_out, not_3_out,
       not_4_out, not_5_out, not_6_out, not_7_out, not_8_out;

  not not_1 (not_1_out, n2[1]);
  not not_2 (not_2_out, n2[0]);
  not not_3 (not_3_out, n2[1]);
  not not_4 (not_4_out, n2[0]);
  not not_5 (not_5_out, n2[1]);
  not not_6 (not_6_out, \input );
  not not_7 (not_7_out, n2[0]);
  not not_8 (not_8_out, \input );
  and and_1 (and_1_out, not_1_out, n2[0]);
  and and_2 (and_2_out, n2[1], not_2_out);
  and and_3 (and_3_out, not_3_out, not_4_out, \input );
  and and_4 (and_4_out, not_5_out, n2[0], not_6_out);
  and and_5 (and_5_out, n2[1], not_7_out, not_8_out);
  and and_6 (and_6_out, n2[1], n2[0], \input );
  or or_1 (out_3[1], and_1_out, and_2_out);
  or or_2 (out_3[0], and_3_out, and_4_out, and_5_out, and_6_out);
endmodule

module \状态输出  (
  input  [1:0] n2,
  input  \input ,
  output [2:0] out_3
);

  wire and_1_out, and_2_out, and_3_out, and_4_out, and_5_out, and_6_out, not_1_out, not_2_out, not_3_out,
       not_4_out, not_5_out, not_6_out, not_7_out, not_8_out, not_9_out, not_10_out;

  not not_1 (not_1_out, n2[1]);
  not not_2 (not_2_out, \input );
  not not_3 (not_3_out, n2[0]);
  not not_4 (not_4_out, \input );
  not not_5 (not_5_out, n2[1]);
  not not_6 (not_6_out, n2[0]);
  not not_7 (not_7_out, \input );
  not not_8 (not_8_out, n2[1]);
  not not_9 (not_9_out, n2[0]);
  not not_10 (not_10_out, \input );
  and and_1 (and_1_out, not_1_out, n2[0], not_2_out);
  and and_2 (and_2_out, n2[1], not_3_out, not_4_out);
  and and_3 (and_3_out, not_5_out, not_6_out, not_7_out);
  and and_4 (and_4_out, not_8_out, n2[0], \input );
  and and_5 (and_5_out, n2[1], not_9_out, \input );
  and and_6 (and_6_out, n2[1], n2[0], not_10_out);
  or or_1 (out_3[2], and_1_out, and_2_out);
  or or_2 (out_3[0], and_3_out, and_4_out, and_5_out, and_6_out);

  assign out_3[1] = \input ;
endmodule

module _2nmod5 (
  input  in_1,
  output [2:0] out_2
);

  wire clock_1_out;
  wire [1:0] register_1_q, \状态转移_1_out_3 ;

  \状态转移  \u_状态转移_1  (.n2(register_1_q), .\input (in_1), .out_3(\状态转移_1_out_3 ));
  Clock clock_1 (.out(clock_1_out));
  Register #(.width(2)) register_1 (.D(\状态转移_1_out_3 ), .Q(register_1_q), .clk(clock_1_out));  // open: en, clr
  \状态输出  \u_状态输出_1  (.n2(register_1_q), .\input (in_1), .out_3(out_2));
endmodule
