// Logisim project test5.circ as structural Verilog: 1 circuit, main circuit sort
module sort (
  input  [3:0] in_1,
  input  [3:0] in_2,
  input  [3:0] in_3,
  input  [3:0] in_4,
  output [3:0] out_5,
  output [3:0] out_6,
  output [3:0] out_7,
  output [3:0] out_8
);

  wire comparator_1_lt, comparator_2_lt, comparator_3_lt, comparator_4_lt, comparator_5_lt;
  wire [3:0] multiplexer_1_out, multiplexer_2_out, multiplexer_3_out, multiplexer_4_out, multiplexer_5_out,
       multiplexer_7_out;

  Comparator #(.width(4), .mode("unsigned")) comparator_1 (.a(in_1), .b(in_2), .lt(comparator_1_lt));  // open: gt, eq
  Comparator #(.width(4), .mode("unsigned")) comparator_2 (.a(in_3), .b(in_4), .lt(comparator_2_lt));  // open: gt, eq
  Multiplexer #(.width(4)) multiplexer_1 (
    .in0(in_1), .in1(in_2), .out(multiplexer_1_out), .sel(comparator_1_lt));  // open: en
  Multiplexer #(.width(4)) multiplexer_2 (
    .in0(in_2), .in1(in_1), .out(multiplexer_2_out), .sel(comparator_1_lt));  // open: en
  Multiplexer #(.width(4)) multiplexer_3 (
    .in0(in_3), .in1(in_4), .out(multiplexer_3_out), .sel(comparator_2_lt));  // open: en
  Multiplexer #(.width(4)) multiplexer_4 (
    .in0(in_4), .in1(in_3), .out(multiplexer_4_out), .sel(comparator_2_lt));  // open: en
  Comparator #(.width(4), .mode("unsigned")) comparator_3 (
    .a(multiplexer_1_out), .b(multiplexer_3_out), .lt(comparator_3_lt));  // open: gt, eq
  Comparator #(.width(4), .mode("unsigned")) comparator_4 (
    .a(multiplexer_2_out), .b(multiplexer_4_out), .lt(comparator_4_lt));  // open: gt, eq
  Multiplexer #(.width(4)) multiplexer_5 (
    .in0(multiplexer_3_out), .in1(multiplexer_1_out), .out(multiplexer_5_out), .sel(comparator_3_lt));  // open: en
  Multiplexer #(.width(4)) multiplexer_6 (
    .in0(multiplexer_1_out), .in1(multiplexer_3_out), .out(out_5), .sel(comparator_3_lt));  // open: en
  Multiplexer #(.width(4)) multiplexer_7 (
    .in0(multiplexer_2_out), .in1(multiplexer_4_out), .out(multiplexer_7_out), .sel(comparator_4_lt));  // open: en
  Multiplexer #(.width(4)) multiplexer_8 (
    .in0(multiplexer_4_out), .in1(multiplexer_2_out), .out(out_8), .sel(comparator_4_lt));  // open: en
  Comparator #(.width(4), .mode("unsigned")) comparator_5 (
    .a(multiplexer_5_out), .b(multiplexer_7_out), .lt(comparator_5_lt));  // open: gt, eq
  Multiplexer #(.width(4)) multiplexer_9 (
    .in0(multiplexer_5_out), .in1(multiplexer_7_out), .out(out_6), .sel(comparator_5_lt));  // open: en
  Multiplexer #(.width(4)) multiplexer_10 (
    .in0(multiplexer_7_out), .in1(multiplexer_5_out), .out(out_7), .sel(comparator_5_lt));  // open: en
endmodule
