// Logisim project text.circ as structural Verilog: 1 circuit, main circuit vote0
module vote0 (
  input  in_1,
  input  in_2,
  input  in_3,
  input  in_4,
  input  in_5,
  output out_6
);

  wire and_1_out, and_2_out, and_3_out, and_4_out, and_5_out, and_6_out, and_7_out, and_8_out, and_9_out,
       and_10_out;

  and and_1 (and_1_out, in_1, in_2, in_3);
  and and_2 (and_2_out, in_1, in_2, in_4);
  and and_3 (and_3_out, in_1, in_2, in_5);
  and and_4 (and_4_out, in_1, in_3, in_4);
  and and_5 (and_5_out, in_1, in_3, in_5);
  and and_6 (and_6_out, in_1, in_4, in_5);
  and and_7 (and_7_out, in_2, in_3, in_4);
  and and_8 (and_8_out, in_2, in_3, in_5);
  and and_9 (and_9_out, in_2, in_4, in_5);
  and and_10 (and_10_out, in_3, in_4, in_5);
  or or_1 (out_6, and_1_out, and_2_out, and_3_out, and_4_out, and_5_out, and_6_out, and_7_out, and_8_out, and_9_out, and_10_out);
endmodule
